// Logisim project console.circ as structural Verilog: 1 circuit, main circuit main
module main (
  input  in_1,
  input  in_2,
  input  in_3
);

  wire and_1_out, uart_1_p3, uart_1_p6;
  wire [7:0] register_1_q, uart_1_p1;

  Register register_1 (.D(uart_1_p1), .Q(register_1_q), .clk(and_1_out));  // open: en, clr
  and and_1 (and_1_out, uart_1_p3, in_2);
  // UART uart_1: pin names not known; wires that end beside it: uart_1_p1, register_1_q, uart_1_p3, in_2, in_3, uart_1_p6, uart_1_p6, in_1
endmodule
