// Logisim project Minimap.circ as structural Verilog: 9 circuits, main circuit maps
// Maps
module maps (
  input  [7:0] ADDR,
  input  [11:0] ELEM,
  output [11:0] Width,
  output [11:0] Height,
  output [7:0] Xpp,
  output [7:0] Ypp,
  output [7:0] DATA,
  output [11:0] LEN
);

  wire [7:0] mgeD0, mgeD1, mgeD2, undriven_4, undriven_5;
  wire [11:0] undriven, undriven_2, undriven_3;

  ROM #(.addrWidth(12)) rom_1 (.addr(ELEM), .data(mgeD0));  // open: sel
  ROM #(.addrWidth(12)) rom_2 (.addr(ELEM), .data(mgeD1));  // open: sel
  ROM #(.addrWidth(12)) rom_3 (.addr(ELEM), .data(mgeD2));  // open: sel
  Multiplexer #(.select(5), .width(8), .enable("false")) multiplexer_1 (
    .in0(mgeD0), .in1(mgeD1), .in2(mgeD2), .out(DATA), .sel(ADDR[4:0]));  // open: in3, in4, in5, in6, in7, in8, in9, in10, in11, in12, in13, in14, in15, in16, in17, in18, in19, in20, in21, in22, in23, in24, in25, in26, in27, in28, in29, in30, in31
  Multiplexer #(.select(5), .width(12), .enable("false")) multiplexer_2 (
    .in0(12'h64), .in1(12'h2e5), .in2(12'hab), .in30(undriven), .in31(undriven), .out(LEN), .sel(ADDR[4:0]));  // open: in3, in4, in5, in6, in7, in8, in9, in10, in11, in12, in13, in14, in15, in16, in17, in18, in19, in20, in21, in22, in23, in24, in25, in26, in27, in28, in29
  Multiplexer #(.select(5), .width(12), .enable("false")) multiplexer_3 (
    .in0(12'hb), .in1(12'h25), .in2(12'h11), .in30(undriven_2), .in31(undriven_2), .out(Width),
    .sel(ADDR[4:0]));  // open: in3, in4, in5, in6, in7, in8, in9, in10, in11, in12, in13, in14, in15, in16, in17, in18, in19, in20, in21, in22, in23, in24, in25, in26, in27, in28, in29
  Multiplexer #(.select(5), .width(12), .enable("false")) multiplexer_4 (
    .in0(12'h8), .in1(12'h14), .in2(12'ha), .in30(undriven_3), .in31(undriven_3), .out(Height),
    .sel(ADDR[4:0]));  // open: in3, in4, in5, in6, in7, in8, in9, in10, in11, in12, in13, in14, in15, in16, in17, in18, in19, in20, in21, in22, in23, in24, in25, in26, in27, in28, in29
  Multiplexer #(.select(5), .width(8), .enable("false")) multiplexer_5 (
    .in0(8'h4), .in1(8'h13), .in2(8'h4), .in30(undriven_4), .in31(undriven_4), .out(Xpp), .sel(ADDR[4:0]));  // open: in3, in4, in5, in6, in7, in8, in9, in10, in11, in12, in13, in14, in15, in16, in17, in18, in19, in20, in21, in22, in23, in24, in25, in26, in27, in28, in29
  Multiplexer #(.select(5), .width(8), .enable("false")) multiplexer_6 (
    .in0(8'h3), .in1(8'hc), .in2(8'h4), .in30(undriven_5), .in31(undriven_5), .out(Ypp), .sel(ADDR[4:0]));  // open: in3, in4, in5, in6, in7, in8, in9, in10, in11, in12, in13, in14, in15, in16, in17, in18, in19, in20, in21, in22, in23, in24, in25, in26, in27, in28, in29

  // Other names for the same wires on the sheet: mdeMux1[7:0] = DATA; mdeMuxl1[11:0] = LEN; mgeAddr1[4:0] = ADDR[4:0];
  //   mgeEl[11:0] = ELEM; mhMuxl1[11:0] = Height; mwMuxl1[11:0] = Width; mXMuxl1[7:0] = Xpp; mYMuxl1[7:0] = Ypp

  // Notes on the sheet:
  //   TEST MAP
  //   Level 1
  //   Level 2
  //   contents of rom_1 (hex, n*v repeats v):
  //   36*23 20 66 6a 61 20 6*23 20 23 23 20 32 6*23 20 20 23 23 20 36*23
  //   contents of rom_2 (hex, n*v repeats v):
  //   114*23 20 45 23 63 4*20 23 20 20 20 23 20 20 20 23 4*20 23 20 62 20 20 32 31 31 31 68 6*23 20 23 23
  //   20 23 23 23 20 23 20 23 63 23 20 23 20 20 20 23 23 20 23 23 20 23 20 11*23 33 23 23 20 20 20 23 20
  //   31 20 23 20 20 20 5*23 20 20 20 32 20 23 4*20 23 67 6*23 20 64 23 23 23 20 5*23 20 4*23 20 20 23 20
  //   5*23 20 23 20 20 23 34 6*23 34 23 23 20 20 20 23 20 23 23 23 20 20 62 20 23 20 4*23 20 20 20 23 23
  //   23 20 23 23 32 6*23 34 23 23 20 23 20 23 20 20 20 23 20 20 23 31 23 20 23 23 20 23 20 23 5*20 62 20
  //   20 6*23 4*20 23 20 20 20 23 20 20 61 23 23 20 23 20 23 4*20 15*23 20 5*23 20 23 23 31 23 23 23 4*20
  //   23 32 23 23 4*20 64 23 4*20 6*23 31 23 23 4*20 23 6*20 4*23 20 23 23 23 20 4*23 20 23 20 7*23 20 23
  //   23 20 23 20 9*23 66 4*20 6a 23 6*20 23 20 20 6*23 20 23 20 20 23 20 20 23 20 23 23 20 20 23 23 20
  //   6*23 20 23 20 5*23 20 6*23 20 23 23 20 4*23 20 31 20 20 20 23 62 8*20 23 5*20 23 31 6*23 20 23 23 32
  //   20 20 20 23 20 7*23 20 23 23 23 20 23 20 5*23 20 23 20 6*23 20 20 20 61 23 7*20 62 5*20 23 20 20 20
  //   31 32 20 69 20 23 20 20 63 114*23
  //   contents of rom_3 (hex, n*v repeats v):
  //   54*23 4*20 23 20 20 23 20 20 20 6*23 20 20 23 4*20 45 20 23 20 6*23 20 20 8*23 20 6*23 11*20 54*23
  //   Возращает данные карты по адресу
  //   Предоставляет поэлементный доступ к ее элеменнтам
endmodule

module x_y__to_memory_elem_number (
  input  [11:0] H,
  input  [7:0] Y,
  input  [7:0] X,
  output [11:0] ELEM
);

  wire [11:0] bit_extender_1_out, bit_extender_2_out, multiplier_1_out;

  assign bit_extender_1_out = {{4{1'b0}}, Y};  // Bit_Extender bit_extender_1
  Multiplier #(.width(12)) multiplier_1 (.a(H), .b(bit_extender_1_out), .out(multiplier_1_out));  // open: cin, cout
  assign bit_extender_2_out = {{4{1'b0}}, X};  // Bit_Extender bit_extender_2
  Adder #(.width(12)) adder_1 (.a(multiplier_1_out), .b(bit_extender_2_out), .out(ELEM));  // open: cin, cout

  // Notes on the sheet:
  //   Переводит координаты ячейки в номер в массиве
  //   H - ширина карты
endmodule

module cond_en_weap (
  input  Error_undefined_byte,
  input  [1:0] input_char,
  output todisplay,
  output Exit
);

  wire comparator_1_eq, comparator_2_eq, comparator_4_eq, or_1_out;

  Comparator #(.width(2), .mode("unsigned")) comparator_1 (
    .a(input_char), .b(2'b00), .eq(comparator_1_eq));  // open: gt, lt
  Comparator #(.width(2), .mode("unsigned")) comparator_2 (
    .a(input_char), .b(2'b01), .eq(comparator_2_eq));  // open: gt, lt
  Comparator #(.width(2), .mode("unsigned")) comparator_3 (.a(input_char), .b(2'b10), .eq(Exit));  // open: gt, lt
  Comparator #(.width(2), .mode("unsigned")) comparator_4 (
    .a(input_char), .b(2'b11), .eq(comparator_4_eq));  // open: gt, lt
  or or_1 (or_1_out, comparator_1_eq, Exit);
  assign todisplay = or_1_out ? 1'b0 : 1'bz;  // Controlled_Buffer controlled_buffer_1
  assign todisplay = comparator_4_eq ? Error_undefined_byte : 1'bz;  // Controlled_Buffer controlled_buffer_2
  assign todisplay = comparator_2_eq ? 1'b1 : 1'bz;  // Controlled_Buffer controlled_buffer_3
endmodule

module cond_wall_pass (
  input  [7:0] in_1,
  output out
);

  wire comparator_1_eq, not_1_out;

  Comparator comparator_1 (.a(in_1), .b(8'h23), .eq(comparator_1_eq));  // open: gt, lt
  assign out = comparator_1_eq ? 1'b0 : 1'bz;  // Controlled_Buffer controlled_buffer_1
  assign out = not_1_out ? 1'b1 : 1'bz;  // Controlled_Buffer controlled_buffer_2
  not not_1 (not_1_out, comparator_1_eq);
endmodule

module plr_in_cond_of_dir (
  input  [1:0] in_1,
  output [1:0] out_2,
  output [1:0] out_3
);

  wire comparator_1_eq, comparator_2_eq, comparator_3_eq, comparator_4_eq;

  Comparator #(.width(2), .mode("unsigned")) comparator_1 (.a(in_1), .b(2'b00), .eq(comparator_1_eq));  // open: gt, lt
  Comparator #(.width(2), .mode("unsigned")) comparator_2 (.a(in_1), .b(2'b01), .eq(comparator_2_eq));  // open: gt, lt
  Comparator #(.width(2), .mode("unsigned")) comparator_3 (.a(in_1), .b(2'b10), .eq(comparator_3_eq));  // open: gt, lt
  Comparator #(.width(2), .mode("unsigned")) comparator_4 (.a(in_1), .b(2'b11), .eq(comparator_4_eq));  // open: gt, lt
  assign out_2 = comparator_2_eq ? 2'b01 : 2'bz;  // Controlled_Buffer controlled_buffer_1
  assign out_2 = comparator_1_eq ? 2'b11 : 2'bz;  // Controlled_Buffer controlled_buffer_2
  assign out_3 = comparator_1_eq ? 2'b00 : 2'bz;  // Controlled_Buffer controlled_buffer_3
  assign out_2 = comparator_3_eq ? 2'b00 : 2'bz;  // Controlled_Buffer controlled_buffer_4
  assign out_2 = comparator_4_eq ? 2'b10 : 2'bz;  // Controlled_Buffer controlled_buffer_5
  assign out_3 = comparator_4_eq ? 2'b10 : 2'bz;  // Controlled_Buffer controlled_buffer_6
  assign out_3 = comparator_3_eq ? 2'b11 : 2'bz;  // Controlled_Buffer controlled_buffer_7
  assign out_3 = comparator_2_eq ? 2'b01 : 2'bz;  // Controlled_Buffer controlled_buffer_8
endmodule

module mmap_matrix (
  input  [7:0] No_of_map,
  input  [7:0] Xpp,
  input  [7:0] Ypp,
  output [7:0] out_4,
  output [7:0] out_5,
  output [7:0] out_6,
  output [7:0] out_7,
  output [7:0] out_8,
  output [7:0] out_9,
  output [7:0] out_10,
  output [7:0] out_11,
  output [7:0] out_12,
  output [7:0] out_13,
  output [7:0] out_14,
  output [7:0] out_15,
  output [7:0] out_16,
  output [7:0] out_17,
  output [7:0] out_18,
  output [7:0] out_19,
  output [7:0] out_20,
  output [7:0] out_21,
  output [7:0] out_22,
  output [7:0] out_23,
  output [7:0] out_24,
  output [7:0] out_25,
  output [7:0] out_26,
  output [7:0] out_27,
  output [7:0] out_28,
  output [7:0] out_29,
  output [7:0] out_30,
  output [7:0] out_31,
  output [7:0] out_32,
  output [7:0] out_33,
  output [7:0] out_34,
  output [7:0] out_35,
  output [7:0] out_36,
  output [7:0] out_37,
  output [7:0] out_38,
  output [7:0] out_39,
  output [7:0] out_40,
  output [7:0] out_41,
  output [7:0] out_42,
  output [7:0] out_43,
  output [7:0] out_44,
  output [7:0] out_45,
  output [7:0] out_46,
  output [7:0] out_47,
  output [7:0] out_48,
  output [7:0] out_49,
  output [7:0] out_50,
  output [7:0] out_51,
  output [7:0] out_52
);

  wire maps_32_p3;
  wire [11:0] adder_21_out, adder_36_out, addr0, addr1, addr2, addr3, addr4, addr5, addr6, multiplier_1_out,
       num1, num2, num3, num4, num5, num6, num7, num8, num9, num10, num11, num12, num13, num14, num15, num16,
       num17, num18, num19, num20, num21, num22, num23, num24, num25, num26, num27, num28, num29, num30,
       num31, num32, num33, num34, num35, num36, num37, num38, num39, num40, num41, num42, num43, num44,
       num45, num46, num47, num48, num49, Width;

  Adder #(.width(12)) adder_1 (.a(addr0), .b(Width), .out(addr1));  // open: cin, cout
  Adder #(.width(12)) adder_2 (.a(addr1), .b(Width), .out(addr2));  // open: cin, cout
  Adder #(.width(12)) adder_3 (.a(addr2), .b(Width), .out(addr3));  // open: cin, cout
  Adder #(.width(12)) adder_4 (.a(addr3), .b(Width), .out(addr4));  // open: cin, cout
  Adder #(.width(12)) adder_5 (.a(addr4), .b(Width), .out(addr5));  // open: cin, cout
  Adder #(.width(12)) adder_6 (.a(addr5), .b(Width), .out(addr6));  // open: cin, cout
  Adder #(.width(12)) adder_7 (.a(addr0), .b({12{1'b0}}), .out(num1));  // open: cin, cout
  Adder #(.width(12)) adder_8 (.a(addr0), .b(12'h1), .out(num2));  // open: cin, cout
  Adder #(.width(12)) adder_9 (.a(addr0), .b(12'h2), .out(num3));  // open: cin, cout
  Adder #(.width(12)) adder_10 (.a(addr0), .b(12'h3), .out(num4));  // open: cin, cout
  Adder #(.width(12)) adder_11 (.a(addr0), .b(12'h4), .out(num5));  // open: cin, cout
  Adder #(.width(12)) adder_12 (.a(addr0), .b(12'h5), .out(num6));  // open: cin, cout
  Adder #(.width(12)) adder_13 (.a(addr0), .b(12'h6), .out(num7));  // open: cin, cout
  Adder #(.width(12)) adder_14 (.a(addr1), .b({12{1'b0}}), .out(num8));  // open: cin, cout
  Adder #(.width(12)) adder_15 (.a(addr1), .b(12'h1), .out(num9));  // open: cin, cout
  Adder #(.width(12)) adder_16 (.a(addr1), .b(12'h2), .out(num10));  // open: cin, cout
  Adder #(.width(12)) adder_17 (.a(addr1), .b(12'h3), .out(num11));  // open: cin, cout
  Adder #(.width(12)) adder_18 (.a(addr1), .b(12'h4), .out(num12));  // open: cin, cout
  Adder #(.width(12)) adder_19 (.a(addr1), .b(12'h5), .out(num13));  // open: cin, cout
  Adder #(.width(12)) adder_20 (.a(addr1), .b(12'h6), .out(num14));  // open: cin, cout
  Adder #(.width(12)) adder_21 (.a({4'b0000, Ypp}), .b(12'hffd), .out(adder_21_out));  // open: cin, cout
  Adder #(.width(12)) adder_22 (.a(addr2), .b({12{1'b0}}), .out(num15));  // open: cin, cout
  Adder #(.width(12)) adder_23 (.a(addr2), .b(12'h1), .out(num16));  // open: cin, cout
  Adder #(.width(12)) adder_24 (.a(addr2), .b(12'h2), .out(num17));  // open: cin, cout
  Adder #(.width(12)) adder_25 (.a(addr2), .b(12'h3), .out(num18));  // open: cin, cout
  Adder #(.width(12)) adder_26 (.a(addr2), .b(12'h4), .out(num19));  // open: cin, cout
  Adder #(.width(12)) adder_27 (.a(addr2), .b(12'h5), .out(num20));  // open: cin, cout
  Adder #(.width(12)) adder_28 (.a(addr2), .b(12'h6), .out(num21));  // open: cin, cout
  Adder #(.width(12)) adder_29 (.a(addr3), .b({12{1'b0}}), .out(num22));  // open: cin, cout
  Adder #(.width(12)) adder_30 (.a(addr3), .b(12'h1), .out(num23));  // open: cin, cout
  Adder #(.width(12)) adder_31 (.a(addr3), .b(12'h2), .out(num24));  // open: cin, cout
  Adder #(.width(12)) adder_32 (.a(addr3), .b(12'h3), .out(num25));  // open: cin, cout
  Adder #(.width(12)) adder_33 (.a(addr3), .b(12'h4), .out(num26));  // open: cin, cout
  Adder #(.width(12)) adder_34 (.a(addr3), .b(12'h5), .out(num27));  // open: cin, cout
  Adder #(.width(12)) adder_35 (.a(addr3), .b(12'h6), .out(num28));  // open: cin, cout
  Adder #(.width(12)) adder_36 (.a({4'b0000, Xpp}), .b(12'hffd), .out(adder_36_out));  // open: cin, cout
  Multiplier #(.width(12)) multiplier_1 (.a(Width), .b(adder_21_out), .out(multiplier_1_out));  // open: cin, cout
  // Probe on multiplier_1_out
  Adder #(.width(12)) adder_37 (.a(addr4), .b({12{1'b0}}), .out(num29));  // open: cin, cout
  Adder #(.width(12)) adder_38 (.a(addr4), .b(12'h1), .out(num30));  // open: cin, cout
  Adder #(.width(12)) adder_39 (.a(addr4), .b(12'h2), .out(num31));  // open: cin, cout
  Adder #(.width(12)) adder_40 (.a(addr4), .b(12'h3), .out(num32));  // open: cin, cout
  Adder #(.width(12)) adder_41 (.a(addr4), .b(12'h4), .out(num33));  // open: cin, cout
  Adder #(.width(12)) adder_42 (.a(addr4), .b(12'h5), .out(num34));  // open: cin, cout
  Adder #(.width(12)) adder_43 (.a(addr4), .b(12'h6), .out(num35));  // open: cin, cout
  Adder #(.width(12)) adder_44 (.a(addr5), .b({12{1'b0}}), .out(num36));  // open: cin, cout
  Adder #(.width(12)) adder_45 (.a(addr5), .b(12'h1), .out(num37));  // open: cin, cout
  Adder #(.width(12)) adder_46 (.a(addr5), .b(12'h2), .out(num38));  // open: cin, cout
  Adder #(.width(12)) adder_47 (.a(addr5), .b(12'h3), .out(num39));  // open: cin, cout
  Adder #(.width(12)) adder_48 (.a(addr5), .b(12'h4), .out(num40));  // open: cin, cout
  Adder #(.width(12)) adder_49 (.a(addr5), .b(12'h5), .out(num41));  // open: cin, cout
  Adder #(.width(12)) adder_50 (.a(addr5), .b(12'h6), .out(num42));  // open: cin, cout
  // Probe on addr0
  Adder #(.width(12)) adder_51 (.a(adder_36_out), .b(multiplier_1_out), .out(addr0));  // open: cin, cout
  Adder #(.width(12)) adder_52 (.a(addr6), .b({12{1'b0}}), .out(num43));  // open: cin, cout
  Adder #(.width(12)) adder_53 (.a(addr6), .b(12'h1), .out(num44));  // open: cin, cout
  Adder #(.width(12)) adder_54 (.a(addr6), .b(12'h2), .out(num45));  // open: cin, cout
  Adder #(.width(12)) adder_55 (.a(addr6), .b(12'h3), .out(num46));  // open: cin, cout
  Adder #(.width(12)) adder_56 (.a(addr6), .b(12'h4), .out(num47));  // open: cin, cout
  Adder #(.width(12)) adder_57 (.a(addr6), .b(12'h5), .out(num48));  // open: cin, cout
  Adder #(.width(12)) adder_58 (.a(addr6), .b(12'h6), .out(num49));  // open: cin, cout
  maps maps_1 (.ADDR(No_of_map), .ELEM(num3), .DATA(out_18));  // open: Width, Height, Xpp, Ypp, LEN
  maps maps_2 (.ADDR(No_of_map), .ELEM(num4), .DATA(out_25));  // open: Width, Height, Xpp, Ypp, LEN
  maps maps_3 (.ADDR(No_of_map), .ELEM(num5), .DATA(out_32));  // open: Width, Height, Xpp, Ypp, LEN
  maps maps_4 (.ADDR(No_of_map), .ELEM(num6), .DATA(out_39));  // open: Width, Height, Xpp, Ypp, LEN
  maps maps_5 (.ADDR(No_of_map), .ELEM(num7), .DATA(out_46));  // open: Width, Height, Xpp, Ypp, LEN
  maps maps_6 (.ADDR(No_of_map), .ELEM(num1), .Width(Width), .DATA(out_4));  // open: Height, Xpp, Ypp, LEN
  // Probe on out_4
  maps maps_7 (.ADDR(No_of_map), .ELEM(num2), .DATA(out_11));  // open: Width, Height, Xpp, Ypp, LEN
  // Probe on out_11
  // Probe on out_18
  // Probe on out_25
  // Probe on out_32
  // Probe on out_39
  // Probe on out_46
  maps maps_8 (.ADDR(No_of_map), .ELEM(num8), .DATA(out_5));  // open: Width, Height, Xpp, Ypp, LEN
  // Probe on out_5
  maps maps_9 (.ADDR(No_of_map), .ELEM(num9), .DATA(out_12));  // open: Width, Height, Xpp, Ypp, LEN
  // Probe on out_12
  maps maps_10 (.ADDR(No_of_map), .ELEM(num10), .DATA(out_19));  // open: Width, Height, Xpp, Ypp, LEN
  // Probe on out_19
  // Probe on out_26
  maps maps_11 (.ADDR(No_of_map), .ELEM(num11), .DATA(out_26));  // open: Width, Height, Xpp, Ypp, LEN
  maps maps_12 (.ADDR(No_of_map), .ELEM(num12), .DATA(out_33));  // open: Width, Height, Xpp, Ypp, LEN
  // Probe on out_33
  // Probe on out_40
  maps maps_13 (.ADDR(No_of_map), .ELEM(num13), .DATA(out_40));  // open: Width, Height, Xpp, Ypp, LEN
  maps maps_14 (.ADDR(No_of_map), .ELEM(num14), .DATA(out_47));  // open: Width, Height, Xpp, Ypp, LEN
  // Probe on out_47
  // Probe on num15
  // Probe on num16
  // Probe on num17
  // Probe on num18
  // Probe on num19
  // Probe on num20
  // Probe on num21
  maps maps_15 (.ADDR(No_of_map), .ELEM(num15), .DATA(out_6));  // open: Width, Height, Xpp, Ypp, LEN
  // Probe on out_6
  maps maps_16 (.ADDR(No_of_map), .ELEM(num16), .DATA(out_13));  // open: Width, Height, Xpp, Ypp, LEN
  // Probe on out_13
  // Probe on out_20
  maps maps_17 (.ADDR(No_of_map), .ELEM(num17), .DATA(out_20));  // open: Width, Height, Xpp, Ypp, LEN
  // Probe on out_27
  maps maps_18 (.ADDR(No_of_map), .ELEM(num18), .DATA(out_27));  // open: Width, Height, Xpp, Ypp, LEN
  // Probe on out_34
  maps maps_19 (.ADDR(No_of_map), .ELEM(num19), .DATA(out_34));  // open: Width, Height, Xpp, Ypp, LEN
  maps maps_20 (.ADDR(No_of_map), .ELEM(num20), .DATA(out_41));  // open: Width, Height, Xpp, Ypp, LEN
  // Probe on out_41
  maps maps_21 (.ADDR(No_of_map), .ELEM(num21), .DATA(out_48));  // open: Width, Height, Xpp, Ypp, LEN
  // Probe on out_48
  // Probe on num22
  // Probe on num23
  // Probe on num24
  // Probe on num25
  // Probe on num26
  // Probe on num27
  // Probe on num28
  maps maps_22 (.ADDR(No_of_map), .ELEM(num22), .DATA(out_7));  // open: Width, Height, Xpp, Ypp, LEN
  maps maps_23 (.ADDR(No_of_map), .ELEM(num23), .DATA(out_14));  // open: Width, Height, Xpp, Ypp, LEN
  maps maps_24 (.ADDR(No_of_map), .ELEM(num24), .DATA(out_21));  // open: Width, Height, Xpp, Ypp, LEN
  maps maps_25 (.ADDR(No_of_map), .ELEM(num25), .DATA(out_28));  // open: Width, Height, Xpp, Ypp, LEN
  maps maps_26 (.ADDR(No_of_map), .ELEM(num26), .DATA(out_35));  // open: Width, Height, Xpp, Ypp, LEN
  maps maps_27 (.ADDR(No_of_map), .ELEM(num27), .DATA(out_42));  // open: Width, Height, Xpp, Ypp, LEN
  maps maps_28 (.ADDR(No_of_map), .ELEM(num28), .DATA(out_49));  // open: Width, Height, Xpp, Ypp, LEN
  // Probe on out_7
  // Probe on out_14
  // Probe on out_21
  // Probe on out_28
  // Probe on out_35
  // Probe on out_42
  // Probe on out_49
  // Probe on num29
  // Probe on num30
  // Probe on num31
  // Probe on num32
  // Probe on num33
  // Probe on num34
  // Probe on num35
  maps maps_29 (.ADDR(No_of_map), .ELEM(num29), .DATA(out_8));  // open: Width, Height, Xpp, Ypp, LEN
  maps maps_30 (.ADDR(No_of_map), .ELEM(num30), .DATA(out_15));  // open: Width, Height, Xpp, Ypp, LEN
  maps maps_31 (.ADDR(No_of_map), .ELEM(num31), .DATA(out_22));  // open: Width, Height, Xpp, Ypp, LEN
  // maps maps_32: pin names not known; wires that end beside it: No_of_map, num32, maps_32_p3, out_29, maps_32_p3
  maps maps_33 (.ADDR(No_of_map), .ELEM(num33), .DATA(out_36));  // open: Width, Height, Xpp, Ypp, LEN
  maps maps_34 (.ADDR(No_of_map), .ELEM(num34), .DATA(out_43));  // open: Width, Height, Xpp, Ypp, LEN
  maps maps_35 (.ADDR(No_of_map), .ELEM(num35), .DATA(out_50));  // open: Width, Height, Xpp, Ypp, LEN
  // Probe on out_8
  // Probe on out_15
  // Probe on out_22
  // Probe on out_29
  // Probe on out_36
  // Probe on out_43
  // Probe on out_50
  // Probe on num36
  // Probe on num37
  // Probe on num38
  // Probe on num39
  // Probe on num40
  // Probe on num41
  // Probe on num42
  maps maps_36 (.ADDR(No_of_map), .ELEM(num36), .DATA(out_9));  // open: Width, Height, Xpp, Ypp, LEN
  maps maps_37 (.ADDR(No_of_map), .ELEM(num37), .DATA(out_16));  // open: Width, Height, Xpp, Ypp, LEN
  maps maps_38 (.ADDR(No_of_map), .ELEM(num38), .DATA(out_23));  // open: Width, Height, Xpp, Ypp, LEN
  maps maps_39 (.ADDR(No_of_map), .ELEM(num39), .DATA(out_30));  // open: Width, Height, Xpp, Ypp, LEN
  maps maps_40 (.ADDR(No_of_map), .ELEM(num40), .DATA(out_37));  // open: Width, Height, Xpp, Ypp, LEN
  maps maps_41 (.ADDR(No_of_map), .ELEM(num41), .DATA(out_44));  // open: Width, Height, Xpp, Ypp, LEN
  maps maps_42 (.ADDR(No_of_map), .ELEM(num42), .DATA(out_51));  // open: Width, Height, Xpp, Ypp, LEN
  // Probe on out_9
  // Probe on out_16
  // Probe on out_23
  // Probe on out_30
  // Probe on out_37
  // Probe on out_44
  // Probe on out_51
  // Probe on num43
  // Probe on num44
  // Probe on num45
  // Probe on num46
  // Probe on num47
  // Probe on num48
  // Probe on num49
  maps maps_43 (.ADDR(No_of_map), .ELEM(num43), .DATA(out_10));  // open: Width, Height, Xpp, Ypp, LEN
  maps maps_44 (.ADDR(No_of_map), .ELEM(num44), .DATA(out_17));  // open: Width, Height, Xpp, Ypp, LEN
  maps maps_45 (.ADDR(No_of_map), .ELEM(num45), .DATA(out_24));  // open: Width, Height, Xpp, Ypp, LEN
  maps maps_46 (.ADDR(No_of_map), .ELEM(num46), .DATA(out_31));  // open: Width, Height, Xpp, Ypp, LEN
  maps maps_47 (.ADDR(No_of_map), .ELEM(num47), .DATA(out_38));  // open: Width, Height, Xpp, Ypp, LEN
  maps maps_48 (.ADDR(No_of_map), .ELEM(num48), .DATA(out_45));  // open: Width, Height, Xpp, Ypp, LEN
  maps maps_49 (.ADDR(No_of_map), .ELEM(num49), .DATA(out_52));  // open: Width, Height, Xpp, Ypp, LEN
  // Probe on out_10
  // Probe on out_17
  // Probe on out_24
  // Probe on out_31
  // Probe on out_38
  // Probe on out_45
  // Probe on out_52

  // Other names for the same wires on the sheet: No[7:0] = No_of_map
endmodule

module driver_mm (
  input  [25:0] Bus1,
  input  [16:0] Bus2,
  output [17:0] out_3,
  output [17:0] out_4,
  output [15:0] out_5,
  output [17:0] out_6,
  output [15:0] out_7,
  output [17:0] out_8,
  output [17:0] out_9,
  output [17:0] out_10,
  output [13:0] out_11,
  output [17:0] out_12,
  output [15:0] out_13,
  output [1:0] out_14,
  output [13:0] out_15,
  output [15:0] out_16,
  output [1:0] out_17,
  output [17:0] out_18,
  output [13:0] out_19,
  output [15:0] out_20,
  output [13:0] out_21,
  output [17:0] out_22,
  output [15:0] out_23,
  output [13:0] out_24,
  output [17:0] out_25,
  output [15:0] out_26,
  output [13:0] out_27,
  output [15:0] out_28,
  output [13:0] out_29,
  output [17:0] out_30,
  output [13:0] out_31,
  output [15:0] out_32,
  output [17:0] out_33,
  output [13:0] out_34,
  output [15:0] out_35,
  output [13:0] out_36,
  output [17:0] out_37,
  output [15:0] out_38,
  output [13:0] out_39,
  output [15:0] out_40,
  output [17:0] out_41,
  output [13:0] out_42,
  output [15:0] out_43,
  output [13:0] out_44,
  output [17:0] out_45,
  output [15:0] out_46,
  output [13:0] out_47,
  output [17:0] out_48,
  output [15:0] out_49,
  output [15:0] out_50,
  output [17:0] out_51,
  output [17:0] out_52,
  output [8:0] To_print3D_walls
);

  wire _1_3, _1_exit, _2_3, _2_exit, _3_1, _3_2, _3_4, _3_5, _3_exit, _4_3, _4_exit, _5_3, _5_exit, _6_exit,
       _7_exit, _8_exit, cond_dir_to3d_1__0, cond_dir_to3d_1__1, cond_dir_to3d_1__2, cond_dir_to3d_1__3,
       controlled_buffer_1_out, controlled_buffer_2_out, controlled_buffer_3_out, controlled_buffer_4_out,
       controlled_buffer_5_out, controlled_buffer_6_out, controlled_buffer_7_out, controlled_buffer_8_out,
       controlled_buffer_9_out, m_1_0, m_1_1, m_1_2, m_1_3, m_1_4, m_1_5, m_1_6, m_2_0, m_2_1, m_2_2, m_2_3,
       m_2_4, m_2_5, m_2_6, m_3_0, m_3_1, m_3_2, m_3_3, m_3_4, m_3_5, m_3_6, m_4_0, m_4_1, m_4_2, m_4_3,
       m_4_4, m_4_5, m_4_6, m_5_0, m_5_1, m_5_2, m_5_3, m_5_4, m_5_5, m_5_6, m_6_0, m_6_1, m_6_2, m_6_3,
       m_6_4, m_6_5, m_6_6, m__0_0, m__0_1, m__0_2, m__0_3, m__0_4, m__0_5, m__0_6;
  wire [7:0] char1, char2, char3, char4, char5, char6, char7, char8, char9, char10, char11, char12, char13,
       char14, char15, char16, char17, char18, char19, char20, char21, char22, char23, char24, char25,
       char26, char27, char28, char29, char30, char31, char32, char33, char34, char35, char36, char37,
       char38, char39, char40, char41, char42, char43, char44, char45, char46, char47, char48, char49;

  plr_in_cond_of_dir plr_in_cond_of_dir_1 (.in_1(Bus1[25:24]), .out_2(out_14), .out_3(out_17));
  mmap_matrix mmap_matrix_1 (
    .Xpp(Bus1[7:0]), .Ypp(Bus1[15:8]), .out_4(char1), .out_5(char8), .out_6(char15), .out_7(char22),
    .out_8(char29), .out_9(char36), .out_10(char43), .out_11(char2), .out_12(char9), .out_13(char16),
    .out_14(char23), .out_15(char30), .out_16(char37), .out_17(char44), .out_18(char3), .out_19(char10),
    .out_20(char17), .out_21(char24), .out_22(char31), .out_23(char38), .out_24(char45), .out_25(char4),
    .out_26(char11), .out_27(char18), .out_28(char25), .out_29(char32), .out_30(char39), .out_31(char46),
    .out_32(char5), .out_33(char12), .out_34(char19), .out_35(char26), .out_36(char33), .out_37(char40),
    .out_38(char47), .out_39(char6), .out_40(char13), .out_41(char20), .out_42(char27), .out_43(char34),
    .out_44(char41), .out_45(char48), .out_46(char7), .out_47(char14), .out_48(char21), .out_49(char28),
    .out_50(char35), .out_51(char42), .out_52(char49), .No_of_map(Bus1[23:16]));
  cond_en_weap cond_en_weap_1 (.input_char(Bus2[1:0]), .todisplay(_3_4), .Exit(_7_exit));  // open: Error_undefined_byte
  cond_en_weap cond_en_weap_2 (.input_char(Bus2[3:2]), .todisplay(_3_2), .Exit(_2_exit));  // open: Error_undefined_byte
  cond_en_weap cond_en_weap_3 (.input_char(Bus2[5:4]), .todisplay(_2_3), .Exit(_4_exit));  // open: Error_undefined_byte
  cond_en_weap cond_en_weap_4 (.input_char(Bus2[7:6]), .todisplay(_4_3), .Exit(_5_exit));  // open: Error_undefined_byte
  cond_en_weap cond_en_weap_5 (.input_char(Bus2[9:8]), .todisplay(_5_3), .Exit(_6_exit));  // open: Error_undefined_byte
  cond_en_weap cond_en_weap_6 (
    .input_char(Bus2[11:10]), .todisplay(_1_3), .Exit(_3_exit));  // open: Error_undefined_byte
  cond_en_weap cond_en_weap_7 (
    .input_char(Bus2[13:12]), .todisplay(_3_5), .Exit(_8_exit));  // open: Error_undefined_byte
  cond_en_weap cond_en_weap_8 (
    .input_char(Bus2[15:14]), .todisplay(_3_1), .Exit(_1_exit));  // open: Error_undefined_byte
  cond_dir_to3d cond_dir_to3d_1 (
    .dir(Bus1[25:24]), ._0(cond_dir_to3d_1__0), ._1(cond_dir_to3d_1__1), ._2(cond_dir_to3d_1__2),
    ._3(cond_dir_to3d_1__3));
  assign controlled_buffer_1_out = cond_dir_to3d_1__0 ? m__0_4 : 1'bz;  // Controlled_Buffer controlled_buffer_1
  assign controlled_buffer_2_out = cond_dir_to3d_1__0 ? m__0_3 : 1'bz;  // Controlled_Buffer controlled_buffer_2
  assign controlled_buffer_3_out = cond_dir_to3d_1__0 ? m__0_2 : 1'bz;  // Controlled_Buffer controlled_buffer_3
  assign controlled_buffer_4_out = cond_dir_to3d_1__0 ? m_1_4 : 1'bz;  // Controlled_Buffer controlled_buffer_4
  assign controlled_buffer_5_out = cond_dir_to3d_1__0 ? m_1_2 : 1'bz;  // Controlled_Buffer controlled_buffer_5
  assign controlled_buffer_6_out = cond_dir_to3d_1__0 ? m_2_4 : 1'bz;  // Controlled_Buffer controlled_buffer_6
  assign controlled_buffer_7_out = cond_dir_to3d_1__0 ? m_2_2 : 1'bz;  // Controlled_Buffer controlled_buffer_7
  assign controlled_buffer_8_out = cond_dir_to3d_1__0 ? m_3_4 : 1'bz;  // Controlled_Buffer controlled_buffer_8
  assign controlled_buffer_9_out = cond_dir_to3d_1__0 ? m_3_2 : 1'bz;  // Controlled_Buffer controlled_buffer_9
  assign controlled_buffer_1_out = cond_dir_to3d_1__1 ? m_2_0 : 1'bz;  // Controlled_Buffer controlled_buffer_10
  assign controlled_buffer_2_out = cond_dir_to3d_1__1 ? m_3_0 : 1'bz;  // Controlled_Buffer controlled_buffer_11
  assign controlled_buffer_3_out = cond_dir_to3d_1__1 ? m_4_0 : 1'bz;  // Controlled_Buffer controlled_buffer_12
  assign controlled_buffer_4_out = cond_dir_to3d_1__1 ? m_2_1 : 1'bz;  // Controlled_Buffer controlled_buffer_13
  assign controlled_buffer_5_out = cond_dir_to3d_1__1 ? m_4_1 : 1'bz;  // Controlled_Buffer controlled_buffer_14
  assign controlled_buffer_6_out = cond_dir_to3d_1__1 ? m_2_2 : 1'bz;  // Controlled_Buffer controlled_buffer_15
  assign controlled_buffer_7_out = cond_dir_to3d_1__1 ? m_4_2 : 1'bz;  // Controlled_Buffer controlled_buffer_16
  assign controlled_buffer_8_out = cond_dir_to3d_1__1 ? m_2_3 : 1'bz;  // Controlled_Buffer controlled_buffer_17
  assign controlled_buffer_9_out = cond_dir_to3d_1__1 ? m_4_3 : 1'bz;  // Controlled_Buffer controlled_buffer_18
  assign controlled_buffer_1_out = cond_dir_to3d_1__2 ? m_6_2 : 1'bz;  // Controlled_Buffer controlled_buffer_19
  assign controlled_buffer_2_out = cond_dir_to3d_1__2 ? m_6_3 : 1'bz;  // Controlled_Buffer controlled_buffer_20
  assign controlled_buffer_3_out = cond_dir_to3d_1__2 ? m_6_4 : 1'bz;  // Controlled_Buffer controlled_buffer_21
  assign controlled_buffer_4_out = cond_dir_to3d_1__2 ? m_5_2 : 1'bz;  // Controlled_Buffer controlled_buffer_22
  assign controlled_buffer_5_out = cond_dir_to3d_1__2 ? m_5_4 : 1'bz;  // Controlled_Buffer controlled_buffer_23
  assign controlled_buffer_6_out = cond_dir_to3d_1__2 ? m_4_2 : 1'bz;  // Controlled_Buffer controlled_buffer_24
  assign controlled_buffer_7_out = cond_dir_to3d_1__2 ? m_4_4 : 1'bz;  // Controlled_Buffer controlled_buffer_25
  assign controlled_buffer_8_out = cond_dir_to3d_1__2 ? m_3_2 : 1'bz;  // Controlled_Buffer controlled_buffer_26
  assign controlled_buffer_9_out = cond_dir_to3d_1__2 ? m_3_4 : 1'bz;  // Controlled_Buffer controlled_buffer_27
  Multiplexer #(.width(18), .enable("false")) multiplexer_1 (
    .in0({18{1'b0}}), .in1({18{1'b0}}), .out(out_8), .sel(Bus2[16]));
  Multiplexer #(.width(18), .enable("false")) multiplexer_2 (
    .in0({18{1'b0}}), .in1({{8{1'b0}}, {2{_3_5}}, {8{1'b0}}}), .out(out_12), .sel(Bus2[16]));
  Multiplexer #(.width(18), .enable("false")) multiplexer_3 (
    .in0({18{1'b0}}), .in1({{8{1'b0}}, {2{_3_4}}, {8{1'b0}}}), .out(out_22), .sel(Bus2[16]));
  Multiplexer #(.width(18), .enable("false")) multiplexer_4 (
    .in0({18{1'b0}}), .in1({4'b0000, {2{_1_3}}, {2{_2_3}}, 2'b00, {2{_4_3}}, {2{_5_3}}, 4'b0000}),
    .out(out_30), .sel(Bus2[16]));
  Multiplexer #(.width(18), .enable("false")) multiplexer_5 (
    .in0({18{1'b0}}), .in1({{8{1'b0}}, {2{_3_2}}, {8{1'b0}}}), .out(out_37), .sel(Bus2[16]));
  Multiplexer #(.width(18), .enable("false")) multiplexer_6 (
    .in0({18{1'b0}}), .in1({{8{1'b0}}, {2{_3_1}}, {8{1'b0}}}), .out(out_45), .sel(Bus2[16]));
  Multiplexer #(.width(18), .enable("false")) multiplexer_7 (
    .in0({18{1'b0}}), .in1({18{1'b0}}), .out(out_51), .sel(Bus2[16]));
  assign controlled_buffer_1_out = cond_dir_to3d_1__3 ? m_4_6 : 1'bz;  // Controlled_Buffer controlled_buffer_28
  assign controlled_buffer_2_out = cond_dir_to3d_1__3 ? m_3_6 : 1'bz;  // Controlled_Buffer controlled_buffer_29
  assign controlled_buffer_3_out = cond_dir_to3d_1__3 ? m_2_6 : 1'bz;  // Controlled_Buffer controlled_buffer_30
  assign controlled_buffer_4_out = cond_dir_to3d_1__3 ? m_4_5 : 1'bz;  // Controlled_Buffer controlled_buffer_31
  assign controlled_buffer_5_out = cond_dir_to3d_1__3 ? m_2_5 : 1'bz;  // Controlled_Buffer controlled_buffer_32
  assign controlled_buffer_6_out = cond_dir_to3d_1__3 ? m_4_4 : 1'bz;  // Controlled_Buffer controlled_buffer_33
  assign controlled_buffer_7_out = cond_dir_to3d_1__3 ? m_2_4 : 1'bz;  // Controlled_Buffer controlled_buffer_34
  assign controlled_buffer_8_out = cond_dir_to3d_1__3 ? m_4_3 : 1'bz;  // Controlled_Buffer controlled_buffer_35
  assign controlled_buffer_9_out = cond_dir_to3d_1__3 ? m_2_3 : 1'bz;  // Controlled_Buffer controlled_buffer_36
  not not_1 (To_print3D_walls[0], controlled_buffer_1_out);
  not not_2 (To_print3D_walls[1], controlled_buffer_2_out);
  not not_3 (To_print3D_walls[2], controlled_buffer_3_out);
  not not_4 (To_print3D_walls[3], controlled_buffer_4_out);
  not not_5 (To_print3D_walls[4], controlled_buffer_5_out);
  not not_6 (To_print3D_walls[6], controlled_buffer_7_out);
  not not_7 (To_print3D_walls[7], controlled_buffer_8_out);
  not not_8 (To_print3D_walls[5], controlled_buffer_6_out);
  not not_9 (To_print3D_walls[8], controlled_buffer_9_out);
  cond_wall_pass cond_wall_pass_1 (.in_1(char1), .out(m__0_6));
  cond_wall_pass cond_wall_pass_2 (.in_1(char2), .out(m__0_5));
  cond_wall_pass cond_wall_pass_3 (.in_1(char3), .out(m__0_4));
  cond_wall_pass cond_wall_pass_4 (.in_1(char4), .out(m__0_3));
  cond_wall_pass cond_wall_pass_5 (.in_1(char5), .out(m__0_2));
  cond_wall_pass cond_wall_pass_6 (.in_1(char6), .out(m__0_1));
  cond_wall_pass cond_wall_pass_7 (.in_1(char7), .out(m__0_0));
  cond_wall_pass cond_wall_pass_8 (.in_1(char8), .out(m_1_6));
  cond_wall_pass cond_wall_pass_9 (.in_1(char9), .out(m_1_5));
  cond_wall_pass cond_wall_pass_10 (.in_1(char10), .out(m_1_4));
  cond_wall_pass cond_wall_pass_11 (.in_1(char11), .out(m_1_3));
  cond_wall_pass cond_wall_pass_12 (.in_1(char12), .out(m_1_2));
  cond_wall_pass cond_wall_pass_13 (.in_1(char13), .out(m_1_1));
  cond_wall_pass cond_wall_pass_14 (.in_1(char14), .out(m_1_0));
  cond_wall_pass cond_wall_pass_15 (.in_1(char15), .out(m_2_6));
  cond_wall_pass cond_wall_pass_16 (.in_1(char16), .out(m_2_5));
  cond_wall_pass cond_wall_pass_17 (.in_1(char17), .out(m_2_4));
  cond_wall_pass cond_wall_pass_18 (.in_1(char18), .out(m_2_3));
  cond_wall_pass cond_wall_pass_19 (.in_1(char19), .out(m_2_2));
  cond_wall_pass cond_wall_pass_20 (.in_1(char20), .out(m_2_1));
  cond_wall_pass cond_wall_pass_21 (.in_1(char21), .out(m_2_0));
  cond_wall_pass cond_wall_pass_22 (.in_1(char22), .out(m_3_6));
  cond_wall_pass cond_wall_pass_23 (.in_1(char23), .out(m_3_5));
  cond_wall_pass cond_wall_pass_24 (.in_1(char24), .out(m_3_4));
  cond_wall_pass cond_wall_pass_25 (.in_1(char25), .out(m_3_3));
  cond_wall_pass cond_wall_pass_26 (.in_1(char26), .out(m_3_2));
  cond_wall_pass cond_wall_pass_27 (.in_1(char27), .out(m_3_1));
  cond_wall_pass cond_wall_pass_28 (.in_1(char28), .out(m_3_0));
  cond_wall_pass cond_wall_pass_29 (.in_1(char29), .out(m_4_6));
  cond_wall_pass cond_wall_pass_30 (.in_1(char30), .out(m_4_5));
  cond_wall_pass cond_wall_pass_31 (.in_1(char31), .out(m_4_4));
  cond_wall_pass cond_wall_pass_32 (.in_1(char32), .out(m_4_3));
  cond_wall_pass cond_wall_pass_33 (.in_1(char33), .out(m_4_2));
  cond_wall_pass cond_wall_pass_34 (.in_1(char34), .out(m_4_1));
  cond_wall_pass cond_wall_pass_35 (.in_1(char35), .out(m_4_0));
  cond_wall_pass cond_wall_pass_36 (.in_1(char36), .out(m_5_6));
  cond_wall_pass cond_wall_pass_37 (.in_1(char37), .out(m_5_5));
  cond_wall_pass cond_wall_pass_38 (.in_1(char38), .out(m_5_4));
  cond_wall_pass cond_wall_pass_39 (.in_1(char39), .out(m_5_3));
  cond_wall_pass cond_wall_pass_40 (.in_1(char40), .out(m_5_2));
  cond_wall_pass cond_wall_pass_41 (.in_1(char41), .out(m_5_1));
  cond_wall_pass cond_wall_pass_42 (.in_1(char42), .out(m_5_0));
  cond_wall_pass cond_wall_pass_43 (.in_1(char43), .out(m_6_6));
  cond_wall_pass cond_wall_pass_44 (.in_1(char44), .out(m_6_5));
  cond_wall_pass cond_wall_pass_45 (.in_1(char45), .out(m_6_4));
  cond_wall_pass cond_wall_pass_46 (.in_1(char46), .out(m_6_3));
  cond_wall_pass cond_wall_pass_47 (.in_1(char47), .out(m_6_2));
  cond_wall_pass cond_wall_pass_48 (.in_1(char48), .out(m_6_1));
  cond_wall_pass cond_wall_pass_49 (.in_1(char49), .out(m_6_0));
  Multiplexer #(.width(14), .enable("false")) multiplexer_8 (
    .in0({14{1'b1}}),
    .in1({{2{m__0_6}}, {2{m__0_5}}, {2{m__0_4}}, {2{m__0_3}}, {2{m__0_2}}, {2{m__0_1}}, {2{m__0_0}}}),
    .out(out_11), .sel(Bus2[16]));
  Multiplexer #(.width(14), .enable("false")) multiplexer_9 (
    .in0({14{1'b1}}),
    .in1({{2{m_1_6}}, {2{m_1_5}}, {2{m_1_4}}, {2{m_1_3}}, {2{m_1_2}}, {2{m_1_1}}, {2{m_1_0}}}), .out(out_19),
    .sel(Bus2[16]));
  Multiplexer #(.width(14), .enable("false")) multiplexer_10 (
    .in0({14{1'b1}}),
    .in1({{2{m_2_6}}, {2{m_2_5}}, {2{m_2_4}}, {2{m_2_3}}, {2{m_2_2}}, {2{m_2_1}}, {2{m_2_0}}}), .out(out_24),
    .sel(Bus2[16]));
  Multiplexer #(.width(14), .enable("false")) multiplexer_11 (
    .in0({14{1'b1}}),
    .in1({{2{m_3_6}}, {2{m_3_5}}, {2{m_3_4}}, {2{m_3_3}}, {2{m_3_2}}, {2{m_3_1}}, {2{m_3_0}}}), .out(out_29),
    .sel(Bus2[16]));
  Multiplexer #(.width(14), .enable("false")) multiplexer_12 (
    .in0({14{1'b1}}),
    .in1({{2{m_4_6}}, {2{m_4_5}}, {2{m_4_4}}, {2{m_4_3}}, {2{m_4_2}}, {2{m_4_1}}, {2{m_4_0}}}), .out(out_34),
    .sel(Bus2[16]));
  Multiplexer #(.width(14), .enable("false")) multiplexer_13 (
    .in0({14{1'b1}}),
    .in1({{2{m_5_6}}, {2{m_5_5}}, {2{m_5_4}}, {2{m_5_3}}, {2{m_5_2}}, {2{m_5_1}}, {2{m_5_0}}}), .out(out_39),
    .sel(Bus2[16]));
  Multiplexer #(.width(14), .enable("false")) multiplexer_14 (
    .in0({14{1'b1}}),
    .in1({{2{m_6_6}}, {2{m_6_5}}, {2{m_6_4}}, {2{m_6_3}}, {2{m_6_2}}, {2{m_6_1}}, {2{m_6_0}}}), .out(out_44),
    .sel(Bus2[16]));
  Multiplexer #(.width(16), .enable("false")) multiplexer_15 (
    .in0({16{1'b0}}), .in1({16{1'b0}}), .out(out_13), .sel(Bus2[16]));
  Multiplexer #(.width(16), .enable("false")) multiplexer_16 (
    .in0({16{1'b0}}), .in1({{7{1'b0}}, {2{_8_exit}}, {7{1'b0}}}), .out(out_20), .sel(Bus2[16]));
  Multiplexer #(.width(16), .enable("false")) multiplexer_17 (
    .in0({16{1'b0}}), .in1({{7{1'b0}}, {2{_7_exit}}, {7{1'b0}}}), .out(out_26), .sel(Bus2[16]));
  Multiplexer #(.width(16), .enable("false")) multiplexer_18 (
    .in0({16{1'b0}}), .in1({3'b000, {2{_3_exit}}, {2{_4_exit}}, 2'b00, {2{_5_exit}}, {2{_6_exit}}, 3'b000}),
    .out(out_32), .sel(Bus2[16]));
  Multiplexer #(.width(16), .enable("false")) multiplexer_19 (
    .in0({16{1'b0}}), .in1({{7{1'b0}}, {2{_2_exit}}, {7{1'b0}}}), .out(out_38), .sel(Bus2[16]));
  Multiplexer #(.width(16), .enable("false")) multiplexer_20 (
    .in0({16{1'b0}}), .in1({{7{1'b0}}, {2{_1_exit}}, {7{1'b0}}}), .out(out_43), .sel(Bus2[16]));
  Multiplexer #(.width(16), .enable("false")) multiplexer_21 (
    .in0({16{1'b0}}), .in1({16{1'b0}}), .out(out_49), .sel(Bus2[16]));

  assign out_3 = {18{1'b0}};
  assign out_4 = {18{1'b0}};
  assign out_5 = {16{1'b0}};
  assign out_6 = {18{1'b0}};
  assign out_7 = {16{1'b0}};
  assign out_9 = {18{1'b0}};
  assign out_10 = out_8;
  assign out_15 = out_11;
  assign out_16 = out_13;
  assign out_18 = out_12;
  assign out_21 = out_19;
  assign out_23 = out_20;
  assign out_25 = out_22;
  assign out_27 = out_24;
  assign out_28 = out_26;
  assign out_31 = out_29;
  assign out_33 = out_30;
  assign out_35 = out_32;
  assign out_36 = out_34;
  assign out_40 = out_38;
  assign out_41 = out_37;
  assign out_42 = out_39;
  assign out_46 = out_43;
  assign out_47 = out_44;
  assign out_48 = out_45;
  assign out_50 = out_49;
  assign out_52 = out_51;

  // Other names for the same wires on the sheet: p_x_y_1[1:0] = Bus2[1:0]; p_x__y_1[1:0] = Bus2[3:2];
  //   p_x_1__y_t[1:0] = Bus2[5:4]; p_x_1__y[1:0] = Bus2[7:6]; p_x_2__y[1:0] = Bus2[9:8];
  //   p_x_2__y_t[1:0] = Bus2[11:10]; p_x__y_2_t[1:0] = Bus2[13:12]; p_x__y_2[1:0] = Bus2[15:14]; gs1 = Bus2[16];
  //   Direction[1:0] = Bus1[25:24]; mapLevelCurrent[7:0] = Bus1[23:16]; X[7:0] = Bus1[7:0]; Y[7:0] = Bus1[15:8]

  // Notes on the sheet:
  //   0 dir
  //   Big matrix(enemy/weapon)
  //   1 dir
  //   2 dir
  //   3 dir
  //   Mid Matrix(wall/pass)
  //   Exit_Matrix
endmodule

module cond_dir_to3d (
  input  [1:0] dir,
  output _0,
  output _1,
  output _2,
  output _3
);

  Comparator #(.width(2), .mode("unsigned")) comparator_1 (.a(dir), .b(2'b00), .eq(_0));  // open: gt, lt
  Comparator #(.width(2), .mode("unsigned")) comparator_2 (.a(dir), .b(2'b01), .eq(_1));  // open: gt, lt
  Comparator #(.width(2), .mode("unsigned")) comparator_3 (.a(dir), .b(2'b10), .eq(_2));  // open: gt, lt
  Comparator #(.width(2), .mode("unsigned")) comparator_4 (.a(dir), .b(2'b11), .eq(_3));  // open: gt, lt
endmodule

module lookup_onMMap (
  input  [16:0] in_1,
  input  [25:0] in_2
);

  wire [1:0] driver_mm_1_out_14, driver_mm_1_out_17;
  wire [8:0] b;
  wire [13:0] driver_mm_1_out_11, driver_mm_1_out_15, driver_mm_1_out_19, driver_mm_1_out_21,
       driver_mm_1_out_24, driver_mm_1_out_27, driver_mm_1_out_29, driver_mm_1_out_31, driver_mm_1_out_34,
       driver_mm_1_out_36, driver_mm_1_out_39, driver_mm_1_out_42, driver_mm_1_out_44, driver_mm_1_out_47;
  wire [15:0] driver_mm_1_out_5, driver_mm_1_out_7, driver_mm_1_out_13, driver_mm_1_out_16,
       driver_mm_1_out_20, driver_mm_1_out_23, driver_mm_1_out_26, driver_mm_1_out_28, driver_mm_1_out_32,
       driver_mm_1_out_35, driver_mm_1_out_38, driver_mm_1_out_40, driver_mm_1_out_43, driver_mm_1_out_46,
       driver_mm_1_out_49, driver_mm_1_out_50;
  wire [17:0] driver_mm_1_out_3, driver_mm_1_out_4, driver_mm_1_out_6, driver_mm_1_out_8, driver_mm_1_out_9,
       driver_mm_1_out_10, driver_mm_1_out_12, driver_mm_1_out_18, driver_mm_1_out_22, driver_mm_1_out_25,
       driver_mm_1_out_30, driver_mm_1_out_33, driver_mm_1_out_37, driver_mm_1_out_41, driver_mm_1_out_45,
       driver_mm_1_out_48, driver_mm_1_out_51, driver_mm_1_out_52;

  driver_mm driver_mm_1 (
    .Bus1(in_2), .Bus2(in_1), .out_3(driver_mm_1_out_3), .out_4(driver_mm_1_out_4),
    .out_6(driver_mm_1_out_6), .out_9(driver_mm_1_out_9), .out_8(driver_mm_1_out_8),
    .out_10(driver_mm_1_out_10), .out_11(driver_mm_1_out_11), .out_12(driver_mm_1_out_12),
    .out_15(driver_mm_1_out_15), .out_18(driver_mm_1_out_18), .out_19(driver_mm_1_out_19),
    .out_21(driver_mm_1_out_21), .out_22(driver_mm_1_out_22), .out_24(driver_mm_1_out_24),
    .out_25(driver_mm_1_out_25), .out_27(driver_mm_1_out_27), .out_14(driver_mm_1_out_14),
    .out_29(driver_mm_1_out_29), .out_17(driver_mm_1_out_17), .out_30(driver_mm_1_out_30),
    .out_31(driver_mm_1_out_31), .out_33(driver_mm_1_out_33), .out_34(driver_mm_1_out_34),
    .out_36(driver_mm_1_out_36), .out_37(driver_mm_1_out_37), .out_39(driver_mm_1_out_39),
    .out_41(driver_mm_1_out_41), .out_42(driver_mm_1_out_42), .out_44(driver_mm_1_out_44),
    .out_45(driver_mm_1_out_45), .out_47(driver_mm_1_out_47), .out_48(driver_mm_1_out_48),
    .out_51(driver_mm_1_out_51), .out_52(driver_mm_1_out_52), .To_print3D_walls(b),
    .out_13(driver_mm_1_out_13), .out_16(driver_mm_1_out_16), .out_20(driver_mm_1_out_20),
    .out_23(driver_mm_1_out_23), .out_26(driver_mm_1_out_26), .out_28(driver_mm_1_out_28),
    .out_32(driver_mm_1_out_32), .out_35(driver_mm_1_out_35), .out_38(driver_mm_1_out_38),
    .out_40(driver_mm_1_out_40), .out_43(driver_mm_1_out_43), .out_46(driver_mm_1_out_46),
    .out_49(driver_mm_1_out_49), .out_50(driver_mm_1_out_50), .out_5(driver_mm_1_out_5),
    .out_7(driver_mm_1_out_7));
  DotMatrix #(.inputtype("row"), .matrixcols(18), .matrixrows(18)) dotmatrix_1 (
    .row0(driver_mm_1_out_3), .row1(driver_mm_1_out_4), .row2(driver_mm_1_out_8), .row3(driver_mm_1_out_10),
    .row4(driver_mm_1_out_12), .row5(driver_mm_1_out_18), .row6(driver_mm_1_out_22),
    .row7(driver_mm_1_out_25), .row8(driver_mm_1_out_30), .row9(driver_mm_1_out_33),
    .row10(driver_mm_1_out_37), .row11(driver_mm_1_out_41), .row12(driver_mm_1_out_45),
    .row13(driver_mm_1_out_48), .row14(driver_mm_1_out_51), .row15(driver_mm_1_out_52),
    .row16(driver_mm_1_out_6), .row17(driver_mm_1_out_9));
  DotMatrix #(.inputtype("row"), .matrixcols(16), .matrixrows(16)) dotmatrix_2 (
    .row0(driver_mm_1_out_5), .row1(driver_mm_1_out_13), .row2(driver_mm_1_out_16),
    .row3(driver_mm_1_out_20), .row4(driver_mm_1_out_23), .row5(driver_mm_1_out_26),
    .row6(driver_mm_1_out_28), .row7(driver_mm_1_out_32), .row8(driver_mm_1_out_35),
    .row9(driver_mm_1_out_38), .row10(driver_mm_1_out_40), .row11(driver_mm_1_out_43),
    .row12(driver_mm_1_out_46), .row13(driver_mm_1_out_49), .row14(driver_mm_1_out_50),
    .row15(driver_mm_1_out_7));
  DotMatrix #(.inputtype("row"), .matrixcols(14), .matrixrows(14)) dotmatrix_3 (
    .row0(driver_mm_1_out_11), .row1(driver_mm_1_out_15), .row2(driver_mm_1_out_19),
    .row3(driver_mm_1_out_21), .row4(driver_mm_1_out_24), .row5(driver_mm_1_out_27),
    .row6(driver_mm_1_out_29), .row7(driver_mm_1_out_31), .row8(driver_mm_1_out_34),
    .row9(driver_mm_1_out_36), .row10(driver_mm_1_out_39), .row11(driver_mm_1_out_42),
    .row12(driver_mm_1_out_44), .row13(driver_mm_1_out_47));
  DotMatrix #(.inputtype("row"), .matrixcols(2), .matrixrows(2)) dotmatrix_4 (
    .row0(driver_mm_1_out_14), .row1(driver_mm_1_out_17));
endmodule
