// Logisim project Quickers.circ as structural Verilog: 2 circuits, main circuit quick
module quick (
  input  IN,
  output OUT
);

  wire not_1_out, not_2_out;

  not not_1 (not_1_out, IN);
  Register #(.width(1)) register_1 (.D(IN), .Q(OUT), .clk(IN), .clr(not_2_out));  // open: en
  not not_2 (not_2_out, not_1_out);

  // Notes on the sheet:
  //   Короткий сигнал когда на IN 0 переходит в 1
endmodule

module Lquick (
  input  IN,
  input  CLC,
  output OUT
);

  wire and_1_out, comparator_1_eq, quick_1_out;
  wire [2:0] adder_1_out, register_1_q;

  Register #(.width(3)) register_1 (.D(adder_1_out), .Q(register_1_q), .clk(and_1_out), .clr(quick_1_out));  // open: en
  and and_1 (and_1_out, CLC, ~comparator_1_eq);  // AND_Gate
  Adder #(.width(3)) adder_1 (.a(3'b001), .b(register_1_q), .out(adder_1_out));  // open: cin, cout
  Comparator #(.width(3), .mode("unsigned")) comparator_1 (
    .a(3'b111), .b(register_1_q), .gt(OUT), .eq(comparator_1_eq));  // open: lt
  quick quick_1 (.IN(IN), .OUT(quick_1_out));

  // Notes on the sheet:
  //   Создает 'длинный' еденичный сигнал
endmodule
