// Logisim project scores.circ as structural Verilog: 1 circuit, main circuit main
module main (
  input  main_res,
  input  Clock,
  input  add_points,
  input  [6:0] amount_of_points,
  output [3:0] hund,
  output [3:0] ten,
  output [3:0] one
);

  wire _0xf0, _0xf1, _0xf2, and_2_out, and_4_out, and_8_out, and_9_out, and_10_out, cdm_8_mark5_1_p1,
       cdm_8_mark5_1_p2, cdm_8_mark5_1_p4, cdm_8_mark5_1_p5, cdm_8_mark5_1_p6, cdm_8_mark5_1_p7,
       cdm_8_mark5_1_p8, cdm_8_mark5_1_p9, code, data_t, decoder_2_out0, decoder_2_out1, I_Osel, In_Out, mem,
       nor_1_out, nor_2_out, not_1_out, not_2_out, not_3_out, not_4_out, not_5_out, not_6_out, or_1_out, RAM,
       transistor_1_out;
  wire [6:0] amount_of_points_q, controlled_buffer_1_out;
  wire [7:0] _1_q, _10_q, _100_q, ADDR, cdm_8_mark5_1_p13, cdm_8_mark5_1_p14, Data;
  wire [7:7] s_r_ff_1_q;

  nor nor_1 (nor_1_out, transistor_1_out, not_1_out);
  not not_1 (not_1_out, transistor_1_out);
  nor nor_2 (nor_2_out, decoder_2_out1, not_2_out);
  not not_2 (not_2_out, decoder_2_out1);
  and and_1 (I_Osel, and_2_out, Clock, data_t);
  Transistor #(.\type ("n")) transistor_1 (.in(1'b0), .out(transistor_1_out), .gate(add_points));
  assign controlled_buffer_1_out = add_points ? amount_of_points : 7'bz;  // Controlled_Buffer controlled_buffer_1
  not not_3 (not_3_out, not_5_out);
  // Probe on cdm_8_mark5_1_p1
  // Probe on cdm_8_mark5_1_p2
  // Probe on cdm_8_mark5_1_p4
  // Probe on cdm_8_mark5_1_p5
  and and_2 (and_2_out, ADDR[4], ADDR[5], ADDR[6], ADDR[7]);
  and and_3 (RAM, ~and_2_out, data_t);  // AND_Gate
  Pull_Resistor #(.pull(1)) pull_resistor_1 (.node(transistor_1_out));
  Register #(.width(7), .trigger("falling")) u_amount_of_points (
    .D(controlled_buffer_1_out), .Q(amount_of_points_q), .clk(transistor_1_out), .clr(decoder_2_out0));  // open: en
  S_R_Flip_Flop #(.trigger("low")) s_r_ff_1 (
    .S(nor_1_out), .clk(not_3_out), .R(nor_2_out), .Q(s_r_ff_1_q[7]));  // open: Qn, preset, reset, en
  not not_4 (not_4_out, transistor_1_out);
  not not_5 (not_5_out, not_4_out);
  // Probe on cdm_8_mark5_1_p8
  // Probe on cdm_8_mark5_1_p6
  // Probe on cdm_8_mark5_1_p7
  // CdM_8_mark5 cdm_8_mark5_1: pin names not known; wires that end beside it: cdm_8_mark5_1_p1, cdm_8_mark5_1_p2, Clock, cdm_8_mark5_1_p4, cdm_8_mark5_1_p5, cdm_8_mark5_1_p6, cdm_8_mark5_1_p7, cdm_8_mark5_1_p8, cdm_8_mark5_1_p9, mem, In_Out, ADDR, cdm_8_mark5_1_p13, cdm_8_mark5_1_p14
  // Probe on ADDR
  Decoder #(.disabled(0)) decoder_1 (.out0(code), .out1(data_t), .sel(cdm_8_mark5_1_p9), .en(mem));
  not not_6 (not_6_out, In_Out);
  assign Data = not_6_out ? cdm_8_mark5_1_p13 : 8'bz;  // Controlled_Buffer controlled_buffer_2
  assign cdm_8_mark5_1_p14 = In_Out ? Data : 8'bz;  // Controlled_Buffer controlled_buffer_3
  assign Data = decoder_2_out1 ? {s_r_ff_1_q[7], amount_of_points_q} : 8'bz;  // Controlled_Buffer controlled_buffer_4
  // Probe on {s_r_ff_1_q[7], amount_of_points_q}
  // Probe on Data
  Hex_Digit_Display hex_digit_display_1 (.value(hund));  // open: dp
  Register _100 (.D(Data), .Q(_100_q), .clk(and_8_out), .clr(main_res));  // open: en
  RAM ram_1 (.addr(ADDR), .data(Data), .sel(RAM), .clk(Clock), .ld(In_Out), .clr(main_res));
  ROM rom_1 (.addr(ADDR), .data(Data), .sel(code));
  Hex_Digit_Display hex_digit_display_2 (.value(ten));  // open: dp
  Bit_Extender #(.out_width(4)) bit_extender_1 (.in(_100_q), .out(hund));
  Register _10 (.D(Data), .Q(_10_q), .clk(and_9_out), .clr(main_res));  // open: en
  // Probe on Data
  and and_4 (and_4_out, I_Osel, ADDR[0], ADDR[1], ~ADDR[2], ~ADDR[3]);  // AND_Gate
  and and_5 (_0xf0, I_Osel, ~ADDR[0], ~ADDR[1], ~ADDR[2], ~ADDR[3]);  // AND_Gate
  and and_6 (_0xf1, I_Osel, ADDR[0], ~ADDR[1], ~ADDR[2], ~ADDR[3]);  // AND_Gate
  and and_7 (_0xf2, I_Osel, ~ADDR[0], ADDR[1], ~ADDR[2], ~ADDR[3]);  // AND_Gate
  Hex_Digit_Display hex_digit_display_3 (.value(one));  // open: dp
  Bit_Extender #(.out_width(4)) bit_extender_2 (.in(_10_q), .out(ten));
  Register _1 (.D(Data), .Q(_1_q), .clk(and_10_out), .clr(main_res));  // open: en
  or or_1 (or_1_out, and_4_out, _0xf0, _0xf1, _0xf2);
  Bit_Extender #(.out_width(4)) bit_extender_3 (.in(_1_q), .out(one));
  and and_8 (and_8_out, decoder_2_out0, _0xf0);
  and and_9 (and_9_out, decoder_2_out0, _0xf1);
  and and_10 (and_10_out, decoder_2_out0, _0xf2);
  Decoder #(.disabled(0)) decoder_2 (.out0(decoder_2_out0), .out1(decoder_2_out1), .sel(In_Out), .en(or_1_out));

  // Other names for the same wires on the sheet: I_Oadr[3:0] = ADDR[3:0]; clk = Clock; I_Odat[7:0] = Data;
  //   rd_wr = In_Out; res = main_res

  // Notes on the sheet:
  //   сигнал о конце боя\сигнал о съедении еды
  //   RAM
  //   ROM
  //   contents of rom_1 (hex, n*v repeats v):
  //   d0 f3 d1 0 b1 5 e4 4 5 e1 d ee 0 d2 a4 a9 d0 a6 b2 d1 a5 a6 d0 a4 b1 d0 a5 b2 d0 0 16 e3 22 8c d1 a6
  //   a6 8d b7 13 a7 d1 a6 b6 d1 0 d0 a 3 3b e3 39 38 8d 2 ee 2e d0 aa a2 6 d1 0 d0 a 3 3b e3 4a 38 8d 2
  //   ee 3f d0 a8 a1 8c a2 d1 a6 8d b7 f e0 90 d0 aa b1 d2 6 19 d2 a b 37 e3 6b 36 a2 d0 a9 b1 8d a1 ee 6c
  //   a1 d0 a9 b1 d2 5 19 d2 a b 37 e3 81 36 a2 d0 a8 b1 8d a1 ee 82 a1 d0 a8 b1 d2 2 19 a1 8b d0 a6 8c a3
  //   ee 4f d0 a8 b0 d1 f0 a4 d0 a9 b0 d1 f1 a4 d0 aa b0 d1 f2 a4 ee
  //   0xf3 -- input
  //   0xf0 -- output
  //   0xf1 -- output
  //   0xf2 -- output
endmodule
