// Logisim project weapons.circ as structural Verilog
module enemies (
  input  [1:0] ADDR,
  output [7:0] HP,
  output [7:0] DMG
);

  Multiplexer #(.select(2), .width(8), .disabled(0), .enable("false")) multiplexer_1 (
    .in0(8'h14), .in1(8'ha), .in2(8'h32), .in3(8'h1e), .out(HP), .sel(ADDR));
  Multiplexer #(.select(2), .width(8), .disabled(0), .enable("false")) multiplexer_2 (
    .in0(8'h5), .in1(8'h3), .in2(8'h14), .in3(8'ha), .out(DMG), .sel(ADDR));

  // Notes on the sheet:
  //   Получение урона и здоровья для противника
endmodule

module weapon (
  input  GenRnd,
  input  [7:0] WEAPON,
  output [7:0] DMG,
  output nW
);

  wire and_1_out, comparator_1_lt, comparator_2_gt, comparator_3_eq, not_1_out;
  wire [2:0] bit_extender_1_out;
  wire [7:0] multiplexer_1_out, plusminus1_1_out, subtractor_1_out;

  Subtractor subtractor_1 (.a(WEAPON), .b(8'h66), .out(subtractor_1_out));  // open: bin, bout
  Comparator comparator_1 (.a(WEAPON), .b(8'h6b), .lt(comparator_1_lt));  // open: gt, eq
  Comparator comparator_2 (.a(WEAPON), .b(8'h65), .gt(comparator_2_gt));  // open: eq, lt
  Comparator comparator_3 (.a(WEAPON), .b({8{1'b0}}), .eq(comparator_3_eq));  // open: gt, lt
  Multiplexer #(.select(3), .width(8), .enable("false")) multiplexer_1 (
    .in0(8'h5), .in1(8'h14), .in2(8'hf), .in3(8'ha), .in4(8'h63), .out(multiplexer_1_out),
    .sel(bit_extender_1_out));  // open: in5, in6, in7
  Bit_Extender #(.out_width(3)) bit_extender_1 (.in(subtractor_1_out), .out(bit_extender_1_out));
  not not_1 (not_1_out, and_1_out);
  and and_1 (and_1_out, comparator_1_lt, comparator_2_gt);
  and and_2 (nW, not_1_out, ~comparator_3_eq);  // AND_Gate
  plusMinus1 plusminus1_1 (.inp(multiplexer_1_out), .out(plusminus1_1_out), .GenRnd(GenRnd));
  Multiplexer #(.width(8), .enable("false")) multiplexer_2 (
    .in0(plusminus1_1_out), .in1({8{1'b0}}), .out(DMG), .sel(not_1_out));

  // Notes on the sheet:
  //   Возвращает заданный урон в пределах (-1 0 +1)
  //   Такт для рандома
  //   Это не оружие
endmodule

module weaponSelected (
  input  [7:0] INVENTORY1p,
  input  [7:0] INVENTORY2p,
  input  _1oninp,
  input  [7:0] INVENTORY3p,
  input  [7:0] INVENTORY4p,
  input  _2oninp,
  input  [7:0] INVENTORY5p,
  input  _3oninp,
  input  _4oninp,
  input  _5oninp,
  output weaponSelected
);

  wire and_1_out, and_2_out, and_3_out, and_4_out, and_5_out, comparator_1_lt, comparator_2_gt,
       comparator_3_lt, comparator_4_gt, comparator_5_lt, comparator_6_gt, comparator_7_lt, comparator_8_gt,
       comparator_9_lt, comparator_10_gt;

  Comparator comparator_1 (.a(INVENTORY1p), .b(8'h6b), .lt(comparator_1_lt));  // open: gt, eq
  Comparator comparator_2 (.a(INVENTORY1p), .b(8'h65), .gt(comparator_2_gt));  // open: eq, lt
  Comparator comparator_3 (.a(INVENTORY2p), .b(8'h6b), .lt(comparator_3_lt));  // open: gt, eq
  Comparator comparator_4 (.a(INVENTORY2p), .b(8'h65), .gt(comparator_4_gt));  // open: eq, lt
  Comparator comparator_5 (.a(INVENTORY3p), .b(8'h6b), .lt(comparator_5_lt));  // open: gt, eq
  Comparator comparator_6 (.a(INVENTORY3p), .b(8'h65), .gt(comparator_6_gt));  // open: eq, lt
  Comparator comparator_7 (.a(INVENTORY4p), .b(8'h6b), .lt(comparator_7_lt));  // open: gt, eq
  Comparator comparator_8 (.a(INVENTORY4p), .b(8'h65), .gt(comparator_8_gt));  // open: eq, lt
  Comparator comparator_9 (.a(INVENTORY5p), .b(8'h6b), .lt(comparator_9_lt));  // open: gt, eq
  Comparator comparator_10 (.a(INVENTORY5p), .b(8'h65), .gt(comparator_10_gt));  // open: eq, lt
  and and_1 (and_1_out, comparator_1_lt, _1oninp, comparator_2_gt);
  and and_2 (and_2_out, comparator_3_lt, _2oninp, comparator_4_gt);
  and and_3 (and_3_out, comparator_5_lt, _3oninp, comparator_6_gt);
  and and_4 (and_4_out, comparator_7_lt, _4oninp, comparator_8_gt);
  and and_5 (and_5_out, comparator_9_lt, _5oninp, comparator_10_gt);
  or or_1 (weaponSelected, and_1_out, and_2_out, and_3_out, and_4_out, and_5_out);

  // Other names for the same wires on the sheet: INVENTORY1pws[7:0] = INVENTORY1p; INVENTORY2pws[7:0] = INVENTORY2p;
  //   INVENTORY3pws[7:0] = INVENTORY3p; INVENTORY4pws[7:0] = INVENTORY4p; INVENTORY5pws[7:0] = INVENTORY5p

  // Notes on the sheet:
  //   ПРОВЕРЯЕТ ВЫБРАНО ЛИ ОРУЖИЕ
endmodule

module whatIs (
  input  [7:0] input_element,
  output [1:0] output_key
);

  wire and_1_out, and_2_out, and_3_out, comparator_1_lt, comparator_2_gt, comparator_3_lt, comparator_4_gt,
       comparator_5_lt, comparator_6_gt;

  Comparator comparator_1 (.a(input_element), .b(8'h65), .lt(comparator_1_lt));  // open: gt, eq
  assign output_key = and_1_out ? 2'b01 : 2'bz;  // Controlled_Buffer controlled_buffer_1
  and and_1 (and_1_out, comparator_1_lt, comparator_2_gt);
  Comparator comparator_2 (.a(input_element), .b(8'h60), .gt(comparator_2_gt));  // open: eq, lt
  Comparator comparator_3 (.a(input_element), .b(8'h6b), .lt(comparator_3_lt));  // open: gt, eq
  assign output_key = and_2_out ? 2'b10 : 2'bz;  // Controlled_Buffer controlled_buffer_2
  and and_2 (and_2_out, comparator_3_lt, comparator_4_gt);
  Comparator comparator_4 (.a(input_element), .b(8'h65), .gt(comparator_4_gt));  // open: eq, lt
  Comparator comparator_5 (.a(input_element), .b(8'h35), .lt(comparator_5_lt));  // open: gt, eq
  assign output_key = and_3_out ? 2'b11 : 2'bz;  // Controlled_Buffer controlled_buffer_3
  and and_3 (and_3_out, comparator_5_lt, comparator_6_gt);
  Pull_Resistor pull_resistor_1 (.node(output_key));
  Comparator comparator_6 (.a(input_element), .b(8'h30), .gt(comparator_6_gt));  // open: eq, lt

  // Other names for the same wires on the sheet: elem[7:0] = input_element

  // Notes on the sheet:
  //   is it eat in cell
  //   is it weapon in cell
  //   is it enemy in cell
  //   Проверка входного значения
  //   0 - не сущность
  //   1 - еда
  //   2 - оружие
  //   3 - враг
endmodule

module plusMinus1 (
  input  GenRnd,
  input  [7:0] inp,
  output [7:0] out
);

  wire [2:0] random_1_out;
  wire [7:0] adder_1_out, bit_extender_1_out, bit_extender_2_out, subtractor_1_out;

  Random #(.width(3)) random_1 (.clk(GenRnd), .out(random_1_out));  // open: next, clr
  assign bit_extender_1_out = {{7{1'b0}}, random_1_out[1]};  // Bit_Extender bit_extender_1
  Subtractor subtractor_1 (.a(inp), .b(bit_extender_1_out), .out(subtractor_1_out));  // open: bin, bout
  assign bit_extender_2_out = {{7{1'b0}}, random_1_out[2]};  // Bit_Extender bit_extender_2
  Adder adder_1 (.a(bit_extender_2_out), .b(inp), .out(adder_1_out));  // open: cin, cout
  Multiplexer #(.width(8), .enable("false")) multiplexer_1 (
    .in0(subtractor_1_out), .in1(adder_1_out), .out(out), .sel(random_1_out[0]));

  // Notes on the sheet:
  //   Такт для рандома
  //   Возвращает inp в пределах (-1 0 +1)
endmodule
