// Logisim project main.circ as structural Verilog: 20 circuits, main circuit main
module main (
);

  wire _1onInp, _1onInpff, _1second, _2onInp, _2onInpff, _3onInp, _3onInpff, _4onInp, _4onInpff, _5onInp,
       _5onInpff, AddNewHunger, and_1_out, and_3_out, and_4_out, and_5_out, and_7_out, and_11_out,
       and_12_out, and_13_out, and_14_out, and_15_out, and_16_out, and_17_out, and_18_out, and_20_out,
       and_21_out, and_23_out, and_25_out, and_26_out, and_27_out, and_28_out, and_29_out, and_30_out,
       AonInp, ATCcorrectINP, ATCenMoved, ATCinisW, ATCinit, ATCInpFlpre, ATCnewENclc, ATCplAttaked1,
       buffer_1_out, buffer_4_out, buffer_7_out, buffer_8_out, buffer_11_out, button_1_out, changePCx,
       changePCy, CHHPinmove, clock_1_out, comparator_1_eq, comparator_1_gt, comparator_2_eq,
       comparator_3_eq, comparator_5_eq, comparator_6_gt, comparator_7_eq, comparator_8_gt, comparator_9_eq,
       comparator_10_eq, comparator_11_eq, comparator_12_eq, comparator_13_eq, comparator_19_eq,
       comparator_19_gt, comparator_20_gt, comparator_21_eq, comparator_22_eq, comparator_23_eq,
       comparator_24_eq, comparator_25_eq, comparator_26_eq, comparator_27_eq, comparator_28_eq,
       comparator_29_eq, DonInp, EATflare, gS0, gS2, gS3, iCF, InpFl1, InpFlpreC, InpFlpreM, InpFlpreSTRT,
       INV1ch, INV2ch, INV3ch, INV4ch, INV5ch, invchn, itemRES1, itemRES2, itemRES3, itemRES4, itemRES5,
       keyPress, LoadMap, lquick_1_out, lquick_2_out, lquick_3_out, mainRES, MAPisBYSU, MapLevelCh,
       MapLoaded, mapLoading, mapPREst, mapPREst1, MoveFl, MOVEinited, newText, not_1_out, not_2_out,
       not_3_out, not_4_out, not_5_out, not_6_out, not_8_out, not_10_out, not_11_out, not_12_out, not_13_out,
       not_14_out, not_15_out, not_16_out, not_17_out, not_18_out, not_19_out, not_20_out, not_21_out,
       not_22_out, not_23_out, not_24_out, not_25_out, not_26_out, not_27_out, not_28_out, not_29_out,
       not_30_out, not_31_out, not_32_out, not_33_out, not_34_out, not_35_out, not_36_out, not_37_out,
       not_38_out, not_39_out, not_40_out, nRand, or_1_out, or_2_out, or_3_out, or_4_out, or_5_out, or_7_out,
       or_8_out, or_9_out, or_10_out, or_11_out, or_12_out, or_13_out, or_14_out, or_16_out, or_18_out,
       or_21_out, or_22_out, or_23_out, or_24_out, or_25_out, or_26_out, or_28_out, or_29_out, or_30_out,
       or_35_out, PlayerDeathRes, PLAYERHPCH, PlayerLoseRes, PlDirCh, printitem_1_eat, printitem_1_weapon,
       printitem_2_eat, printitem_2_weapon, printitem_3_eat, printitem_3_weapon, printitem_4_eat,
       printitem_4_weapon, printitem_5_eat, printitem_5_weapon, PrintLose, printtext_1_ptclc,
       printtext_1_ptd, printtext_1_res, printtext_2_ptclc, printtext_2_ptd, printtext_2_res,
       printtext_3_ptclc, printtext_3_ptd, printtext_3_res, printtext_4_ptclc, printtext_4_ptd,
       printtext_4_res, printtext_5_ptclc, printtext_5_ptd, printtext_5_res, printtext_6_ptclc,
       printtext_6_ptd, printtext_6_res, printtext_7_ptclc, printtext_7_ptd, printtext_7_res,
       printtext_8_ptclc, printtext_8_ptd, printtext_8_res, PrintWIN, pull_resistor_6_node,
       pull_resistor_7_node, pull_resistor_9_node, pull_resistor_14_node, pull_resistor_16_node,
       pull_resistor_17_node, qres, qreset, quick_2_out, quick_3_out, quick_5_out, quick_6_out, quick_7_out,
       quick_8_out, quick_10_out, quick_12_out, quick_13_out, quick_15_out, quick_16_out, quick_17_out,
       quick_18_out, quick_19_out, quick_20_out, quick_21_out, quick_22_out, quick_23_out, quick_24_out,
       quick_25_out, quick_26_out, quick_27_out, quick_28_out, quick_29_out, quick_30_out, register_6_q,
       StateCh, stMapCLC, stMapCLC1, stMapCLC2, weapon_1_nw, weaponselected_1_weaponselected, win, WonInp,
       WonInpff;
  wire [1:0] adder_3_out, ATCcurEN, ATCnewEN, bit_extender_3_out, bit_extender_4_out, bit_extender_5_out,
       bit_extender_6_out, driver_mm_1_p50, driver_mm_1_p51, gameState, gSto, NewPlDir, subtractor_5_out,
       whatis_1_output_key, whatis_2_output_key, whatis_3_output_key, whatis_4_output_key;
  wire [2:0] pull_resistor_1_node, pull_resistor_5_node;
  wire [3:0] hund, one, printhp_1_high, printhp_1_low, printhp_2_high, printhp_2_low, printhp_3_high,
       printhp_3_low, ten;
  wire [4:0] adder_7_out, bit_extender_9_out, bit_extender_10_out, bit_extender_11_out, bit_extender_12_out,
       bit_extender_13_out, bit_extender_14_out, miniMScrT, multiplexer_12_out, multiplexer_13_out,
       pull_resistor_13_node, register_34_q, TextText;
  wire [5:0] bit_extender_15_out, bit_extender_16_out, curEnDmg, curPlDmg, lstEnDmg, lstPlDmg,
       multiplexer_25_out, multiplexer_26_out;
  wire [6:0] adder_5_out, bit_extender_7_out, bit_extender_8_out, iCR, printtext_1_char, printtext_2_char,
       printtext_3_char, printtext_4_char, printtext_5_char, printtext_6_char, printtext_7_char,
       printtext_8_char;
  wire [7:0] adder_1_out, adder_4_out, AddHunger, AddNewHungerVal, counter_1_q, CurHunger, ENDMG, ENDMGst,
       enemies_1_hp, ENHP, ENHPst, gStdtScrMem, INVENTORY1, INVENTORY1p, INVENTORY2, INVENTORY2p, INVENTORY3,
       INVENTORY3p, INVENTORY4, INVENTORY4p, INVENTORY5, INVENTORY5p, maps_1_xpp, maps_1_ypp,
       mapSTDATAreaded, multiplexer_1_out, multiplexer_2_out, multiplexer_3_out, multiplexer_5_out,
       multiplexer_7_out, multiplexer_8_out, multiplexer_10_out, NewMapLevelCh, NewPlayerHP, NewPLxOM,
       NewPLyOM, objectONmap, p_x_1_y, p_x_1_y_t, p_x_2_y, p_x_2_y_t, p_x_y, p_x_y_1, p_x_y_1_t, p_x_y_2,
       p_x_y_2_t, playerHPCUR, plusminus1_1_out, register_30_q, subtractor_1_out, subtractor_2_out,
       subtractor_3_out, subtractor_4_out, subtractor_6_out, subtractor_7_out, subtractor_8_out,
       subtractor_9_out, subtractor_10_out, subtractor_11_out, subtractor_12_out, subtractor_13_out,
       subtractor_14_out, weapon_1_dmg;
  wire [8:0] b, printitem_1_str1, printitem_1_str2, printitem_1_str3, printitem_1_str4, printitem_1_str5,
       printitem_1_str6, printitem_1_str7, printitem_1_str8, printitem_1_str9, printitem_2_str1,
       printitem_2_str2, printitem_2_str3, printitem_2_str4, printitem_2_str5, printitem_2_str6,
       printitem_2_str7, printitem_2_str8, printitem_2_str9, printitem_3_str1, printitem_3_str2,
       printitem_3_str3, printitem_3_str4, printitem_3_str5, printitem_3_str6, printitem_3_str7,
       printitem_3_str8, printitem_3_str9, printitem_4_str1, printitem_4_str2, printitem_4_str3,
       printitem_4_str4, printitem_4_str5, printitem_4_str6, printitem_4_str7, printitem_4_str8,
       printitem_4_str9, printitem_5_str1, printitem_5_str2, printitem_5_str3, printitem_5_str4,
       printitem_5_str5, printitem_5_str6, printitem_5_str7, printitem_5_str8, printitem_5_str9;
  wire [11:0] adder_2_out, MAP_tospace_ELEM, MapH, mapLen, maps_1_height, maps_1_width, mapSTelemREAD, MapW,
       moveinitialization_1_where, multiplexer_4_out, p_x_1_y__elemOnMap, p_x_1_y__elemOnMap_t,
       p_x_y_1__elemOnMap, p_x_y_1__elemOnMap_t, p_x_y__elemOnMap;
  wire [13:0] driver_mm_1_p35, driver_mm_1_p36, driver_mm_1_p37, driver_mm_1_p38, driver_mm_1_p39,
       driver_mm_1_p40, driver_mm_1_p41, driver_mm_1_p42, driver_mm_1_p43, driver_mm_1_p44, driver_mm_1_p45,
       driver_mm_1_p46, driver_mm_1_p47, driver_mm_1_p48;
  wire [15:0] ASSH, driver_mm_1_p19, driver_mm_1_p20, driver_mm_1_p21, driver_mm_1_p22, driver_mm_1_p23,
       driver_mm_1_p24, driver_mm_1_p25, driver_mm_1_p26, driver_mm_1_p27, driver_mm_1_p28, driver_mm_1_p29,
       driver_mm_1_p30, driver_mm_1_p31, driver_mm_1_p32, driver_mm_1_p33, driver_mm_1_p34;
  wire [16:0] gBus2;
  wire [17:0] driver_mm_1_p1, driver_mm_1_p2, driver_mm_1_p3, driver_mm_1_p4, driver_mm_1_p5, driver_mm_1_p6,
       driver_mm_1_p7, driver_mm_1_p8, driver_mm_1_p9, driver_mm_1_p10, driver_mm_1_p11, driver_mm_1_p12,
       driver_mm_1_p13, driver_mm_1_p14, driver_mm_1_p15, driver_mm_1_p16, driver_mm_1_p17, driver_mm_1_p18;
  wire [20:0] miniScrT;
  wire [25:0] _1Bus, _2Bus, _3Bus, _4Bus, _5Bus, gBus1, mainScrT;
  wire [25:6] textBus;
  wire [27:0] driver_l_1_out_8, driver_l_1_out_12, driver_l_1_out_16, driver_l_1_out_20, driver_l_1_out_24,
       driver_l_1_out_28, driver_l_1_out_32, driver_l_1_out_36, driver_l_1_out_40, driver_l_1_out_44,
       driver_l_1_out_48, driver_l_1_out_52, driver_l_1_out_56, driver_l_1_out_60, driver_l_1_out_64,
       driver_l_1_out_68, driver_l_1_out_72, driver_l_1_out_76, driver_l_1_out_80, driver_l_1_out_84,
       driver_l_1_out_88, driver_l_1_out_92, driver_l_1_out_96, driver_l_1_out_100, driver_l_1_out_104,
       driver_l_1_out_108, driver_l_1_out_112, driver_l_1_out_116, driver_l_1_out_120, driver_l_1_out_124,
       driver_l_1_out_128, driver_l_1_out_132;
  wire [28:0] driver_l_1_out_7, driver_l_1_out_11, driver_l_1_out_15, driver_l_1_out_19, driver_l_1_out_23,
       driver_l_1_out_27, driver_l_1_out_31, driver_l_1_out_35, driver_l_1_out_39, driver_l_1_out_43,
       driver_l_1_out_47, driver_l_1_out_51, driver_l_1_out_55, driver_l_1_out_59, driver_l_1_out_63,
       driver_l_1_out_67, driver_l_1_out_71, driver_l_1_out_75, driver_l_1_out_79, driver_l_1_out_83,
       driver_l_1_out_87, driver_l_1_out_91, driver_l_1_out_95, driver_l_1_out_99, driver_l_1_out_103,
       driver_l_1_out_107, driver_l_1_out_111, driver_l_1_out_115, driver_l_1_out_119, driver_l_1_out_123,
       driver_l_1_out_127, driver_l_1_out_131, driver_r_1_out_8, driver_r_1_out_12, driver_r_1_out_16,
       driver_r_1_out_20, driver_r_1_out_24, driver_r_1_out_28, driver_r_1_out_32, driver_r_1_out_36,
       driver_r_1_out_40, driver_r_1_out_44, driver_r_1_out_48, driver_r_1_out_52, driver_r_1_out_56,
       driver_r_1_out_60, driver_r_1_out_64, driver_r_1_out_68, driver_r_1_out_72, driver_r_1_out_76,
       driver_r_1_out_80, driver_r_1_out_84, driver_r_1_out_88, driver_r_1_out_92, driver_r_1_out_96,
       driver_r_1_out_100, driver_r_1_out_104, driver_r_1_out_108, driver_r_1_out_112, driver_r_1_out_116,
       driver_r_1_out_120, driver_r_1_out_124, driver_r_1_out_128, driver_r_1_out_132;
  wire [29:0] driver_l_1_out_6, driver_l_1_out_10, driver_l_1_out_14, driver_l_1_out_18, driver_l_1_out_22,
       driver_l_1_out_26, driver_l_1_out_30, driver_l_1_out_34, driver_l_1_out_38, driver_l_1_out_42,
       driver_l_1_out_46, driver_l_1_out_50, driver_l_1_out_54, driver_l_1_out_58, driver_l_1_out_62,
       driver_l_1_out_66, driver_l_1_out_70, driver_l_1_out_74, driver_l_1_out_78, driver_l_1_out_82,
       driver_l_1_out_86, driver_l_1_out_90, driver_l_1_out_94, driver_l_1_out_98, driver_l_1_out_102,
       driver_l_1_out_106, driver_l_1_out_110, driver_l_1_out_114, driver_l_1_out_118, driver_l_1_out_122,
       driver_l_1_out_126, driver_l_1_out_130, driver_r_1_out_7, driver_r_1_out_11, driver_r_1_out_15,
       driver_r_1_out_19, driver_r_1_out_23, driver_r_1_out_27, driver_r_1_out_31, driver_r_1_out_35,
       driver_r_1_out_39, driver_r_1_out_43, driver_r_1_out_47, driver_r_1_out_51, driver_r_1_out_55,
       driver_r_1_out_59, driver_r_1_out_63, driver_r_1_out_67, driver_r_1_out_71, driver_r_1_out_75,
       driver_r_1_out_79, driver_r_1_out_83, driver_r_1_out_87, driver_r_1_out_91, driver_r_1_out_95,
       driver_r_1_out_99, driver_r_1_out_103, driver_r_1_out_107, driver_r_1_out_111, driver_r_1_out_115,
       driver_r_1_out_119, driver_r_1_out_123, driver_r_1_out_127, driver_r_1_out_131;
  wire [30:0] driver_l_1_out_5, driver_l_1_out_9, driver_l_1_out_13, driver_l_1_out_17, driver_l_1_out_21,
       driver_l_1_out_25, driver_l_1_out_29, driver_l_1_out_33, driver_l_1_out_37, driver_l_1_out_41,
       driver_l_1_out_45, driver_l_1_out_49, driver_l_1_out_53, driver_l_1_out_57, driver_l_1_out_61,
       driver_l_1_out_65, driver_l_1_out_69, driver_l_1_out_73, driver_l_1_out_77, driver_l_1_out_81,
       driver_l_1_out_85, driver_l_1_out_89, driver_l_1_out_93, driver_l_1_out_97, driver_l_1_out_101,
       driver_l_1_out_105, driver_l_1_out_109, driver_l_1_out_113, driver_l_1_out_117, driver_l_1_out_121,
       driver_l_1_out_125, driver_l_1_out_129, driver_r_1_out_6, driver_r_1_out_10, driver_r_1_out_14,
       driver_r_1_out_18, driver_r_1_out_22, driver_r_1_out_26, driver_r_1_out_30, driver_r_1_out_34,
       driver_r_1_out_38, driver_r_1_out_42, driver_r_1_out_46, driver_r_1_out_50, driver_r_1_out_54,
       driver_r_1_out_58, driver_r_1_out_62, driver_r_1_out_66, driver_r_1_out_70, driver_r_1_out_74,
       driver_r_1_out_78, driver_r_1_out_82, driver_r_1_out_86, driver_r_1_out_90, driver_r_1_out_94,
       driver_r_1_out_98, driver_r_1_out_102, driver_r_1_out_106, driver_r_1_out_110, driver_r_1_out_114,
       driver_r_1_out_118, driver_r_1_out_122, driver_r_1_out_126, driver_r_1_out_130;
  wire [31:0] driver_r_1_out_5, driver_r_1_out_9, driver_r_1_out_13, driver_r_1_out_17, driver_r_1_out_21,
       driver_r_1_out_25, driver_r_1_out_29, driver_r_1_out_33, driver_r_1_out_37, driver_r_1_out_41,
       driver_r_1_out_45, driver_r_1_out_49, driver_r_1_out_53, driver_r_1_out_57, driver_r_1_out_61,
       driver_r_1_out_65, driver_r_1_out_69, driver_r_1_out_73, driver_r_1_out_77, driver_r_1_out_81,
       driver_r_1_out_85, driver_r_1_out_89, driver_r_1_out_93, driver_r_1_out_97, driver_r_1_out_101,
       driver_r_1_out_105, driver_r_1_out_109, driver_r_1_out_113, driver_r_1_out_117, driver_r_1_out_121,
       driver_r_1_out_125, driver_r_1_out_129;

  Register register_1 (.D(p_x_y), .Q(INVENTORY1), .clk(INV1ch), .clr(or_1_out));  // open: en
  Register register_2 (.D(p_x_y), .Q(INVENTORY2), .clk(INV2ch), .clr(or_2_out));  // open: en
  Register register_3 (.D(p_x_y), .Q(INVENTORY3), .clk(INV3ch), .clr(or_3_out));  // open: en
  Register register_4 (.D(p_x_y), .Q(INVENTORY4), .clk(INV4ch), .clr(or_4_out));  // open: en
  Register register_5 (.D(p_x_y), .Q(INVENTORY5), .clk(INV5ch), .clr(or_5_out));  // open: en
  or or_1 (or_1_out, mainRES, itemRES1);
  or or_2 (or_2_out, mainRES, itemRES2);
  or or_3 (or_3_out, mainRES, itemRES3);
  or or_4 (or_4_out, mainRES, itemRES4);
  or or_5 (or_5_out, mainRES, itemRES5);
  Pull_Resistor pull_resistor_1 (.node(pull_resistor_1_node));
  assign pull_resistor_1_node = _4onInp ? 3'b011 : 3'bz;  // Controlled_Buffer controlled_buffer_1
  assign pull_resistor_1_node = _5onInp ? 3'b100 : 3'bz;  // Controlled_Buffer controlled_buffer_2
  not not_1 (not_1_out, register_6_q);
  and and_1 (and_1_out, ATCinit, _1Bus[19]);
  Bit_Extender #(.out_width(6)) bit_extender_1 (.in(plusminus1_1_out), .out(curEnDmg));
  quick quick_1 (.IN(mapPREst1), .OUT(stMapCLC1));
  assign MAP_tospace_ELEM = mapPREst1 ? p_x_y__elemOnMap : 12'bz;  // Controlled_Buffer controlled_buffer_3
  food food_1 (.FOOD(multiplexer_1_out), .GIVEHP(AddNewHungerVal));  // open: ES
  Multiplexer #(.select(3), .width(8), .enable("false")) multiplexer_1 (
    .in0(INVENTORY1p), .in1(INVENTORY2p), .in2(INVENTORY3p), .in3(INVENTORY4p), .in4(INVENTORY5p),
    .in5({8{1'b0}}), .in6({8{1'b0}}), .in7({8{1'b0}}), .out(multiplexer_1_out), .sel(pull_resistor_1_node));
  assign pull_resistor_1_node = _2onInp ? 3'b001 : 3'bz;  // Controlled_Buffer controlled_buffer_4
  assign pull_resistor_1_node = _3onInp ? 3'b010 : 3'bz;  // Controlled_Buffer controlled_buffer_5
  Register #(.width(1)) register_6 (.D(not_1_out), .Q(register_6_q), .clk(and_1_out), .clr(ATCnewENclc));  // open: en
  enemies enemies_1 (.ADDR(ATCcurEN), .HP(enemies_1_hp), .DMG(ENDMGst));
  plusMinus1 plusminus1_1 (.inp(ENDMG), .out(plusminus1_1_out), .GenRnd(nRand));
  quick quick_2 (.IN(ATCplAttaked1), .OUT(quick_2_out));
  assign pull_resistor_1_node = _1onInp ? 3'b000 : 3'bz;  // Controlled_Buffer controlled_buffer_6
  Pull_Resistor pull_resistor_2 (.node(ATCinit));
  assign ATCinit = not_2_out ? not_2_out : 1'bz;  // Controlled_Buffer controlled_buffer_7
  not not_2 (not_2_out, register_6_q);
  assign ENHPst = not_2_out ? enemies_1_hp : 8'bz;  // Controlled_Buffer controlled_buffer_8
  assign NewPlayerHP = ATCenMoved ? subtractor_1_out : 8'bz;  // Controlled_Buffer controlled_buffer_9
  Subtractor subtractor_1 (.a(playerHPCUR), .b(plusminus1_1_out), .out(subtractor_1_out));  // open: bin, bout
  assign PLAYERHPCH = ATCenMoved ? 1'b1 : 1'bz;  // Controlled_Buffer controlled_buffer_10
  not not_3 (not_3_out, ATCenMoved);
  Register #(.width(1)) register_7 (.D(not_3_out), .Q(ATCenMoved), .clk(quick_2_out), .clr(buffer_1_out));  // open: en
  buf buffer_1 (buffer_1_out, PLAYERHPCH);
  Pull_Resistor pull_resistor_3 (.node(buffer_1_out));
  pickUpAnItem pickupanitem_1 (
    .p_x_y(p_x_y), ._1oninp(_1onInpff), ._2oninp(_2onInpff), ._3oninp(_3onInpff), ._4oninp(_4onInpff),
    ._5oninp(_5onInpff), .MOVEinited(MOVEinited), .INV1ch(INV1ch), .INV2ch(INV2ch), .INV3ch(INV3ch),
    .INV4ch(INV4ch), .INV5ch(INV5ch), .chMap(mapPREst1));  // open: ITEMinCELL, InpFl1
  Register register_8 (.D(INVENTORY1), .Q(INVENTORY1p), .clk(invchn));  // open: en, clr
  Register register_9 (.D(INVENTORY2), .Q(INVENTORY2p), .clk(invchn));  // open: en, clr
  Register register_10 (.D(INVENTORY3), .Q(INVENTORY3p), .clk(invchn));  // open: en, clr
  Register register_11 (.D(INVENTORY4), .Q(INVENTORY4p), .clk(invchn));  // open: en, clr
  Register register_12 (.D(INVENTORY5), .Q(INVENTORY5p), .clk(invchn));  // open: en, clr
  eatFood eatfood_1 (
    .INVENTORY1p(INVENTORY1p), ._1onInpff(_1onInpff), .INVENTORY2p(INVENTORY2p), ._2onInpff(_2onInpff),
    .INVENTORY3p(INVENTORY3p), ._3onInpff(_3onInpff), .INVENTORY4p(INVENTORY4p), ._4onInpff(_4onInpff),
    .INVENTORY5p(INVENTORY5p), ._5onInpff(_5onInpff), .itemRES1(itemRES1), .itemRES2(itemRES2),
    .itemRES3(itemRES3), .itemRES4(itemRES4), .itemRES5(itemRES5), .EatFlare(EATflare),
    .CHHPinmove(CHHPinmove));
  Adder adder_1 (.a(AddNewHungerVal), .b(playerHPCUR), .out(adder_1_out));  // open: cin, cout
  Multiplexer #(.width(8), .enable("false")) multiplexer_2 (
    .in0(adder_1_out), .in1(8'h32), .out(multiplexer_2_out), .sel(or_7_out));
  Pull_Resistor pull_resistor_4 (.node(adder_1_out));
  Comparator comparator_1 (.a(adder_1_out), .b(8'h32), .gt(comparator_1_gt), .eq(comparator_1_eq));  // open: lt
  assign newText = ATCenMoved ? ATCenMoved : 1'bz;  // Controlled_Buffer controlled_buffer_11
  or or_6 (EATflare, MOVEinited, ATCInpFlpre);
  assign NewPlayerHP = AddNewHunger ? multiplexer_2_out : 8'bz;  // Controlled_Buffer controlled_buffer_12
  assign PLAYERHPCH = AddNewHunger ? 1'b1 : 1'bz;  // Controlled_Buffer controlled_buffer_13
  or or_7 (or_7_out, comparator_1_gt, comparator_1_eq);
  and and_2 (AddNewHunger, EATflare, ~ATCenMoved, CHHPinmove);  // AND_Gate
  Comparator comparator_2 (.a(8'h45), .b(p_x_y), .eq(comparator_2_eq));  // open: gt, lt
  Comparator comparator_3 (.a(8'h2), .b(gBus1[23:16]), .eq(comparator_3_eq));  // open: gt, lt
  Comparator comparator_4 (.a(8'h57), .b(p_x_y), .eq(qreset));  // open: gt, lt
  assign TextText = ATCenMoved ? 5'b10100 : 5'bz;  // Controlled_Buffer controlled_buffer_14
  assign MapLevelCh = quick_3_out ? quick_3_out : 1'bz;  // Controlled_Buffer controlled_buffer_15
  and and_3 (and_3_out, comparator_2_eq, ~comparator_3_eq);  // AND_Gate
  quick quick_3 (.IN(and_3_out), .OUT(quick_3_out));
  Register #(.width(1)) register_13 (.D(1'b1), .Q(PrintWIN), .clk(qreset), .clr(InpFlpreSTRT));  // open: en
  Comparator #(.mode("unsigned")) comparator_5 (.a(ENHP), .b({8{1'b0}}), .eq(comparator_5_eq));  // open: gt, lt
  Comparator #(.mode("unsigned")) comparator_6 (.a(ENHP), .b(8'h32), .gt(comparator_6_gt));  // open: eq, lt
  Pull_Resistor pull_resistor_5 (.node(pull_resistor_5_node));
  assign pull_resistor_5_node = _5onInp ? 3'b101 : 3'bz;  // Controlled_Buffer controlled_buffer_16
  and and_4 (and_4_out, ATCplAttaked1, or_8_out);
  or or_8 (or_8_out, comparator_5_eq, comparator_6_gt);
  Pull_Resistor pull_resistor_6 (.node(pull_resistor_6_node));
  buf buffer_2 (pull_resistor_6_node, MapLevelCh);
  Pull_Resistor pull_resistor_7 (.node(pull_resistor_7_node));
  buf buffer_3 (pull_resistor_7_node, PLAYERHPCH);
  Register #(.width(6)) register_14 (.D(curPlDmg), .Q(lstPlDmg), .clk(ATCcorrectINP), .clr(ATCinit));  // open: en
  or or_9 (or_9_out, InpFlpreM, InpFlpreSTRT, MoveFl, InpFlpreC);
  assign pull_resistor_5_node = _4onInp ? 3'b100 : 3'bz;  // Controlled_Buffer controlled_buffer_17
  assign pull_resistor_5_node = _3onInp ? 3'b011 : 3'bz;  // Controlled_Buffer controlled_buffer_18
  assign StateCh = win ? win : 1'bz;  // Controlled_Buffer controlled_buffer_19
  quick quick_4 (.IN(and_4_out), .OUT(win));
  assign newText = win ? win : 1'bz;  // Controlled_Buffer controlled_buffer_20
  Register register_15 (.D(NewMapLevelCh), .Q(gBus1[23:16]), .clk(pull_resistor_6_node), .clr(mainRES));  // open: en
  Register register_16 (.D(NewPlayerHP), .Q(playerHPCUR), .clk(pull_resistor_7_node), .clr(mainRES));  // open: en
  Register #(.width(2)) register_17 (.D(ATCnewEN), .Q(ATCcurEN), .clk(ATCnewENclc), .clr(mainRES));  // open: en
  assign MAP_tospace_ELEM = MAPisBYSU ? moveinitialization_1_where : 12'bz;  // Controlled_Buffer controlled_buffer_21
  Multiplexer #(.select(3), .width(8), .enable("false")) multiplexer_3 (
    .in0({8{1'b1}}), .in1(INVENTORY1p), .in2(INVENTORY2p), .in3(INVENTORY3p), .in4(INVENTORY4p),
    .in5(INVENTORY5p), .out(multiplexer_3_out), .sel(pull_resistor_5_node));  // open: in6, in7
  weapon weapon_1 (.WEAPON(multiplexer_3_out), .DMG(weapon_1_dmg), .GenRnd(nRand), .nW(weapon_1_nw));
  assign pull_resistor_5_node = _2onInp ? 3'b010 : 3'bz;  // Controlled_Buffer controlled_buffer_22
  assign pull_resistor_5_node = _1onInp ? 3'b001 : 3'bz;  // Controlled_Buffer controlled_buffer_23
  Register #(.width(6)) register_18 (.D(curEnDmg), .Q(lstEnDmg), .clk(ATCenMoved), .clr(ATCinit));  // open: en
  and and_5 (and_5_out, MOVEinited, WonInpff);
  or or_10 (or_10_out, _1onInp, _2onInp, _3onInp, _4onInp, _5onInp);
  assign TextText = win ? 5'b10101 : 5'bz;  // Controlled_Buffer controlled_buffer_24
  Register #(.width(2)) register_19 (.D(gSto), .Q(gameState), .clk(buffer_4_out), .clr(mainRES));  // open: en
  buf buffer_4 (buffer_4_out, StateCh);
  Pull_Resistor pull_resistor_8 (.node(buffer_4_out));
  Register #(.width(2)) register_20 (.D(NewPlDir), .Q(gBus1[25:24]), .clk(PlDirCh), .clr(mainRES));  // open: en
  Register register_21 (.D(ENDMGst), .Q(ENDMG), .clk(ATCinit), .clr(mainRES));  // open: en
  Register register_22 (.D(ENHPst), .Q(ENHP), .clk(or_11_out), .clr(mainRES));  // open: en
  or or_11 (or_11_out, ATCcorrectINP, ATCinit);
  moveInitialization moveinitialization_1 (
    .InpFlare(or_9_out), .mapW(MapW), .y(gBus1[15:8]), .x(gBus1[7:0]), .p_x_y(p_x_y), .p_x_y_1(p_x_y_1_t),
    .p_x_y_1_2(p_x_y_1), .p_x_1_y(p_x_1_y_t), .p_x_1_y_2(p_x_1_y), .p_x_2_y(p_x_2_y), .p_x_2_y_2(p_x_2_y_t),
    .p_x_y_2(p_x_y_2_t), .p_x_y_2_2(p_x_y_2), .MoveInited(MOVEinited), .where(moveinitialization_1_where),
    .objMap(objectONmap), .workWithMap(MAPisBYSU), .x_y_elonmap(p_x_y__elemOnMap),
    .x_y_1_elonmap_2(p_x_y_1__elemOnMap_t), .x_y_1_elonmap(p_x_y_1__elemOnMap),
    .x_1_y_elonmap_2(p_x_1_y__elemOnMap_t), .x_1_y_elonmap(p_x_1_y__elemOnMap), .MainCLC(_1Bus[19]),
    .Stop(mapLoading));
  and and_6 (nRand, gS2, or_10_out);
  Lquick lquick_1 (.IN(nRand), .OUT(lquick_1_out), .CLC(_1Bus[19]));
  and and_7 (and_7_out, nRand, ~weapon_1_nw);  // AND_Gate
  Subtractor subtractor_2 (.a(ENHP), .b(weapon_1_dmg), .out(subtractor_2_out));  // open: bin, bout
  Bit_Extender #(.out_width(6)) bit_extender_2 (.in(weapon_1_dmg), .out(curPlDmg));
  weaponSelected weaponselected_1 (
    .weaponSelected(weaponselected_1_weaponselected), .INVENTORY1p(INVENTORY1p), ._1oninp(_1onInpff),
    .INVENTORY2p(INVENTORY2p), ._2oninp(_2onInpff), ._3oninp(_3onInpff), .INVENTORY3p(INVENTORY3p),
    ._4oninp(_4onInpff), ._5oninp(_5onInpff), .INVENTORY4p(INVENTORY4p), .INVENTORY5p(INVENTORY5p));
  Comparator #(.mode("unsigned")) comparator_7 (.a(playerHPCUR), .b({8{1'b0}}), .eq(comparator_7_eq));  // open: gt, lt
  Comparator #(.mode("unsigned")) comparator_8 (.a(playerHPCUR), .b(8'h32), .gt(comparator_8_gt));  // open: eq, lt
  doForwardStep doforwardstep_1 (
    .PlDir(gBus1[25:24]), .NewPLyOM(NewPLyOM), .changePCy(changePCy), .NewPLxOM(NewPLxOM),
    .changePCx(changePCx), .WonInp(and_5_out), .p_x_1_y(p_x_1_y_t), .p_x_1_y_2(p_x_1_y), .p_x_y_1(p_x_y_1),
    .p_x_y_1_2(p_x_y_1_t), .plX(gBus1[7:0]), .plY(gBus1[15:8]), .moved(MoveFl));
  and and_8 (ATCcorrectINP, nRand, ~lquick_1_out);  // AND_Gate
  not not_4 (not_4_out, not_6_out);
  not not_5 (not_5_out, and_7_out);
  not not_6 (not_6_out, not_5_out);
  assign ENHPst = and_7_out ? subtractor_2_out : 8'bz;  // Controlled_Buffer controlled_buffer_25
  and and_9 (ATCinisW, ATCInpFlpre, weaponselected_1_weaponselected);
  or or_12 (or_12_out, comparator_7_eq, comparator_8_gt);
  quick quick_5 (.IN(or_12_out), .OUT(quick_5_out));
  printText printtext_1 (
    .Input({mainScrT[25:20], _1Bus[19], 7'b1010110, mainScrT[11:0]}), .pTclc(printtext_1_ptclc),
    .char(printtext_1_char), .ptd(printtext_1_ptd), .res(printtext_1_res));
  TTY #(.rows(2), .cols(44)) tty_1 (
    .data(printtext_1_char), .clk(printtext_1_ptclc), .we(printtext_1_ptd), .clr(printtext_1_res));
  driver_l driver_l_1 (
    .b(b), .ASSH(ASSH), .out_5(driver_l_1_out_5), .out_6(driver_l_1_out_6), .out_7(driver_l_1_out_7),
    .out_8(driver_l_1_out_8), .out_9(driver_l_1_out_9), .out_10(driver_l_1_out_10),
    .out_11(driver_l_1_out_11), .out_12(driver_l_1_out_12), .out_13(driver_l_1_out_13),
    .out_14(driver_l_1_out_14), .out_15(driver_l_1_out_15), .out_16(driver_l_1_out_16),
    .out_17(driver_l_1_out_17), .out_18(driver_l_1_out_18), .out_19(driver_l_1_out_19),
    .out_20(driver_l_1_out_20), .out_21(driver_l_1_out_21), .out_22(driver_l_1_out_22),
    .out_23(driver_l_1_out_23), .out_24(driver_l_1_out_24), .out_25(driver_l_1_out_25),
    .out_26(driver_l_1_out_26), .out_27(driver_l_1_out_27), .out_28(driver_l_1_out_28),
    .out_29(driver_l_1_out_29), .out_30(driver_l_1_out_30), .out_31(driver_l_1_out_31),
    .out_32(driver_l_1_out_32), .out_33(driver_l_1_out_33), .out_34(driver_l_1_out_34),
    .out_35(driver_l_1_out_35), .out_36(driver_l_1_out_36), .out_37(driver_l_1_out_37),
    .out_38(driver_l_1_out_38), .out_39(driver_l_1_out_39), .out_40(driver_l_1_out_40),
    .out_41(driver_l_1_out_41), .out_42(driver_l_1_out_42), .out_43(driver_l_1_out_43),
    .out_44(driver_l_1_out_44), .out_45(driver_l_1_out_45), .out_46(driver_l_1_out_46),
    .out_47(driver_l_1_out_47), .out_48(driver_l_1_out_48), .out_49(driver_l_1_out_49),
    .out_50(driver_l_1_out_50), .out_51(driver_l_1_out_51), .out_52(driver_l_1_out_52),
    .out_53(driver_l_1_out_53), .out_54(driver_l_1_out_54), .out_55(driver_l_1_out_55),
    .out_56(driver_l_1_out_56), .out_57(driver_l_1_out_57), .out_58(driver_l_1_out_58),
    .out_59(driver_l_1_out_59), .out_60(driver_l_1_out_60), .out_61(driver_l_1_out_61),
    .out_62(driver_l_1_out_62), .out_63(driver_l_1_out_63), .out_64(driver_l_1_out_64),
    .out_65(driver_l_1_out_65), .out_66(driver_l_1_out_66), .out_67(driver_l_1_out_67),
    .out_68(driver_l_1_out_68), .out_69(driver_l_1_out_69), .out_70(driver_l_1_out_70),
    .out_71(driver_l_1_out_71), .out_72(driver_l_1_out_72), .out_73(driver_l_1_out_73),
    .out_74(driver_l_1_out_74), .out_75(driver_l_1_out_75), .out_76(driver_l_1_out_76),
    .out_77(driver_l_1_out_77), .out_78(driver_l_1_out_78), .out_79(driver_l_1_out_79),
    .out_80(driver_l_1_out_80), .out_81(driver_l_1_out_81), .out_82(driver_l_1_out_82),
    .out_83(driver_l_1_out_83), .out_84(driver_l_1_out_84), .out_85(driver_l_1_out_85),
    .out_86(driver_l_1_out_86), .out_87(driver_l_1_out_87), .out_88(driver_l_1_out_88),
    .out_89(driver_l_1_out_89), .out_90(driver_l_1_out_90), .out_91(driver_l_1_out_91),
    .out_92(driver_l_1_out_92), .out_93(driver_l_1_out_93), .out_94(driver_l_1_out_94),
    .out_95(driver_l_1_out_95), .out_96(driver_l_1_out_96), .out_97(driver_l_1_out_97),
    .out_98(driver_l_1_out_98), .out_99(driver_l_1_out_99), .out_100(driver_l_1_out_100),
    .out_101(driver_l_1_out_101), .out_102(driver_l_1_out_102), .out_103(driver_l_1_out_103),
    .out_104(driver_l_1_out_104), .out_105(driver_l_1_out_105), .out_106(driver_l_1_out_106),
    .out_107(driver_l_1_out_107), .out_108(driver_l_1_out_108), .out_109(driver_l_1_out_109),
    .out_110(driver_l_1_out_110), .out_111(driver_l_1_out_111), .out_112(driver_l_1_out_112),
    .out_113(driver_l_1_out_113), .out_114(driver_l_1_out_114), .out_115(driver_l_1_out_115),
    .out_116(driver_l_1_out_116), .out_117(driver_l_1_out_117), .out_118(driver_l_1_out_118),
    .out_119(driver_l_1_out_119), .out_120(driver_l_1_out_120), .out_121(driver_l_1_out_121),
    .out_122(driver_l_1_out_122), .out_123(driver_l_1_out_123), .out_124(driver_l_1_out_124),
    .out_125(driver_l_1_out_125), .out_126(driver_l_1_out_126), .out_127(driver_l_1_out_127),
    .out_128(driver_l_1_out_128), .out_129(driver_l_1_out_129), .out_130(driver_l_1_out_130),
    .out_131(driver_l_1_out_131), .out_132(driver_l_1_out_132), .curr_enem(ATCcurEN), .gameState(gameState));
  DotMatrix #(.inputtype("row"), .matrixcols(28), .matrixrows(32)) dotmatrix_1 (
    .row0(driver_l_1_out_8), .row1(driver_l_1_out_12), .row2(driver_l_1_out_16), .row3(driver_l_1_out_20),
    .row4(driver_l_1_out_24), .row5(driver_l_1_out_28), .row6(driver_l_1_out_32), .row7(driver_l_1_out_36),
    .row8(driver_l_1_out_40), .row9(driver_l_1_out_44), .row10(driver_l_1_out_48), .row11(driver_l_1_out_52),
    .row12(driver_l_1_out_56), .row13(driver_l_1_out_60), .row14(driver_l_1_out_64),
    .row15(driver_l_1_out_68), .row16(driver_l_1_out_72), .row17(driver_l_1_out_76),
    .row18(driver_l_1_out_80), .row19(driver_l_1_out_84), .row20(driver_l_1_out_88),
    .row21(driver_l_1_out_92), .row22(driver_l_1_out_96), .row23(driver_l_1_out_100),
    .row24(driver_l_1_out_104), .row25(driver_l_1_out_108), .row26(driver_l_1_out_112),
    .row27(driver_l_1_out_116), .row28(driver_l_1_out_120), .row29(driver_l_1_out_124),
    .row30(driver_l_1_out_128), .row31(driver_l_1_out_132));
  DotMatrix #(.inputtype("row"), .matrixcols(29), .matrixrows(32)) dotmatrix_2 (
    .row0(driver_l_1_out_7), .row1(driver_l_1_out_11), .row2(driver_l_1_out_15), .row3(driver_l_1_out_19),
    .row4(driver_l_1_out_23), .row5(driver_l_1_out_27), .row6(driver_l_1_out_31), .row7(driver_l_1_out_35),
    .row8(driver_l_1_out_39), .row9(driver_l_1_out_43), .row10(driver_l_1_out_47), .row11(driver_l_1_out_51),
    .row12(driver_l_1_out_55), .row13(driver_l_1_out_59), .row14(driver_l_1_out_63),
    .row15(driver_l_1_out_67), .row16(driver_l_1_out_71), .row17(driver_l_1_out_75),
    .row18(driver_l_1_out_79), .row19(driver_l_1_out_83), .row20(driver_l_1_out_87),
    .row21(driver_l_1_out_91), .row22(driver_l_1_out_95), .row23(driver_l_1_out_99),
    .row24(driver_l_1_out_103), .row25(driver_l_1_out_107), .row26(driver_l_1_out_111),
    .row27(driver_l_1_out_115), .row28(driver_l_1_out_119), .row29(driver_l_1_out_123),
    .row30(driver_l_1_out_127), .row31(driver_l_1_out_131));
  DotMatrix #(.inputtype("row"), .matrixcols(31), .matrixrows(32)) dotmatrix_3 (
    .row0(driver_l_1_out_5), .row1(driver_l_1_out_9), .row2(driver_l_1_out_13), .row3(driver_l_1_out_17),
    .row4(driver_l_1_out_21), .row5(driver_l_1_out_25), .row6(driver_l_1_out_29), .row7(driver_l_1_out_33),
    .row8(driver_l_1_out_37), .row9(driver_l_1_out_41), .row10(driver_l_1_out_45), .row11(driver_l_1_out_49),
    .row12(driver_l_1_out_53), .row13(driver_l_1_out_57), .row14(driver_l_1_out_61),
    .row15(driver_l_1_out_65), .row16(driver_l_1_out_69), .row17(driver_l_1_out_73),
    .row18(driver_l_1_out_77), .row19(driver_l_1_out_81), .row20(driver_l_1_out_85),
    .row21(driver_l_1_out_89), .row22(driver_l_1_out_93), .row23(driver_l_1_out_97),
    .row24(driver_l_1_out_101), .row25(driver_l_1_out_105), .row26(driver_l_1_out_109),
    .row27(driver_l_1_out_113), .row28(driver_l_1_out_117), .row29(driver_l_1_out_121),
    .row30(driver_l_1_out_125), .row31(driver_l_1_out_129));
  DotMatrix #(.inputtype("row"), .matrixcols(30), .matrixrows(32)) dotmatrix_4 (
    .row0(driver_l_1_out_6), .row1(driver_l_1_out_10), .row2(driver_l_1_out_14), .row3(driver_l_1_out_18),
    .row4(driver_l_1_out_22), .row5(driver_l_1_out_26), .row6(driver_l_1_out_30), .row7(driver_l_1_out_34),
    .row8(driver_l_1_out_38), .row9(driver_l_1_out_42), .row10(driver_l_1_out_46), .row11(driver_l_1_out_50),
    .row12(driver_l_1_out_54), .row13(driver_l_1_out_58), .row14(driver_l_1_out_62),
    .row15(driver_l_1_out_66), .row16(driver_l_1_out_70), .row17(driver_l_1_out_74),
    .row18(driver_l_1_out_78), .row19(driver_l_1_out_82), .row20(driver_l_1_out_86),
    .row21(driver_l_1_out_90), .row22(driver_l_1_out_94), .row23(driver_l_1_out_98),
    .row24(driver_l_1_out_102), .row25(driver_l_1_out_106), .row26(driver_l_1_out_110),
    .row27(driver_l_1_out_114), .row28(driver_l_1_out_118), .row29(driver_l_1_out_122),
    .row30(driver_l_1_out_126), .row31(driver_l_1_out_130));
  not not_7 (ATCplAttaked1, not_4_out);
  and and_10 (PlayerDeathRes, quick_5_out, gS2);
  printText printtext_2 (
    .Input({textBus[25:20], _1Bus[19], 7'b1010110, textBus[11:6], lstEnDmg}), .pTclc(printtext_2_ptclc),
    .char(printtext_2_char), .ptd(printtext_2_ptd), .res(printtext_2_res));
  TTY #(.rows(1), .cols(66)) tty_2 (
    .data(printtext_2_char), .clk(printtext_2_ptclc), .we(printtext_2_ptd), .clr(printtext_2_res));
  DotMatrix #(.inputtype("row"), .matrixcols(9), .matrixrows(9)) dotmatrix_5 (
    .row0(printitem_1_str1), .row1(printitem_1_str2), .row2(printitem_1_str3), .row3(printitem_1_str4),
    .row4(printitem_1_str5), .row5(printitem_1_str6), .row6(printitem_1_str7), .row7(printitem_1_str8),
    .row8(printitem_1_str9));
  printItem printitem_1 (
    .item(INVENTORY1), .str1(printitem_1_str1), .str5(printitem_1_str5), .str9(printitem_1_str9),
    .str2(printitem_1_str2), .str6(printitem_1_str6), .str3(printitem_1_str3), .str7(printitem_1_str7),
    .str4(printitem_1_str4), .str8(printitem_1_str8), .eat(printitem_1_eat), .weapon(printitem_1_weapon));
  printText printtext_3 (
    .Input({_1Bus[25:19], 7'b0001101, _1Bus[11:0]}), .pTclc(printtext_3_ptclc), .char(printtext_3_char),
    .ptd(printtext_3_ptd), .res(printtext_3_res));
  TTY #(.rows(1), .cols(13)) tty_3 (
    .data(printtext_3_char), .clk(printtext_3_ptclc), .we(printtext_3_ptd), .clr(printtext_3_res));
  DotMatrix #(.inputtype("row"), .matrixcols(1), .matrixrows(1)) dotmatrix_6 (.row0(printitem_1_weapon));
  printItem printitem_2 (
    .item(INVENTORY2), .str1(printitem_2_str1), .str5(printitem_2_str5), .str9(printitem_2_str9),
    .str2(printitem_2_str2), .str6(printitem_2_str6), .str3(printitem_2_str3), .str7(printitem_2_str7),
    .str4(printitem_2_str4), .str8(printitem_2_str8), .eat(printitem_2_eat), .weapon(printitem_2_weapon));
  DotMatrix #(.inputtype("row"), .matrixcols(9), .matrixrows(9)) dotmatrix_7 (
    .row0(printitem_2_str1), .row1(printitem_2_str2), .row2(printitem_2_str3), .row3(printitem_2_str4),
    .row4(printitem_2_str5), .row5(printitem_2_str6), .row6(printitem_2_str7), .row7(printitem_2_str8),
    .row8(printitem_2_str9));
  DotMatrix #(.inputtype("row"), .matrixcols(1), .matrixrows(1)) dotmatrix_8 (.row0(printitem_1_eat));
  printText printtext_4 (
    .Input({_2Bus[25:20], _1Bus[19], 7'b0001101, _2Bus[11:0]}), .pTclc(printtext_4_ptclc),
    .char(printtext_4_char), .ptd(printtext_4_ptd), .res(printtext_4_res));
  TTY #(.rows(1), .cols(13)) tty_4 (
    .data(printtext_4_char), .clk(printtext_4_ptclc), .we(printtext_4_ptd), .clr(printtext_4_res));
  Multiplexer #(.width(12), .enable("false")) multiplexer_4 (
    .in0(MAP_tospace_ELEM), .in1(mapSTelemREAD), .out(multiplexer_4_out), .sel(mapLoading));
  Register #(.width(12)) register_23 (
    .D(adder_2_out), .Q(mapSTelemREAD), .clk(and_11_out), .clr(or_14_out));  // open: en
  Adder #(.width(12)) adder_2 (.a(mapSTelemREAD), .b(12'h1), .out(adder_2_out));  // open: cin, cout
  and and_11 (and_11_out, mapLoading, _1Bus[19]);
  driver_r driver_r_1 (
    .out_5(driver_r_1_out_5), .out_6(driver_r_1_out_6), .out_7(driver_r_1_out_7), .out_8(driver_r_1_out_8),
    .out_9(driver_r_1_out_9), .out_10(driver_r_1_out_10), .out_11(driver_r_1_out_11),
    .out_12(driver_r_1_out_12), .out_13(driver_r_1_out_13), .out_14(driver_r_1_out_14),
    .out_15(driver_r_1_out_15), .out_16(driver_r_1_out_16), .out_17(driver_r_1_out_17),
    .out_18(driver_r_1_out_18), .out_19(driver_r_1_out_19), .out_20(driver_r_1_out_20),
    .out_21(driver_r_1_out_21), .out_22(driver_r_1_out_22), .out_23(driver_r_1_out_23),
    .out_24(driver_r_1_out_24), .out_25(driver_r_1_out_25), .out_26(driver_r_1_out_26),
    .out_27(driver_r_1_out_27), .out_28(driver_r_1_out_28), .out_29(driver_r_1_out_29),
    .out_30(driver_r_1_out_30), .out_31(driver_r_1_out_31), .out_32(driver_r_1_out_32),
    .out_33(driver_r_1_out_33), .out_34(driver_r_1_out_34), .out_35(driver_r_1_out_35),
    .out_36(driver_r_1_out_36), .out_37(driver_r_1_out_37), .out_38(driver_r_1_out_38),
    .out_39(driver_r_1_out_39), .out_40(driver_r_1_out_40), .out_41(driver_r_1_out_41),
    .out_42(driver_r_1_out_42), .out_43(driver_r_1_out_43), .out_44(driver_r_1_out_44),
    .out_45(driver_r_1_out_45), .out_46(driver_r_1_out_46), .out_47(driver_r_1_out_47),
    .out_48(driver_r_1_out_48), .out_49(driver_r_1_out_49), .out_50(driver_r_1_out_50),
    .out_51(driver_r_1_out_51), .out_52(driver_r_1_out_52), .out_53(driver_r_1_out_53),
    .out_54(driver_r_1_out_54), .out_55(driver_r_1_out_55), .out_56(driver_r_1_out_56),
    .out_57(driver_r_1_out_57), .out_58(driver_r_1_out_58), .out_59(driver_r_1_out_59),
    .out_60(driver_r_1_out_60), .out_61(driver_r_1_out_61), .out_62(driver_r_1_out_62),
    .out_63(driver_r_1_out_63), .out_64(driver_r_1_out_64), .out_65(driver_r_1_out_65),
    .out_66(driver_r_1_out_66), .out_67(driver_r_1_out_67), .out_68(driver_r_1_out_68),
    .out_69(driver_r_1_out_69), .out_70(driver_r_1_out_70), .out_71(driver_r_1_out_71),
    .out_72(driver_r_1_out_72), .out_73(driver_r_1_out_73), .out_74(driver_r_1_out_74),
    .out_75(driver_r_1_out_75), .out_76(driver_r_1_out_76), .out_77(driver_r_1_out_77),
    .out_78(driver_r_1_out_78), .out_79(driver_r_1_out_79), .out_80(driver_r_1_out_80),
    .out_81(driver_r_1_out_81), .out_82(driver_r_1_out_82), .out_83(driver_r_1_out_83),
    .out_84(driver_r_1_out_84), .out_85(driver_r_1_out_85), .out_86(driver_r_1_out_86),
    .out_87(driver_r_1_out_87), .out_88(driver_r_1_out_88), .out_89(driver_r_1_out_89),
    .out_90(driver_r_1_out_90), .out_91(driver_r_1_out_91), .out_92(driver_r_1_out_92),
    .out_93(driver_r_1_out_93), .out_94(driver_r_1_out_94), .out_95(driver_r_1_out_95),
    .out_96(driver_r_1_out_96), .out_97(driver_r_1_out_97), .out_98(driver_r_1_out_98),
    .out_99(driver_r_1_out_99), .out_100(driver_r_1_out_100), .out_101(driver_r_1_out_101),
    .out_102(driver_r_1_out_102), .out_103(driver_r_1_out_103), .out_104(driver_r_1_out_104),
    .out_105(driver_r_1_out_105), .out_106(driver_r_1_out_106), .out_107(driver_r_1_out_107),
    .out_108(driver_r_1_out_108), .out_109(driver_r_1_out_109), .out_110(driver_r_1_out_110),
    .out_111(driver_r_1_out_111), .out_112(driver_r_1_out_112), .out_113(driver_r_1_out_113),
    .out_114(driver_r_1_out_114), .out_115(driver_r_1_out_115), .out_116(driver_r_1_out_116),
    .out_117(driver_r_1_out_117), .out_118(driver_r_1_out_118), .out_119(driver_r_1_out_119),
    .out_120(driver_r_1_out_120), .out_121(driver_r_1_out_121), .out_122(driver_r_1_out_122),
    .out_123(driver_r_1_out_123), .out_124(driver_r_1_out_124), .out_125(driver_r_1_out_125),
    .out_126(driver_r_1_out_126), .out_127(driver_r_1_out_127), .out_128(driver_r_1_out_128),
    .out_129(driver_r_1_out_129), .out_130(driver_r_1_out_130), .out_131(driver_r_1_out_131),
    .out_132(driver_r_1_out_132), .ASSH(ASSH), .b(b), .curr_enem(ATCcurEN), .gameState(gameState));
  DotMatrix #(.inputtype("row"), .matrixcols(32), .matrixrows(32)) dotmatrix_9 (
    .row0(driver_r_1_out_5), .row1(driver_r_1_out_9), .row2(driver_r_1_out_13), .row3(driver_r_1_out_17),
    .row4(driver_r_1_out_21), .row5(driver_r_1_out_25), .row6(driver_r_1_out_29), .row7(driver_r_1_out_33),
    .row8(driver_r_1_out_37), .row9(driver_r_1_out_41), .row10(driver_r_1_out_45), .row11(driver_r_1_out_49),
    .row12(driver_r_1_out_53), .row13(driver_r_1_out_57), .row14(driver_r_1_out_61),
    .row15(driver_r_1_out_65), .row16(driver_r_1_out_69), .row17(driver_r_1_out_73),
    .row18(driver_r_1_out_77), .row19(driver_r_1_out_81), .row20(driver_r_1_out_85),
    .row21(driver_r_1_out_89), .row22(driver_r_1_out_93), .row23(driver_r_1_out_97),
    .row24(driver_r_1_out_101), .row25(driver_r_1_out_105), .row26(driver_r_1_out_109),
    .row27(driver_r_1_out_113), .row28(driver_r_1_out_117), .row29(driver_r_1_out_121),
    .row30(driver_r_1_out_125), .row31(driver_r_1_out_129));
  DotMatrix #(.inputtype("row"), .matrixcols(1), .matrixrows(1)) dotmatrix_10 (.row0(printitem_2_weapon));
  printItem printitem_3 (
    .item(INVENTORY3), .str1(printitem_3_str1), .str5(printitem_3_str5), .str9(printitem_3_str9),
    .str2(printitem_3_str2), .str6(printitem_3_str6), .str3(printitem_3_str3), .str7(printitem_3_str7),
    .str4(printitem_3_str4), .str8(printitem_3_str8), .eat(printitem_3_eat), .weapon(printitem_3_weapon));
  DotMatrix #(.inputtype("row"), .matrixcols(9), .matrixrows(9)) dotmatrix_11 (
    .row0(printitem_3_str1), .row1(printitem_3_str2), .row2(printitem_3_str3), .row3(printitem_3_str4),
    .row4(printitem_3_str5), .row5(printitem_3_str6), .row6(printitem_3_str7), .row7(printitem_3_str8),
    .row8(printitem_3_str9));
  DotMatrix #(.inputtype("row"), .matrixcols(1), .matrixrows(1)) dotmatrix_12 (.row0(printitem_2_eat));
  printText printtext_5 (
    .Input({_3Bus[25:20], _1Bus[19], 7'b0001101, _3Bus[11:0]}), .pTclc(printtext_5_ptclc),
    .char(printtext_5_char), .ptd(printtext_5_ptd), .res(printtext_5_res));
  TTY #(.rows(1), .cols(13)) tty_5 (
    .data(printtext_5_char), .clk(printtext_5_ptclc), .we(printtext_5_ptd), .clr(printtext_5_res));
  Keyboard #(.buflen(1)) keyboard_1 (.clk(or_13_out), .clr(button_1_out), .avail(iCF), .data(iCR));  // open: re
  Button button_1 (.out(button_1_out));
  or or_13 (or_13_out, quick_7_out, quick_8_out, qres);
  Comparator #(.width(2)) comparator_9 (.a(gBus1[25:24]), .b(2'b00), .eq(comparator_9_eq));  // open: gt, lt
  Comparator #(.width(2)) comparator_10 (.a(gBus1[25:24]), .b(2'b10), .eq(comparator_10_eq));  // open: gt, lt
  Comparator #(.width(2)) comparator_11 (.a(gBus1[25:24]), .b(2'b01), .eq(comparator_11_eq));  // open: gt, lt
  Comparator #(.width(2)) comparator_12 (.a(gBus1[25:24]), .b(2'b11), .eq(comparator_12_eq));  // open: gt, lt
  or or_14 (or_14_out, mainRES, pull_resistor_9_node);
  Pull_Resistor pull_resistor_9 (.node(pull_resistor_9_node));
  buf buffer_5 (pull_resistor_9_node, MapLevelCh);
  quick quick_6 (.IN(stMapCLC2), .OUT(quick_6_out));
  DotMatrix #(.inputtype("row"), .matrixcols(29), .matrixrows(32)) dotmatrix_13 (
    .row0(driver_r_1_out_8), .row1(driver_r_1_out_12), .row2(driver_r_1_out_16), .row3(driver_r_1_out_20),
    .row4(driver_r_1_out_24), .row5(driver_r_1_out_28), .row6(driver_r_1_out_32), .row7(driver_r_1_out_36),
    .row8(driver_r_1_out_40), .row9(driver_r_1_out_44), .row10(driver_r_1_out_48), .row11(driver_r_1_out_52),
    .row12(driver_r_1_out_56), .row13(driver_r_1_out_60), .row14(driver_r_1_out_64),
    .row15(driver_r_1_out_68), .row16(driver_r_1_out_72), .row17(driver_r_1_out_76),
    .row18(driver_r_1_out_80), .row19(driver_r_1_out_84), .row20(driver_r_1_out_88),
    .row21(driver_r_1_out_92), .row22(driver_r_1_out_96), .row23(driver_r_1_out_100),
    .row24(driver_r_1_out_104), .row25(driver_r_1_out_108), .row26(driver_r_1_out_112),
    .row27(driver_r_1_out_116), .row28(driver_r_1_out_120), .row29(driver_r_1_out_124),
    .row30(driver_r_1_out_128), .row31(driver_r_1_out_132));
  DotMatrix #(.inputtype("row"), .matrixcols(30), .matrixrows(32)) dotmatrix_14 (
    .row0(driver_r_1_out_7), .row1(driver_r_1_out_11), .row2(driver_r_1_out_15), .row3(driver_r_1_out_19),
    .row4(driver_r_1_out_23), .row5(driver_r_1_out_27), .row6(driver_r_1_out_31), .row7(driver_r_1_out_35),
    .row8(driver_r_1_out_39), .row9(driver_r_1_out_43), .row10(driver_r_1_out_47), .row11(driver_r_1_out_51),
    .row12(driver_r_1_out_55), .row13(driver_r_1_out_59), .row14(driver_r_1_out_63),
    .row15(driver_r_1_out_67), .row16(driver_r_1_out_71), .row17(driver_r_1_out_75),
    .row18(driver_r_1_out_79), .row19(driver_r_1_out_83), .row20(driver_r_1_out_87),
    .row21(driver_r_1_out_91), .row22(driver_r_1_out_95), .row23(driver_r_1_out_99),
    .row24(driver_r_1_out_103), .row25(driver_r_1_out_107), .row26(driver_r_1_out_111),
    .row27(driver_r_1_out_115), .row28(driver_r_1_out_119), .row29(driver_r_1_out_123),
    .row30(driver_r_1_out_127), .row31(driver_r_1_out_131));
  DotMatrix #(.inputtype("row"), .matrixcols(31), .matrixrows(32)) dotmatrix_15 (
    .row0(driver_r_1_out_6), .row1(driver_r_1_out_10), .row2(driver_r_1_out_14), .row3(driver_r_1_out_18),
    .row4(driver_r_1_out_22), .row5(driver_r_1_out_26), .row6(driver_r_1_out_30), .row7(driver_r_1_out_34),
    .row8(driver_r_1_out_38), .row9(driver_r_1_out_42), .row10(driver_r_1_out_46), .row11(driver_r_1_out_50),
    .row12(driver_r_1_out_54), .row13(driver_r_1_out_58), .row14(driver_r_1_out_62),
    .row15(driver_r_1_out_66), .row16(driver_r_1_out_70), .row17(driver_r_1_out_74),
    .row18(driver_r_1_out_78), .row19(driver_r_1_out_82), .row20(driver_r_1_out_86),
    .row21(driver_r_1_out_90), .row22(driver_r_1_out_94), .row23(driver_r_1_out_98),
    .row24(driver_r_1_out_102), .row25(driver_r_1_out_106), .row26(driver_r_1_out_110),
    .row27(driver_r_1_out_114), .row28(driver_r_1_out_118), .row29(driver_r_1_out_122),
    .row30(driver_r_1_out_126), .row31(driver_r_1_out_130));
  not not_8 (not_8_out, lquick_2_out);
  quick quick_7 (.IN(not_8_out), .OUT(quick_7_out));
  Lquick lquick_2 (.IN(iCF), .OUT(lquick_2_out), .CLC(_1Bus[19]));
  quick quick_8 (.IN(and_12_out), .OUT(quick_8_out));
  and and_12 (and_12_out, ~quick_7_out, ~iCF);  // AND_Gate
  Multiplexer #(.width(8), .enable("false")) multiplexer_5 (
    .in0(8'h20), .in1(mapSTDATAreaded), .out(multiplexer_5_out), .sel(mapLoading));
  Comparator #(.width(12)) comparator_13 (.a(mapSTelemREAD), .b(mapLen), .eq(comparator_13_eq));  // open: gt, lt
  not not_9 (mapLoading, comparator_13_eq);
  or or_15 (stMapCLC, and_11_out, stMapCLC1, quick_6_out);
  Hex_Digit_Display hex_digit_display_1 (.value(ten));  // open: dp
  Hex_Digit_Display hex_digit_display_2 (.value(hund));  // open: dp
  DotMatrix #(.inputtype("row"), .matrixcols(1), .matrixrows(1)) dotmatrix_16 (.row0(printitem_3_weapon));
  printItem printitem_4 (
    .item(INVENTORY4), .str1(printitem_4_str1), .str5(printitem_4_str5), .str9(printitem_4_str9),
    .str2(printitem_4_str2), .str6(printitem_4_str6), .str3(printitem_4_str3), .str7(printitem_4_str7),
    .str4(printitem_4_str4), .str8(printitem_4_str8), .eat(printitem_4_eat), .weapon(printitem_4_weapon));
  DotMatrix #(.inputtype("row"), .matrixcols(9), .matrixrows(9)) dotmatrix_17 (
    .row0(printitem_4_str1), .row1(printitem_4_str2), .row2(printitem_4_str3), .row3(printitem_4_str4),
    .row4(printitem_4_str5), .row5(printitem_4_str6), .row6(printitem_4_str7), .row7(printitem_4_str8),
    .row8(printitem_4_str9));
  DotMatrix #(.inputtype("row"), .matrixcols(1), .matrixrows(1)) dotmatrix_18 (.row0(printitem_3_eat));
  printText printtext_6 (
    .Input({_4Bus[25:20], _1Bus[19], 7'b0001101, _4Bus[11:0]}), .pTclc(printtext_6_ptclc),
    .char(printtext_6_char), .ptd(printtext_6_ptd), .res(printtext_6_res));
  TTY #(.rows(1), .cols(13)) tty_6 (
    .data(printtext_6_char), .clk(printtext_6_ptclc), .we(printtext_6_ptd), .clr(printtext_6_res));
  not not_10 (not_10_out, not_11_out);
  or or_16 (or_16_out, AonInp, DonInp);
  not not_11 (not_11_out, or_16_out);
  or or_17 (invchn, _1onInp, _2onInp, _3onInp, _4onInp, _5onInp, AonInp, DonInp, WonInp);
  Subtractor subtractor_3 (.a(p_x_y_1_t), .b(8'h31), .out(subtractor_3_out));  // open: bin, bout
  whatIs whatis_1 (.input_element(p_x_y_1_t), .output_key(whatis_1_output_key));
  whatIs whatis_2 (.input_element(p_x_y_1), .output_key(whatis_2_output_key));
  whatIs whatis_3 (.input_element(p_x_1_y), .output_key(whatis_3_output_key));
  whatIs whatis_4 (.input_element(p_x_1_y_t), .output_key(whatis_4_output_key));
  Subtractor subtractor_4 (.a(p_x_1_y_t), .b(8'h31), .out(subtractor_4_out));  // open: bin, bout
  Comparator #(.width(12)) comparator_14 (.a(12'ha), .b(mapSTelemREAD), .eq(MapLoaded));  // open: gt, lt
  Hex_Digit_Display hex_digit_display_3 (.value(one));  // open: dp
  DotMatrix #(.inputtype("row"), .matrixcols(1), .matrixrows(1)) dotmatrix_19 (.row0(printitem_4_weapon));
  DotMatrix #(.inputtype("row"), .matrixcols(9), .matrixrows(9)) dotmatrix_20 (
    .row0(printitem_5_str1), .row1(printitem_5_str2), .row2(printitem_5_str3), .row3(printitem_5_str4),
    .row4(printitem_5_str5), .row5(printitem_5_str6), .row6(printitem_5_str7), .row7(printitem_5_str8),
    .row8(printitem_5_str9));
  printItem printitem_5 (
    .item(INVENTORY5), .str1(printitem_5_str1), .str5(printitem_5_str5), .str9(printitem_5_str9),
    .str2(printitem_5_str2), .str6(printitem_5_str6), .str3(printitem_5_str3), .str7(printitem_5_str7),
    .str4(printitem_5_str4), .str8(printitem_5_str8), .eat(printitem_5_eat), .weapon(printitem_5_weapon));
  DotMatrix #(.inputtype("row"), .matrixcols(1), .matrixrows(1)) dotmatrix_21 (.row0(printitem_4_eat));
  printText printtext_7 (
    .Input({_5Bus[25:20], _1Bus[19], 7'b0001101, _5Bus[11:0]}), .pTclc(printtext_7_ptclc),
    .char(printtext_7_char), .ptd(printtext_7_ptd), .res(printtext_7_res));
  TTY #(.rows(1), .cols(13)) tty_7 (
    .data(printtext_7_char), .clk(printtext_7_ptclc), .we(printtext_7_ptd), .clr(printtext_7_res));
  Adder #(.width(2)) adder_3 (.a(gBus1[25:24]), .b(2'b01), .out(adder_3_out));  // open: cin, cout
  Multiplexer #(.width(2), .enable("false")) multiplexer_6 (
    .in0(adder_3_out), .in1(subtractor_5_out), .out(NewPlDir), .sel(AonInp));
  Subtractor #(.width(2)) subtractor_5 (.a(gBus1[25:24]), .b(2'b01), .out(subtractor_5_out));  // open: bin, bout
  and and_13 (and_13_out, MOVEinited, not_10_out);
  assign InpFl1 = and_13_out ? and_13_out : 1'bz;  // Controlled_Buffer controlled_buffer_26
  quick quick_9 (.IN(not_10_out), .OUT(PlDirCh));
  Pull_Resistor pull_resistor_10 (.node(StateCh));
  or or_18 (or_18_out, StateCh, quick_10_out);
  quick quick_10 (.IN(invchn), .OUT(quick_10_out));
  quick quick_11 (.IN(invchn), .OUT(keyPress));
  not not_12 (not_12_out, or_18_out);
  assign MAP_tospace_ELEM = and_14_out ? p_x_y_1__elemOnMap_t : 12'bz;  // Controlled_Buffer controlled_buffer_27
  Bit_Extender #(.out_width(2)) bit_extender_3 (.in(subtractor_3_out), .out(bit_extender_3_out));
  assign ATCnewEN = and_14_out ? bit_extender_3_out : 2'bz;  // Controlled_Buffer controlled_buffer_28
  and and_14 (and_14_out, comparator_9_eq, whatis_1_output_key[0], whatis_1_output_key[1], ~MAPisBYSU);  // AND_Gate
  and and_15 (and_15_out, comparator_10_eq, whatis_2_output_key[0], whatis_2_output_key[1], ~MAPisBYSU);  // AND_Gate
  or or_19 (ATCnewENclc, and_14_out, and_15_out, and_16_out, and_17_out);
  and and_16 (and_16_out, comparator_11_eq, whatis_3_output_key[0], whatis_3_output_key[1], ~MAPisBYSU);  // AND_Gate
  and and_17 (and_17_out, comparator_12_eq, whatis_4_output_key[0], whatis_4_output_key[1], ~MAPisBYSU);  // AND_Gate
  Bit_Extender #(.out_width(2)) bit_extender_4 (.in(subtractor_4_out), .out(bit_extender_4_out));
  assign ATCnewEN = and_17_out ? bit_extender_4_out : 2'bz;  // Controlled_Buffer controlled_buffer_29
  assign MAP_tospace_ELEM = and_17_out ? p_x_1_y__elemOnMap_t : 12'bz;  // Controlled_Buffer controlled_buffer_30
  RAM #(.addrWidth(12), .bus("separate")) ram_1 (
    .addr(multiplexer_4_out), .din(multiplexer_5_out), .data(objectONmap), .str(mapPREst), .clk(stMapCLC));  // open: sel, ld, clr
  or or_20 (mapPREst, mapLoading, ATCnewENclc, mapPREst1);
  printText printtext_8 (
    .Input({miniMScrT, miniScrT[20], _1Bus[19], 7'b0010101, miniScrT[11:0]}), .pTclc(printtext_8_ptclc),
    .char(printtext_8_char), .ptd(printtext_8_ptd), .res(printtext_8_res));
  TTY #(.rows(1), .cols(21)) tty_8 (
    .data(printtext_8_char), .clk(printtext_8_ptclc), .we(printtext_8_ptd), .clr(printtext_8_res));
  DotMatrix #(.inputtype("row"), .matrixcols(1), .matrixrows(1)) dotmatrix_22 (.row0(printitem_5_weapon));
  DotMatrix #(.inputtype("row"), .matrixcols(1), .matrixrows(1)) dotmatrix_23 (.row0(printitem_5_eat));
  Register #(.width(1)) register_24 (.D(WonInp), .Q(WonInpff), .clk(not_13_out), .clr(or_21_out));  // open: en
  or or_21 (or_21_out, or_18_out, MoveFl);
  not not_13 (not_13_out, not_14_out);
  not not_14 (not_14_out, not_15_out);
  not not_15 (not_15_out, not_16_out);
  not not_16 (not_16_out, or_18_out);
  Register #(.width(1)) register_25 (.D(_3onInp), .Q(_3onInpff), .clk(not_17_out), .clr(or_18_out));  // open: en
  not not_17 (not_17_out, not_12_out);
  Subtractor subtractor_6 (.a(p_x_y_1), .b(8'h31), .out(subtractor_6_out));  // open: bin, bout
  Subtractor subtractor_7 (.a(p_x_1_y), .b(8'h31), .out(subtractor_7_out));  // open: bin, bout
  DotMatrix #(.inputtype("row"), .matrixcols(18), .matrixrows(18)) dotmatrix_24 (
    .row0(driver_mm_1_p1), .row1(driver_mm_1_p2), .row2(driver_mm_1_p3), .row3(driver_mm_1_p4),
    .row4(driver_mm_1_p5), .row5(driver_mm_1_p6), .row6(driver_mm_1_p7), .row7(driver_mm_1_p8),
    .row8(driver_mm_1_p9), .row9(driver_mm_1_p10), .row10(driver_mm_1_p11), .row11(driver_mm_1_p12),
    .row12(driver_mm_1_p13), .row13(driver_mm_1_p14), .row14(driver_mm_1_p15), .row15(driver_mm_1_p16),
    .row16(driver_mm_1_p17), .row17(driver_mm_1_p18));
  DotMatrix #(.inputtype("row"), .matrixcols(18), .matrixrows(18)) dotmatrix_25 (
    .row0(driver_mm_1_p1), .row1(driver_mm_1_p2), .row2(driver_mm_1_p3), .row3(driver_mm_1_p4),
    .row4(driver_mm_1_p5), .row5(driver_mm_1_p6), .row6(driver_mm_1_p7), .row7(driver_mm_1_p8),
    .row8(driver_mm_1_p9), .row9(driver_mm_1_p10), .row10(driver_mm_1_p11), .row11(driver_mm_1_p12),
    .row12(driver_mm_1_p13), .row13(driver_mm_1_p14), .row14(driver_mm_1_p15), .row15(driver_mm_1_p16),
    .row16(driver_mm_1_p17), .row17(driver_mm_1_p18));
  // driver_mm driver_mm_1: pin names not known; wires that end beside it: driver_mm_1_p1, driver_mm_1_p2, driver_mm_1_p3, driver_mm_1_p4, driver_mm_1_p5, driver_mm_1_p6, driver_mm_1_p7, driver_mm_1_p8, driver_mm_1_p9, driver_mm_1_p10, driver_mm_1_p11, driver_mm_1_p12, driver_mm_1_p13, driver_mm_1_p14, driver_mm_1_p15, driver_mm_1_p16, driver_mm_1_p17, driver_mm_1_p18, driver_mm_1_p19, driver_mm_1_p20, driver_mm_1_p21, driver_mm_1_p22, driver_mm_1_p23, driver_mm_1_p24, driver_mm_1_p25, driver_mm_1_p26, driver_mm_1_p27, driver_mm_1_p28, driver_mm_1_p29, driver_mm_1_p30, driver_mm_1_p31, driver_mm_1_p32, driver_mm_1_p33, driver_mm_1_p34, driver_mm_1_p35, driver_mm_1_p36, driver_mm_1_p37, driver_mm_1_p38, driver_mm_1_p39, driver_mm_1_p40, driver_mm_1_p41, driver_mm_1_p42, driver_mm_1_p43, driver_mm_1_p44, driver_mm_1_p45, driver_mm_1_p46, driver_mm_1_p47, driver_mm_1_p48, gBus2, driver_mm_1_p50, driver_mm_1_p51, gBus1, b
  // driver_mm driver_mm_2: pin names not known; wires that end beside it: driver_mm_1_p1, driver_mm_1_p2, driver_mm_1_p3, driver_mm_1_p4, driver_mm_1_p5, driver_mm_1_p6, driver_mm_1_p7, driver_mm_1_p8, driver_mm_1_p9, driver_mm_1_p10, driver_mm_1_p11, driver_mm_1_p12, driver_mm_1_p13, driver_mm_1_p14, driver_mm_1_p15, driver_mm_1_p16, driver_mm_1_p17, driver_mm_1_p18, driver_mm_1_p19, driver_mm_1_p20, driver_mm_1_p21, driver_mm_1_p22, driver_mm_1_p23, driver_mm_1_p24, driver_mm_1_p25, driver_mm_1_p26, driver_mm_1_p27, driver_mm_1_p28, driver_mm_1_p29, driver_mm_1_p30, driver_mm_1_p31, driver_mm_1_p32, driver_mm_1_p33, driver_mm_1_p34, driver_mm_1_p35, driver_mm_1_p36, driver_mm_1_p37, driver_mm_1_p38, driver_mm_1_p39, driver_mm_1_p40, driver_mm_1_p41, driver_mm_1_p42, driver_mm_1_p43, driver_mm_1_p44, driver_mm_1_p45, driver_mm_1_p46, driver_mm_1_p47, driver_mm_1_p48, gBus2, driver_mm_1_p50, driver_mm_1_p51, gBus1, b
  DotMatrix #(.inputtype("row"), .matrixcols(16), .matrixrows(16)) dotmatrix_26 (
    .row0(driver_mm_1_p19), .row1(driver_mm_1_p20), .row2(driver_mm_1_p21), .row3(driver_mm_1_p22),
    .row4(driver_mm_1_p23), .row5(driver_mm_1_p24), .row6(driver_mm_1_p25), .row7(driver_mm_1_p26),
    .row8(driver_mm_1_p27), .row9(driver_mm_1_p28), .row10(driver_mm_1_p29), .row11(driver_mm_1_p30),
    .row12(driver_mm_1_p31), .row13(driver_mm_1_p32), .row14(driver_mm_1_p33), .row15(driver_mm_1_p34));
  DotMatrix #(.inputtype("row"), .matrixcols(16), .matrixrows(16)) dotmatrix_27 (
    .row0(driver_mm_1_p19), .row1(driver_mm_1_p20), .row2(driver_mm_1_p21), .row3(driver_mm_1_p22),
    .row4(driver_mm_1_p23), .row5(driver_mm_1_p24), .row6(driver_mm_1_p25), .row7(driver_mm_1_p26),
    .row8(driver_mm_1_p27), .row9(driver_mm_1_p28), .row10(driver_mm_1_p29), .row11(driver_mm_1_p30),
    .row12(driver_mm_1_p31), .row13(driver_mm_1_p32), .row14(driver_mm_1_p33), .row15(driver_mm_1_p34));
  DotMatrix #(.inputtype("row"), .matrixcols(14), .matrixrows(14)) dotmatrix_28 (
    .row0(driver_mm_1_p35), .row1(driver_mm_1_p36), .row2(driver_mm_1_p37), .row3(driver_mm_1_p38),
    .row4(driver_mm_1_p39), .row5(driver_mm_1_p40), .row6(driver_mm_1_p41), .row7(driver_mm_1_p42),
    .row8(driver_mm_1_p43), .row9(driver_mm_1_p44), .row10(driver_mm_1_p45), .row11(driver_mm_1_p46),
    .row12(driver_mm_1_p47), .row13(driver_mm_1_p48));
  DotMatrix #(.inputtype("row"), .matrixcols(14), .matrixrows(14)) dotmatrix_29 (
    .row0(driver_mm_1_p35), .row1(driver_mm_1_p36), .row2(driver_mm_1_p37), .row3(driver_mm_1_p38),
    .row4(driver_mm_1_p39), .row5(driver_mm_1_p40), .row6(driver_mm_1_p41), .row7(driver_mm_1_p42),
    .row8(driver_mm_1_p43), .row9(driver_mm_1_p44), .row10(driver_mm_1_p45), .row11(driver_mm_1_p46),
    .row12(driver_mm_1_p47), .row13(driver_mm_1_p48));
  Hex_Digit_Display hex_digit_display_4 (.value(printhp_1_high));  // open: dp
  printHP printhp_1 (.Inp(CurHunger), .High(printhp_1_high), .Low(printhp_1_low), .print(gBus2[16]));
  LED led_1 (.in(mapLoading));
  not not_18 (not_18_out, or_18_out);
  not not_19 (not_19_out, or_18_out);
  assign MAP_tospace_ELEM = and_15_out ? p_x_y_1__elemOnMap : 12'bz;  // Controlled_Buffer controlled_buffer_31
  Bit_Extender #(.out_width(2)) bit_extender_5 (.in(subtractor_6_out), .out(bit_extender_5_out));
  assign ATCnewEN = and_15_out ? bit_extender_5_out : 2'bz;  // Controlled_Buffer controlled_buffer_32
  not not_20 (not_20_out, not_22_out);
  not not_21 (not_21_out, not_20_out);
  not not_22 (not_22_out, ATCnewENclc);
  assign ATCnewEN = and_16_out ? bit_extender_6_out : 2'bz;  // Controlled_Buffer controlled_buffer_33
  Bit_Extender #(.out_width(2)) bit_extender_6 (.in(subtractor_7_out), .out(bit_extender_6_out));
  assign MAP_tospace_ELEM = and_16_out ? p_x_1_y__elemOnMap : 12'bz;  // Controlled_Buffer controlled_buffer_34
  or or_22 (or_22_out, MapLoaded, gS0);
  not not_23 (not_23_out, MapLoaded);
  not not_24 (not_24_out, not_23_out);
  DotMatrix #(.inputtype("row"), .matrixcols(2), .matrixrows(2)) dotmatrix_30 (
    .row0(driver_mm_1_p50), .row1(driver_mm_1_p51));
  DotMatrix #(.inputtype("row"), .matrixcols(2), .matrixrows(2)) dotmatrix_31 (
    .row0(driver_mm_1_p50), .row1(driver_mm_1_p51));
  Hex_Digit_Display hex_digit_display_5 (.value(printhp_1_low));  // open: dp
  Hex_Digit_Display hex_digit_display_6 (.value(printhp_3_high));  // open: dp
  Hex_Digit_Display hex_digit_display_7 (.value(printhp_2_high));  // open: dp
  printHP printhp_2 (.Inp(ENHP), .High(printhp_2_high), .Low(printhp_2_low), .print(gS2));
  Register #(.width(1)) register_26 (.D(_1onInp), .Q(_1onInpff), .clk(not_25_out), .clr(or_18_out));  // open: en
  not not_25 (not_25_out, not_18_out);
  Register #(.width(1)) register_27 (.D(_2onInp), .Q(_2onInpff), .clk(not_26_out), .clr(or_18_out));  // open: en
  not not_26 (not_26_out, not_19_out);
  Lquick lquick_3 (.IN(not_27_out), .OUT(lquick_3_out), .CLC(_1Bus[19]));
  not not_27 (not_27_out, not_21_out);
  not not_28 (not_28_out, lquick_3_out);
  and and_18 (and_18_out, ATCnewENclc, gBus2[16]);
  quick quick_12 (.IN(not_30_out), .OUT(quick_12_out));
  not not_29 (not_29_out, not_24_out);
  not not_30 (not_30_out, not_29_out);
  or or_23 (or_23_out, quick_12_out, LoadMap);
  Hex_Digit_Display hex_digit_display_8 (.value(printhp_3_low));  // open: dp
  printHP printhp_3 (.Inp(playerHPCUR), .High(printhp_3_high), .Low(printhp_3_low), .print(not_31_out));
  not not_31 (not_31_out, gS0);
  Hex_Digit_Display hex_digit_display_9 (.value(printhp_2_low));  // open: dp
  Demultiplexer #(.select(2), .disabled(0), .enable("false")) demultiplexer_1 (
    .out1(InpFlpreC), .in(quick_13_out), .sel(gameState));  // open: out0, out2, out3
  quick quick_13 (.IN(invchn), .OUT(quick_13_out));
  Demultiplexer #(.select(2), .disabled(0), .enable("false")) demultiplexer_2 (
    .out0(InpFlpreSTRT), .out2(ATCInpFlpre), .in(invchn), .sel(gameState));  // open: out1, out3
  not not_32 (not_32_out, or_18_out);
  not not_33 (not_33_out, not_32_out);
  not not_34 (not_34_out, or_18_out);
  not not_35 (not_35_out, not_34_out);
  quick quick_14 (.IN(not_28_out), .OUT(InpFlpreM));
  and and_19 (stMapCLC2, not_28_out, ATCnewENclc);
  assign StateCh = quick_15_out ? quick_15_out : 1'bz;  // Controlled_Buffer controlled_buffer_35
  quick quick_15 (.IN(and_18_out), .OUT(quick_15_out));
  assign newText = quick_15_out ? quick_15_out : 1'bz;  // Controlled_Buffer controlled_buffer_36
  Multiplexer #(.width(8), .enable("false")) multiplexer_7 (
    .in0(NewPLxOM), .in1(maps_1_xpp), .out(multiplexer_7_out), .sel(or_22_out));
  or or_24 (or_24_out, changePCx, quick_12_out, LoadMap);
  Register #(.width(12)) u_mapW (.D(maps_1_width), .Q(MapW), .clk(or_23_out), .clr(mainRES));  // open: en
  and and_20 (and_20_out, iCF, not_36_out);
  not not_36 (not_36_out, mapLoading);
  Register #(.width(1)) register_28 (.D(_4onInp), .Q(_4onInpff), .clk(not_33_out), .clr(or_18_out));  // open: en
  Register #(.width(1)) register_29 (.D(_5onInp), .Q(_5onInpff), .clk(not_35_out), .clr(or_18_out));  // open: en
  Register Xpp (.D(multiplexer_7_out), .Q(gBus1[7:0]), .clk(or_24_out), .clr(mainRES));  // open: en
  or or_25 (or_25_out, quick_12_out, LoadMap);
  Comparator #(.width(2)) comparator_15 (.a(2'b00), .b(gameState), .eq(gS0));  // open: gt, lt
  Comparator #(.width(2)) comparator_16 (.a(2'b01), .b(gameState), .eq(gBus2[16]));  // open: gt, lt
  Comparator #(.width(2)) comparator_17 (.a(2'b10), .b(gameState), .eq(gS2));  // open: gt, lt
  Comparator #(.width(2)) comparator_18 (.a(2'b11), .b(gameState), .eq(gS3));  // open: gt, lt
  quick quick_16 (.IN(qreset), .OUT(quick_16_out));
  Register #(.trigger("falling")) register_30 (
    .D(AddHunger), .Q(register_30_q), .clk(quick_17_out), .clr(quick_19_out));  // open: en
  quick quick_17 (.IN(AddNewHunger), .OUT(quick_17_out));
  Counter counter_1 (
    .count(ATCplAttaked1), .Q(counter_1_q), .clk(ATCplAttaked1), .clr(quick_25_out));  // open: load, D, carry
  parseInpKey parseinpkey_1 (
    .char(iCR), .flush(and_20_out), ._1(_1onInp), ._2(_2onInp), ._3(_3onInp), ._4(_4onInp), ._5(_5onInp),
    .w(WonInp), .a(AonInp), .d(DonInp), .q(qres));
  assign TextText = quick_15_out ? 5'b10111 : 5'bz;  // Controlled_Buffer controlled_buffer_37
  or or_26 (or_26_out, MapLoaded, gS0);
  Register #(.width(12)) u_mapH (.D(maps_1_height), .Q(MapH), .clk(or_25_out), .clr(mainRES));  // open: en
  assign NewPlayerHP = LoadMap ? 8'h32 : 8'bz;  // Controlled_Buffer controlled_buffer_38
  buf buffer_6 (LoadMap, and_21_out);
  and and_21 (and_21_out, InpFlpreSTRT, gS0);
  or or_27 (mainRES, PlayerDeathRes, quick_16_out, qres, PlayerLoseRes);
  Bit_Extender #(.out_width(7)) bit_extender_7 (.in(register_30_q), .out(bit_extender_7_out));
  quick quick_18 (.IN(quick_17_out), .OUT(quick_18_out));
  quick quick_19 (.IN(quick_20_out), .OUT(quick_19_out));
  quick quick_20 (.IN(quick_22_out), .OUT(quick_20_out));
  Bit_Extender #(.out_width(7)) bit_extender_8 (.in(counter_1_q), .out(bit_extender_8_out));
  quick quick_21 (.IN(win), .OUT(quick_21_out));
  Multiplexer #(.width(8), .enable("false")) multiplexer_8 (
    .in0(NewPLyOM), .in1(maps_1_ypp), .out(multiplexer_8_out), .sel(or_26_out));
  Register Ypp (.D(multiplexer_8_out), .Q(gBus1[15:8]), .clk(or_28_out), .clr(mainRES));  // open: en
  or or_28 (or_28_out, changePCy, quick_12_out, LoadMap);
  maps maps_1 (
    .ADDR(gBus1[23:16]), .ELEM(mapSTelemREAD), .DATA(mapSTDATAreaded), .LEN(mapLen), .Xpp(maps_1_xpp),
    .Ypp(maps_1_ypp), .Width(maps_1_width), .Height(maps_1_height));
  assign StateCh = and_21_out ? and_21_out : 1'bz;  // Controlled_Buffer controlled_buffer_39
  assign newText = and_21_out ? and_21_out : 1'bz;  // Controlled_Buffer controlled_buffer_40
  and and_22 (_1Bus[19], ~mainRES, clock_1_out);  // AND_Gate
  Clock clock_1 (.out(clock_1_out));
  quick quick_22 (.IN(quick_18_out), .OUT(quick_22_out));
  quick quick_23 (.IN(quick_21_out), .OUT(quick_23_out));
  quick quick_24 (.IN(quick_23_out), .OUT(quick_24_out));
  quick quick_25 (.IN(quick_26_out), .OUT(quick_25_out));
  quick quick_26 (.IN(quick_24_out), .OUT(quick_26_out));
  Adder adder_4 (.a(CurHunger), .b(8'h1), .out(adder_4_out));  // open: cin, cout
  Subtractor subtractor_8 (.a(adder_4_out), .b(AddHunger), .out(subtractor_8_out));  // open: bin, bout
  or or_29 (or_29_out, comparator_19_gt, comparator_19_eq);
  Comparator #(.mode("unsigned")) comparator_19 (
    .a(CurHunger), .b(playerHPCUR), .gt(comparator_19_gt), .eq(comparator_19_eq));  // open: lt
  and and_23 (and_23_out, or_29_out, _1second);
  assign MapLevelCh = quick_27_out ? quick_27_out : 1'bz;  // Controlled_Buffer controlled_buffer_41
  assign PLAYERHPCH = quick_27_out ? quick_27_out : 1'bz;  // Controlled_Buffer controlled_buffer_42
  quick quick_27 (.IN(and_21_out), .OUT(quick_27_out));
  Multiplexer #(.select(2), .width(2), .enable("false")) multiplexer_9 (
    .in0(2'b01), .in1(2'b10), .in2(2'b01), .out(gSto), .sel({gS2, gBus2[16]}));  // open: in3
  or or_30 (or_30_out, quick_22_out, quick_24_out);
  scores_main main_1 (
    .Clock(_1Bus[19]), .add_points(or_30_out), .amount_of_points(adder_5_out), .hund(hund), .ten(ten),
    .one(one), .main_res(mainRES));
  Adder #(.width(7)) adder_5 (.a(bit_extender_7_out), .b(bit_extender_8_out), .out(adder_5_out));  // open: cin, cout
  Multiplexer #(.width(8), .enable("false")) multiplexer_10 (
    .in0(subtractor_8_out), .in1({8{1'b0}}), .out(multiplexer_10_out), .sel(comparator_20_gt));
  Comparator #(.mode("unsigned")) comparator_20 (
    .a(subtractor_8_out), .b(8'h32), .gt(comparator_20_gt));  // open: eq, lt
  quick quick_28 (.IN(and_23_out), .OUT(quick_28_out));
  and and_24 (PlayerLoseRes, quick_28_out, gBus2[16]);
  Register #(.width(1)) register_31 (.D(1'b1), .Q(PrintLose), .clk(PlayerLoseRes), .clr(quick_29_out));  // open: en
  quick quick_29 (.IN(InpFlpreSTRT), .OUT(quick_29_out));
  assign TextText = and_21_out ? 5'b11000 : 5'bz;  // Controlled_Buffer controlled_buffer_43
  Comparator comparator_21 (.a(p_x_y), .b(8'h20), .eq(comparator_21_eq));  // open: gt, lt
  Comparator comparator_22 (.a(p_x_y), .b(8'h45), .eq(comparator_22_eq));  // open: gt, lt
  Register register_32 (.D(multiplexer_10_out), .Q(CurHunger), .clk(_1second), .clr(buffer_7_out));  // open: en
  buf buffer_7 (buffer_7_out, MapLevelCh);
  Pull_Resistor pull_resistor_11 (.node(buffer_7_out));
  not not_37 (not_37_out, _1second);
  not not_38 (not_38_out, not_37_out);
  Register register_33 (.D(AddNewHungerVal), .Q(AddHunger), .clk(AddNewHunger), .clr(not_38_out));  // open: en
  Multiplexer #(.select(2), .width(8), .enable("false")) multiplexer_11 (
    .in0(8'h1f), .in1({8{1'b0}}), .in2(8'h1e), .out(gStdtScrMem), .sel({gS2, gBus2[16]}));  // open: in3
  not not_39 (not_39_out, comparator_21_eq);
  and and_25 (and_25_out, not_39_out, not_40_out);
  not not_40 (not_40_out, comparator_22_eq);
  Multiplexer #(.select(2), .width(5), .enable("false")) multiplexer_12 (
    .in0(5'b00001), .in1(5'b00010), .in2(5'b00011), .out(multiplexer_12_out), .sel({gS2, gBus2[16]}));  // open: in3
  assign bit_extender_9_out = {{3{1'b0}}, ATCcurEN};  // Bit_Extender bit_extender_9
  Adder adder_6 (.a(gBus1[23:16]), .b(8'h1), .out(NewMapLevelCh));  // open: cin, cout
  assign newText = quick_30_out ? quick_30_out : 1'bz;  // Controlled_Buffer controlled_buffer_44
  quick quick_30 (.IN(and_26_out), .OUT(quick_30_out));
  and and_26 (and_26_out, MOVEinited, gBus2[16]);
  and and_27 (and_27_out, and_26_out, and_28_out);
  and and_28 (and_28_out, gBus2[16], and_25_out);
  and and_29 (and_29_out, _1Bus[19], ~mapLoading, gBus2[16]);  // AND_Gate
  Adder #(.width(5)) adder_7 (.a(bit_extender_9_out), .b(5'b00110), .out(adder_7_out));  // open: cin, cout
  whatIs whatis_5 (.input_element(p_x_y_1_t), .output_key(gBus2[1:0]));
  whatIs whatis_6 (.input_element(p_x_y_1), .output_key(gBus2[3:2]));
  whatIs whatis_7 (.input_element(p_x_1_y_t), .output_key(gBus2[5:4]));
  whatIs whatis_8 (.input_element(p_x_1_y), .output_key(gBus2[7:6]));
  whatIs whatis_9 (.input_element(p_x_2_y), .output_key(gBus2[9:8]));
  whatIs whatis_10 (.input_element(p_x_2_y_t), .output_key(gBus2[11:10]));
  whatIs whatis_11 (.input_element(p_x_y_2_t), .output_key(gBus2[13:12]));
  whatIs whatis_12 (.input_element(p_x_y_2), .output_key(gBus2[15:14]));
  assign newText = and_27_out ? and_27_out : 1'bz;  // Controlled_Buffer controlled_buffer_45
  Counter #(.width(12), .max('h200)) counter_2 (.carry(_1second), .clk(and_29_out));  // open: load, D, count, Q, clr
  Multiplexer #(.width(5), .enable("false")) multiplexer_13 (
    .in0(multiplexer_12_out), .in1(5'b11001), .out(multiplexer_13_out), .sel(PrintWIN));
  Multiplexer #(.width(5), .enable("false")) multiplexer_14 (
    .in0(multiplexer_13_out), .in1(5'b11010), .out(mainScrT[25:21]), .sel(PrintLose));
  Multiplexer #(.select(2), .width(5), .enable("false")) multiplexer_15 (
    .in0({5{1'b0}}), .in1(5'b00100), .in2(adder_7_out), .out(miniMScrT), .sel({gS2, gBus2[16]}));  // open: in3
  assign TextText = and_27_out ? 5'b10110 : 5'bz;  // Controlled_Buffer controlled_buffer_46
  Subtractor subtractor_9 (.a(INVENTORY1), .b(8'h57), .out(subtractor_9_out));  // open: bin, bout
  Bit_Extender #(.out_width(5)) bit_extender_10 (.in(subtractor_9_out), .out(bit_extender_10_out));
  Comparator comparator_23 (.a(INVENTORY1), .b({8{1'b0}}), .eq(comparator_23_eq));  // open: gt, lt
  Bit_Extender #(.out_width(5)) bit_extender_11 (.in(subtractor_10_out), .out(bit_extender_11_out));
  Subtractor subtractor_10 (.a(INVENTORY3), .b(8'h57), .out(subtractor_10_out));  // open: bin, bout
  Comparator comparator_24 (.a(INVENTORY3), .b({8{1'b0}}), .eq(comparator_24_eq));  // open: gt, lt
  Subtractor subtractor_11 (.a(INVENTORY5), .b(8'h57), .out(subtractor_11_out));  // open: bin, bout
  Bit_Extender #(.out_width(5)) bit_extender_12 (.in(subtractor_11_out), .out(bit_extender_12_out));
  Comparator comparator_25 (.a(INVENTORY5), .b({8{1'b0}}), .eq(comparator_25_eq));  // open: gt, lt
  buf buffer_8 (buffer_8_out, StateCh);
  Pull_Resistor pull_resistor_12 (.node(buffer_8_out));
  or or_31 (mainScrT[20], buffer_8_out, mainRES);
  or or_32 (_1Bus[20], INV1ch, itemRES1, mainRES);
  Multiplexer #(.width(5), .enable("false")) multiplexer_16 (
    .in0(bit_extender_10_out), .in1({5{1'b0}}), .out(_1Bus[25:21]), .sel(comparator_23_eq));
  or or_33 (_3Bus[20], INV3ch, itemRES3, mainRES);
  Multiplexer #(.width(5), .enable("false")) multiplexer_17 (
    .in0(bit_extender_11_out), .in1({5{1'b0}}), .out(_3Bus[25:21]), .sel(comparator_24_eq));
  or or_34 (_5Bus[20], INV5ch, itemRES5, mainRES);
  Multiplexer #(.width(5), .enable("false")) multiplexer_18 (
    .in0(bit_extender_12_out), .in1({5{1'b0}}), .out(_5Bus[25:21]), .sel(comparator_25_eq));
  Pull_Resistor pull_resistor_13 (.node(pull_resistor_13_node));
  assign pull_resistor_13_node = TextText;  // Buffer buffer_9, 5 bits wide
  Multiplexer #(.select(2), .width(8), .enable("false")) multiplexer_19 (
    .in0(p_x_y_1_t), .in1(p_x_1_y), .in2(p_x_y_1), .in3(p_x_1_y_t), .out(ASSH[7:0]), .sel(gBus1[25:24]));
  Multiplexer #(.select(2), .width(8), .enable("false")) multiplexer_20 (
    .in0(p_x_y_2_t), .in1(p_x_2_y), .in2(p_x_y_2), .in3(p_x_2_y_t), .out(ASSH[15:8]), .sel(gBus1[25:24]));
  Subtractor subtractor_12 (.a(INVENTORY2), .b(8'h57), .out(subtractor_12_out));  // open: bin, bout
  Bit_Extender #(.out_width(5)) bit_extender_13 (.in(subtractor_12_out), .out(bit_extender_13_out));
  Comparator comparator_26 (.a(INVENTORY2), .b({8{1'b0}}), .eq(comparator_26_eq));  // open: gt, lt
  Bit_Extender #(.out_width(5)) bit_extender_14 (.in(subtractor_13_out), .out(bit_extender_14_out));
  Subtractor subtractor_13 (.a(INVENTORY4), .b(8'h57), .out(subtractor_13_out));  // open: bin, bout
  Comparator comparator_27 (.a(INVENTORY4), .b({8{1'b0}}), .eq(comparator_27_eq));  // open: gt, lt
  Comparator comparator_28 (.a(p_x_y), .b(8'h20), .eq(comparator_28_eq));  // open: gt, lt
  Register #(.width(5)) register_34 (
    .D(pull_resistor_13_node), .Q(register_34_q), .clk(pull_resistor_14_node), .clr(or_35_out));  // open: en
  Pull_Resistor pull_resistor_14 (.node(pull_resistor_14_node));
  buf buffer_10 (pull_resistor_14_node, newText);
  or or_35 (or_35_out, mainRES, stMapCLC1);
  buf buffer_11 (buffer_11_out, StateCh);
  Pull_Resistor pull_resistor_15 (.node(buffer_11_out));
  or or_36 (miniScrT[20], buffer_11_out, mainRES);
  or or_37 (_2Bus[20], INV2ch, itemRES2, mainRES);
  Multiplexer #(.width(5), .enable("false")) multiplexer_21 (
    .in0(bit_extender_13_out), .in1({5{1'b0}}), .out(_2Bus[25:21]), .sel(comparator_26_eq));
  or or_38 (_4Bus[20], INV4ch, itemRES4, mainRES);
  Multiplexer #(.width(5), .enable("false")) multiplexer_22 (
    .in0(bit_extender_14_out), .in1({5{1'b0}}), .out(_4Bus[25:21]), .sel(comparator_27_eq));
  Subtractor subtractor_14 (.a(p_x_y), .b(8'h5d), .out(subtractor_14_out));  // open: bin, bout
  Bit_Extender #(.out_width(6)) bit_extender_15 (.in(subtractor_14_out), .out(bit_extender_15_out));
  Multiplexer #(.width(6), .enable("false")) multiplexer_23 (
    .in0(multiplexer_25_out), .in1(multiplexer_26_out), .out(textBus[11:6]), .sel(gS2));
  Pull_Resistor pull_resistor_16 (.node(pull_resistor_16_node));
  buf buffer_12 (pull_resistor_16_node, newText);
  or or_39 (textBus[20], pull_resistor_16_node, pull_resistor_17_node, mainRES);
  Multiplexer #(.width(5), .enable("false")) multiplexer_24 (
    .in0(register_34_q), .in1(5'b01110), .out(textBus[25:21]), .sel(gS0));
  Multiplexer #(.width(6), .enable("false")) multiplexer_25 (
    .in0(bit_extender_15_out), .in1({6{1'b1}}), .out(multiplexer_25_out), .sel(comparator_28_eq));
  Pull_Resistor pull_resistor_17 (.node(pull_resistor_17_node));
  buf buffer_13 (pull_resistor_17_node, StateCh);
  Multiplexer #(.width(6), .enable("false")) multiplexer_26 (
    .in0(bit_extender_16_out), .in1(lstPlDmg), .out(multiplexer_26_out), .sel(and_30_out));
  assign bit_extender_16_out = {{4{1'b0}}, ATCcurEN};  // Bit_Extender bit_extender_16
  and and_30 (and_30_out, gS2, ~comparator_29_eq);  // AND_Gate
  // NOT_Gate not_41 has open pins: in=and_30_out, out=open
  Comparator #(.width(6)) comparator_29 (.a({6{1'b0}}), .b(lstEnDmg), .eq(comparator_29_eq));  // open: gt, lt

  // Other names for the same wires on the sheet: gS1 = gBus2[16]; PLxOM[7:0] = gBus1[7:0]; PLyOM[7:0] = gBus1[15:8];
  //   mapLevelCur[7:0] = gBus1[23:16]; PlDir[1:0] = gBus1[25:24]; textBus (some bits) = {_1Bus[19], lstEnDmg};
  //   mainScrText[4:0] = mainScrT[25:21]; mapPREst2 = ATCnewENclc; miniScrT (some bits) = {miniMScrT, _1Bus[19]};
  //   newtEnDmg = ATCenMoved; ATCnEhp = ATCcorrectINP; nwetPlDmg = ATCcorrectINP; TextRes = stMapCLC1;
  //   _2Bus[19] = _1Bus[19]; _3Bus[19] = _1Bus[19]; _4Bus[19] = _1Bus[19]; _5Bus[19] = _1Bus[19]; mainClk = _1Bus[19];
  //   mainScrT[19] = _1Bus[19]

  // Notes on the sheet:
  //   CURRENT STATE
  //   INVETORY
  //   Переводит координаты ячейки в номер в массиве
  //   INVENTORY REGISTERS
  //   BATTLE MODE
  //   ENEMY INIT
  //   ENEMY ATTACK
  //   EAT FOOD
  //   PREVIOUS STATE
  //   Switch map
  //   enemy attaked
  //   If PLAYER WON
  //   Curent map level
  //   Player HP
  //   last player damage
  //   SOME GLOBAL VARIBLES
  //   Current Enemy number
  //   last enemy damage
  //   PLAYER MOVEMENT
  //   BATTLE MODE VARIBLES
  //   Game state
  //   0 - start screen 1 - walking 2 - battle
  //   Player Direction
  //   Current Enemy dmg
  //   Current Enemy hp
  //   DO FORWARD STEP
  //   ATTACK THE ENEMY
  //   CHECK ENEMY WON
  //   green dot - food
  //   red dot - weapon
  //   GAME MAP
  //   input: 
  //   Future is closer, than you think
  //   Current_score
  //   Memory access
  //   MAKE A TURN
  //   MET ENEMY AND CHANGE GAME MODE TO BATTLE
  //   PARSE INPUT
  //   turn were
  //   HUNGER
  //   if hunger equals health, you will die!
  //   enemy HP
  //   Map Loading..
  //   you can't move
  //   player HP
  //   INITIALIZING GAME MAP
  //   GAME MODE CHANGER
  //   Clock and reset game
  //   HUNGER COUNTER
  //   PLAYER LOSE BY HUNGER COUNTER
  //   Current hunger
  //   TEXT SELECTORS
  //   PLAYER FIND ITEM
endmodule

// Maps
module maps (
  input  [7:0] ADDR,
  input  [11:0] ELEM,
  output [11:0] Width,
  output [11:0] Height,
  output [7:0] Xpp,
  output [7:0] Ypp,
  output [7:0] DATA,
  output [11:0] LEN
);

  wire [7:0] mgeD0, mgeD1, mgeD2, undriven_4, undriven_5;
  wire [11:0] undriven, undriven_2, undriven_3;

  ROM #(.addrWidth(12)) rom_1 (.addr(ELEM), .data(mgeD0));  // open: sel
  ROM #(.addrWidth(12)) rom_2 (.addr(ELEM), .data(mgeD1));  // open: sel
  ROM #(.addrWidth(12)) rom_3 (.addr(ELEM), .data(mgeD2));  // open: sel
  Multiplexer #(.select(5), .width(8), .enable("false")) multiplexer_1 (
    .in0(mgeD0), .in1(mgeD1), .in2(mgeD2), .out(DATA), .sel(ADDR[4:0]));  // open: in3, in4, in5, in6, in7, in8, in9, in10, in11, in12, in13, in14, in15, in16, in17, in18, in19, in20, in21, in22, in23, in24, in25, in26, in27, in28, in29, in30, in31
  Multiplexer #(.select(5), .width(12), .enable("false")) multiplexer_2 (
    .in0(12'h64), .in1(12'h2e5), .in2(12'hab), .in30(undriven), .in31(undriven), .out(LEN), .sel(ADDR[4:0]));  // open: in3, in4, in5, in6, in7, in8, in9, in10, in11, in12, in13, in14, in15, in16, in17, in18, in19, in20, in21, in22, in23, in24, in25, in26, in27, in28, in29
  Multiplexer #(.select(5), .width(12), .enable("false")) multiplexer_3 (
    .in0(12'hb), .in1(12'h25), .in2(12'h11), .in30(undriven_2), .in31(undriven_2), .out(Width),
    .sel(ADDR[4:0]));  // open: in3, in4, in5, in6, in7, in8, in9, in10, in11, in12, in13, in14, in15, in16, in17, in18, in19, in20, in21, in22, in23, in24, in25, in26, in27, in28, in29
  Multiplexer #(.select(5), .width(12), .enable("false")) multiplexer_4 (
    .in0(12'h8), .in1(12'h14), .in2(12'ha), .in30(undriven_3), .in31(undriven_3), .out(Height),
    .sel(ADDR[4:0]));  // open: in3, in4, in5, in6, in7, in8, in9, in10, in11, in12, in13, in14, in15, in16, in17, in18, in19, in20, in21, in22, in23, in24, in25, in26, in27, in28, in29
  Multiplexer #(.select(5), .width(8), .enable("false")) multiplexer_5 (
    .in0(8'h4), .in1(8'h13), .in2(8'h4), .in30(undriven_4), .in31(undriven_4), .out(Xpp), .sel(ADDR[4:0]));  // open: in3, in4, in5, in6, in7, in8, in9, in10, in11, in12, in13, in14, in15, in16, in17, in18, in19, in20, in21, in22, in23, in24, in25, in26, in27, in28, in29
  Multiplexer #(.select(5), .width(8), .enable("false")) multiplexer_6 (
    .in0(8'h3), .in1(8'hc), .in2(8'h4), .in30(undriven_5), .in31(undriven_5), .out(Ypp), .sel(ADDR[4:0]));  // open: in3, in4, in5, in6, in7, in8, in9, in10, in11, in12, in13, in14, in15, in16, in17, in18, in19, in20, in21, in22, in23, in24, in25, in26, in27, in28, in29

  // Other names for the same wires on the sheet: mdeMux1[7:0] = DATA; mdeMuxl1[11:0] = LEN; mgeAddr1[4:0] = ADDR[4:0];
  //   mgeEl[11:0] = ELEM; mhMuxl1[11:0] = Height; mwMuxl1[11:0] = Width; mXMuxl1[7:0] = Xpp; mYMuxl1[7:0] = Ypp

  // Notes on the sheet:
  //   TEST MAP
  //   Level 1
  //   Level 2
  //   contents of rom_1 (hex, n*v repeats v):
  //   36*23 20 14*23 32 47*23
  //   contents of rom_2 (hex, n*v repeats v):
  //   114*23 20 45 23 63 4*20 23 20 20 20 23 20 20 20 23 4*20 23 20 62 20 20 32 31 31 31 68 6*23 20 23 23
  //   20 23 23 23 20 23 20 23 63 23 20 23 20 20 20 23 23 20 23 23 20 23 20 11*23 33 23 23 20 20 20 23 20
  //   31 20 23 20 20 20 5*23 20 20 20 32 20 23 4*20 23 67 6*23 20 64 23 23 23 20 5*23 20 4*23 20 20 23 20
  //   5*23 20 23 20 20 23 34 6*23 34 23 23 20 20 20 23 20 23 23 23 20 20 62 20 23 20 4*23 20 20 20 23 23
  //   23 20 23 23 32 6*23 34 23 23 20 23 20 23 20 20 20 23 20 20 23 31 23 20 23 23 20 23 20 23 5*20 62 20
  //   20 6*23 4*20 23 20 20 20 23 20 20 61 23 23 20 23 20 23 4*20 15*23 20 5*23 20 23 23 31 23 23 23 4*20
  //   23 32 23 23 4*20 64 23 4*20 6*23 31 23 23 4*20 23 6*20 4*23 20 23 23 23 20 4*23 20 23 20 7*23 20 23
  //   23 20 23 20 9*23 66 4*20 6a 23 6*20 23 20 20 6*23 20 23 20 20 23 20 20 23 20 23 23 20 20 23 23 20
  //   6*23 20 23 20 5*23 20 6*23 20 23 23 20 4*23 20 31 20 20 20 23 62 8*20 23 5*20 23 31 6*23 20 23 23 32
  //   20 20 20 23 20 7*23 20 23 23 23 20 23 20 5*23 20 23 20 6*23 20 20 20 61 23 7*20 62 5*20 23 20 20 20
  //   31 32 20 69 20 23 20 20 63 114*23
  //   contents of rom_3 (hex, n*v repeats v):
  //   54*23 4*20 23 20 20 23 20 20 20 6*23 20 20 23 4*20 57 20 23 20 6*23 20 20 8*23 20 6*23 11*20 54*23
  //   Возращает данные карты по адресу
  //   Предоставляет поэлементный доступ к ее элеменнтам
endmodule

module x_y__to_memory_elem_number (
  input  [11:0] H,
  input  [7:0] Y,
  input  [7:0] X,
  output [11:0] ELEM
);

  wire [11:0] bit_extender_1_out, bit_extender_2_out, multiplier_1_out;

  assign bit_extender_1_out = {{4{1'b0}}, Y};  // Bit_Extender bit_extender_1
  Multiplier #(.width(12)) multiplier_1 (.a(H), .b(bit_extender_1_out), .out(multiplier_1_out));  // open: cin, cout
  assign bit_extender_2_out = {{4{1'b0}}, X};  // Bit_Extender bit_extender_2
  Adder #(.width(12)) adder_1 (.a(multiplier_1_out), .b(bit_extender_2_out), .out(ELEM));  // open: cin, cout

  // Notes on the sheet:
  //   Переводит координаты ячейки в номер в массиве
  //   H - ширина карты
endmodule

module enemies (
  input  [1:0] ADDR,
  output [7:0] HP,
  output [7:0] DMG
);

  Multiplexer #(.select(2), .width(8), .disabled(0), .enable("false")) multiplexer_1 (
    .in0(8'h14), .in1(8'ha), .in2(8'h32), .in3(8'h1e), .out(HP), .sel(ADDR));
  Multiplexer #(.select(2), .width(8), .disabled(0), .enable("false")) multiplexer_2 (
    .in0(8'h5), .in1(8'h3), .in2(8'h14), .in3(8'ha), .out(DMG), .sel(ADDR));

  // Notes on the sheet:
  //   get enemy states
endmodule

module quick (
  input  IN,
  output OUT
);

  wire not_1_out, not_2_out;

  not not_1 (not_1_out, IN);
  Register #(.width(1)) register_1 (.D(IN), .Q(OUT), .clk(IN), .clr(not_2_out));  // open: en
  not not_2 (not_2_out, not_1_out);

  // Notes on the sheet:
  //   Короткий сигнал когда на IN 0 переходит в 1
endmodule

module food (
  input  [7:0] FOOD,
  output [7:0] GIVEHP,
  output ES
);

  wire comparator_1_lt, comparator_2_gt;
  wire [1:0] bit_extender_1_out;
  wire [7:0] subtractor_1_out;

  Subtractor subtractor_1 (.a(FOOD), .b(8'h61), .out(subtractor_1_out));  // open: bin, bout
  Multiplexer #(.select(2), .width(8), .enable("false")) multiplexer_1 (
    .in0(8'ha), .in1(8'h6), .in2(8'hf), .in3(8'h14), .out(GIVEHP), .sel(bit_extender_1_out));
  Bit_Extender #(.out_width(2)) bit_extender_1 (.in(subtractor_1_out), .out(bit_extender_1_out));
  Comparator comparator_1 (.a(FOOD), .b(8'h65), .lt(comparator_1_lt));  // open: gt, eq
  Pull_Resistor pull_resistor_1 (.node(ES));
  and and_1 (ES, comparator_1_lt, comparator_2_gt);
  Comparator comparator_2 (.a(FOOD), .b(8'h60), .gt(comparator_2_gt));  // open: eq, lt

  // Notes on the sheet:
  //   Возвращает HP приносимое едой
  //   is it eat
endmodule

module Lquick (
  input  IN,
  input  CLC,
  output OUT
);

  wire and_1_out, comparator_1_eq, quick_1_out;
  wire [2:0] adder_1_out, register_1_q;

  and and_1 (and_1_out, CLC, ~comparator_1_eq);  // AND_Gate
  Adder #(.width(3)) adder_1 (.a(3'b001), .b(register_1_q), .out(adder_1_out));  // open: cin, cout
  Register #(.width(3)) register_1 (.D(adder_1_out), .Q(register_1_q), .clk(and_1_out), .clr(quick_1_out));  // open: en
  quick quick_1 (.IN(IN), .OUT(quick_1_out));
  Comparator #(.width(3), .mode("unsigned")) comparator_1 (
    .a(3'b111), .b(register_1_q), .gt(OUT), .eq(comparator_1_eq));  // open: lt

  // Notes on the sheet:
  //   Создает 'длинный' еденичный сигнал
endmodule

module weapon (
  input  GenRnd,
  input  [7:0] WEAPON,
  output [7:0] DMG,
  output nW
);

  wire and_1_out, comparator_1_lt, comparator_2_gt, comparator_3_eq, not_1_out;
  wire [2:0] bit_extender_1_out;
  wire [7:0] multiplexer_1_out, plusminus1_1_out, subtractor_1_out;

  Subtractor subtractor_1 (.a(WEAPON), .b(8'h66), .out(subtractor_1_out));  // open: bin, bout
  Comparator comparator_1 (.a(WEAPON), .b(8'h6b), .lt(comparator_1_lt));  // open: gt, eq
  Comparator comparator_2 (.a(WEAPON), .b(8'h65), .gt(comparator_2_gt));  // open: eq, lt
  Comparator comparator_3 (.a(WEAPON), .b({8{1'b0}}), .eq(comparator_3_eq));  // open: gt, lt
  Multiplexer #(.select(3), .width(8), .enable("false")) multiplexer_1 (
    .in0(8'h5), .in1(8'h14), .in2(8'hf), .in3(8'ha), .in4(8'h63), .out(multiplexer_1_out),
    .sel(bit_extender_1_out));  // open: in5, in6, in7
  Bit_Extender #(.out_width(3)) bit_extender_1 (.in(subtractor_1_out), .out(bit_extender_1_out));
  not not_1 (not_1_out, and_1_out);
  and and_1 (and_1_out, comparator_1_lt, comparator_2_gt);
  and and_2 (nW, not_1_out, ~comparator_3_eq);  // AND_Gate
  plusMinus1 plusminus1_1 (.inp(multiplexer_1_out), .out(plusminus1_1_out), .GenRnd(GenRnd));
  Multiplexer #(.width(8), .enable("false")) multiplexer_2 (
    .in0(plusminus1_1_out), .in1({8{1'b0}}), .out(DMG), .sel(not_1_out));

  // Notes on the sheet:
  //   Возвращает заданный урон в пределах (-1 0 +1)
  //   Random
  //   not weapon
endmodule

module doForwardStep (
  input  WonInp,
  input  [7:0] plY,
  input  [7:0] plX,
  input  [1:0] PlDir,
  input  [7:0] p_x_1_y,
  input  [7:0] p_x_1_y_2,
  input  [7:0] p_x_y_1,
  input  [7:0] p_x_y_1_2,
  output changePCy,
  output moved,
  output changePCx,
  output [7:0] NewPLyOM,
  output [7:0] NewPLxOM
);

  wire and_1_out, and_2_out, and_3_out, and_4_out, comparator_1_eq, comparator_2_eq, comparator_3_eq,
       comparator_4_eq, comparator_5_eq, comparator_6_eq, comparator_7_eq, comparator_8_eq, not_1_out,
       not_2_out, not_3_out, not_4_out, or_1_out, or_3_out;
  wire [7:0] adder_1_out, adder_2_out, subtractor_1_out, subtractor_2_out;

  Comparator #(.width(2)) comparator_1 (.a(PlDir), .b(2'b00), .eq(comparator_1_eq));  // open: gt, lt
  Comparator #(.width(2)) comparator_2 (.a(PlDir), .b(2'b10), .eq(comparator_2_eq));  // open: gt, lt
  Comparator #(.width(2)) comparator_3 (.a(PlDir), .b(2'b01), .eq(comparator_3_eq));  // open: gt, lt
  Comparator #(.width(2)) comparator_4 (.a(PlDir), .b(2'b11), .eq(comparator_4_eq));  // open: gt, lt
  Comparator comparator_5 (.a(p_x_y_1_2), .b(8'h23), .eq(comparator_5_eq));  // open: gt, lt
  Comparator comparator_6 (.a(p_x_y_1), .b(8'h23), .eq(comparator_6_eq));  // open: gt, lt
  Comparator comparator_7 (.a(p_x_1_y_2), .b(8'h23), .eq(comparator_7_eq));  // open: gt, lt
  Comparator comparator_8 (.a(p_x_1_y), .b(8'h23), .eq(comparator_8_eq));  // open: gt, lt
  not not_1 (not_1_out, comparator_5_eq);
  and and_1 (and_1_out, not_1_out, WonInp, comparator_1_eq);
  not not_2 (not_2_out, comparator_6_eq);
  and and_2 (and_2_out, not_2_out, WonInp, comparator_2_eq);
  not not_3 (not_3_out, comparator_7_eq);
  and and_3 (and_3_out, not_3_out, WonInp, comparator_3_eq);
  not not_4 (not_4_out, comparator_8_eq);
  and and_4 (and_4_out, not_4_out, WonInp, comparator_4_eq);
  assign NewPLyOM = and_1_out ? subtractor_1_out : 8'bz;  // Controlled_Buffer controlled_buffer_1
  Subtractor subtractor_1 (.a(plY), .b(8'h1), .out(subtractor_1_out));  // open: bin, bout
  Adder adder_1 (.a(plY), .b(8'h1), .out(adder_1_out));  // open: cin, cout
  assign NewPLyOM = and_2_out ? adder_1_out : 8'bz;  // Controlled_Buffer controlled_buffer_2
  Adder adder_2 (.a(plX), .b(8'h1), .out(adder_2_out));  // open: cin, cout
  assign NewPLxOM = and_3_out ? adder_2_out : 8'bz;  // Controlled_Buffer controlled_buffer_3
  Subtractor subtractor_2 (.a(plX), .b(8'h1), .out(subtractor_2_out));  // open: bin, bout
  assign NewPLxOM = and_4_out ? subtractor_2_out : 8'bz;  // Controlled_Buffer controlled_buffer_4
  or or_1 (or_1_out, and_1_out, and_2_out);
  quick quick_1 (.IN(or_1_out), .OUT(changePCy));
  or or_2 (moved, or_1_out, or_3_out);
  or or_3 (or_3_out, and_3_out, and_4_out);
  quick quick_2 (.IN(or_3_out), .OUT(changePCx));

  // Other names for the same wires on the sheet: NewPLxOMdfs[7:0] = NewPLxOM; NewPLyOMdfs[7:0] = NewPLyOM;
  //   p_x_1_y_dfs[7:0] = p_x_1_y_2; p_x_1_y_dfs_t[7:0] = p_x_1_y; p_x_y_1_dfs[7:0] = p_x_y_1;
  //   p_x_y_1_dfs_t[7:0] = p_x_y_1_2; PlDirdfs[1:0] = PlDir; PLxOMdfs[7:0] = plX; PLyOMdfs[7:0] = plY

  // Notes on the sheet:
  //   Передвигает персонажа вперед если там нет стены
endmodule

module pickUpAnItem (
  input  [7:0] p_x_y,
  input  _1oninp,
  input  _2oninp,
  input  _3oninp,
  input  _4oninp,
  input  _5oninp,
  input  MOVEinited,
  output ITEMinCELL,
  output INV1ch,
  output INV2ch,
  output INV3ch,
  output INV4ch,
  output INV5ch,
  output chMap,
  output InpFl1
);

  wire and_1_out, and_2_out, and_3_out, and_4_out, and_5_out, and_6_out, and_7_out, and_8_out, MOVEinited_t,
       or_2_out;
  wire [1:0] whatis_1_output_key;

  and and_1 (and_1_out, _1oninp, MOVEinited, ITEMinCELL);
  and and_2 (and_2_out, _2oninp, MOVEinited, ITEMinCELL);
  and and_3 (and_3_out, _3oninp, MOVEinited, ITEMinCELL);
  and and_4 (and_4_out, _4oninp, MOVEinited, ITEMinCELL);
  and and_5 (and_5_out, _5oninp, MOVEinited, ITEMinCELL);
  quick quick_1 (.IN(and_1_out), .OUT(INV1ch));
  quick quick_2 (.IN(and_2_out), .OUT(INV2ch));
  quick quick_3 (.IN(and_3_out), .OUT(INV3ch));
  quick quick_4 (.IN(and_4_out), .OUT(INV4ch));
  quick quick_5 (.IN(and_5_out), .OUT(INV5ch));
  or or_1 (chMap, and_1_out, and_2_out, and_3_out, and_4_out, and_5_out);
  and and_6 (and_6_out, chMap, MOVEinited);
  and and_7 (and_7_out, ~ITEMinCELL, or_2_out);  // AND_Gate
  or or_2 (or_2_out, _1oninp, _2oninp, _3oninp, _4oninp, _5oninp);
  or or_3 (InpFl1, and_6_out, and_8_out);
  and and_8 (and_8_out, and_7_out, MOVEinited_t);
  whatIs whatis_1 (.input_element(p_x_y), .output_key(whatis_1_output_key));
  Comparator #(.width(2)) comparator_1 (.a(whatis_1_output_key), .b(2'b01), .eq(ITEMinCELL));  // open: gt, lt

  // Other names for the same wires on the sheet: _1onInppui = _1oninp; _2onInppui = _2oninp; _3onInppui = _3oninp;
  //   _4onInppui = _4oninp; _5onInppui = _5oninp; chMappui = chMap; InpFl1pui = InpFl1; INV1chpui = INV1ch;
  //   INV2chpui = INV2ch; INV3chpui = INV3ch; INV4chpui = INV4ch; INV5chpui = INV5ch; ITEMinCELLpui = ITEMinCELL;
  //   MOVEinitedpui = MOVEinited; p_x_y_pui[7:0] = p_x_y

  // Notes on the sheet:
  //   ПОДБИРАЕМ ПРЕДМЕТ С МИНИКАРТЫ
  //   Оружие или Еда в слоте
endmodule

module weaponSelected (
  input  [7:0] INVENTORY1p,
  input  [7:0] INVENTORY2p,
  input  _1oninp,
  input  [7:0] INVENTORY3p,
  input  [7:0] INVENTORY4p,
  input  _2oninp,
  input  [7:0] INVENTORY5p,
  input  _3oninp,
  input  _4oninp,
  input  _5oninp,
  output weaponSelected
);

  wire and_1_out, and_2_out, and_3_out, and_4_out, and_5_out, comparator_1_lt, comparator_2_gt,
       comparator_3_lt, comparator_4_gt, comparator_5_lt, comparator_6_gt, comparator_7_lt, comparator_8_gt,
       comparator_9_lt, comparator_10_gt;

  Comparator comparator_1 (.a(INVENTORY1p), .b(8'h6b), .lt(comparator_1_lt));  // open: gt, eq
  Comparator comparator_2 (.a(INVENTORY1p), .b(8'h65), .gt(comparator_2_gt));  // open: eq, lt
  Comparator comparator_3 (.a(INVENTORY2p), .b(8'h6b), .lt(comparator_3_lt));  // open: gt, eq
  Comparator comparator_4 (.a(INVENTORY2p), .b(8'h65), .gt(comparator_4_gt));  // open: eq, lt
  Comparator comparator_5 (.a(INVENTORY3p), .b(8'h6b), .lt(comparator_5_lt));  // open: gt, eq
  Comparator comparator_6 (.a(INVENTORY3p), .b(8'h65), .gt(comparator_6_gt));  // open: eq, lt
  Comparator comparator_7 (.a(INVENTORY4p), .b(8'h6b), .lt(comparator_7_lt));  // open: gt, eq
  Comparator comparator_8 (.a(INVENTORY4p), .b(8'h65), .gt(comparator_8_gt));  // open: eq, lt
  Comparator comparator_9 (.a(INVENTORY5p), .b(8'h6b), .lt(comparator_9_lt));  // open: gt, eq
  Comparator comparator_10 (.a(INVENTORY5p), .b(8'h65), .gt(comparator_10_gt));  // open: eq, lt
  and and_1 (and_1_out, comparator_1_lt, _1oninp, comparator_2_gt);
  and and_2 (and_2_out, comparator_3_lt, _2oninp, comparator_4_gt);
  and and_3 (and_3_out, comparator_5_lt, _3oninp, comparator_6_gt);
  and and_4 (and_4_out, comparator_7_lt, _4oninp, comparator_8_gt);
  and and_5 (and_5_out, comparator_9_lt, _5oninp, comparator_10_gt);
  or or_1 (weaponSelected, and_1_out, and_2_out, and_3_out, and_4_out, and_5_out);

  // Other names for the same wires on the sheet: INVENTORY1pws[7:0] = INVENTORY1p; INVENTORY2pws[7:0] = INVENTORY2p;
  //   INVENTORY3pws[7:0] = INVENTORY3p; INVENTORY4pws[7:0] = INVENTORY4p; INVENTORY5pws[7:0] = INVENTORY5p

  // Notes on the sheet:
  //   ПРОВЕРЯЕТ ВЫБРАНО ЛИ ОРУЖИЕ
endmodule
module moveInitialization (
  input  [11:0] mapW,
  input  [7:0] y,
  input  [7:0] x,
  input  MainCLC,
  input  InpFlare,
  input  Stop,
  input  [7:0] objMap,
  output [11:0] x_1_y_elonmap,
  output MoveInited,
  output workWithMap,
  output [11:0] x_1_y_elonmap_2,
  output [11:0] where,
  output [11:0] x_y_1_elonmap,
  output [7:0] p_x_y,
  output [11:0] x_y_elonmap,
  output [11:0] x_y_1_elonmap_2,
  output [7:0] p_x_y_1,
  output [7:0] p_x_y_1_2,
  output [7:0] p_x_1_y,
  output [7:0] p_x_1_y_2,
  output [7:0] p_x_2_y,
  output [7:0] p_x_2_y_2,
  output [7:0] p_x_y_2,
  output [7:0] p_x_y_2_2
);

  wire and_1_out, comparator_1_eq, comparator_1_gt, comparator_1_lt, comparator_2_eq, comparator_3_eq,
       comparator_4_eq, comparator_5_eq, comparator_6_eq, comparator_7_eq, comparator_8_eq, comparator_9_eq,
       comparator_10_eq, comparator_11_eq, comparator_12_eq, comparator_13_eq, comparator_14_eq,
       comparator_15_eq, comparator_16_eq, comparator_17_eq, comparator_18_eq, comparator_19_eq;
  wire [3:0] adder_1_out, register_1_q;
  wire [7:0] adder_2_out, adder_3_out, adder_4_out, adder_5_out, subtractor_1_out, subtractor_2_out,
       subtractor_3_out, subtractor_4_out;
  wire [11:0] p_x_2_y__elemOnMap, p_x_2_y__elemOnMap_t, p_x_y_2__elemOnMap, p_x_y_2__elemOnMap_t;

  Register #(.width(4)) register_1 (.D(adder_1_out), .Q(register_1_q), .clk(and_1_out), .clr(InpFlare));  // open: en
  Adder #(.width(4)) adder_1 (.a(register_1_q), .b(4'b0001), .out(adder_1_out));  // open: cin, cout
  and and_1 (and_1_out, workWithMap, ~Stop, MainCLC);  // AND_Gate
  Comparator #(.width(4)) comparator_1 (
    .a(4'b1100), .b(register_1_q), .gt(comparator_1_gt), .eq(comparator_1_eq), .lt(comparator_1_lt));
  Comparator #(.width(4)) comparator_2 (.a(register_1_q), .b(4'b0010), .eq(comparator_2_eq));  // open: gt, lt
  Comparator #(.width(4)) comparator_3 (.a(register_1_q), .b(4'b0011), .eq(comparator_3_eq));  // open: gt, lt
  Comparator #(.width(4)) comparator_4 (.a(register_1_q), .b(4'b0011), .eq(comparator_4_eq));  // open: gt, lt
  Comparator #(.width(4)) comparator_5 (.a(register_1_q), .b(4'b0100), .eq(comparator_5_eq));  // open: gt, lt
  Comparator #(.width(4)) comparator_6 (.a(register_1_q), .b(4'b0100), .eq(comparator_6_eq));  // open: gt, lt
  Comparator #(.width(4)) comparator_7 (.a(register_1_q), .b(4'b0101), .eq(comparator_7_eq));  // open: gt, lt
  Comparator #(.width(4)) comparator_8 (.a(register_1_q), .b(4'b0101), .eq(comparator_8_eq));  // open: gt, lt
  Comparator #(.width(4)) comparator_9 (.a(register_1_q), .b(4'b0110), .eq(comparator_9_eq));  // open: gt, lt
  Comparator #(.width(4)) comparator_10 (.a(register_1_q), .b(4'b0110), .eq(comparator_10_eq));  // open: gt, lt
  Comparator #(.width(4)) comparator_11 (.a(register_1_q), .b(4'b0111), .eq(comparator_11_eq));  // open: gt, lt
  Comparator #(.width(4)) comparator_12 (.a(register_1_q), .b(4'b0111), .eq(comparator_12_eq));  // open: gt, lt
  Comparator #(.width(4)) comparator_13 (.a(register_1_q), .b(4'b1000), .eq(comparator_13_eq));  // open: gt, lt
  Comparator #(.width(4)) comparator_14 (.a(register_1_q), .b(4'b1000), .eq(comparator_14_eq));  // open: gt, lt
  Comparator #(.width(4)) comparator_15 (.a(register_1_q), .b(4'b1001), .eq(comparator_15_eq));  // open: gt, lt
  Comparator #(.width(4)) comparator_16 (.a(register_1_q), .b(4'b1001), .eq(comparator_16_eq));  // open: gt, lt
  Comparator #(.width(4)) comparator_17 (.a(register_1_q), .b(4'b1010), .eq(comparator_17_eq));  // open: gt, lt
  Comparator #(.width(4)) comparator_18 (.a(register_1_q), .b(4'b1010), .eq(comparator_18_eq));  // open: gt, lt
  Comparator #(.width(4)) comparator_19 (.a(register_1_q), .b(4'b1011), .eq(comparator_19_eq));  // open: gt, lt
  Lquick lquick_1 (.IN(comparator_1_eq), .OUT(MoveInited), .CLC(MainCLC));
  or or_1 (workWithMap, comparator_1_gt, comparator_1_lt);
  assign where = comparator_2_eq ? x_y_elonmap : 12'bz;  // Controlled_Buffer controlled_buffer_1
  assign where = comparator_4_eq ? x_y_1_elonmap_2 : 12'bz;  // Controlled_Buffer controlled_buffer_2
  assign where = comparator_6_eq ? x_y_1_elonmap : 12'bz;  // Controlled_Buffer controlled_buffer_3
  assign where = comparator_8_eq ? x_1_y_elonmap_2 : 12'bz;  // Controlled_Buffer controlled_buffer_4
  assign where = comparator_10_eq ? x_1_y_elonmap : 12'bz;  // Controlled_Buffer controlled_buffer_5
  assign where = comparator_12_eq ? p_x_2_y__elemOnMap : 12'bz;  // Controlled_Buffer controlled_buffer_6
  assign where = comparator_14_eq ? p_x_2_y__elemOnMap_t : 12'bz;  // Controlled_Buffer controlled_buffer_7
  assign where = comparator_16_eq ? p_x_y_2__elemOnMap_t : 12'bz;  // Controlled_Buffer controlled_buffer_8
  assign where = comparator_18_eq ? p_x_y_2__elemOnMap : 12'bz;  // Controlled_Buffer controlled_buffer_9
  Register register_2 (.D(objMap), .Q(p_x_y), .clk(comparator_3_eq));  // open: en, clr
  Register register_3 (.D(objMap), .Q(p_x_y_1), .clk(comparator_5_eq));  // open: en, clr
  Register register_4 (.D(objMap), .Q(p_x_y_1_2), .clk(comparator_7_eq));  // open: en, clr
  Register register_5 (.D(objMap), .Q(p_x_1_y), .clk(comparator_9_eq));  // open: en, clr
  Register register_6 (.D(objMap), .Q(p_x_1_y_2), .clk(comparator_11_eq));  // open: en, clr
  Register register_7 (.D(objMap), .Q(p_x_2_y), .clk(comparator_13_eq));  // open: en, clr
  Register register_8 (.D(objMap), .Q(p_x_2_y_2), .clk(comparator_15_eq));  // open: en, clr
  Register register_9 (.D(objMap), .Q(p_x_y_2), .clk(comparator_17_eq));  // open: en, clr
  Register register_10 (.D(objMap), .Q(p_x_y_2_2), .clk(comparator_19_eq));  // open: en, clr
  Adder adder_2 (.a(y), .b(8'h1), .out(adder_2_out));  // open: cin, cout
  Adder adder_3 (.a(x), .b(8'h1), .out(adder_3_out));  // open: cin, cout
  x_y__to_memory_elem_number x_y_____elem (.H(mapW), .Y(y), .X(x), .ELEM(x_y_elonmap));
  x_y__to_memory_elem_number x_y_____elem_2 (.H(mapW), .Y(adder_2_out), .X(x), .ELEM(x_y_1_elonmap));
  x_y__to_memory_elem_number x_y_____elem_3 (.H(mapW), .Y(y), .X(adder_3_out), .ELEM(x_1_y_elonmap));
  Subtractor subtractor_1 (.a(y), .b(8'h1), .out(subtractor_1_out));  // open: bin, bout
  Subtractor subtractor_2 (.a(x), .b(8'h1), .out(subtractor_2_out));  // open: bin, bout
  Adder adder_4 (.a(x), .b(8'h2), .out(adder_4_out));  // open: cin, cout
  x_y__to_memory_elem_number x_y_____elem_4 (.H(mapW), .Y(subtractor_1_out), .X(x), .ELEM(x_y_1_elonmap_2));
  x_y__to_memory_elem_number x_y_____elem_5 (.H(mapW), .Y(y), .X(subtractor_2_out), .ELEM(x_1_y_elonmap_2));
  x_y__to_memory_elem_number x_y_____elem_6 (.H(mapW), .Y(y), .X(adder_4_out), .ELEM(p_x_2_y__elemOnMap));
  x_y__to_memory_elem_number x_y_____elem_7 (.H(mapW), .Y(subtractor_3_out), .X(x), .ELEM(p_x_y_2__elemOnMap_t));
  Subtractor subtractor_3 (.a(y), .b(8'h2), .out(subtractor_3_out));  // open: bin, bout
  x_y__to_memory_elem_number x_y_____elem_8 (.H(mapW), .Y(y), .X(subtractor_4_out), .ELEM(p_x_2_y__elemOnMap_t));
  Subtractor subtractor_4 (.a(x), .b(8'h2), .out(subtractor_4_out));  // open: bin, bout
  x_y__to_memory_elem_number x_y_____elem_9 (.H(mapW), .Y(adder_5_out), .X(x), .ELEM(p_x_y_2__elemOnMap));
  Adder adder_5 (.a(y), .b(8'h2), .out(adder_5_out));  // open: cin, cout

  // Other names for the same wires on the sheet: mainClk = MainCLC; MAP_tospace_ELEM[11:0] = where;
  //   objectONmap[7:0] = objMap; p_x_1_y__elemOnMap[11:0] = x_1_y_elonmap;
  //   p_x_1_y__elemOnMap_t[11:0] = x_1_y_elonmap_2; p_x_y_1__elemOnMap[11:0] = x_y_1_elonmap;
  //   p_x_y_1__elemOnMap_t[11:0] = x_y_1_elonmap_2; p_x_y__elemOnMap[11:0] = x_y_elonmap; PLxOM[7:0] = x;
  //   PLyOM[7:0] = y

  // Notes on the sheet:
  //   GET SOME ADJACENT CELLS CONTENT
  //   Player (y+1,x) cell
  //   Player (y,x+1) cell
  //   Player cell
  //   Player (y-1,x) cell
  //   Player (y,x-1) cell
  //   Player (y,x+2) cell
  //   GET SOME ADJACENT CELLS COORDINATES
  //   Player (y-2,x) cell
  //   Player (y,x-2) cell
  //   Player (y+2,x) cell
endmodule

module printText (
  input  [25:0] Input,
  output [6:0] char,
  output ptd,
  output res,
  output pTclc
);

  wire comparator_1_eq;
  wire [6:0] adder_1_out, register_1_q;

  Register #(.width(7)) register_1 (.D(adder_1_out), .en(ptd), .Q(register_1_q), .clk(Input[19]), .clr(Input[20]));
  Adder #(.width(7)) adder_1 (.a(7'b0000001), .b(register_1_q), .out(adder_1_out));  // open: cin, cout
  Comparator #(.width(7)) comparator_1 (.a(Input[18:12]), .b(adder_1_out), .eq(comparator_1_eq));  // open: gt, lt
  not not_1 (ptd, comparator_1_eq);
  TextS texts_1 (
    .enemy_item(Input[11:6]), .Addr(Input[25:21]), .N(register_1_q), .Char(char), .second_elem(Input[5:0]));

  assign pTclc = Input[19];
  assign res = Input[20];

  // Other names for the same wires on the sheet: pTres = Input[20]; pEIn[5:0] = Input[11:6]; pEIn2[5:0] = Input[5:0];
  //   pTmxLen[6:0] = Input[18:12]; pTptd = ptd; pTtxt[4:0] = Input[25:21]

  // Notes on the sheet:
  //   Драйвер
  //   Взаимодествует с текстовым терминалом
  //   Выводит сообщения 
  //   data bus
endmodule

module printItem (
  input  [7:0] item,
  output [8:0] str1,
  output [8:0] str5,
  output [8:0] str9,
  output [8:0] str2,
  output [8:0] str6,
  output eat,
  output [8:0] str3,
  output [8:0] str7,
  output weapon,
  output [8:0] str4,
  output [8:0] str8
);

  wire comparator_1_lt, comparator_2_gt, comparator_3_lt, comparator_4_gt;
  wire [3:0] pIitemImg;
  wire [7:0] subtractor_1_out;

  Bit_Extender #(.out_width(4)) bit_extender_1 (.in(subtractor_1_out), .out(pIitemImg));
  Subtractor subtractor_1 (.a(item), .b(8'h60), .out(subtractor_1_out));  // open: bin, bout
  Comparator comparator_1 (.a(item), .b(8'h65), .lt(comparator_1_lt));  // open: gt, eq
  and and_1 (eat, comparator_1_lt, comparator_2_gt);
  Comparator comparator_2 (.a(item), .b(8'h60), .gt(comparator_2_gt));  // open: eq, lt
  Comparator comparator_3 (.a(item), .b(8'h6b), .lt(comparator_3_lt));  // open: gt, eq
  and and_2 (weapon, comparator_3_lt, comparator_4_gt);
  Comparator comparator_4 (.a(item), .b(8'h65), .gt(comparator_4_gt));  // open: eq, lt
  Multiplexer #(.select(4), .width(9), .enable("false")) multiplexer_1 (
    .in0({9{1'b1}}), .in1(9'h92), .in2(9'h82), .in3({9{1'b0}}), .in4(9'h6), .in6({9{1'b0}}), .in7(9'h6),
    .in8(9'hf), .in9(9'he), .in10(9'h80), .out(str1), .sel(pIitemImg));  // open: in5, in11, in12, in13, in14, in15
  Multiplexer #(.select(4), .width(9), .enable("false")) multiplexer_2 (
    .in0({9{1'b1}}), .in1(9'h54), .in2(9'h44), .in3({9{1'b0}}), .in4(9'hf), .in6(9'h2), .in7(9'h7),
    .in8(9'h1f), .in9(9'hf), .in10({9{1'b1}}), .out(str2), .sel(pIitemImg));  // open: in5, in11, in12, in13, in14, in15
  Multiplexer #(.select(4), .width(9), .enable("false")) multiplexer_3 (
    .in0({9{1'b1}}), .in1(9'h38), .in2(9'h54), .in3({9{1'b0}}), .in4(9'h3), .in6(9'h4), .in7(9'hf),
    .in8(9'h3f), .in9(9'hf), .in10({9{1'b1}}), .out(str3), .sel(pIitemImg));  // open: in5, in11, in12, in13, in14, in15
  Multiplexer #(.select(4), .width(9), .enable("false")) multiplexer_4 (
    .in0({9{1'b1}}), .in1(9'h7c), .in2(9'h139), .in3(9'h30), .in4(9'h7), .in6(9'h8), .in7(9'hc), .in8(9'h7c),
    .in9(9'h3f), .in10(9'h64), .out(str4), .sel(pIitemImg));  // open: in5, in11, in12, in13, in14, in15
  Multiplexer #(.select(4), .width(9), .enable("false")) multiplexer_5 (
    .in0({9{1'b1}}), .in1({9{1'b1}}), .in2(9'hfe), .in3(9'h78), .in4(9'h3e), .in6(9'h10), .in7(9'h10),
    .in8(9'hf0), .in9(9'h38), .in10(9'hf8), .out(str5), .sel(pIitemImg));  // open: in5, in11, in12, in13, in14, in15
  Multiplexer #(.select(4), .width(9), .enable("false")) multiplexer_6 (
    .in0({9{1'b1}}), .in1(9'h7c), .in2(9'h38), .in3(9'hfd), .in4(9'hfc), .in6(9'h20), .in7(9'h60),
    .in8(9'h1e0), .in9(9'h78), .in10(9'h1e0), .out(str6), .sel(pIitemImg));  // open: in5, in11, in12, in13, in14, in15
  Multiplexer #(.select(4), .width(9), .enable("false")) multiplexer_7 (
    .in0({9{1'b1}}), .in1(9'h7c), .in2(9'h44), .in3(9'h1fe), .in4(9'h1c0), .in6(9'h40), .in7(9'h1e0),
    .in8(9'h1c0), .in9(9'h60), .in10(9'h1c0), .out(str7), .sel(pIitemImg));  // open: in5, in11, in12, in13, in14, in15
  Multiplexer #(.select(4), .width(9), .enable("false")) multiplexer_8 (
    .in0({9{1'b1}}), .in1(9'h7c), .in2(9'h44), .in3(9'ha8), .in4(9'h180), .in6(9'h80), .in7(9'h1c0),
    .in8(9'hc8), .in9(9'h80), .in10(9'h1c0), .out(str8), .sel(pIitemImg));  // open: in5, in11, in12, in13, in14, in15
  Multiplexer #(.select(4), .width(9), .enable("false")) multiplexer_9 (
    .in0({9{1'b1}}), .in1(9'h183), .in2(9'h82), .in3(9'h124), .in4(9'he0), .in6({9{1'b0}}), .in7(9'hc0),
    .in8(9'h70), .in9(9'h100), .in10(9'h1c0), .out(str9), .sel(pIitemImg));  // open: in5, in11, in12, in13, in14, in15

  // Other names for the same wires on the sheet: elem[7:0] = item

  // Notes on the sheet:
  //   Драйвер
  //   Возвращает картинку для предмета
  //   is it eat in cell
  //   is it weapon in cell
endmodule

module printHP (
  input  [7:0] Inp,
  input  print,
  output [3:0] High,
  output [3:0] Low
);

  wire comparator_1_gt, comparator_2_gt, comparator_3_gt, comparator_4_gt, comparator_5_gt, comparator_6_gt,
       not_1_out;
  wire [3:0] bit_extender_1_out, bit_extender_2_out;
  wire [7:0] multiplexer_1_out, multiplexer_2_out, multiplexer_3_out, multiplexer_4_out, multiplexer_5_out,
       multiplexer_6_out, multiplexer_7_out, multiplexer_8_out, multiplexer_9_out, multiplexer_10_out,
       multiplexer_11_out, multiplexer_12_out, subtractor_1_out, subtractor_2_out, subtractor_3_out,
       subtractor_4_out, subtractor_5_out;

  Comparator #(.mode("unsigned")) comparator_1 (.a(8'h3c), .b(Inp), .gt(comparator_1_gt));  // open: eq, lt
  Subtractor subtractor_1 (.a(Inp), .b(8'h32), .out(subtractor_1_out));  // open: bin, bout
  Comparator #(.mode("unsigned")) comparator_2 (.a(8'h32), .b(Inp), .gt(comparator_2_gt));  // open: eq, lt
  Subtractor subtractor_2 (.a(Inp), .b(8'h28), .out(subtractor_2_out));  // open: bin, bout
  Comparator #(.mode("unsigned")) comparator_3 (.a(8'h28), .b(Inp), .gt(comparator_3_gt));  // open: eq, lt
  Multiplexer #(.width(8), .enable("false")) multiplexer_1 (
    .in0(8'he), .in1(8'h5), .out(multiplexer_1_out), .sel(comparator_1_gt));
  Multiplexer #(.width(8), .enable("false")) multiplexer_2 (
    .in0(8'he), .in1(subtractor_1_out), .out(multiplexer_2_out), .sel(comparator_1_gt));
  Multiplexer #(.width(8), .enable("false")) multiplexer_3 (
    .in0(multiplexer_1_out), .in1(8'h4), .out(multiplexer_3_out), .sel(comparator_2_gt));
  Multiplexer #(.width(8), .enable("false")) multiplexer_4 (
    .in0(multiplexer_2_out), .in1(subtractor_2_out), .out(multiplexer_4_out), .sel(comparator_2_gt));
  Subtractor subtractor_3 (.a(Inp), .b(8'h1e), .out(subtractor_3_out));  // open: bin, bout
  Comparator #(.mode("unsigned")) comparator_4 (.a(8'h1e), .b(Inp), .gt(comparator_4_gt));  // open: eq, lt
  Comparator #(.mode("unsigned")) comparator_5 (.a(8'ha), .b(Inp), .gt(comparator_5_gt));  // open: eq, lt
  Multiplexer #(.width(8), .enable("false")) multiplexer_5 (
    .in0(multiplexer_3_out), .in1(8'h3), .out(multiplexer_5_out), .sel(comparator_3_gt));
  Multiplexer #(.width(8), .enable("false")) multiplexer_6 (
    .in0(multiplexer_4_out), .in1(subtractor_3_out), .out(multiplexer_6_out), .sel(comparator_3_gt));
  Multiplexer #(.width(8), .enable("false")) multiplexer_7 (
    .in0(multiplexer_5_out), .in1(8'h2), .out(multiplexer_7_out), .sel(comparator_4_gt));
  Multiplexer #(.width(8), .enable("false")) multiplexer_8 (
    .in0(multiplexer_6_out), .in1(subtractor_4_out), .out(multiplexer_8_out), .sel(comparator_4_gt));
  Subtractor subtractor_4 (.a(Inp), .b(8'h14), .out(subtractor_4_out));  // open: bin, bout
  Comparator #(.mode("unsigned")) comparator_6 (.a(8'h14), .b(Inp), .gt(comparator_6_gt));  // open: eq, lt
  Subtractor subtractor_5 (.a(Inp), .b(8'ha), .out(subtractor_5_out));  // open: bin, bout
  Multiplexer #(.width(8), .enable("false")) multiplexer_9 (
    .in0(multiplexer_7_out), .in1(8'h1), .out(multiplexer_9_out), .sel(comparator_6_gt));
  Multiplexer #(.width(8), .enable("false")) multiplexer_10 (
    .in0(multiplexer_8_out), .in1(subtractor_5_out), .out(multiplexer_10_out), .sel(comparator_6_gt));
  Multiplexer #(.width(8), .enable("false")) multiplexer_11 (
    .in0(multiplexer_9_out), .in1({8{1'b0}}), .out(multiplexer_11_out), .sel(comparator_5_gt));
  Multiplexer #(.width(8), .enable("false")) multiplexer_12 (
    .in0(multiplexer_10_out), .in1(Inp), .out(multiplexer_12_out), .sel(comparator_5_gt));
  Bit_Extender #(.out_width(4)) bit_extender_1 (.in(multiplexer_11_out), .out(bit_extender_1_out));
  Multiplexer #(.width(4), .enable("false")) multiplexer_13 (
    .in0(bit_extender_1_out), .out(High), .sel(not_1_out));  // open: in1
  Bit_Extender #(.out_width(4)) bit_extender_2 (.in(multiplexer_12_out), .out(bit_extender_2_out));
  Multiplexer #(.width(4), .enable("false")) multiplexer_14 (
    .in0(bit_extender_2_out), .out(Low), .sel(not_1_out));  // open: in1
  not not_1 (not_1_out, print);

  // Notes on the sheet:
  //   Декодирует число как две цифры в двух младших разрядах
  //   Только для числе меньше 60
endmodule

module TextS (
  input  [5:0] second_elem,
  input  [5:0] enemy_item,
  input  [4:0] Addr,
  input  [6:0] N,
  output [6:0] Char
);

  wire and_1_out, and_2_out, and_3_out, and_4_out, and_5_out, and_6_out, comparator_1_eq, comparator_2_eq,
       comparator_3_eq, comparator_4_eq, comparator_5_eq, comparator_6_lt, comparator_7_gt, comparator_8_eq,
       comparator_9_lt, comparator_10_gt, comparator_11_eq, multiplexer_4_out, newN11, not_1_out, not_2_out,
       not_3_out, or_1_out, or_2_out, or_3_out, or_4_out, or_5_out;
  wire [3:0] bit_extender_4_out, bit_extender_5_out, printhp_1_high, printhp_1_low;
  wire [5:0] multiplexer_1_out;
  wire [6:0] adder_1_out, adder_2_out, bit_extender_2_out, bit_extender_3_out, controlled_buffer_1_out, iemN,
       multiplexer_2_out, multiplexer_3_out, multiplexer_7_out, TSbf, TSCh1, TSCh2, TSCh3, TSCh4, TSCh5,
       TSCh6, TSCh7, TSCh8, TSCh9, TSCh10, TSCh11, TSCh12, TSCh13, TSCh14, TSCh15, TSCh16, TSCh17, TSCh18,
       TSCh19, TSCh20, TSCh21, TSCh22, TSCh23, TSCh24, TSCh25, TSCh26, TScu, TSn, TSnb, TSnbn, TSnc, TSncf,
       TSncl, TSncm, TSncr, TSncs, TSns, TSnst, TSnw, undriven, undriven_2, undriven_3;
  wire [7:0] bit_extender_1_out;

  Multiplexer #(.width(6), .enable("false")) multiplexer_1 (
    .in0(enemy_item), .in1(second_elem), .out(multiplexer_1_out), .sel(not_2_out));
  ROM #(.addrWidth(7), .dataWidth(7)) rom_1 (.addr(TSn), .data(TSCh1));  // open: sel
  ROM #(.addrWidth(7), .dataWidth(7)) rom_2 (.addr(TSn), .data(TSCh2));  // open: sel
  ROM #(.addrWidth(7), .dataWidth(7)) rom_3 (.addr(TSn), .data(TSCh3));  // open: sel
  ROM #(.addrWidth(7), .dataWidth(7)) rom_4 (.addr(TSn), .data(TSCh4));  // open: sel
  ROM #(.addrWidth(7), .dataWidth(7)) rom_5 (.addr(TSn), .data(TSCh5));  // open: sel
  ROM #(.addrWidth(7), .dataWidth(7)) rom_6 (.addr(TSn), .data(TSCh6));  // open: sel
  ROM #(.addrWidth(7), .dataWidth(7)) rom_7 (.addr(TSn), .data(TSCh7));  // open: sel
  ROM #(.addrWidth(7), .dataWidth(7)) rom_8 (.addr(TSn), .data(TSCh8));  // open: sel
  ROM #(.addrWidth(7), .dataWidth(7)) rom_9 (.addr(TSn), .data(TSCh9));  // open: sel
  assign bit_extender_1_out = {{2{1'b0}}, multiplexer_1_out};  // Bit_Extender bit_extender_1
  printHP printhp_1 (.Inp(bit_extender_1_out), .High(printhp_1_high), .Low(printhp_1_low), .print(1'b1));
  Multiplexer #(.select(5), .width(7), .enable("false")) multiplexer_2 (
    .in0({7{1'b0}}), .in1(TSCh1), .in2(TSCh2), .in3(TSCh3), .in4(TSCh4), .in5(TSCh5), .in6(TSCh6),
    .in7(TSCh7), .in8(TSCh8), .in9(TSCh9), .in10(TSCh10), .in11(TSCh11), .in12(TSCh12), .in13(TSCh13),
    .in14(TSCh14), .in15(TSCh15), .in16(TSCh16), .in17(TSCh17), .in18(TSCh18), .in19(TSCh19), .in20(TSCh20),
    .in21(TSCh21), .in22(TSCh22), .in23(TSCh23), .in24(TSCh24), .in25(TSCh25), .in26(TSCh26),
    .out(multiplexer_2_out), .sel(Addr));  // open: in27, in28, in29, in30, in31
  assign bit_extender_2_out = {{3{1'b0}}, printhp_1_low};  // Bit_Extender bit_extender_2
  assign bit_extender_3_out = {{3{1'b0}}, printhp_1_high};  // Bit_Extender bit_extender_3
  Adder #(.width(7)) adder_1 (.a(7'b0110000), .b(bit_extender_2_out), .out(adder_1_out));  // open: cin, cout
  Adder #(.width(7)) adder_2 (.a(7'b0110000), .b(bit_extender_3_out), .out(adder_2_out));  // open: cin, cout
  not not_1 (not_1_out, comparator_1_eq);
  Comparator #(.width(7), .mode("unsigned")) comparator_1 (
    .a(N), .b(7'b0010110), .eq(comparator_1_eq));  // open: gt, lt
  Comparator #(.width(7), .mode("unsigned")) comparator_2 (
    .a(N), .b(7'b0010101), .eq(comparator_2_eq));  // open: gt, lt
  Multiplexer #(.width(7), .enable("false")) multiplexer_3 (
    .in0(adder_1_out), .in1(adder_2_out), .out(multiplexer_3_out), .sel(multiplexer_4_out));
  Multiplexer #(.enable("false")) multiplexer_4 (
    .in0(not_1_out), .in1(not_3_out), .out(multiplexer_4_out), .sel(not_2_out));
  or or_1 (or_1_out, comparator_1_eq, comparator_2_eq);
  not not_2 (not_2_out, or_1_out);
  Comparator #(.width(5), .mode("unsigned")) comparator_3 (
    .a(Addr), .b(5'b10100), .eq(comparator_3_eq));  // open: gt, lt
  not not_3 (not_3_out, comparator_4_eq);
  Comparator #(.width(7), .mode("unsigned")) comparator_4 (
    .a(N), .b(7'b0110101), .eq(comparator_4_eq));  // open: gt, lt
  Comparator #(.width(7), .mode("unsigned")) comparator_5 (
    .a(N), .b(7'b0110100), .eq(comparator_5_eq));  // open: gt, lt
  Comparator #(.width(7), .mode("unsigned")) comparator_6 (
    .a(N), .b(7'b0011001), .lt(comparator_6_lt));  // open: gt, eq
  Comparator #(.width(7), .mode("unsigned")) comparator_7 (
    .a(N), .b(7'b0001111), .gt(comparator_7_gt));  // open: eq, lt
  Multiplexer #(.width(7), .enable("false")) multiplexer_5 (
    .in0(multiplexer_2_out), .in1(controlled_buffer_1_out), .out(Char), .sel(and_1_out));
  and and_1 (and_1_out, or_2_out, newN11);
  or or_2 (or_2_out, comparator_3_eq, comparator_8_eq, comparator_11_eq);
  ROM #(.addrWidth(7), .dataWidth(7)) rom_10 (.addr(TSn), .data(TSCh10));  // open: sel
  ROM #(.addrWidth(7), .dataWidth(7)) rom_11 (.addr(TSn), .data(TSCh11));  // open: sel
  ROM #(.addrWidth(7), .dataWidth(7)) rom_12 (.addr(TSn), .data(TSCh12));  // open: sel
  ROM #(.addrWidth(7), .dataWidth(7)) rom_13 (.addr(TSn), .data(TSCh13));  // open: sel
  ROM #(.addrWidth(7), .dataWidth(7)) rom_14 (.addr(TSn), .data(TSCh15));  // open: sel
  ROM #(.addrWidth(7), .dataWidth(7)) rom_15 (.addr(TSn), .data(TSCh16));  // open: sel
  ROM #(.addrWidth(7), .dataWidth(7)) rom_16 (.addr(TSn), .data(TSCh17));  // open: sel
  ROM #(.addrWidth(7), .dataWidth(7)) rom_17 (.addr(TSn), .data(TSCh18));  // open: sel
  ROM #(.addrWidth(7), .dataWidth(7)) rom_18 (.addr(TSn), .data(TSCh19));  // open: sel
  or or_3 (or_3_out, comparator_4_eq, comparator_5_eq);
  or or_4 (or_4_out, or_3_out, or_1_out);
  and and_2 (and_2_out, comparator_6_lt, comparator_7_gt);
  and and_3 (and_3_out, and_2_out, comparator_8_eq);
  Comparator #(.width(5), .mode("unsigned")) comparator_8 (
    .a(Addr), .b(5'b10110), .eq(comparator_8_eq));  // open: gt, lt
  assign controlled_buffer_1_out = and_4_out ? multiplexer_3_out : 7'bz;  // Controlled_Buffer controlled_buffer_1
  and and_4 (and_4_out, comparator_3_eq, or_4_out);
  Comparator #(.width(7), .mode("unsigned")) comparator_9 (
    .a(N), .b(7'b0111101), .lt(comparator_9_lt));  // open: gt, eq
  and and_5 (and_5_out, comparator_9_lt, comparator_10_gt);
  Comparator #(.width(7), .mode("unsigned")) comparator_10 (
    .a(N), .b(7'b0101000), .gt(comparator_10_gt));  // open: eq, lt
  Comparator #(.width(5), .mode("unsigned")) comparator_11 (
    .a(Addr), .b(5'b10111), .eq(comparator_11_eq));  // open: gt, lt
  assign controlled_buffer_1_out = or_5_out ? multiplexer_7_out : 7'bz;  // Controlled_Buffer controlled_buffer_2
  or or_5 (or_5_out, and_3_out, and_6_out);
  and and_6 (and_6_out, and_5_out, comparator_11_eq);
  or or_6 (newN11, and_4_out, or_5_out);
  ROM #(.addrWidth(7), .dataWidth(7)) rom_19 (.addr(TSn), .data(TSCh14));  // open: sel
  ROM #(.addrWidth(7), .dataWidth(7)) rom_20 (.addr(TSn), .data(TSCh20));  // open: sel
  ROM #(.addrWidth(7), .dataWidth(7)) rom_21 (.addr(TSn), .data(TSCh21));  // open: sel
  ROM #(.addrWidth(7), .dataWidth(7)) rom_22 (.addr(TSn), .data(TSCh22));  // open: sel
  ROM #(.addrWidth(7), .dataWidth(7)) rom_23 (.addr(TSn), .data(TSCh23));  // open: sel
  ROM #(.addrWidth(7), .dataWidth(7)) rom_24 (.addr(TSn), .data(TSCh24));  // open: sel
  ROM #(.addrWidth(7), .dataWidth(7)) rom_25 (.addr(TSn), .data(TSCh25));  // open: sel
  ROM #(.addrWidth(7), .dataWidth(7)) rom_26 (.addr(TSn), .data(TSCh26));  // open: sel
  Bit_Extender #(.in_width(6), .out_width(4)) bit_extender_4 (.in(enemy_item), .out(bit_extender_4_out));
  Multiplexer #(.width(7), .enable("false")) multiplexer_6 (.in0(N), .in1(iemN), .out(TSn), .sel(newN11));
  Multiplexer #(.select(4), .width(7), .enable("false")) multiplexer_7 (
    .in0(TSCh6), .in1(TSCh7), .in2(TSCh8), .in3(TSCh9), .in4(TSCh10), .in5(TSCh11), .in6(TSCh12),
    .in7(TSCh13), .in9(TSCh15), .in10(TSCh16), .in11(TSCh17), .in12(TSCh18), .in13(TSCh19), .in14(undriven),
    .in15(undriven_2), .out(multiplexer_7_out), .sel(bit_extender_4_out));  // open: in8
  Multiplexer #(.select(4), .width(7), .enable("false")) multiplexer_8 (
    .in0(TSncr), .in1(TSncm), .in2(TSncf), .in3(TSncs), .in4(TSnb), .in5(TSns), .in6(TSnc), .in7(TSnw),
    .in9(TSnst), .in10(TSnbn), .in11(TSncl), .in12(TScu), .in13(TSbf), .in14(undriven_3), .out(iemN),
    .sel(bit_extender_5_out));  // open: in8, in15
  Bit_Extender #(.in_width(6), .out_width(4)) bit_extender_5 (.in(enemy_item), .out(bit_extender_5_out));
  Subtractor #(.width(7)) subtractor_1 (.a(N), .b(7'b0100011), .out(TSncr));  // open: bin, bout
  Subtractor #(.width(7)) subtractor_2 (.a(N), .b(7'b0100100), .out(TSncm));  // open: bin, bout
  Subtractor #(.width(7)) subtractor_3 (.a(N), .b(7'b0100101), .out(TSncf));  // open: bin, bout
  Subtractor #(.width(7)) subtractor_4 (.a(N), .b(7'b0100101), .out(TSncs));  // open: bin, bout
  Subtractor #(.width(7)) subtractor_5 (.a(N), .b(7'b0001100), .out(TSnb));  // open: bin, bout
  Subtractor #(.width(7)) subtractor_6 (.a(N), .b(7'b0001110), .out(TSns));  // open: bin, bout
  Subtractor #(.width(7)) subtractor_7 (.a(N), .b(7'b0010000), .out(TSnc));  // open: bin, bout
  Subtractor #(.width(7)) subtractor_8 (.a(N), .b(7'b0001101), .out(TSnw));  // open: bin, bout
  Subtractor #(.width(7)) subtractor_9 (.a(N), .b(7'b0001101), .out(TSnst));  // open: bin, bout
  Subtractor #(.width(7)) subtractor_10 (.a(N), .b(7'b0001101), .out(TSnbn));  // open: bin, bout
  Subtractor #(.width(7)) subtractor_11 (.a(N), .b(7'b0001100), .out(TSncl));  // open: bin, bout
  Subtractor #(.width(7)) subtractor_12 (.a(N), .b(7'b0001110), .out(TScu));  // open: bin, bout
  Subtractor #(.width(7)) subtractor_13 (.a(N), .b(7'b0001110), .out(TSbf));  // open: bin, bout

  // Other names for the same wires on the sheet: TSb[6:0] = N

  // Notes on the sheet:
  //   Welcome to moles burrow!
  //   contents of rom_1 (hex, n*v repeats v):
  //   57 45 4c 43 4f 4d 45 20 54 4f 20 54 48 45 20 4d 4f 4c 45 20 42 55 52 52 4f 57 21 20 20 47 61 6d 65
  //   20 77 68 65 72 65 20 79 6f 75 20 61 72 65 20 4d 6f 6c 65 20 61 67 61 69 6e 73 74 20 65 76 65 72 79
  //   6f 6e 65
  //   contents of rom_2 (hex, n*v repeats v):
  //   4*20 54 48 52 45 45 2d 44 49 4d 45 4e 53 49 4f 4e 41 4c 20 56 49 45 57 20 4f 46 20 54 48 45 20 42 55
  //   52 52 4f 57 4*20
  //   contents of rom_3 (hex, n*v repeats v):
  //   18*20 49 54 20 49 53 20 59 4f 55 17*20
  //   contents of rom_4 (hex, n*v repeats v):
  //   7*20 4d 49 4e 49 4d 41 50 7*20
  //   contents of rom_6 (hex, n*v repeats v):
  //   6*20 53 43 41 52 59 20 52 41 54 5*20
  //   contents of rom_7 (hex, n*v repeats v):
  //   5*20 45 56 49 4c 20 4d 4f 55 53 45 5*20
  //   contents of rom_8 (hex, n*v repeats v):
  //   4*20 43 55 54 45 20 46 45 52 52 45 54 5*20
  //   contents of rom_9 (hex, n*v repeats v):
  //   4*20 4c 49 54 54 4c 45 20 53 4e 41 4b 45 4*20
  //   3d view
  //   its you
  //   minimap(11)
  //   enemy(11)
  //   rat
  //   mouse
  //   ferret
  //   snake
  //   Схема обеспечивает доступ к памяти строк со вставкой цифр
  //   Для адресов 16 и 17 подменяет подстроки строк
  //   Для адреса 14 подменяет две подстроки на два числа из двух цифр
  //   (13)
  //   contents of rom_10 (hex, n*v repeats v):
  //   4*20 42 55 47 4*20
  //   contents of rom_11 (hex, n*v repeats v):
  //   20 20 53 50 49 44 45 52 20 20 20
  //   contents of rom_12 (hex, n*v repeats v):
  //   43 45 4e 54 49 50 45 44 45 20 20
  //   contents of rom_13 (hex, n*v repeats v):
  //   20 20 20 57 4f 52 4d 4*20
  //   contents of rom_14 (hex, n*v repeats v):
  //   20 20 20 53 54 49 43 4b 20 20 20
  //   contents of rom_15 (hex, n*v repeats v):
  //   20 20 20 42 4f 4e 45 4*20
  //   contents of rom_16 (hex, n*v repeats v):
  //   4*20 43 4c 41 57 20 20 20
  //   contents of rom_17 (hex, n*v repeats v):
  //   20 20 43 55 44 47 45 4c 20 20 20
  //   contents of rom_18 (hex, n*v repeats v):
  //   20 20 42 46 47 39 30 30 30 20 20
  //   BUG
  //   SPIDER
  //   CENTIPEDE
  //   WORM
  //   STICK
  //   BONE
  //   CLAW
  //   CUDGEL
  //   BFG9000
  //   (66)
  //   contents of rom_19 (hex, n*v repeats v):
  //   19*20 50 52 45 53 53 20 41 4e 59 20 4b 45 59 20 54 4f 20 53 54 41 52 54 20 47 41 4d 45 20*20
  //   contents of rom_20 (hex, n*v repeats v):
  //   6*20 59 4f 55 20 48 41 56 45 20 44 45 41 4c 54 4*20 44 41 4d 41 47 45 2e 20 54 48 45 20 45 4e 45 4d
  //   59 20 48 41 53 20 44 45 41 4c 54 4*20 44 41 4d 41 47 45 5*20
  //   contents of rom_21 (hex, n*v repeats v):
  //   18*20 59 4f 55 20 48 41 56 45 20 44 45 46 45 41 54 45 44 20 59 4f 55 52 20 45 4e 45 4d 59 21 19*20
  //   contents of rom_22 (hex, n*v repeats v):
  //   6*20 59 4f 55 20 46 4f 55 4e 44 11*20 2e 20 57 48 49 43 48 20 53 4c 4f 54 20 57 49 4c 4c 20 59 4f 55
  //   20 54 41 4b 45 20 49 54 20 54 4f 3f 7*20
  //   contents of rom_23 (hex, n*v repeats v):
  //   17*20 59 4f 55 20 41 52 45 20 55 4e 44 45 52 20 41 54 54 41 43 4b 20 42 59 22*20 21 20 20 20
  //   contents of rom_24 (hex, n*v repeats v):
  //   59 4f 55 52 45 20 41 57 41 4b 45 2e 20 4f 4e 45 20 54 48 49 4e 47 20 49 53 20 43 4c 45 41 52 20 2d
  //   20 49 54 53 20 54 49 4d 45 20 54 4f 20 47 45 54 20 4f 55 54 20 4f 46 20 54 48 45 20 48 4f 4c 45 20
  //   contents of rom_25 (hex, n*v repeats v):
  //   18*20 59 6f 75 20 77 6f 6e 21 16*20 2e 16*20 74 79 70 65 20 73 6f 6d 65 74 68 69 6e 67 20 74 6f 20
  //   72 65 73 74 61 72 74
  //   contents of rom_26 (hex, n*v repeats v):
  //   16*20 59 6f 75 20 4c 6f 73 65 20 67 61 6d 65 20 62 79 20 68 75 6e 67 65 72 13*20 74 79 70 65 20 73
  //   6f 6d 65 74 68 69 6e 67 20 74 6f 20 72 65 73 74 61 72 74
  //   press to continue
  //   you attak enemy
  //   you win
  //   you find
  //   you attaked by enemy
  //   you awake
  //   you won game
  //   you lose
endmodule

module whatIs (
  input  [7:0] input_element,
  output [1:0] output_key
);

  wire and_1_out, and_2_out, and_3_out, comparator_1_lt, comparator_2_gt, comparator_3_lt, comparator_4_gt,
       comparator_5_lt, comparator_6_gt, comparator_7_eq, comparator_8_eq, or_1_out, or_2_out;

  Comparator comparator_1 (.a(input_element), .b(8'h65), .lt(comparator_1_lt));  // open: gt, eq
  and and_1 (and_1_out, comparator_1_lt, comparator_2_gt);
  Comparator comparator_2 (.a(input_element), .b(8'h60), .gt(comparator_2_gt));  // open: eq, lt
  Comparator comparator_3 (.a(input_element), .b(8'h6b), .lt(comparator_3_lt));  // open: gt, eq
  and and_2 (and_2_out, comparator_3_lt, comparator_4_gt);
  Comparator comparator_4 (.a(input_element), .b(8'h65), .gt(comparator_4_gt));  // open: eq, lt
  Comparator comparator_5 (.a(input_element), .b(8'h35), .lt(comparator_5_lt));  // open: gt, eq
  and and_3 (and_3_out, comparator_5_lt, comparator_6_gt);
  Comparator comparator_6 (.a(input_element), .b(8'h30), .gt(comparator_6_gt));  // open: eq, lt
  Comparator comparator_7 (.a(input_element), .b(8'h45), .eq(comparator_7_eq));  // open: gt, lt
  or or_1 (or_1_out, comparator_7_eq, comparator_8_eq);
  Comparator comparator_8 (.a(input_element), .b(8'h57), .eq(comparator_8_eq));  // open: gt, lt
  assign output_key = or_2_out ? 2'b01 : 2'bz;  // Controlled_Buffer controlled_buffer_1
  or or_2 (or_2_out, and_1_out, and_2_out);
  assign output_key = and_3_out ? 2'b11 : 2'bz;  // Controlled_Buffer controlled_buffer_2
  assign output_key = or_1_out ? 2'b10 : 2'bz;  // Controlled_Buffer controlled_buffer_3
  Pull_Resistor pull_resistor_1 (.node(output_key));

  // Other names for the same wires on the sheet: elem[7:0] = input_element

  // Notes on the sheet:
  //   is it eat in cell
  //   is it weapon in cell
  //   is it enemy in cell
  //   is it exit in cell
  //   Проверка входного значения
  //   0 - не сущность
  //   1 - еда / оружие
  //   2 - выход
  //   3 - враг
endmodule

module plusMinus1 (
  input  GenRnd,
  input  [7:0] inp,
  output [7:0] out
);

  wire [2:0] random_1_out;
  wire [7:0] adder_1_out, bit_extender_1_out, bit_extender_2_out, subtractor_1_out;

  Random #(.width(3)) random_1 (.clk(GenRnd), .out(random_1_out));  // open: next, clr
  assign bit_extender_1_out = {{7{1'b0}}, random_1_out[1]};  // Bit_Extender bit_extender_1
  Subtractor subtractor_1 (.a(inp), .b(bit_extender_1_out), .out(subtractor_1_out));  // open: bin, bout
  assign bit_extender_2_out = {{7{1'b0}}, random_1_out[2]};  // Bit_Extender bit_extender_2
  Adder adder_1 (.a(bit_extender_2_out), .b(inp), .out(adder_1_out));  // open: cin, cout
  Multiplexer #(.width(8), .enable("false")) multiplexer_1 (
    .in0(subtractor_1_out), .in1(adder_1_out), .out(out), .sel(random_1_out[0]));

  // Notes on the sheet:
  //   Такт для рандома
  //   out = random choice (inp - 1, inp, inp + 1)
endmodule

module eatFood (
  input  [7:0] INVENTORY1p,
  input  _1onInpff,
  input  [7:0] INVENTORY2p,
  input  _2onInpff,
  input  [7:0] INVENTORY3p,
  input  _3onInpff,
  input  [7:0] INVENTORY4p,
  input  _4onInpff,
  input  [7:0] INVENTORY5p,
  input  _5onInpff,
  input  EatFlare,
  output itemRES1,
  output itemRES2,
  output itemRES3,
  output itemRES4,
  output itemRES5,
  output CHHPinmove
);

  wire and_1_out, and_2_out, and_3_out, and_4_out, and_5_out, and_6_out, and_7_out, and_8_out, and_9_out,
       and_10_out, comparator_1_lt, comparator_2_gt, comparator_3_lt, comparator_4_gt, comparator_5_lt,
       comparator_6_gt, comparator_7_lt, comparator_8_gt, comparator_9_lt, comparator_10_gt;

  Comparator comparator_1 (.a(INVENTORY1p), .b(8'h65), .lt(comparator_1_lt));  // open: gt, eq
  and and_1 (and_1_out, comparator_1_lt, _1onInpff, comparator_2_gt);
  Comparator comparator_2 (.a(INVENTORY1p), .b(8'h60), .gt(comparator_2_gt));  // open: eq, lt
  Comparator comparator_3 (.a(INVENTORY2p), .b(8'h65), .lt(comparator_3_lt));  // open: gt, eq
  and and_2 (and_2_out, comparator_3_lt, _2onInpff, comparator_4_gt);
  Comparator comparator_4 (.a(INVENTORY2p), .b(8'h60), .gt(comparator_4_gt));  // open: eq, lt
  Comparator comparator_5 (.a(INVENTORY3p), .b(8'h65), .lt(comparator_5_lt));  // open: gt, eq
  and and_3 (and_3_out, comparator_5_lt, _3onInpff, comparator_6_gt);
  Comparator comparator_6 (.a(INVENTORY3p), .b(8'h60), .gt(comparator_6_gt));  // open: eq, lt
  Comparator comparator_7 (.a(INVENTORY4p), .b(8'h65), .lt(comparator_7_lt));  // open: gt, eq
  and and_4 (and_4_out, comparator_7_lt, _4onInpff, comparator_8_gt);
  Comparator comparator_8 (.a(INVENTORY4p), .b(8'h60), .gt(comparator_8_gt));  // open: eq, lt
  Comparator comparator_9 (.a(INVENTORY5p), .b(8'h65), .lt(comparator_9_lt));  // open: gt, eq
  and and_5 (and_5_out, comparator_9_lt, _5onInpff, comparator_10_gt);
  Comparator comparator_10 (.a(INVENTORY5p), .b(8'h60), .gt(comparator_10_gt));  // open: eq, lt
  and and_6 (and_6_out, EatFlare, and_1_out);
  and and_7 (and_7_out, EatFlare, and_2_out);
  and and_8 (and_8_out, EatFlare, and_3_out);
  and and_9 (and_9_out, EatFlare, and_4_out);
  and and_10 (and_10_out, EatFlare, and_5_out);
  quick quick_1 (.IN(and_6_out), .OUT(itemRES1));
  quick quick_2 (.IN(and_7_out), .OUT(itemRES2));
  quick quick_3 (.IN(and_8_out), .OUT(itemRES3));
  quick quick_4 (.IN(and_9_out), .OUT(itemRES4));
  quick quick_5 (.IN(and_10_out), .OUT(itemRES5));
  or or_1 (CHHPinmove, and_5_out, and_4_out, and_3_out, and_2_out, and_1_out);

  // Notes on the sheet:
  //   EAT FOOD
endmodule

module parseInpKey (
  input  flush,
  input  [6:0] char,
  output _1,
  output w,
  output _2,
  output a,
  output _3,
  output d,
  output _4,
  output q,
  output _5
);

  wire comparator_1_eq, comparator_2_eq, comparator_3_eq, comparator_4_eq, comparator_5_eq, comparator_6_eq,
       comparator_7_eq, comparator_8_eq, comparator_9_eq;

  Pull_Resistor pull_resistor_1 (.node(_1));
  assign _1 = comparator_1_eq ? flush : 1'bz;  // Controlled_Buffer controlled_buffer_1
  Comparator #(.width(7)) comparator_1 (.a(char), .b(7'b0110001), .eq(comparator_1_eq));  // open: gt, lt
  assign _2 = comparator_2_eq ? flush : 1'bz;  // Controlled_Buffer controlled_buffer_2
  Pull_Resistor pull_resistor_2 (.node(_2));
  Comparator #(.width(7)) comparator_2 (.a(char), .b(7'b0110010), .eq(comparator_2_eq));  // open: gt, lt
  assign _3 = comparator_3_eq ? flush : 1'bz;  // Controlled_Buffer controlled_buffer_3
  Pull_Resistor pull_resistor_3 (.node(_3));
  Comparator #(.width(7)) comparator_3 (.a(char), .b(7'b0110011), .eq(comparator_3_eq));  // open: gt, lt
  assign _4 = comparator_4_eq ? flush : 1'bz;  // Controlled_Buffer controlled_buffer_4
  Pull_Resistor pull_resistor_4 (.node(_4));
  Comparator #(.width(7)) comparator_4 (.a(char), .b(7'b0110100), .eq(comparator_4_eq));  // open: gt, lt
  Pull_Resistor pull_resistor_5 (.node(_5));
  assign _5 = comparator_5_eq ? flush : 1'bz;  // Controlled_Buffer controlled_buffer_5
  Comparator #(.width(7)) comparator_5 (.a(char), .b(7'b0110101), .eq(comparator_5_eq));  // open: gt, lt
  assign w = comparator_6_eq ? flush : 1'bz;  // Controlled_Buffer controlled_buffer_6
  Pull_Resistor pull_resistor_6 (.node(w));
  Comparator #(.width(7)) comparator_6 (.a(char), .b(7'b1110111), .eq(comparator_6_eq));  // open: gt, lt
  assign a = comparator_7_eq ? flush : 1'bz;  // Controlled_Buffer controlled_buffer_7
  Pull_Resistor pull_resistor_7 (.node(a));
  Comparator #(.width(7)) comparator_7 (.a(char), .b(7'b1100001), .eq(comparator_7_eq));  // open: gt, lt
  assign d = comparator_8_eq ? flush : 1'bz;  // Controlled_Buffer controlled_buffer_8
  Pull_Resistor pull_resistor_8 (.node(d));
  Comparator #(.width(7)) comparator_8 (.a(char), .b(7'b1100100), .eq(comparator_8_eq));  // open: gt, lt
  assign q = comparator_9_eq ? flush : 1'bz;  // Controlled_Buffer controlled_buffer_9
  Pull_Resistor pull_resistor_9 (.node(q));
  Comparator #(.width(7)) comparator_9 (.a(char), .b(7'b1110001), .eq(comparator_9_eq));  // open: gt, lt

  // Other names for the same wires on the sheet: iCF = flush; iCR[6:0] = char

  // Notes on the sheet:
  //   Пускает импульс на выход соответсвующий нажатой клавише
endmodule
