// Logisim project main1.circ as structural Verilog
module main (
);

  wire _1onInp, _1onInpff, _2onInp, _2onInpff, _3onInp, _3onInpff, _4onInp, _4onInpff, _5onInp, _5onInpff,
       adder_1_out, and_1_out, and_2_out, and_3_out, and_4_out, and_5_out, and_6_out, and_7_out, and_8_out,
       and_9_out, and_10_out, and_11_out, and_12_out, and_13_out, and_15_out, and_16_out, and_17_out,
       and_20_out, and_21_out, and_22_out, and_23_out, and_24_out, and_25_out, and_29_out, and_30_out,
       and_31_out, and_32_out, and_33_out, AonInp, ATCcorrectINP, ATCenMove, ATCenMoved, ATCinisW, ATCinit,
       ATCInpFlpre, ATCnewENclc, ATCplAttaked1, buffer_1_out, buffer_3_out, buffer_4_out, buffer_8_out,
       buffer_9_out, buffer_10_out, buffer_11_out, changePCx, changePCy, chGM, CHHPinmove, clock_1_out,
       comparator_1_eq, comparator_2_eq, comparator_3_gt, comparator_4_lt, comparator_5_gt, comparator_6_lt,
       comparator_7_gt, comparator_8_lt, comparator_9_gt, comparator_10_lt, comparator_11_gt,
       comparator_12_lt, comparator_13_gt, comparator_14_eq, comparator_14_gt, comparator_15_eq,
       comparator_15_gt, comparator_16_eq, comparator_17_eq, comparator_18_eq, comparator_19_eq,
       comparator_20_gt, comparator_21_gt, comparator_22_gt, comparator_23_gt, comparator_24_lt,
       comparator_25_lt, comparator_26_lt, comparator_27_lt, comparator_28_eq, comparator_32_eq,
       comparator_33_eq, comparator_34_eq, comparator_35_eq, comparator_36_eq, comparator_37_eq,
       comparator_38_eq, comparator_39_eq, demultiplexer_1_out0, demultiplexer_1_out1, demultiplexer_1_out2,
       demultiplexer_1_out3, demultiplexer_4_out0, demultiplexer_4_out1, demultiplexer_4_out2, DonInp,
       EATflare, gS0, gS1, gS2, InpFl1, InpFlpreC, InpFlpreM, InpFlpreSTRT, INV1ch, INV2ch, INV3ch, INV4ch,
       INV5ch, invchn, itemRES1, itemRES2, itemRES3, itemRES4, itemRES5, keyPress, LoadMap, lquick_1_out,
       lquick_2_out, mainRES, MapLevelCh, mapPREst, mapPREst1, MOVEenHERE, MoveFl, MOVEinited,
       moveinitialization_1_workwithmap, newtEnDmg, newText, not_1_out, not_2_out, not_3_out, not_4_out,
       not_5_out, not_7_out, not_8_out, not_9_out, not_10_out, not_11_out, not_12_out, not_13_out,
       not_14_out, not_15_out, not_16_out, not_17_out, not_18_out, not_19_out, not_20_out, not_21_out,
       not_22_out, not_23_out, not_24_out, not_25_out, not_26_out, not_27_out, not_28_out, not_29_out,
       not_30_out, nwetPlDmg, or_1_out, or_2_out, or_3_out, or_4_out, or_5_out, or_6_out, or_8_out,
       or_10_out, or_11_out, or_12_out, or_13_out, or_15_out, or_17_out, or_19_out, or_22_out, or_23_out,
       or_24_out, or_29_out, PlayerDeathRes, PLAYERHPCH, PlDirCh, printtext_1_ptclc, printtext_1_ptd,
       printtext_1_res, printtext_2_ptclc, printtext_2_ptd, printtext_2_res, printtext_3_ptclc,
       printtext_3_ptd, printtext_3_res, printtext_4_ptclc, printtext_4_ptd, printtext_4_res,
       printtext_5_ptclc, printtext_5_ptd, printtext_5_res, printtext_6_ptclc, printtext_6_ptd,
       printtext_6_res, printtext_7_ptclc, printtext_7_ptd, printtext_7_res, printtext_8_ptclc,
       printtext_8_ptd, printtext_8_res, pull_resistor_6_node, pull_resistor_10_node, Q_out, qres,
       quick_1_out, quick_3_out, quick_5_out, quick_11_out, quick_12_out, quick_14_out, quick_17_out,
       quick_19_out, quick_20_out, quick_22_out, quick_23_out, quick_24_out, random_1_out, register_6_q,
       StateCh, stMapCLC, stMapCLC1, stMapCLC2, weapon_1_nw, weaponselected_1_weaponselected, WonInp,
       WonInpff;
  wire [1:0] adder_5_out, ATCcurEN, ATCnewEN, bit_extender_4_out, bit_extender_5_out, bit_extender_6_out,
       bit_extender_7_out, gameState, gSto, NewPlDir, PlDir, subtractor_5_out;
  wire [2:0] pull_resistor_1_node, pull_resistor_5_node;
  wire [3:0] printhp_1_high, printhp_1_low, printhp_2_high, printhp_2_low;
  wire [4:0] adder_6_out, bit_extender_8_out, bit_extender_9_out, bit_extender_10_out, bit_extender_11_out,
       bit_extender_12_out, bit_extender_14_out, miniMScrT, pull_resistor_9_node, register_29_q, TextText;
  wire [5:0] bit_extender_13_out, bit_extender_15_out, curEnDmg, curPlDmg, lstEnDmg, lstPlDmg,
       multiplexer_17_out, multiplexer_21_out;
  wire [6:0] printtext_1_char, printtext_2_char, printtext_3_char, printtext_4_char, printtext_5_char,
       printtext_6_char, printtext_7_char, printtext_8_char;
  wire [7:0] adder_2_out, adder_3_out, bit_extender_2_out, ENDMG, ENDMGst, enemies_1_hp, ENHP, ENHPst,
       food_1_givehp, gStdtScrMem, INVENTORY1, INVENTORY1p, INVENTORY2, INVENTORY2p, INVENTORY3, INVENTORY3p,
       INVENTORY4, INVENTORY4p, INVENTORY5, INVENTORY5p, mapLevelCur, maps_1_xpp, maps_1_ypp,
       mapSTDATAreaded, multiplexer_1_out, multiplexer_2_out, multiplexer_3_out, multiplexer_5_out,
       multiplexer_7_out, multiplexer_8_out, NewMapLevelCh, NewPlayerHP, NewPLxOM, NewPLyOM, objectONmap,
       p__y_2, p_x_1_y, p_x_1_y_t, p_x_2_y, p_x_2_y_t, p_x_y, p_x_y_1, p_x_y_1_t, p_x_y_2, playerHPCUR,
       PLxOM, PLyOM, subtractor_1_out, subtractor_2_out, subtractor_3_out, subtractor_4_out,
       subtractor_6_out, subtractor_7_out, subtractor_8_out, subtractor_9_out, subtractor_10_out,
       subtractor_11_out, subtractor_12_out, subtractor_13_out, weapon_1_dmg;
  wire [8:0] printitem_1_str1, printitem_1_str2, printitem_1_str3, printitem_1_str4, printitem_1_str5,
       printitem_1_str6, printitem_1_str7, printitem_1_str8, printitem_1_str9, printitem_2_str1,
       printitem_2_str2, printitem_2_str3, printitem_2_str4, printitem_2_str5, printitem_2_str6,
       printitem_2_str7, printitem_2_str8, printitem_2_str9, printitem_3_str1, printitem_3_str2,
       printitem_3_str3, printitem_3_str4, printitem_3_str5, printitem_3_str6, printitem_3_str7,
       printitem_3_str8, printitem_3_str9, printitem_4_str1, printitem_4_str2, printitem_4_str3,
       printitem_4_str4, printitem_4_str5, printitem_4_str6, printitem_4_str7, printitem_4_str8,
       printitem_4_str9, printitem_5_str1, printitem_5_str2, printitem_5_str3, printitem_5_str4,
       printitem_5_str5, printitem_5_str6, printitem_5_str7, printitem_5_str8, printitem_5_str9;
  wire [11:0] adder_4_out, MAP_tospace_ELEM, MapH, maps_1_height, maps_1_width, mapSTelemREAD, MapW,
       moveinitialization_1_where, multiplexer_4_out, p_x_1_y__elemOnMap, p_x_1_y__elemOnMap_t,
       p_x_y_1__elemOnMap, p_x_y_1__elemOnMap_t, p_x_y__elemOnMap;
  wire [20:0] miniScrT;
  wire [25:0] _1Bus, _2Bus, _3Bus, _4Bus, _5Bus, mainScrT;
  wire [25:6] textBus;

  Register register_1 (.D(p_x_y), .Q(INVENTORY1), .clk(INV1ch), .clr(or_1_out));  // open: en
  Register register_2 (.D(p_x_y), .Q(INVENTORY2), .clk(INV2ch), .clr(or_2_out));  // open: en
  Register register_3 (.D(p_x_y), .Q(INVENTORY3), .clk(INV3ch), .clr(or_3_out));  // open: en
  Register register_4 (.D(p_x_y), .Q(INVENTORY4), .clk(INV4ch), .clr(or_4_out));  // open: en
  Register register_5 (.D(p_x_y), .Q(INVENTORY5), .clk(INV5ch), .clr(or_5_out));  // open: en
  Pull_Resistor pull_resistor_1 (.node(pull_resistor_1_node));
  assign pull_resistor_1_node = _5onInp ? 3'b100 : 3'bz;  // Controlled_Buffer controlled_buffer_1
  or or_1 (or_1_out, mainRES, itemRES1);
  or or_2 (or_2_out, mainRES, itemRES2);
  or or_3 (or_3_out, mainRES, itemRES3);
  or or_4 (or_4_out, mainRES, itemRES4);
  or or_5 (or_5_out, mainRES, itemRES5);
  assign pull_resistor_1_node = _4onInp ? 3'b011 : 3'bz;  // Controlled_Buffer controlled_buffer_2
  Adder #(.width(1)) adder_1 (.a(register_6_q), .b(1'b1), .out(adder_1_out));  // open: cin, cout
  and and_1 (and_1_out, ATCinit, _1Bus[19]);
  quick quick_1 (.IN(ATCenMove), .OUT(quick_1_out));
  Random #(.width(1)) random_1 (.clk(quick_1_out), .out(random_1_out));  // open: next, clr
  Bit_Extender #(.out_width(6)) bit_extender_1 (.in(adder_2_out), .out(curEnDmg));
  quick quick_2 (.IN(mapPREst1), .OUT(stMapCLC1));
  assign MAP_tospace_ELEM = mapPREst1 ? p_x_y__elemOnMap : 12'bz;  // Controlled_Buffer controlled_buffer_3
  Multiplexer #(.select(3), .width(8), .enable("false")) multiplexer_1 (
    .in0(INVENTORY1p), .in1(INVENTORY2p), .in2(INVENTORY3p), .in3(INVENTORY4p), .in4(INVENTORY5p),
    .in5({8{1'b0}}), .in6({8{1'b0}}), .in7({8{1'b0}}), .out(multiplexer_1_out), .sel(pull_resistor_1_node));
  assign pull_resistor_1_node = _2onInp ? 3'b001 : 3'bz;  // Controlled_Buffer controlled_buffer_4
  assign pull_resistor_1_node = _3onInp ? 3'b010 : 3'bz;  // Controlled_Buffer controlled_buffer_5
  Register #(.width(1)) register_6 (.D(adder_1_out), .Q(register_6_q), .clk(and_1_out), .clr(ATCnewENclc));  // open: en
  Comparator #(.width(1)) comparator_1 (.a(register_6_q), .b(1'b1), .eq(comparator_1_eq));  // open: gt, lt
  enemies enemies_1 (.ADDR(ATCcurEN), .HP(enemies_1_hp), .DMG(ENDMGst));  // open: ELEMIm, ELEMNm, Img, Txt
  assign bit_extender_2_out = {{7{1'b0}}, random_1_out};  // Bit_Extender bit_extender_2
  Adder adder_2 (.a(bit_extender_2_out), .b(ENDMG), .out(adder_2_out));  // open: cin, cout
  quick quick_3 (.IN(ATCplAttaked1), .OUT(quick_3_out));
  Comparator #(.mode("unsigned")) comparator_2 (.a(ENHP), .b({8{1'b0}}), .eq(comparator_2_eq));  // open: gt, lt
  Comparator #(.mode("unsigned")) comparator_3 (.a(ENHP), .b(8'h32), .gt(comparator_3_gt));  // open: eq, lt
  Comparator comparator_4 (.a(INVENTORY1p), .b(8'h65), .lt(comparator_4_lt));  // open: gt, eq
  and and_2 (and_2_out, comparator_4_lt, _1onInpff, comparator_5_gt);
  Comparator comparator_5 (.a(INVENTORY1p), .b(8'h60), .gt(comparator_5_gt));  // open: eq, lt
  Comparator comparator_6 (.a(INVENTORY2p), .b(8'h65), .lt(comparator_6_lt));  // open: gt, eq
  and and_3 (and_3_out, comparator_6_lt, _2onInpff, comparator_7_gt);
  Comparator comparator_7 (.a(INVENTORY2p), .b(8'h60), .gt(comparator_7_gt));  // open: eq, lt
  Comparator comparator_8 (.a(INVENTORY3p), .b(8'h65), .lt(comparator_8_lt));  // open: gt, eq
  and and_4 (and_4_out, comparator_8_lt, _3onInpff, comparator_9_gt);
  Comparator comparator_9 (.a(INVENTORY3p), .b(8'h60), .gt(comparator_9_gt));  // open: eq, lt
  Comparator comparator_10 (.a(INVENTORY4p), .b(8'h65), .lt(comparator_10_lt));  // open: gt, eq
  and and_5 (and_5_out, comparator_10_lt, _4onInpff, comparator_11_gt);
  Comparator comparator_11 (.a(INVENTORY4p), .b(8'h60), .gt(comparator_11_gt));  // open: eq, lt
  Comparator comparator_12 (.a(INVENTORY5p), .b(8'h65), .lt(comparator_12_lt));  // open: gt, eq
  and and_6 (and_6_out, comparator_12_lt, _5onInpff, comparator_13_gt);
  Comparator comparator_13 (.a(INVENTORY5p), .b(8'h60), .gt(comparator_13_gt));  // open: eq, lt
  food food_1 (.FOOD(multiplexer_1_out), .GIVEHP(food_1_givehp));  // open: ES
  assign pull_resistor_1_node = _1onInp ? 3'b000 : 3'bz;  // Controlled_Buffer controlled_buffer_6
  Pull_Resistor pull_resistor_2 (.node(ATCinit));
  assign ATCinit = not_1_out ? not_1_out : 1'bz;  // Controlled_Buffer controlled_buffer_7
  not not_1 (not_1_out, comparator_1_eq);
  assign ENHPst = not_1_out ? enemies_1_hp : 8'bz;  // Controlled_Buffer controlled_buffer_8
  quick quick_4 (.IN(ATCenMoved), .OUT(newtEnDmg));
  assign NewPlayerHP = ATCenMoved ? subtractor_1_out : 8'bz;  // Controlled_Buffer controlled_buffer_9
  Subtractor subtractor_1 (.a(playerHPCUR), .b(adder_2_out), .out(subtractor_1_out));  // open: bin, bout
  assign PLAYERHPCH = ATCenMoved ? 1'b1 : 1'bz;  // Controlled_Buffer controlled_buffer_10
  not not_2 (not_2_out, ATCenMoved);
  Register #(.width(1)) register_7 (.D(not_2_out), .Q(ATCenMoved), .clk(quick_3_out), .clr(buffer_1_out));  // open: en
  buf buffer_1 (buffer_1_out, PLAYERHPCH);
  Pull_Resistor pull_resistor_3 (.node(buffer_1_out));
  or or_6 (or_6_out, comparator_2_eq, comparator_3_gt);
  pickUpAnItem pickupanitem_1 (
    .p_x_y(p_x_y), ._1oninp(_1onInpff), ._2oninp(_2onInpff), ._3oninp(_3onInpff), ._4oninp(_4onInpff),
    ._5oninp(_5onInpff), .MOVEinited(MOVEinited), .INV1ch(INV1ch), .INV2ch(INV2ch), .INV3ch(INV3ch),
    .INV4ch(INV4ch), .INV5ch(INV5ch), .chMap(mapPREst1));  // open: ITEMinCELL, InpFl1
  Register register_8 (.D(INVENTORY1), .Q(INVENTORY1p), .clk(invchn));  // open: en, clr
  Register register_9 (.D(INVENTORY2), .Q(INVENTORY2p), .clk(invchn));  // open: en, clr
  Register register_10 (.D(INVENTORY3), .Q(INVENTORY3p), .clk(invchn));  // open: en, clr
  Register register_11 (.D(INVENTORY4), .Q(INVENTORY4p), .clk(invchn));  // open: en, clr
  Register register_12 (.D(INVENTORY5), .Q(INVENTORY5p), .clk(invchn));  // open: en, clr
  and and_7 (and_7_out, EATflare, and_2_out);
  and and_8 (and_8_out, EATflare, and_3_out);
  and and_9 (and_9_out, EATflare, and_4_out);
  and and_10 (and_10_out, EATflare, and_5_out);
  Adder adder_3 (.a(food_1_givehp), .b(playerHPCUR), .out(adder_3_out));  // open: cin, cout
  Pull_Resistor pull_resistor_4 (.node(adder_3_out));
  Comparator comparator_14 (.a(adder_3_out), .b(8'h32), .gt(comparator_14_gt), .eq(comparator_14_eq));  // open: lt
  quick quick_5 (.IN(and_11_out), .OUT(quick_5_out));
  assign StateCh = quick_5_out ? quick_5_out : 1'bz;  // Controlled_Buffer controlled_buffer_11
  and and_11 (and_11_out, ATCplAttaked1, or_6_out);
  assign newText = quick_5_out ? quick_5_out : 1'bz;  // Controlled_Buffer controlled_buffer_12
  quick quick_6 (.IN(and_7_out), .OUT(itemRES1));
  quick quick_7 (.IN(and_8_out), .OUT(itemRES2));
  quick quick_8 (.IN(and_9_out), .OUT(itemRES3));
  quick quick_9 (.IN(and_10_out), .OUT(itemRES4));
  or or_7 (CHHPinmove, and_6_out, and_5_out, and_4_out, and_3_out, and_2_out);
  Multiplexer #(.width(8), .enable("false")) multiplexer_2 (
    .in0(adder_3_out), .in1(8'h32), .out(multiplexer_2_out), .sel(or_8_out));
  assign NewPlayerHP = and_12_out ? multiplexer_2_out : 8'bz;  // Controlled_Buffer controlled_buffer_13
  assign PLAYERHPCH = and_12_out ? 1'b1 : 1'bz;  // Controlled_Buffer controlled_buffer_14
  or or_8 (or_8_out, comparator_14_gt, comparator_14_eq);
  and and_12 (and_12_out, EATflare, ~ATCenMoved, CHHPinmove);  // AND_Gate
  assign TextText = quick_5_out ? 5'b10101 : 5'bz;  // Controlled_Buffer controlled_buffer_15
  quick quick_10 (.IN(and_13_out), .OUT(itemRES5));
  and and_13 (and_13_out, EATflare, and_6_out);
  or or_9 (EATflare, MOVEinited, ATCInpFlpre);
  Pull_Resistor pull_resistor_5 (.node(pull_resistor_5_node));
  assign pull_resistor_5_node = _5onInp ? 3'b101 : 3'bz;  // Controlled_Buffer controlled_buffer_16
  or or_10 (or_10_out, comparator_15_gt, comparator_15_eq);
  Comparator #(.mode("unsigned")) comparator_15 (
    .a(playerHPCUR), .b(8'h32), .gt(comparator_15_gt), .eq(comparator_15_eq));  // open: lt
  or or_11 (or_11_out, InpFlpreM, MoveFl, InpFlpreC);
  assign pull_resistor_5_node = _3onInp ? 3'b011 : 3'bz;  // Controlled_Buffer controlled_buffer_17
  assign pull_resistor_5_node = _4onInp ? 3'b100 : 3'bz;  // Controlled_Buffer controlled_buffer_18
  quick quick_11 (.IN(or_10_out), .OUT(quick_11_out));
  and and_14 (PlayerDeathRes, quick_11_out, gS2);
  Register #(.width(6)) register_13 (.D(curPlDmg), .Q(lstPlDmg), .clk(nwetPlDmg));  // open: en, clr
  assign MAP_tospace_ELEM = moveinitialization_1_workwithmap ? moveinitialization_1_where : 12'bz;  // Controlled_Buffer controlled_buffer_19
  quick quick_12 (.IN(ATCinisW), .OUT(quick_12_out));
  weapon weapon_1 (.WEAPON(multiplexer_3_out), .DMG(weapon_1_dmg), .GenRnd(quick_12_out), .nW(weapon_1_nw));
  Multiplexer #(.select(3), .width(8), .enable("false")) multiplexer_3 (
    .in0({8{1'b1}}), .in1(INVENTORY1p), .in2(INVENTORY2p), .in3(INVENTORY3p), .in4(INVENTORY4p),
    .in5(INVENTORY5p), .out(multiplexer_3_out), .sel(pull_resistor_5_node));  // open: in6, in7
  assign pull_resistor_5_node = _2onInp ? 3'b010 : 3'bz;  // Controlled_Buffer controlled_buffer_20
  assign pull_resistor_5_node = _1onInp ? 3'b001 : 3'bz;  // Controlled_Buffer controlled_buffer_21
  Register register_14 (.D(NewMapLevelCh), .Q(mapLevelCur), .clk(MapLevelCh), .clr(mainRES));  // open: en
  Register register_15 (.D(NewPlayerHP), .Q(playerHPCUR), .clk(pull_resistor_6_node), .clr(mainRES));  // open: en
  Pull_Resistor pull_resistor_6 (.node(pull_resistor_6_node));
  buf buffer_2 (pull_resistor_6_node, PLAYERHPCH);
  Register #(.width(2)) register_16 (.D(ATCnewEN), .Q(ATCcurEN), .clk(ATCnewENclc), .clr(mainRES));  // open: en
  Register #(.width(6)) register_17 (.D(curEnDmg), .Q(lstEnDmg), .clk(newtEnDmg));  // open: en, clr
  and and_15 (and_15_out, MOVEinited, WonInpff);
  or or_12 (or_12_out, _1onInp, _2onInp, _3onInp, _4onInp, _5onInp);
  moveInitialization moveinitialization_1 (
    .InpFlare(or_11_out), .MainCLC(_1Bus[19]), .mapW(MapW), .y(PLyOM), .x(PLxOM), .p_x_y(p_x_y),
    .p_x_y_1(p_x_y_1_t), .p_x_y_1_2(p_x_y_1), .p_x_1_y(p_x_1_y_t), .p_x_1_y_2(p_x_1_y), .p_x_2_y(p_x_2_y),
    .p_x_2_y_2(p_x_2_y_t), .p_x_y_2(p_x_y_2), .p_x_y_2_2(p__y_2), .MoveInited(MOVEinited),
    .where(moveinitialization_1_where), .objMap(objectONmap), .workWithMap(moveinitialization_1_workwithmap),
    .x_y_elonmap(p_x_y__elemOnMap), .x_y_1_elonmap_2(p_x_y_1__elemOnMap_t),
    .x_y_1_elonmap(p_x_y_1__elemOnMap), .x_1_y_elonmap_2(p_x_1_y__elemOnMap_t),
    .x_1_y_elonmap(p_x_1_y__elemOnMap));
  Lquick lquick_1 (.IN(and_16_out), .OUT(lquick_1_out), .CLC(_1Bus[19]));
  and and_16 (and_16_out, gS2, or_12_out);
  and and_17 (and_17_out, and_16_out, weapon_1_nw);
  Subtractor subtractor_2 (.a(ENHP), .b(weapon_1_dmg), .out(subtractor_2_out));  // open: bin, bout
  Bit_Extender #(.out_width(6)) bit_extender_3 (.in(weapon_1_dmg), .out(curPlDmg));
  weaponSelected weaponselected_1 (
    .weaponSelected(weaponselected_1_weaponselected), .INVENTORY1p(INVENTORY1p), ._1oninp(_1onInpff),
    .INVENTORY2p(INVENTORY2p), ._2oninp(_2onInpff), ._3oninp(_3onInpff), .INVENTORY3p(INVENTORY3p),
    ._4oninp(_4onInpff), ._5oninp(_5onInpff), .INVENTORY4p(INVENTORY4p), .INVENTORY5p(INVENTORY5p));
  buf buffer_3 (buffer_3_out, StateCh);
  Pull_Resistor pull_resistor_7 (.node(buffer_3_out));
  Register register_18 (.D(ENDMGst), .Q(ENDMG), .clk(ATCinit), .clr(mainRES));  // open: en
  Register register_19 (.D(ENHPst), .Q(ENHP), .clk(or_13_out), .clr(mainRES));  // open: en
  or or_13 (or_13_out, ATCcorrectINP, ATCinit);
  doForwardStep doforwardstep_1 (
    .PlDir(PlDir), .NewPLyOM(NewPLyOM), .changePCy(changePCy), .NewPLxOM(NewPLxOM), .changePCx(changePCx),
    .WonInp(and_15_out), .p_x_1_y(p_x_1_y_t), .p_x_1_y_2(p_x_1_y), .p_x_y_1(p_x_y_1), .p_x_y_1_2(p_x_y_1_t),
    .plX(PLxOM), .plY(PLyOM), .moved(MoveFl));
  and and_18 (ATCcorrectINP, and_16_out, ~lquick_1_out);  // AND_Gate
  not not_3 (not_3_out, and_17_out);
  not not_4 (not_4_out, not_3_out);
  not not_5 (not_5_out, not_4_out);
  assign ENHPst = and_17_out ? subtractor_2_out : 8'bz;  // Controlled_Buffer controlled_buffer_22
  quick quick_13 (.IN(and_17_out), .OUT(nwetPlDmg));
  and and_19 (ATCinisW, ATCInpFlpre, weaponselected_1_weaponselected);
  Register #(.width(2)) register_20 (.D(gSto), .Q(gameState), .clk(buffer_3_out), .clr(mainRES));  // open: en
  Register #(.width(2)) register_21 (.D(NewPlDir), .Q(PlDir), .clk(PlDirCh), .clr(mainRES));  // open: en
  not not_6 (ATCplAttaked1, not_5_out);
  printText printtext_1 (
    .Input({mainScrT[25:20], _1Bus[19], 7'b1000111, mainScrT[11:0]}), .pTclc(printtext_1_ptclc),
    .char(printtext_1_char), .ptd(printtext_1_ptd), .res(printtext_1_res));
  TTY #(.rows(2), .cols(44)) tty_1 (
    .data(printtext_1_char), .clk(printtext_1_ptclc), .we(printtext_1_ptd), .clr(printtext_1_res));
  DotMatrix #(.inputtype("row"), .matrixcols(32), .matrixrows(17)) dotmatrix_1 ();  // open: row0, row1, row2, row3, row4, row5, row6, row7, row8, row9, row10, row11, row12, row13, row14, row15, row16
  printText printtext_2 (
    .Input({textBus[25:20], _1Bus[19], 7'b1000010, textBus[11:6], lstEnDmg}), .pTclc(printtext_2_ptclc),
    .char(printtext_2_char), .ptd(printtext_2_ptd), .res(printtext_2_res));
  TTY #(.rows(1), .cols(66)) tty_2 (
    .data(printtext_2_char), .clk(printtext_2_ptclc), .we(printtext_2_ptd), .clr(printtext_2_res));
  DotMatrix #(.inputtype("row"), .matrixcols(9), .matrixrows(9)) dotmatrix_2 (
    .row0(printitem_1_str8), .row1(printitem_1_str4), .row2(printitem_1_str7), .row3(printitem_1_str3),
    .row4(printitem_1_str6), .row5(printitem_1_str2), .row6(printitem_1_str9), .row7(printitem_1_str5),
    .row8(printitem_1_str1));
  printItem printitem_1 (
    .item(INVENTORY1), .str1(printitem_1_str1), .str5(printitem_1_str5), .str9(printitem_1_str9),
    .str2(printitem_1_str2), .str6(printitem_1_str6), .str3(printitem_1_str3), .str7(printitem_1_str7),
    .str4(printitem_1_str4), .str8(printitem_1_str8));
  printText printtext_3 (
    .Input({_1Bus[25:19], 7'b0001101, _1Bus[11:0]}), .pTclc(printtext_3_ptclc), .char(printtext_3_char),
    .ptd(printtext_3_ptd), .res(printtext_3_res));
  TTY #(.rows(1), .cols(13)) tty_3 (
    .data(printtext_3_char), .clk(printtext_3_ptclc), .we(printtext_3_ptd), .clr(printtext_3_res));
  DotMatrix #(.inputtype("row"), .matrixcols(22), .matrixrows(17)) dotmatrix_3 ();  // open: row0, row1, row2, row3, row4, row5, row6, row7, row8, row9, row10, row11, row12, row13, row14, row15, row16
  DotMatrix #(.inputtype("row"), .matrixcols(12), .matrixrows(17)) dotmatrix_4 ();  // open: row0, row1, row2, row3, row4, row5, row6, row7, row8, row9, row10, row11, row12, row13, row14, row15, row16
  DotMatrix #(.inputtype("row"), .matrixcols(9), .matrixrows(9)) dotmatrix_5 (
    .row0(printitem_2_str8), .row1(printitem_2_str4), .row2(printitem_2_str7), .row3(printitem_2_str3),
    .row4(printitem_2_str6), .row5(printitem_2_str2), .row6(printitem_2_str9), .row7(printitem_2_str5),
    .row8(printitem_2_str1));
  printItem printitem_2 (
    .item(INVENTORY2), .str1(printitem_2_str1), .str5(printitem_2_str5), .str9(printitem_2_str9),
    .str2(printitem_2_str2), .str6(printitem_2_str6), .str3(printitem_2_str3), .str7(printitem_2_str7),
    .str4(printitem_2_str4), .str8(printitem_2_str8));
  printText printtext_4 (
    .Input({_2Bus[25:20], _1Bus[19], 7'b0001101, _2Bus[11:0]}), .pTclc(printtext_4_ptclc),
    .char(printtext_4_char), .ptd(printtext_4_ptd), .res(printtext_4_res));
  TTY #(.rows(1), .cols(13)) tty_4 (
    .data(printtext_4_char), .clk(printtext_4_ptclc), .we(printtext_4_ptd), .clr(printtext_4_res));
  Button _1 (.out(_1onInp));
  Comparator #(.width(2)) comparator_16 (.a(PlDir), .b(2'b00), .eq(comparator_16_eq));  // open: gt, lt
  Comparator #(.width(2)) comparator_17 (.a(PlDir), .b(2'b10), .eq(comparator_17_eq));  // open: gt, lt
  Comparator #(.width(2)) comparator_18 (.a(PlDir), .b(2'b01), .eq(comparator_18_eq));  // open: gt, lt
  Comparator #(.width(2)) comparator_19 (.a(PlDir), .b(2'b11), .eq(comparator_19_eq));  // open: gt, lt
  Multiplexer #(.width(12), .enable("false")) multiplexer_4 (
    .in0(MAP_tospace_ELEM), .in1(mapSTelemREAD), .out(multiplexer_4_out), .sel(not_7_out));
  Adder #(.width(12)) adder_4 (.a(mapSTelemREAD), .b(12'h1), .out(adder_4_out));  // open: cin, cout
  Register #(.width(12)) register_22 (.D(adder_4_out), .Q(mapSTelemREAD), .clk(and_20_out), .clr(mainRES));  // open: en
  and and_20 (and_20_out, not_7_out, _1Bus[19]);
  DotMatrix #(.inputtype("row"), .matrixcols(4), .matrixrows(17)) dotmatrix_6 ();  // open: row0, row1, row2, row3, row4, row5, row6, row7, row8, row9, row10, row11, row12, row13, row14, row15, row16
  printText printtext_5 (
    .Input({_3Bus[25:20], _1Bus[19], 7'b0001101, _3Bus[11:0]}), .pTclc(printtext_5_ptclc),
    .char(printtext_5_char), .ptd(printtext_5_ptd), .res(printtext_5_res));
  TTY #(.rows(1), .cols(13)) tty_5 (
    .data(printtext_5_char), .clk(printtext_5_ptclc), .we(printtext_5_ptd), .clr(printtext_5_res));
  Button _2 (.out(_2onInp));
  Comparator comparator_20 (.a(p_x_y_1_t), .b(8'h30), .gt(comparator_20_gt));  // open: eq, lt
  Comparator comparator_21 (.a(p_x_y_1), .b(8'h30), .gt(comparator_21_gt));  // open: eq, lt
  Comparator comparator_22 (.a(p_x_1_y), .b(8'h30), .gt(comparator_22_gt));  // open: eq, lt
  Comparator comparator_23 (.a(p_x_1_y_t), .b(8'h30), .gt(comparator_23_gt));  // open: eq, lt
  quick quick_14 (.IN(stMapCLC2), .OUT(quick_14_out));
  DotMatrix #(.inputtype("row"), .matrixcols(9), .matrixrows(9)) dotmatrix_7 (
    .row0(printitem_3_str8), .row1(printitem_3_str4), .row2(printitem_3_str7), .row3(printitem_3_str3),
    .row4(printitem_3_str6), .row5(printitem_3_str2), .row6(printitem_3_str9), .row7(printitem_3_str5),
    .row8(printitem_3_str1));
  printItem printitem_3 (
    .item(INVENTORY3), .str1(printitem_3_str1), .str5(printitem_3_str5), .str9(printitem_3_str9),
    .str2(printitem_3_str2), .str6(printitem_3_str6), .str3(printitem_3_str3), .str7(printitem_3_str7),
    .str4(printitem_3_str4), .str8(printitem_3_str8));
  Button _3 (.out(_3onInp));
  Button W (.out(WonInp));
  Button D (.out(DonInp));
  Button A (.out(AonInp));
  Comparator comparator_24 (.a(p_x_y_1_t), .b(8'h35), .lt(comparator_24_lt));  // open: gt, eq
  Comparator comparator_25 (.a(p_x_y_1), .b(8'h35), .lt(comparator_25_lt));  // open: gt, eq
  Comparator comparator_26 (.a(p_x_1_y), .b(8'h35), .lt(comparator_26_lt));  // open: gt, eq
  Comparator comparator_27 (.a(p_x_1_y_t), .b(8'h35), .lt(comparator_27_lt));  // open: gt, eq
  Multiplexer #(.width(8), .enable("false")) multiplexer_5 (
    .in0(8'h20), .in1(mapSTDATAreaded), .out(multiplexer_5_out), .sel(not_7_out));
  not not_7 (not_7_out, comparator_28_eq);
  Comparator #(.width(12)) comparator_28 (.a(mapSTelemREAD), .b(12'h94), .eq(comparator_28_eq));  // open: gt, lt
  or or_14 (stMapCLC, and_20_out, stMapCLC1, quick_14_out);
  printText printtext_6 (
    .Input({miniMScrT, miniScrT[20], _1Bus[19], 7'b0010101, miniScrT[11:0]}), .pTclc(printtext_6_ptclc),
    .char(printtext_6_char), .ptd(printtext_6_ptd), .res(printtext_6_res));
  TTY #(.rows(1), .cols(21)) tty_6 (
    .data(printtext_6_char), .clk(printtext_6_ptclc), .we(printtext_6_ptd), .clr(printtext_6_res));
  DotMatrix #(.inputtype("row"), .matrixcols(16), .matrixrows(16)) dotmatrix_8 ();  // open: row0, row1, row2, row3, row4, row5, row6, row7, row8, row9, row10, row11, row12, row13, row14, row15
  DotMatrix #(.inputtype("row"), .matrixcols(14), .matrixrows(14)) dotmatrix_9 ();  // open: row0, row1, row2, row3, row4, row5, row6, row7, row8, row9, row10, row11, row12, row13
  DotMatrix #(.inputtype("row"), .matrixcols(9), .matrixrows(9)) dotmatrix_10 (
    .row0(printitem_4_str8), .row1(printitem_4_str4), .row2(printitem_4_str7), .row3(printitem_4_str3),
    .row4(printitem_4_str6), .row5(printitem_4_str2), .row6(printitem_4_str9), .row7(printitem_4_str5),
    .row8(printitem_4_str1));
  printItem printitem_4 (
    .item(INVENTORY4), .str1(printitem_4_str1), .str5(printitem_4_str5), .str9(printitem_4_str9),
    .str2(printitem_4_str2), .str6(printitem_4_str6), .str3(printitem_4_str3), .str7(printitem_4_str7),
    .str4(printitem_4_str4), .str8(printitem_4_str8));
  printText printtext_7 (
    .Input({_4Bus[25:20], _1Bus[19], 7'b0001101, _4Bus[11:0]}), .pTclc(printtext_7_ptclc),
    .char(printtext_7_char), .ptd(printtext_7_ptd), .res(printtext_7_res));
  TTY #(.rows(1), .cols(13)) tty_7 (
    .data(printtext_7_char), .clk(printtext_7_ptclc), .we(printtext_7_ptd), .clr(printtext_7_res));
  Button _4 (.out(_4onInp));
  Button Q (.out(Q_out));
  not not_8 (not_8_out, not_9_out);
  not not_9 (not_9_out, or_15_out);
  or or_15 (or_15_out, AonInp, DonInp);
  or or_16 (invchn, _1onInp, _2onInp, _3onInp, _4onInp, _5onInp, AonInp, DonInp, WonInp);
  Subtractor subtractor_3 (.a(p_x_y_1_t), .b(8'h31), .out(subtractor_3_out));  // open: bin, bout
  Subtractor subtractor_4 (.a(p_x_1_y_t), .b(8'h31), .out(subtractor_4_out));  // open: bin, bout
  DotMatrix #(.inputtype("row"), .matrixcols(2), .matrixrows(2)) dotmatrix_11 (.row0(2'b11), .row1(2'b11));
  DotMatrix #(.inputtype("row"), .matrixcols(9), .matrixrows(9)) dotmatrix_12 (
    .row0(printitem_5_str8), .row1(printitem_5_str4), .row2(printitem_5_str7), .row3(printitem_5_str3),
    .row4(printitem_5_str6), .row5(printitem_5_str2), .row6(printitem_5_str9), .row7(printitem_5_str5),
    .row8(printitem_5_str1));
  printItem printitem_5 (
    .item(INVENTORY5), .str1(printitem_5_str1), .str5(printitem_5_str5), .str9(printitem_5_str9),
    .str2(printitem_5_str2), .str6(printitem_5_str6), .str3(printitem_5_str3), .str7(printitem_5_str7),
    .str4(printitem_5_str4), .str8(printitem_5_str8));
  printText printtext_8 (
    .Input({_5Bus[25:20], _1Bus[19], 7'b0001101, _5Bus[11:0]}), .pTclc(printtext_8_ptclc),
    .char(printtext_8_char), .ptd(printtext_8_ptd), .res(printtext_8_res));
  TTY #(.rows(1), .cols(13)) tty_8 (
    .data(printtext_8_char), .clk(printtext_8_ptclc), .we(printtext_8_ptd), .clr(printtext_8_res));
  quick quick_15 (.IN(Q_out), .OUT(qres));
  Adder #(.width(2)) adder_5 (.a(PlDir), .b(2'b01), .out(adder_5_out));  // open: cin, cout
  Multiplexer #(.width(2), .enable("false")) multiplexer_6 (
    .in0(adder_5_out), .in1(subtractor_5_out), .out(NewPlDir), .sel(AonInp));
  Subtractor #(.width(2)) subtractor_5 (.a(PlDir), .b(2'b01), .out(subtractor_5_out));  // open: bin, bout
  and and_21 (and_21_out, MOVEinited, not_8_out);
  assign InpFl1 = and_21_out ? and_21_out : 1'bz;  // Controlled_Buffer controlled_buffer_23
  quick quick_16 (.IN(not_8_out), .OUT(PlDirCh));
  Pull_Resistor pull_resistor_8 (.node(StateCh));
  or or_17 (or_17_out, StateCh, quick_17_out);
  quick quick_17 (.IN(invchn), .OUT(quick_17_out));
  quick quick_18 (.IN(invchn), .OUT(keyPress));
  not not_10 (not_10_out, or_17_out);
  assign MAP_tospace_ELEM = and_22_out ? p_x_y_1__elemOnMap_t : 12'bz;  // Controlled_Buffer controlled_buffer_24
  Bit_Extender #(.out_width(2)) bit_extender_4 (.in(subtractor_3_out), .out(bit_extender_4_out));
  assign ATCnewEN = and_22_out ? bit_extender_4_out : 2'bz;  // Controlled_Buffer controlled_buffer_25
  and and_22 (and_22_out, comparator_20_gt, comparator_24_lt, comparator_16_eq);
  and and_23 (and_23_out, comparator_21_gt, comparator_25_lt, comparator_17_eq);
  and and_24 (and_24_out, comparator_22_gt, comparator_26_lt, comparator_18_eq);
  and and_25 (and_25_out, comparator_23_gt, comparator_27_lt, comparator_19_eq);
  assign ATCnewEN = and_25_out ? bit_extender_5_out : 2'bz;  // Controlled_Buffer controlled_buffer_26
  Bit_Extender #(.out_width(2)) bit_extender_5 (.in(subtractor_4_out), .out(bit_extender_5_out));
  assign MAP_tospace_ELEM = and_25_out ? p_x_1_y__elemOnMap_t : 12'bz;  // Controlled_Buffer controlled_buffer_27
  RAM #(.addrWidth(12), .bus("separate")) ram_1 (
    .addr(multiplexer_4_out), .din(multiplexer_5_out), .data(objectONmap), .str(mapPREst), .clk(stMapCLC));  // open: sel, ld, clr
  or or_18 (mapPREst, not_7_out, ATCnewENclc, mapPREst1);
  Button _5 (.out(_5onInp));
  Register #(.width(1)) register_23 (.D(WonInp), .Q(WonInpff), .clk(not_12_out), .clr(or_19_out));  // open: en
  or or_19 (or_19_out, or_17_out, MoveFl);
  not not_11 (not_11_out, not_13_out);
  not not_12 (not_12_out, not_11_out);
  not not_13 (not_13_out, not_14_out);
  not not_14 (not_14_out, or_17_out);
  Register #(.width(1)) register_24 (.D(_3onInp), .Q(_3onInpff), .clk(not_15_out), .clr(or_17_out));  // open: en
  not not_15 (not_15_out, not_10_out);
  Subtractor subtractor_6 (.a(p_x_y_1), .b(8'h31), .out(subtractor_6_out));  // open: bin, bout
  buf and_26 (ATCnewENclc, buffer_4_out);  // AND_Gate
  buf buffer_4 (buffer_4_out, MOVEenHERE);
  or or_20 (MOVEenHERE, and_22_out, and_23_out, and_24_out, and_25_out);
  Subtractor subtractor_7 (.a(p_x_1_y), .b(8'h31), .out(subtractor_7_out));  // open: bin, bout
  and and_27 (_1Bus[19], ~mainRES, clock_1_out);  // AND_Gate
  Clock clock_1 (.out(clock_1_out));
  or or_21 (mainRES, PlayerDeathRes, qres);
  Hex_Digit_Display hex_digit_display_1 (.value(printhp_1_low));  // open: dp
  Hex_Digit_Display hex_digit_display_2 (.value(printhp_1_high));  // open: dp
  printHP printhp_1 (.Inp(ENHP), .High(printhp_1_high), .Low(printhp_1_low), .print(gS2));
  Hex_Digit_Display hex_digit_display_3 (.value(printhp_2_high));  // open: dp
  Hex_Digit_Display hex_digit_display_4 (.value(printhp_2_low));  // open: dp
  not not_16 (not_16_out, gS0);
  printHP printhp_2 (.Inp(playerHPCUR), .High(printhp_2_high), .Low(printhp_2_low), .print(not_16_out));
  not not_17 (not_17_out, or_17_out);
  not not_18 (not_18_out, or_17_out);
  assign MAP_tospace_ELEM = and_23_out ? p_x_y_1__elemOnMap : 12'bz;  // Controlled_Buffer controlled_buffer_28
  assign ATCnewEN = and_23_out ? bit_extender_6_out : 2'bz;  // Controlled_Buffer controlled_buffer_29
  Bit_Extender #(.out_width(2)) bit_extender_6 (.in(subtractor_6_out), .out(bit_extender_6_out));
  not not_19 (not_19_out, not_21_out);
  not not_20 (not_20_out, ATCnewENclc);
  not not_21 (not_21_out, not_20_out);
  quick quick_19 (.IN(ATCnewENclc), .OUT(quick_19_out));
  assign StateCh = quick_19_out ? quick_19_out : 1'bz;  // Controlled_Buffer controlled_buffer_30
  assign newText = quick_19_out ? quick_19_out : 1'bz;  // Controlled_Buffer controlled_buffer_31
  assign ATCnewEN = and_24_out ? bit_extender_7_out : 2'bz;  // Controlled_Buffer controlled_buffer_32
  Bit_Extender #(.out_width(2)) bit_extender_7 (.in(subtractor_7_out), .out(bit_extender_7_out));
  assign MAP_tospace_ELEM = and_24_out ? p_x_1_y__elemOnMap : 12'bz;  // Controlled_Buffer controlled_buffer_33
  Register #(.width(1)) register_25 (.D(_1onInp), .Q(_1onInpff), .clk(not_22_out), .clr(or_17_out));  // open: en
  not not_22 (not_22_out, not_17_out);
  Register #(.width(1)) register_26 (.D(_2onInp), .Q(_2onInpff), .clk(not_23_out), .clr(or_17_out));  // open: en
  not not_23 (not_23_out, not_18_out);
  not not_24 (not_24_out, not_19_out);
  not not_25 (not_25_out, lquick_2_out);
  Lquick lquick_2 (.IN(not_24_out), .OUT(lquick_2_out), .CLC(_1Bus[19]));
  Demultiplexer #(.select(2), .enable("false")) demultiplexer_1 (
    .out0(demultiplexer_1_out0), .out1(demultiplexer_1_out1), .out2(demultiplexer_1_out2),
    .out3(demultiplexer_1_out3), .in(1'b1), .sel(PlDir));
  LED led_1 (.in(demultiplexer_1_out3));
  LED led_2 (.in(demultiplexer_1_out3));
  quick quick_20 (.IN(invchn), .OUT(quick_20_out));
  Demultiplexer #(.select(2), .disabled(0), .enable("false")) demultiplexer_2 (
    .out1(InpFlpreC), .in(quick_20_out), .sel(gameState));  // open: out0, out2, out3
  Demultiplexer #(.select(2), .disabled(0), .enable("false")) demultiplexer_3 (
    .out0(InpFlpreSTRT), .out2(ATCInpFlpre), .in(invchn), .sel(gameState));  // open: out1, out3
  not not_26 (not_26_out, not_27_out);
  not not_27 (not_27_out, or_17_out);
  not not_28 (not_28_out, or_17_out);
  not not_29 (not_29_out, not_28_out);
  quick quick_21 (.IN(not_25_out), .OUT(InpFlpreM));
  and and_28 (stMapCLC2, not_25_out, ATCnewENclc);
  assign TextText = quick_19_out ? 5'b10111 : 5'bz;  // Controlled_Buffer controlled_buffer_34
  Multiplexer #(.width(8), .enable("false")) multiplexer_7 (
    .in0(NewPLxOM), .in1(maps_1_xpp), .out(multiplexer_7_out), .sel(gS0));
  or or_22 (or_22_out, changePCx, LoadMap);
  Register #(.width(12)) u_mapW (.D(maps_1_width), .Q(MapW), .clk(LoadMap), .clr(mainRES));  // open: en
  LED led_3 (.in(demultiplexer_1_out0));
  LED led_4 (.in(demultiplexer_1_out0));
  LED led_5 (.in(demultiplexer_1_out1));
  LED led_6 (.in(demultiplexer_1_out1));
  LED led_7 (.in(demultiplexer_1_out2));
  LED led_8 (.in(demultiplexer_1_out2));
  LED led_9 (.in(demultiplexer_4_out0));
  LED led_10 (.in(demultiplexer_4_out1));
  LED led_11 (.in(demultiplexer_4_out2));
  Register #(.width(1)) register_27 (.D(_4onInp), .Q(_4onInpff), .clk(not_26_out), .clr(or_17_out));  // open: en
  Register #(.width(1)) register_28 (.D(_5onInp), .Q(_5onInpff), .clk(not_29_out), .clr(or_17_out));  // open: en
  Register Xpp (.D(multiplexer_7_out), .Q(PLxOM), .clk(or_22_out));  // open: en, clr
  Comparator #(.width(2)) comparator_29 (.a(2'b00), .b(gameState), .eq(gS0));  // open: gt, lt
  Comparator #(.width(2)) comparator_30 (.a(2'b01), .b(gameState), .eq(gS1));  // open: gt, lt
  Comparator #(.width(2)) comparator_31 (.a(2'b10), .b(gameState), .eq(gS2));  // open: gt, lt
  // Probe on PLxOM
  // Probe on PLyOM
  Demultiplexer #(.select(2), .enable("false")) demultiplexer_4 (
    .out0(demultiplexer_4_out0), .out1(demultiplexer_4_out1), .out2(demultiplexer_4_out2), .in(1'b1),
    .sel(gameState));  // open: out3
  Register #(.width(12)) u_mapH (.D(maps_1_height), .Q(MapH), .clk(LoadMap), .clr(mainRES));  // open: en
  assign NewPlayerHP = LoadMap ? 8'h32 : 8'bz;  // Controlled_Buffer controlled_buffer_35
  buf buffer_5 (LoadMap, and_29_out);
  and and_29 (and_29_out, InpFlpreSTRT, gS0);
  quick quick_22 (.IN(chGM), .OUT(quick_22_out));
  Register Ypp (.D(multiplexer_8_out), .Q(PLyOM), .clk(or_23_out));  // open: en, clr
  Multiplexer #(.width(8), .enable("false")) multiplexer_8 (
    .in0(NewPLyOM), .in1(maps_1_ypp), .out(multiplexer_8_out), .sel(gS0));
  or or_23 (or_23_out, changePCy, LoadMap);
  maps maps_1 (
    .ADDR(mapLevelCur), .ELEM(mapSTelemREAD), .DATA(mapSTDATAreaded), .Xpp(maps_1_xpp), .Ypp(maps_1_ypp),
    .Width(maps_1_width), .Height(maps_1_height));  // open: LEN
  or or_24 (or_24_out, and_29_out, quick_22_out);
  assign StateCh = or_24_out ? or_24_out : 1'bz;  // Controlled_Buffer controlled_buffer_36
  assign newText = or_24_out ? or_24_out : 1'bz;  // Controlled_Buffer controlled_buffer_37
  assign PLAYERHPCH = quick_23_out ? quick_23_out : 1'bz;  // Controlled_Buffer controlled_buffer_38
  quick quick_23 (.IN(or_24_out), .OUT(quick_23_out));
  Multiplexer #(.select(2), .width(2), .enable("false")) multiplexer_9 (
    .in0(2'b01), .in1(2'b10), .in2(2'b01), .out(gSto), .sel({gS2, gS1}));  // open: in3
  Multiplexer #(.select(2), .width(8), .enable("false")) multiplexer_10 (
    .in0(8'h1f), .in1({8{1'b0}}), .in2(8'h1e), .out(gStdtScrMem), .sel({gS2, gS1}));  // open: in3
  Comparator comparator_32 (.a(p_x_y), .b(8'h20), .eq(comparator_32_eq));  // open: gt, lt
  not not_30 (not_30_out, comparator_32_eq);
  assign TextText = or_24_out ? 5'b11000 : 5'bz;  // Controlled_Buffer controlled_buffer_39
  assign newText = quick_24_out ? quick_24_out : 1'bz;  // Controlled_Buffer controlled_buffer_40
  quick quick_24 (.IN(and_30_out), .OUT(quick_24_out));
  and and_30 (and_30_out, MOVEinited, gS1);
  and and_31 (and_31_out, and_30_out, and_32_out);
  assign newText = and_31_out ? and_31_out : 1'bz;  // Controlled_Buffer controlled_buffer_41
  and and_32 (and_32_out, gS1, not_30_out);
  assign bit_extender_8_out = {{3{1'b0}}, ATCcurEN};  // Bit_Extender bit_extender_8
  assign TextText = and_31_out ? 5'b10110 : 5'bz;  // Controlled_Buffer controlled_buffer_42
  Adder #(.width(5)) adder_6 (.a(bit_extender_8_out), .b(5'b00110), .out(adder_6_out));  // open: cin, cout
  Subtractor subtractor_8 (.a(INVENTORY1), .b(8'h57), .out(subtractor_8_out));  // open: bin, bout
  Subtractor subtractor_9 (.a(INVENTORY3), .b(8'h57), .out(subtractor_9_out));  // open: bin, bout
  Subtractor subtractor_10 (.a(INVENTORY5), .b(8'h57), .out(subtractor_10_out));  // open: bin, bout
  Multiplexer #(.select(2), .width(5), .enable("false")) multiplexer_11 (
    .in0(5'b00001), .in1(5'b00010), .in2(5'b00011), .out(mainScrT[25:21]), .sel({gS2, gS1}));  // open: in3
  Multiplexer #(.select(2), .width(5), .enable("false")) multiplexer_12 (
    .in0({5{1'b0}}), .in1(5'b00100), .in2(adder_6_out), .out(miniMScrT), .sel({gS2, gS1}));  // open: in3
  Bit_Extender #(.out_width(5)) bit_extender_9 (.in(subtractor_8_out), .out(bit_extender_9_out));
  Comparator comparator_33 (.a(INVENTORY1), .b({8{1'b0}}), .eq(comparator_33_eq));  // open: gt, lt
  Bit_Extender #(.out_width(5)) bit_extender_10 (.in(subtractor_9_out), .out(bit_extender_10_out));
  Multiplexer #(.width(5), .enable("false")) multiplexer_13 (
    .in0(bit_extender_10_out), .in1({5{1'b0}}), .out(_3Bus[25:21]), .sel(comparator_34_eq));
  Comparator comparator_34 (.a(INVENTORY3), .b({8{1'b0}}), .eq(comparator_34_eq));  // open: gt, lt
  Bit_Extender #(.out_width(5)) bit_extender_11 (.in(subtractor_10_out), .out(bit_extender_11_out));
  Comparator comparator_35 (.a(INVENTORY5), .b({8{1'b0}}), .eq(comparator_35_eq));  // open: gt, lt
  or or_25 (_1Bus[20], INV1ch, itemRES1, mainRES);
  Multiplexer #(.width(5), .enable("false")) multiplexer_14 (
    .in0(bit_extender_9_out), .in1({5{1'b0}}), .out(_1Bus[25:21]), .sel(comparator_33_eq));
  or or_26 (_3Bus[20], INV3ch, itemRES3, mainRES);
  or or_27 (_5Bus[20], INV5ch, itemRES5, mainRES);
  Multiplexer #(.width(5), .enable("false")) multiplexer_15 (
    .in0(bit_extender_11_out), .in1({5{1'b0}}), .out(_5Bus[25:21]), .sel(comparator_35_eq));
  Subtractor subtractor_11 (.a(INVENTORY4), .b(8'h57), .out(subtractor_11_out));  // open: bin, bout
  or or_28 (_4Bus[20], INV4ch, itemRES4, mainRES);
  Bit_Extender #(.out_width(5)) bit_extender_12 (.in(subtractor_11_out), .out(bit_extender_12_out));
  Multiplexer #(.width(5), .enable("false")) multiplexer_16 (
    .in0(bit_extender_12_out), .in1({5{1'b0}}), .out(_4Bus[25:21]), .sel(comparator_36_eq));
  Comparator comparator_36 (.a(INVENTORY4), .b({8{1'b0}}), .eq(comparator_36_eq));  // open: gt, lt
  Subtractor subtractor_12 (.a(p_x_y), .b(8'h5d), .out(subtractor_12_out));  // open: bin, bout
  Comparator comparator_37 (.a(p_x_y), .b(8'h20), .eq(comparator_37_eq));  // open: gt, lt
  Pull_Resistor pull_resistor_9 (.node(pull_resistor_9_node));
  assign pull_resistor_9_node = TextText;  // Buffer buffer_6, 5 bits wide
  Register #(.width(5)) register_29 (
    .D(pull_resistor_9_node), .Q(register_29_q), .clk(pull_resistor_10_node), .clr(or_29_out));  // open: en
  Pull_Resistor pull_resistor_10 (.node(pull_resistor_10_node));
  buf buffer_7 (pull_resistor_10_node, newText);
  or or_29 (or_29_out, mainRES, stMapCLC1);
  buf buffer_8 (buffer_8_out, StateCh);
  Pull_Resistor pull_resistor_11 (.node(buffer_8_out));
  or or_30 (mainScrT[20], buffer_8_out, mainRES);
  buf buffer_9 (buffer_9_out, StateCh);
  Pull_Resistor pull_resistor_12 (.node(buffer_9_out));
  or or_31 (miniScrT[20], buffer_9_out, mainRES);
  Subtractor subtractor_13 (.a(INVENTORY2), .b(8'h57), .out(subtractor_13_out));  // open: bin, bout
  Bit_Extender #(.out_width(6)) bit_extender_13 (.in(subtractor_12_out), .out(bit_extender_13_out));
  Multiplexer #(.width(6), .enable("false")) multiplexer_17 (
    .in0(bit_extender_13_out), .in1({6{1'b1}}), .out(multiplexer_17_out), .sel(comparator_37_eq));
  Multiplexer #(.width(6), .enable("false")) multiplexer_18 (
    .in0(multiplexer_17_out), .in1(multiplexer_21_out), .out(textBus[11:6]), .sel(gS2));
  buf buffer_10 (buffer_10_out, newText);
  Pull_Resistor pull_resistor_13 (.node(buffer_10_out));
  or or_32 (textBus[20], buffer_10_out, buffer_11_out, mainRES);
  Multiplexer #(.width(5), .enable("false")) multiplexer_19 (
    .in0(register_29_q), .in1(5'b01110), .out(textBus[25:21]), .sel(gS0));
  or or_33 (_2Bus[20], INV2ch, itemRES2, mainRES);
  Bit_Extender #(.out_width(5)) bit_extender_14 (.in(subtractor_13_out), .out(bit_extender_14_out));
  Multiplexer #(.width(5), .enable("false")) multiplexer_20 (
    .in0(bit_extender_14_out), .in1({5{1'b0}}), .out(_2Bus[25:21]), .sel(comparator_38_eq));
  Comparator comparator_38 (.a(INVENTORY2), .b({8{1'b0}}), .eq(comparator_38_eq));  // open: gt, lt
  buf buffer_11 (buffer_11_out, StateCh);
  Pull_Resistor pull_resistor_14 (.node(buffer_11_out));
  Multiplexer #(.width(6), .enable("false")) multiplexer_21 (
    .in0(bit_extender_15_out), .in1(lstPlDmg), .out(multiplexer_21_out), .sel(and_33_out));
  assign bit_extender_15_out = {{4{1'b0}}, ATCcurEN};  // Bit_Extender bit_extender_15
  and and_33 (and_33_out, gS2, ~comparator_39_eq);  // AND_Gate
  Comparator #(.width(6)) comparator_39 (.a({6{1'b0}}), .b(lstEnDmg), .eq(comparator_39_eq));  // open: gt, lt

  // Other names for the same wires on the sheet: _2Bus[19] = _1Bus[19]; _3Bus[19] = _1Bus[19]; _4Bus[19] = _1Bus[19];
  //   _5Bus[19] = _1Bus[19]; mainClk = _1Bus[19]; mainScrT[19] = _1Bus[19];
  //   miniScrT (some bits) = {miniMScrT, _1Bus[19]}; textBus (some bits) = {_1Bus[19], lstEnDmg};
  //   ATCnEhp = ATCcorrectINP; mainScrText[4:0] = mainScrT[25:21]; mapPREst2 = ATCnewENclc; TextRes = stMapCLC1

  // Notes on the sheet:
  //   CURRENT STATE
  //   INVETORY
  //   INVENTORY REGISTERS
  //   BATTLE MODE
  //   ENEMY INIT
  //   EAT FOOD
  //   ENEMY ATTACK
  //   If PLAYER WON
  //   PREVIOUS STATE
  //   enemy attaked
  //   Не работает текст (и врядли будет)
  //   CHECK ENEMY WON
  //   last player damage
  //   PLAYER MOVEMENT
  //   Curent map level
  //   Player HP
  //   Current Enemy number
  //   last enemy damage
  //   SOME GLOBAL VARIBLES
  //   BATTLE MODE VARIBLES
  //   DO FORWARD STEP
  //   ATTACK THE ENEMY
  //   Game state
  //   0 - start screen 1 - walking 2 - battle
  //   Player Direction
  //   Current Enemy dmg
  //   Current Enemy hp
  //   no connect
  //   no connect
  //   GAME MAP
  //   MainText не запроганы чисел урона в атаке
  //   Memory access
  //   MAKE A TURN
  //   MEET ENEMY AND CHANGE GAME MODE TO BATTLE
  //   DEBUG TOOLS
  //   reset game
  //   PARSE INPUT
  //   turn were
  //   enemy HP
  //   no connect
  //   player HP
  //   START
  //   WALK
  //   BATTLE
  //   INITIALIZING GAME MAP
  //   GAME MODE CHANGER
  //   GAME INFORAMTION
  //   player direction
  //   pX
  //   pY
  //   PLAYER FIND ITEM
  //   TEXT SELECTORS
endmodule

// CP
module consoler (
  input  [7:0] MEM_D,
  input  CLK,
  input  [11:0] PRINT_SIZE,
  input  RESET,
  output IT_WORKED,
  output [7:0] INPUT_CHAR,
  output CONNECTED,
  output INPUT_were,
  output [11:0] MEM_A
);

  wire and_3_out, and_4_out, clc, comparator_1_eq, not_1_out, not_2_out, not_3_out, not_4_out, not_5_out,
       not_6_out, or_1_out, PRND, readConsole, register_2_q, RES, RESET_MEMORY_COUNTER_out, uart_1_p3,
       uart_1_p7;
  wire [7:0] uart_1_p1;
  wire [11:0] adder_1_out;

  and and_1 (IT_WORKED, not_3_out, PRND, INPUT_were);
  not not_1 (not_1_out, INPUT_were);
  Register #(.width(1)) register_1 (.D(not_1_out), .Q(INPUT_were), .clk(or_1_out));  // open: en, clr
  or or_1 (or_1_out, RES, uart_1_p3);
  and and_2 (clc, CLK, not_2_out);
  not not_2 (not_2_out, RES);
  not not_3 (not_3_out, uart_1_p3);
  not not_4 (not_4_out, RESET);
  and and_3 (and_3_out, clc, comparator_1_eq);
  Register #(.width(1)) register_2 (.D(RESET), .Q(register_2_q), .clk(RESET), .clr(not_5_out));  // open: en
  not not_5 (not_5_out, not_4_out);
  Register register_3 (.D(uart_1_p1), .Q(INPUT_CHAR), .clk(and_3_out), .clr(RES));  // open: en
  or or_2 (RES, register_2_q, RESET_MEMORY_COUNTER_out);
  Button RESET_MEMORY_COUNTER (.out(RESET_MEMORY_COUNTER_out));
  Comparator comparator_1 (.a(INPUT_CHAR), .b({8{1'b0}}), .eq(comparator_1_eq));  // open: gt, lt
  not not_6 (not_6_out, PRND);
  Register #(.width(12)) register_4 (.D(adder_1_out), .Q(MEM_A), .clk(and_4_out), .clr(RES));  // open: en
  not not_7 (readConsole, PRND);
  and and_4 (and_4_out, not_6_out, clc);
  // UART uart_1: pin names not known; wires that end beside it: uart_1_p1, MEM_D, uart_1_p3, clc, uart_1_p3, CONNECTED, uart_1_p7
  Adder #(.width(12)) adder_1 (.a(MEM_A), .b(12'h1), .out(adder_1_out));  // open: cin, cout
  or or_3 (uart_1_p7, uart_1_p3, readConsole);
  Comparator #(.width(12)) comparator_2 (.a(MEM_A), .b(PRINT_SIZE), .eq(PRND));  // open: gt, lt

  // Notes on the sheet:
  //   12 бит адрес
  //   Frame Printed
  //   Print Frame
  //   A - Адрес к каторому обращается
  //   B - элемент по адресу
endmodule

// GE
module graphic_elems (
  input  [7:0] ADDR,
  input  [11:0] ELEM,
  output [7:0] DATA,
  output [11:0] LEN
);

  wire [7:0] deMux1, geD0, geD1, geD2, geD2_0, geD2_1, geD3, geD4, geD5, geD6, geD7, geD8, geD9, geD10,
       geD11, geD12, geD13, geD14, geD15;
  wire [11:0] deMuxl1;

  ROM #(.addrWidth(12)) rom_1 (.addr(ELEM), .data(geD0));  // open: sel
  ROM #(.addrWidth(12)) rom_2 (.addr(ELEM), .data(geD1));  // open: sel
  ROM #(.addrWidth(12)) rom_3 (.addr(ELEM), .data(geD2));  // open: sel
  ROM #(.addrWidth(12)) rom_4 (.addr(ELEM), .data(geD3));  // open: sel
  ROM #(.addrWidth(12)) rom_5 (.addr(ELEM), .data(geD4));  // open: sel
  ROM #(.addrWidth(12)) rom_6 (.addr(ELEM), .data(geD5));  // open: sel
  ROM #(.addrWidth(12)) rom_7 (.addr(ELEM), .data(geD6));  // open: sel
  ROM #(.addrWidth(12)) rom_8 (.addr(ELEM), .data(geD7));  // open: sel
  ROM #(.addrWidth(12)) rom_9 (.addr(ELEM), .data(geD8));  // open: sel
  ROM #(.addrWidth(12)) rom_10 (.addr(ELEM), .data(geD9));  // open: sel
  ROM #(.addrWidth(12)) rom_11 (.addr(ELEM), .data(geD10));  // open: sel
  ROM #(.addrWidth(12)) rom_12 (.addr(ELEM), .data(geD11));  // open: sel
  ROM #(.addrWidth(12)) rom_13 (.addr(ELEM), .data(geD12));  // open: sel
  ROM #(.addrWidth(12)) rom_14 (.addr(ELEM), .data(geD13));  // open: sel
  ROM #(.addrWidth(12)) rom_15 (.addr(ELEM), .data(geD14));  // open: sel
  ROM #(.addrWidth(12)) rom_16 (.addr(ELEM), .data(geD15));  // open: sel
  ROM #(.addrWidth(12)) rom_17 (.addr(ELEM), .data(geD2_0));  // open: sel
  ROM #(.addrWidth(12)) rom_18 (.addr(ELEM), .data(geD2_1));  // open: sel
  Multiplexer #(.select(5), .width(8), .enable("false")) multiplexer_1 (
    .in0(geD0), .in1(geD1), .in2(geD2), .in3(geD3), .in4(geD4), .in5(geD5), .in6(geD6), .in7(geD7),
    .in8(geD8), .in9(geD9), .in10(geD10), .in11(geD11), .in12(geD12), .in13(geD13), .in14(geD14),
    .in15(geD15), .in30(geD2_1), .in31(geD2_0), .out(deMux1), .sel(ADDR[4:0]));  // open: in16, in17, in18, in19, in20, in21, in22, in23, in24, in25, in26, in27, in28, in29
  Multiplexer #(.select(5), .width(12), .enable("false")) multiplexer_2 (
    .in0(12'had5), .in1(12'h596), .in2(12'h596), .in3(12'h596), .in4(12'h596), .in5(12'h596), .in6(12'h596),
    .in7(12'h596), .in8(12'h596), .in9(12'h596), .in10(12'h596), .in11(12'h596), .in12(12'h596),
    .in13(12'h596), .in14(12'h596), .in15(12'h596), .in30(12'had5), .in31(12'had5), .out(deMuxl1),
    .sel(ADDR[4:0]));  // open: in16, in17, in18, in19, in20, in21, in22, in23, in24, in25, in26, in27, in28, in29
  Multiplexer #(.select(3), .width(8), .enable("false")) multiplexer_3 (
    .in0(deMux1), .out(DATA), .sel(ADDR[7:5]));  // open: in1, in2, in3, in4, in5, in6, in7
  Multiplexer #(.select(3), .width(12), .enable("false")) multiplexer_4 (
    .in0(deMuxl1), .out(LEN), .sel(ADDR[7:5]));  // open: in1, in2, in3, in4, in5, in6, in7

  // Other names for the same wires on the sheet: geAddr1[4:0] = ADDR[4:0]; geAddr2[2:0] = ADDR[7:5];
  //   geEl[11:0] = ELEM

  // Notes on the sheet:
  //   BOARD
  //   contents of rom_1 (hex, n*v repeats v):
  //   0 76*23 a 23 52*20 23 21*20 23 a 23 52*20 23 21*20 23 a 23 52*20 23 21*20 23 a 23 52*20 23 21*20 23
  //   a 23 52*20 23 21*20 23 a 23 52*20 23 21*20 23 a 23 52*20 23 21*20 23 a 23 52*20 23 21*20 23 a 23
  //   52*20 23 21*20 23 a 23 52*20 23 21*20 23 a 23 52*20 23 21*20 23 a 23 52*20 23 21*20 23 a 23 52*20 23
  //   21*20 23 a 23 52*20 23 21*20 23 a 23 52*20 23 21*20 23 a 23 52*20 23 21*20 23 a 23 52*20 23 21*20 23
  //   a 23 52*20 23 21*20 23 a 23 52*20 23 21*20 23 a 23 52*20 23 21*20 23 a 23 52*20 23 21*20 23 a 23
  //   52*20 23*23 a 23 52*20 23 21*20 23 a 23 52*20 23 21*20 23 a 23 52*20 23 21*20 23 a 23 52*20 23 21*20
  //   23 a 23 52*20 23 21*20 23 a 76*23 a 23 74*20 23 a 76*23 a 23 9*20 23 9*20 23 9*20 23 9*20 23 9*20 23
  //   20 48 50 20 7c 10*20 7c 28 20 20 2f 35 30 29 20 23 a 23 9*20 23 9*20 23 9*20 23 9*20 23 9*20 23
  //   24*20 23 a 23 9*20 23 9*20 23 9*20 23 9*20 23 9*20 23 24*20 23 a 23 9*20 23 9*20 23 9*20 23 9*20 23
  //   9*20 23 24*20 23 a 76*23 a
  //   FFL
  //   contents of rom_2 (hex, n*v repeats v):
  //   0 51*20 a 52*20 a 52*20 a 9*20 34*5f 9*20 a 8*20 7c 34*23 7c 8*20 a 8*20 7c 34*23 7c 8*20 a 8*20 7c
  //   34*23 7c 8*20 a 8*20 7c 34*23 7c 8*20 a 8*20 7c 34*23 7c 8*20 a 8*20 7c 34*23 7c 8*20 a 8*20 7c
  //   34*23 7c 8*20 a 8*20 7c 34*23 7c 8*20 a 8*20 7c 34*23 7c 8*20 a 8*20 7c 34*23 7c 8*20 a 8*20 7c
  //   34*23 7c 8*20 a 8*20 7c 34*23 7c 8*20 a 8*20 7c 34*23 7c 8*20 a 8*20 7c 34*23 7c 8*20 a 8*20 7c
  //   34*23 7c 8*20 a 8*20 7c 34*23 7c 8*20 a 8*20 7c 34*23 7c 8*20 a 8*20 7c 34*23 7c 8*20 a 8*20 7c
  //   34*23 7c 8*20 a 52*20 a 52*20 a 52*20 a 52*20
  //   FFFL
  //   contents of rom_3 (hex, n*v repeats v):
  //   0 51*20 a 52*20 a 52*20 a 52*20 a 52*20 a 52*20 a 52*20 a 18*20 16*5f 18*20 a 17*20 7c 16*23 7c
  //   17*20 a 17*20 7c 16*23 7c 17*20 a 17*20 7c 16*23 7c 17*20 a 17*20 7c 16*23 7c 17*20 a 17*20 7c 16*23
  //   7c 17*20 a 17*20 7c 16*23 7c 17*20 a 17*20 7c 16*23 7c 17*20 a 17*20 7c 16*23 7c 17*20 a 17*20 7c
  //   16*23 7c 17*20 a 17*20 7c 16*23 7c 17*20 a 17*20 7c 16*23 7c 17*20 a 52*20 a 52*20 a 52*20 a 52*20 a
  //   52*20 a 52*20 a 52*20 a 52*20
  //   FFFFL
  //   contents of rom_4 (hex, n*v repeats v):
  //   0 51*20 a 52*20 a 52*20 a 52*20 a 52*20 a 52*20 a 52*20 a 52*20 a 52*20 a 52*20 a 24*20 4*5f 24*20 a
  //   23*20 7c 4*23 7c 23*20 a 23*20 7c 4*23 7c 23*20 a 23*20 7c 4*23 7c 23*20 a 23*20 7c 4*23 7c 23*20 a
  //   23*20 7c 4*23 7c 23*20 a 52*20 a 52*20 a 52*20 a 52*20 a 52*20 a 52*20 a 52*20 a 52*20 a 52*20 a
  //   52*20 a 52*20
  //   LFL
  //   contents of rom_5 (hex, n*v repeats v):
  //   0 5c 5f 49*20 a 23 23 5c 5f 48*20 a 4*23 5c 5f 46*20 a 6*23 5c 5f 44*20 a 8*23 7c 43*20 a 8*23 7c
  //   43*20 a 8*23 7c 43*20 a 8*23 7c 43*20 a 8*23 7c 43*20 a 8*23 7c 43*20 a 8*23 7c 43*20 a 8*23 7c
  //   43*20 a 8*23 7c 43*20 a 8*23 7c 43*20 a 8*23 7c 43*20 a 8*23 7c 43*20 a 8*23 7c 43*20 a 8*23 7c
  //   43*20 a 8*23 7c 43*20 a 8*23 7c 43*20 a 8*23 7c 43*20 a 8*23 7c 43*20 a 8*23 7c 43*20 a 6*23 2f
  //   45*20 a 4*23 2f 47*20 a 23 23 2f 49*20 a 2f 51*20
  //   LFFL
  //   contents of rom_6 (hex, n*v repeats v):
  //   0 51*20 a 52*20 a 52*20 a 8*5f 44*20 a 8*23 7c 43*20 a 8*23 7c 43*20 a 8*23 7c 43*20 a 8*23 7c 43*20
  //   a 8*23 7c 43*20 a 8*23 7c 43*20 a 8*23 7c 43*20 a 8*23 7c 43*20 a 8*23 7c 43*20 a 8*23 7c 43*20 a
  //   8*23 7c 43*20 a 8*23 7c 43*20 a 8*23 7c 43*20 a 8*23 7c 43*20 a 8*23 7c 43*20 a 8*23 7c 43*20 a 8*23
  //   7c 43*20 a 8*23 7c 43*20 a 8*23 7c 43*20 a 52*20 a 52*20 a 52*20 a 52*20
  //   LFFFL
  //   contents of rom_7 (hex, n*v repeats v):
  //   0 51*20 a 52*20 a 52*20 a 52*20 a 52*20 a 52*20 a 52*20 a 17*5f 35*20 a 17*23 7c 34*20 a 17*23 7c
  //   34*20 a 17*23 7c 34*20 a 17*23 7c 34*20 a 17*23 7c 34*20 a 17*23 7c 34*20 a 17*23 7c 34*20 a 17*23
  //   7c 34*20 a 17*23 7c 34*20 a 17*23 7c 34*20 a 17*23 7c 34*20 a 52*20 a 52*20 a 52*20 a 52*20 a 52*20
  //   a 52*20 a 52*20 a 52*20
  //   LFFFFL
  //   contents of rom_8 (hex, n*v repeats v):
  //   0 51*20 a 52*20 a 52*20 a 52*20 a 52*20 a 52*20 a 52*20 a 52*20 a 52*20 a 52*20 a 18*20 5*5f 29*20 a
  //   17*20 7c 5*23 7c 28*20 a 17*20 7c 5*23 7c 28*20 a 17*20 7c 5*23 7c 28*20 a 17*20 7c 5*23 7c 28*20 a
  //   17*20 7c 5*23 7c 28*20 a 52*20 a 52*20 a 52*20 a 52*20 a 52*20 a 52*20 a 52*20 a 52*20 a 52*20 a
  //   52*20 a 52*20
  //   RFL
  //   contents of rom_9 (hex, n*v repeats v):
  //   0 50*20 5f 2f a 48*20 5f 2f 23 23 a 46*20 5f 2f 4*23 a 44*20 5f 2f 6*23 a 43*20 7c 8*23 a 43*20 7c
  //   8*23 a 43*20 7c 8*23 a 43*20 7c 8*23 a 43*20 7c 8*23 a 43*20 7c 8*23 a 43*20 7c 8*23 a 43*20 7c 8*23
  //   a 43*20 7c 8*23 a 43*20 7c 8*23 a 43*20 7c 8*23 a 43*20 7c 8*23 a 43*20 7c 8*23 a 43*20 7c 8*23 a
  //   43*20 7c 8*23 a 43*20 7c 8*23 a 43*20 7c 8*23 a 43*20 7c 8*23 a 43*20 7c 8*23 a 45*20 5c 6*23 a
  //   47*20 5c 4*23 a 49*20 5c 23 23 a 51*20 5c
  //   RFFL
  //   contents of rom_10 (hex, n*v repeats v):
  //   0 51*20 a 52*20 a 52*20 a 52*20 a 41*20 5f 2f 7c 8*20 a 39*20 5f 2f 23 23 7c 8*20 a 37*20 5f 2f 4*23
  //   7c 8*20 a 35*20 5f 2f 6*23 7c 8*20 a 34*20 7c 8*23 7c 8*20 a 34*20 7c 8*23 7c 8*20 a 34*20 7c 8*23
  //   7c 8*20 a 34*20 7c 8*23 7c 8*20 a 34*20 7c 8*23 7c 8*20 a 34*20 7c 8*23 7c 8*20 a 34*20 7c 8*23 7c
  //   8*20 a 34*20 7c 8*23 7c 8*20 a 34*20 7c 8*23 7c 8*20 a 34*20 7c 8*23 7c 8*20 a 34*20 7c 8*23 7c 8*20
  //   a 36*20 5c 6*23 7c 8*20 a 38*20 5c 4*23 7c 8*20 a 40*20 5c 23 23 7c 8*20 a 42*20 5c 7c 8*20 a 52*20
  //   a 52*20 a 52*20 a 52*20
  //   RFFFL
  //   contents of rom_11 (hex, n*v repeats v):
  //   0 51*20 a 52*20 a 52*20 a 52*20 a 52*20 a 52*20 a 52*20 a 35*20 17*5f a 34*20 7c 17*23 a 34*20 7c
  //   17*23 a 34*20 7c 17*23 a 34*20 7c 17*23 a 34*20 7c 17*23 a 34*20 7c 17*23 a 34*20 7c 17*23 a 34*20
  //   7c 17*23 a 34*20 7c 17*23 a 34*20 7c 17*23 a 34*20 7c 17*23 a 52*20 a 52*20 a 52*20 a 52*20 a 52*20
  //   a 52*20 a 52*20 a 52*20
  //   RFFFFL
  //   contents of rom_12 (hex, n*v repeats v):
  //   0 51*20 a 52*20 a 52*20 a 52*20 a 52*20 a 52*20 a 52*20 a 52*20 a 52*20 a 52*20 a 29*20 5*5f 18*20 a
  //   28*20 7c 5*23 7c 17*20 a 28*20 7c 5*23 7c 17*20 a 28*20 7c 5*23 7c 17*20 a 28*20 7c 5*23 7c 17*20 a
  //   28*20 7c 5*23 7c 17*20 a 52*20 a 52*20 a 52*20 a 52*20 a 52*20 a 52*20 a 52*20 a 52*20 a 52*20 a
  //   52*20 a 52*20
  //   FRFL
  //   contents of rom_13 (hex, n*v repeats v):
  //   0 51*20 a 52*20 a 52*20 a 52*20 a 41*20 5f 2f 7c 8*20 a 39*20 5f 2f 23 23 7c 8*20 a 37*20 5f 2f 4*23
  //   7c 8*20 a 35*20 5f 2f 6*23 7c 8*20 a 34*20 7c 8*23 7c 8*20 a 34*20 7c 8*23 7c 8*20 a 34*20 7c 8*23
  //   7c 8*20 a 34*20 7c 8*23 7c 8*20 a 34*20 7c 8*23 7c 8*20 a 34*20 7c 8*23 7c 8*20 a 34*20 7c 8*23 7c
  //   8*20 a 34*20 7c 8*23 7c 8*20 a 34*20 7c 8*23 7c 8*20 a 34*20 7c 8*23 7c 8*20 a 34*20 7c 8*23 7c 8*20
  //   a 36*20 5c 6*23 7c 8*20 a 38*20 5c 4*23 7c 8*20 a 40*20 5c 23 23 7c 8*20 a 42*20 5c 7c 8*20 a 52*20
  //   a 52*20 a 52*20 a 52*20
  //   FLFL
  //   contents of rom_14 (hex, n*v repeats v):
  //   0 51*20 a 52*20 a 52*20 a 52*20 a 8*20 7c 5c 5f 41*20 a 8*20 7c 23 23 5c 5f 39*20 a 8*20 7c 4*23 5c
  //   5f 37*20 a 8*20 7c 6*23 5c 5f 35*20 a 8*20 7c 8*23 7c 34*20 a 8*20 7c 8*23 7c 34*20 a 8*20 7c 8*23
  //   7c 34*20 a 8*20 7c 8*23 7c 34*20 a 8*20 7c 8*23 7c 34*20 a 8*20 7c 8*23 7c 34*20 a 8*20 7c 8*23 7c
  //   34*20 a 8*20 7c 8*23 7c 34*20 a 8*20 7c 8*23 7c 34*20 a 8*20 7c 8*23 7c 34*20 a 8*20 7c 8*23 7c
  //   34*20 a 8*20 7c 6*23 2f 36*20 a 8*20 7c 4*23 2f 38*20 a 8*20 7c 23 23 2f 40*20 a 8*20 7c 2f 42*20 a
  //   52*20 a 52*20 a 52*20 a 52*20
  //   FFRFL
  //   contents of rom_15 (hex, n*v repeats v):
  //   0 51*20 a 52*20 a 52*20 a 52*20 a 52*20 a 52*20 a 52*20 a 52*20 a 32*20 5f 2f 7c 17*20 a 30*20 5f 2f
  //   23 23 7c 17*20 a 29*20 2f 4*23 7c 17*20 a 28*20 7c 5*23 7c 17*20 a 28*20 7c 5*23 7c 17*20 a 28*20 7c
  //   5*23 7c 17*20 a 28*20 7c 5*23 7c 17*20 a 28*20 7c 5*23 7c 17*20 a 29*20 5c 4*23 7c 17*20 a 31*20 5c
  //   23 23 7c 17*20 a 33*20 5c 7c 17*20 a 52*20 a 52*20 a 52*20 a 52*20 a 52*20 a 52*20 a 52*20 a 52*20
  //   FFLFL
  //   contents of rom_16 (hex, n*v repeats v):
  //   0 51*20 a 52*20 a 52*20 a 52*20 a 52*20 a 52*20 a 52*20 a 52*20 a 17*20 7c 5c 5f 32*20 a 17*20 7c 23
  //   23 5c 5f 30*20 a 17*20 7c 4*23 5c 29*20 a 17*20 7c 5*23 7c 28*20 a 17*20 7c 5*23 7c 28*20 a 17*20 7c
  //   5*23 7c 28*20 a 17*20 7c 5*23 7c 28*20 a 17*20 7c 5*23 7c 28*20 a 17*20 7c 4*23 2f 29*20 a 17*20 7c
  //   23 23 2f 31*20 a 17*20 7c 2f 33*20 a 52*20 a 52*20 a 52*20 a 52*20 a 52*20 a 52*20 a 52*20 a 52*20
  //   contents of rom_17 (hex, n*v repeats v):
  //   0 76*23 a 23 74*20 23 a 23 74*20 23 a 23 74*20 23 a 23 26*20 5*5f 20 20 5f 40*20 23 a 23 25*20 7c 5f
  //   20 20 20 5f 7c 7c 20 7c 39*20 23 a 23 27*20 7c 20 7c 20 20 7c 20 7c 5f 5f 4*20 5f 5f 5f 30*20 23 a
  //   23 27*20 7c 20 7c 20 20 7c 20 27 5f 20 5c 20 20 2f 20 5f 20 5c 29*20 23 a 23 27*20 7c 20 7c 20 20 7c
  //   20 7c 20 7c 20 7c 7c 20 20 5f 5f 2f 29*20 23 a 23 27*20 5c 5f 2f 20 20 7c 5f 7c 20 7c 5f 7c 20 5c 5f
  //   5f 5f 7c 29*20 23 a 23 20 5f 5f 5f 20 20 5f 5f 5f 8*20 5f 7*20 5f 7*20 5f 40*20 23 a 23 20 7c 20 20
  //   5c 2f 20 20 7c 7*20 7c 20 7c 5*20 28 20 29 5*20 7c 20 7c 39*20 23 a 23 20 7c 20 2e 20 20 2e 20 7c 20
  //   20 5f 5f 5f 20 20 7c 20 7c 20 20 5f 5f 5f 7c 2f 20 5f 5f 5f 20 20 7c 20 7c 5f 5f 20 20 20 5f 20 20
  //   20 5f 20 20 5f 20 5f 5f 20 20 5f 20 5f 5f 20 20 5f 5f 5f 20 5f 5f 6*20 5f 5f 20 23 a 23 20 7c 20 7c
  //   5c 2f 7c 20 7c 20 2f 20 5f 20 5c 20 7c 20 7c 20 2f 20 5f 20 5c 20 2f 20 5f 5f 7c 20 7c 20 27 5f 20
  //   5c 20 7c 20 7c 20 7c 20 7c 7c 20 27 5f 5f 7c 7c 20 27 5f 5f 7c 2f 20 5f 20 5c 5c 20 5c 20 2f 5c 20
  //   2f 20 2f 20 23 a 23 20 7c 20 7c 20 20 7c 20 7c 7c 20 28 5f 29 20 7c 7c 20 7c 7c 20 20 5f 5f 2f 20 5c
  //   5f 5f 20 5c 20 7c 20 7c 5f 29 20 7c 7c 20 7c 5f 7c 20 7c 7c 20 7c 20 20 20 7c 20 7c 20 20 7c 20 28
  //   5f 29 20 7c 5c 20 56 20 20 56 20 2f 20 20 23 a 23 20 5c 5f 7c 20 20 7c 5f 2f 20 5c 5f 5f 5f 2f 20 7c
  //   5f 7c 20 5c 5f 5f 5f 7c 20 7c 5f 5f 5f 2f 20 7c 5f 2e 5f 5f 2f 20 20 5c 5f 5f 2c 5f 7c 7c 5f 7c 20
  //   20 20 7c 5f 7c 20 20 20 5c 5f 5f 5f 2f 20 20 5c 5f 2f 5c 5f 2f 20 20 20 23 a 23 74*20 23 a 23 74*20
  //   23 a 23 74*20 23 a 23 74*20 23 a 23 74*20 23 a 23 74*20 23 a 23 74*20 23 a 23 74*20 23 a 23 74*20 23
  //   a 23 74*20 23 a 23 74*20 23 a 23 74*20 23 a 23 74*20 23 a 23 74*20 23 a 23 74*20 23 a 23 74*20 23 a
  //   23 74*20 23 a 23 39*20 50 52 45 53 53 20 41 4e 59 20 4b 45 59 20 54 4f 20 43 4f 4e 54 49 4e 55 45 2e
  //   2e 2e 7*20 23 a 23 74*20 23 a 76*23 a 52*20
  //   contents of rom_18 (hex, n*v repeats v):
  //   0 76*23 a 23 74*20 23 a 23 74*20 23 a 23 74*20 23 a 23 74*20 23 a 23 74*20 23 a 23 74*20 23 a 23
  //   74*20 23 a 23 74*20 23 a 23 6*20 7c 8*20 4d 6f 6c 65 8*20 7c 13*20 7c 20*20 7c 20 28 20 20 7c 20 20
  //   29 20 20 20 23 a 23 74*20 23 a 23 74*20 23 a 23 74*20 23 a 23 74*20 23 a 23 74*20 23 a 23 13*20 7b
  //   28 30 2d 30 29 7d 54*20 23 a 23 74*20 23 a 23 74*20 23 a 23 74*20 23 a 23 4*20 65*2d 5*20 23 a 23
  //   74*20 23 a 23 20*20 5e 24*20 2e 28*20 23 a 23 8*20 2e 19*20 2e 10*20 2e 18*20 2e 7*20 2e 7*20 23 a
  //   23 16*20 2e 17*20 2e 17*20 5e 7*20 2e 13*20 23 a 23 23*20 2e 18*20 2e 31*20 23 a 23 6*20 2e 6*20 5e
  //   16*20 5e 23*20 2e 19*20 23 a 23 23*20 2e 11*20 2e 5*20 2e 20*20 5e 11*20 23 a 23 74*20 23 a 76*23 a
  //   23 74*20 23 a 76*23 a 23 9*20 23 9*20 23 9*20 23 9*20 23 9*20 23 20 48 50 20 7c 10*20 7c 28 20 20 2f
  //   35 30 29 20 23 a 23 9*20 23 9*20 23 9*20 23 9*20 23 9*20 23 24*20 23 a 23 9*20 23 9*20 23 9*20 23
  //   9*20 23 9*20 23 24*20 23 a 23 9*20 23 9*20 23 9*20 23 9*20 23 9*20 23 24*20 23 a 76*23 a
  //   START SCREEN
  //   ATACK BOARD
endmodule

// Maps
module maps (
  input  [7:0] ADDR,
  input  [11:0] ELEM,
  output [11:0] Width,
  output [11:0] Height,
  output [7:0] Xpp,
  output [7:0] Ypp,
  output [7:0] DATA,
  output [11:0] LEN
);

  wire [7:0] mgeD0, undriven_4, undriven_5;
  wire [11:0] undriven, undriven_2, undriven_3;

  ROM #(.addrWidth(12)) rom_1 (.addr(ELEM), .data(mgeD0));  // open: sel
  Multiplexer #(.select(5), .width(8), .enable("false")) multiplexer_1 (
    .in0(mgeD0), .out(DATA), .sel(ADDR[4:0]));  // open: in1, in2, in3, in4, in5, in6, in7, in8, in9, in10, in11, in12, in13, in14, in15, in16, in17, in18, in19, in20, in21, in22, in23, in24, in25, in26, in27, in28, in29, in30, in31
  Multiplexer #(.select(5), .width(12), .enable("false")) multiplexer_2 (
    .in0(12'h99), .in30(undriven), .in31(undriven), .out(LEN), .sel(ADDR[4:0]));  // open: in1, in2, in3, in4, in5, in6, in7, in8, in9, in10, in11, in12, in13, in14, in15, in16, in17, in18, in19, in20, in21, in22, in23, in24, in25, in26, in27, in28, in29
  Multiplexer #(.select(5), .width(12), .enable("false")) multiplexer_3 (
    .in0(12'hb), .in30(undriven_2), .in31(undriven_2), .out(Width), .sel(ADDR[4:0]));  // open: in1, in2, in3, in4, in5, in6, in7, in8, in9, in10, in11, in12, in13, in14, in15, in16, in17, in18, in19, in20, in21, in22, in23, in24, in25, in26, in27, in28, in29
  Multiplexer #(.select(5), .width(12), .enable("false")) multiplexer_4 (
    .in0(12'h8), .in30(undriven_3), .in31(undriven_3), .out(Height), .sel(ADDR[4:0]));  // open: in1, in2, in3, in4, in5, in6, in7, in8, in9, in10, in11, in12, in13, in14, in15, in16, in17, in18, in19, in20, in21, in22, in23, in24, in25, in26, in27, in28, in29
  Multiplexer #(.select(5), .width(8), .enable("false")) multiplexer_5 (
    .in0(8'h3), .in30(undriven_4), .in31(undriven_4), .out(Xpp), .sel(ADDR[4:0]));  // open: in1, in2, in3, in4, in5, in6, in7, in8, in9, in10, in11, in12, in13, in14, in15, in16, in17, in18, in19, in20, in21, in22, in23, in24, in25, in26, in27, in28, in29
  Multiplexer #(.select(5), .width(8), .enable("false")) multiplexer_6 (
    .in0(8'h3), .in30(undriven_5), .in31(undriven_5), .out(Ypp), .sel(ADDR[4:0]));  // open: in1, in2, in3, in4, in5, in6, in7, in8, in9, in10, in11, in12, in13, in14, in15, in16, in17, in18, in19, in20, in21, in22, in23, in24, in25, in26, in27, in28, in29

  // Other names for the same wires on the sheet: mdeMux1[7:0] = DATA; mdeMuxl1[11:0] = LEN; mgeAddr1[4:0] = ADDR[4:0];
  //   mgeEl[11:0] = ELEM; mhMuxl1[11:0] = Height; mwMuxl1[11:0] = Width; mXMuxl1[7:0] = Xpp; mYMuxl1[7:0] = Ypp

  // Notes on the sheet:
  //   TEST MAP
  //   contents of rom_1 (hex, n*v repeats v):
  //   0 4 3 2 36*23 20 66 6a 61 20 6*23 20 23 23 20 32 6*23 20 20 23 23 20 36*23
endmodule

module x_y__to_memory_elem_number (
  input  [11:0] H,
  input  [7:0] Y,
  input  [7:0] X,
  input  [11:0] START,
  output [11:0] ELEM
);

  wire [11:0] adder_1_out, bit_extender_1_out, bit_extender_2_out, multiplier_1_out;

  assign bit_extender_1_out = {{4{1'b0}}, Y};  // Bit_Extender bit_extender_1
  Multiplier #(.width(12)) multiplier_1 (.a(H), .b(bit_extender_1_out), .out(multiplier_1_out));  // open: cin, cout
  assign bit_extender_2_out = {{4{1'b0}}, X};  // Bit_Extender bit_extender_2
  Adder #(.width(12)) adder_1 (.a(multiplier_1_out), .b(bit_extender_2_out), .out(adder_1_out));  // open: cin, cout
  Adder #(.width(12)) adder_2 (.a(adder_1_out), .b(START), .out(ELEM));  // open: cin, cout
endmodule

module enemies (
  input  [1:0] ADDR,
  input  [7:0] ELEMIm,
  input  [7:0] ELEMNm,
  output [7:0] Img,
  output [7:0] Txt,
  output [7:0] HP,
  output [7:0] DMG
);

  wire [7:0] EnImEl1, EnImEl1txt, EnImEl2, EnImEl2txt, EnImEl3, EnImEl3txt, EnImEl4, EnImEl4txt;

  ROM rom_1 (.addr(ELEMIm), .data(EnImEl1));  // open: sel
  ROM rom_2 (.addr(ELEMIm), .data(EnImEl2));  // open: sel
  ROM rom_3 (.addr(ELEMIm), .data(EnImEl3));  // open: sel
  ROM rom_4 (.addr(ELEMIm), .data(EnImEl4));  // open: sel
  Multiplexer #(.select(2), .width(8), .enable("false")) multiplexer_1 (
    .in0(EnImEl1), .in1(EnImEl2), .in2(EnImEl3), .in3(EnImEl4), .out(Img), .sel(ADDR));
  Multiplexer #(.select(2), .width(8), .enable("false")) multiplexer_2 (
    .in0(EnImEl1txt), .in1(EnImEl2txt), .in2(EnImEl3txt), .in3(EnImEl4txt), .out(Txt), .sel(ADDR));
  Multiplexer #(.select(2), .width(8), .disabled(0), .enable("false")) multiplexer_3 (
    .in0(8'h14), .in1(8'ha), .in2(8'h32), .in3(8'h1e), .out(HP), .sel(ADDR));
  Multiplexer #(.select(2), .width(8), .disabled(0), .enable("false")) multiplexer_4 (
    .in0(8'h5), .in1(8'h3), .in2(8'h14), .in3(8'ha), .out(DMG), .sel(ADDR));

  // Other names for the same wires on the sheet: enaddr1[1:0] = ADDR; EnImEl[7:0] = ELEMIm; EnImEltxt[7:0] = ELEMNm

  // Notes on the sheet:
  //   rat
  //   mouse
  //   ferret
  //   snake
  //   contents of rom_1 (hex, n*v repeats v):
  //   15*20 35 64 6d 67 2e 9*20 2f 5c 5f 2f 5c 16*20 28 20 6f 20 6f 20 29 15*20 2f 20 20 56 20 20 5c 15*20
  //   2f 20 3e 20 20 3c 20 20 5c 12*20 28 20 2f 5*20 5c 20 29 20 20 20 7c 8*20 5c 5f 20 4*2d 20 5f 2f 5f
  //   5f 5f 2f 24*20
  //   contents of rom_2 (hex, n*v repeats v):
  //   13*20 33 64 6d 67 2e 13*20 2f 5e 5c 5e 5c 5f 10*20 2f 4*20 7c 5*20 6f 5c 5f 7*20 7c 4*20 2f 7*20 5f
  //   2f 7*20 5c 20 20 20 2f 6*20 5f 5f 3e 9*20 5c 5f 5f 7c 20 20 20 5f 5f 5f 29 14*20 5c 5f 5f 5f 7c 5c
  //   5f 5f 30*20
  //   contents of rom_3 (hex, n*v repeats v):
  //   14*20 32 30 64 6d 67 2e 8*20 2f 29 5*5f 28 5c 12*20 28 2f 20 6f 20 20 20 6f 20 5c 29 11*20 7c 4*20
  //   4f 4*20 7c 12*20 5c 20 20 2d 5e 2d 20 20 2f 13*20 2f 7*20 5c 12*20 7c 9*20 7c 28*20
  //   contents of rom_4 (hex, n*v repeats v):
  //   14*20 31 30 64 6d 67 2e 4*20 2e 2d 2e 17*20 3e 2d 30 5f 30 29 29 20 20 7c 20 20 2f 20 29 11*20 2f 2f
  //   20 20 20 7c 2e 2f 5f 5f 29 10*20 28 28 5f 2e 2d 2d 27 20 5f 20 20 27 2e 10*20 60 2d 5f 5f 2d 2d 27
  //   20 27 2d 2e 20 29 16*20 5f 5f 2d 2d 27 28*20
  //   dmg/2
  //   8x22 = 176
  //   20 chars name len
endmodule

module quick (
  input  IN,
  output OUT
);

  wire not_1_out, not_2_out;

  not not_1 (not_1_out, IN);
  Register #(.width(1)) register_1 (.D(IN), .Q(OUT), .clk(IN), .clr(not_2_out));  // open: en
  not not_2 (not_2_out, not_1_out);
endmodule

module food (
  input  [7:0] FOOD,
  output [7:0] GIVEHP,
  output ES
);

  wire comparator_1_lt, comparator_2_gt;
  wire [1:0] bit_extender_1_out;
  wire [7:0] subtractor_1_out;

  Subtractor subtractor_1 (.a(FOOD), .b(8'h61), .out(subtractor_1_out));  // open: bin, bout
  Multiplexer #(.select(2), .width(8), .enable("false")) multiplexer_1 (
    .in0(8'ha), .in1(8'h6), .in2(8'hf), .in3(8'h14), .out(GIVEHP), .sel(bit_extender_1_out));
  Bit_Extender #(.out_width(2)) bit_extender_1 (.in(subtractor_1_out), .out(bit_extender_1_out));
  Comparator comparator_1 (.a(FOOD), .b(8'h65), .lt(comparator_1_lt));  // open: gt, eq
  and and_1 (ES, comparator_1_lt, comparator_2_gt);
  Pull_Resistor pull_resistor_1 (.node(ES));
  Comparator comparator_2 (.a(FOOD), .b(8'h60), .gt(comparator_2_gt));  // open: eq, lt

  // Notes on the sheet:
  //   const/2
  //   is it eat in cell
endmodule

module Lquick (
  input  IN,
  input  CLC,
  output OUT
);

  wire and_1_out, comparator_1_eq, quick_1_out;
  wire [2:0] adder_1_out, register_1_q;

  and and_1 (and_1_out, CLC, ~comparator_1_eq);  // AND_Gate
  quick quick_1 (.IN(IN), .OUT(quick_1_out));
  Adder #(.width(3)) adder_1 (.a(3'b001), .b(register_1_q), .out(adder_1_out));  // open: cin, cout
  Comparator #(.width(3), .mode("unsigned")) comparator_1 (
    .a(3'b111), .b(register_1_q), .gt(OUT), .eq(comparator_1_eq));  // open: lt
  Register #(.width(3)) register_1 (.D(adder_1_out), .Q(register_1_q), .clk(and_1_out), .clr(quick_1_out));  // open: en
endmodule

module weapon (
  input  GenRnd,
  input  [7:0] WEAPON,
  output [7:0] DMG,
  output nW
);

  wire comparator_1_lt, comparator_2_gt, comparator_3_eq, random_1_out;
  wire [2:0] bit_extender_1_out;
  wire [7:0] adder_1_out, bit_extender_2_out, multiplexer_1_out, subtractor_1_out;

  Subtractor subtractor_1 (.a(WEAPON), .b(8'h66), .out(subtractor_1_out));  // open: bin, bout
  Comparator comparator_1 (.a(WEAPON), .b(8'h6b), .lt(comparator_1_lt));  // open: gt, eq
  Comparator comparator_2 (.a(WEAPON), .b(8'h65), .gt(comparator_2_gt));  // open: eq, lt
  Multiplexer #(.select(3), .width(8), .enable("false")) multiplexer_1 (
    .in0(8'h5), .in1(8'h14), .in2(8'hf), .in3(8'ha), .in4(8'h63), .out(multiplexer_1_out),
    .sel(bit_extender_1_out));  // open: in5, in6, in7
  Bit_Extender #(.out_width(3)) bit_extender_1 (.in(subtractor_1_out), .out(bit_extender_1_out));
  and and_1 (nW, comparator_1_lt, comparator_2_gt);
  Random #(.width(1)) random_1 (.clk(GenRnd), .out(random_1_out));  // open: next, clr
  assign bit_extender_2_out = {{7{1'b0}}, random_1_out};  // Bit_Extender bit_extender_2
  Comparator comparator_3 (.a(WEAPON), .b({8{1'b1}}), .eq(comparator_3_eq));  // open: gt, lt
  Adder adder_1 (.a(bit_extender_2_out), .b(multiplexer_1_out), .out(adder_1_out));  // open: cin, cout
  Multiplexer #(.width(8), .enable("false")) multiplexer_2 (
    .in0(adder_1_out), .in1({8{1'b0}}), .out(DMG), .sel(comparator_3_eq));
endmodule

module doForwardStep (
  input  [7:0] plY,
  input  [7:0] plX,
  input  WonInp,
  input  [1:0] PlDir,
  input  [7:0] p_x_1_y,
  input  [7:0] p_x_1_y_2,
  input  [7:0] p_x_y_1,
  input  [7:0] p_x_y_1_2,
  output moved,
  output [7:0] NewPLyOM,
  output changePCy,
  output [7:0] NewPLxOM,
  output changePCx
);

  wire and_1_out, and_2_out, and_3_out, and_4_out, comparator_1_eq, comparator_2_eq, comparator_3_eq,
       comparator_4_eq, comparator_5_eq, comparator_6_eq, comparator_7_eq, comparator_8_eq, not_1_out,
       not_2_out, not_3_out, not_4_out, or_1_out, or_3_out;
  wire [7:0] adder_1_out, adder_2_out, subtractor_1_out, subtractor_2_out;

  Comparator #(.width(2)) comparator_1 (.a(PlDir), .b(2'b00), .eq(comparator_1_eq));  // open: gt, lt
  Comparator #(.width(2)) comparator_2 (.a(PlDir), .b(2'b10), .eq(comparator_2_eq));  // open: gt, lt
  Comparator #(.width(2)) comparator_3 (.a(PlDir), .b(2'b01), .eq(comparator_3_eq));  // open: gt, lt
  Comparator #(.width(2)) comparator_4 (.a(PlDir), .b(2'b11), .eq(comparator_4_eq));  // open: gt, lt
  Comparator comparator_5 (.a(p_x_y_1_2), .b(8'h23), .eq(comparator_5_eq));  // open: gt, lt
  Comparator comparator_6 (.a(p_x_y_1), .b(8'h23), .eq(comparator_6_eq));  // open: gt, lt
  Comparator comparator_7 (.a(p_x_1_y_2), .b(8'h23), .eq(comparator_7_eq));  // open: gt, lt
  Comparator comparator_8 (.a(p_x_1_y), .b(8'h23), .eq(comparator_8_eq));  // open: gt, lt
  not not_1 (not_1_out, comparator_5_eq);
  and and_1 (and_1_out, not_1_out, WonInp, comparator_1_eq);
  not not_2 (not_2_out, comparator_6_eq);
  and and_2 (and_2_out, not_2_out, WonInp, comparator_2_eq);
  not not_3 (not_3_out, comparator_7_eq);
  and and_3 (and_3_out, not_3_out, WonInp, comparator_3_eq);
  not not_4 (not_4_out, comparator_8_eq);
  and and_4 (and_4_out, not_4_out, WonInp, comparator_4_eq);
  assign NewPLyOM = and_1_out ? subtractor_1_out : 8'bz;  // Controlled_Buffer controlled_buffer_1
  Subtractor subtractor_1 (.a(plY), .b(8'h1), .out(subtractor_1_out));  // open: bin, bout
  assign NewPLyOM = and_2_out ? adder_1_out : 8'bz;  // Controlled_Buffer controlled_buffer_2
  Adder adder_1 (.a(plY), .b(8'h1), .out(adder_1_out));  // open: cin, cout
  Adder adder_2 (.a(plX), .b(8'h1), .out(adder_2_out));  // open: cin, cout
  assign NewPLxOM = and_3_out ? adder_2_out : 8'bz;  // Controlled_Buffer controlled_buffer_3
  Subtractor subtractor_2 (.a(plX), .b(8'h1), .out(subtractor_2_out));  // open: bin, bout
  assign NewPLxOM = and_4_out ? subtractor_2_out : 8'bz;  // Controlled_Buffer controlled_buffer_4
  quick quick_1 (.IN(or_1_out), .OUT(changePCy));
  or or_1 (or_1_out, and_1_out, and_2_out);
  or or_2 (moved, or_1_out, or_3_out);
  or or_3 (or_3_out, and_3_out, and_4_out);
  quick quick_2 (.IN(or_3_out), .OUT(changePCx));

  // Other names for the same wires on the sheet: changePCxdfs = changePCx; changePCydfs = changePCy;
  //   NewPLxOMdfs[7:0] = NewPLxOM; NewPLyOMdfs[7:0] = NewPLyOM; p_x_1_y_dfs[7:0] = p_x_1_y_2;
  //   p_x_1_y_dfs_t[7:0] = p_x_1_y; p_x_y_1_dfs[7:0] = p_x_y_1; p_x_y_1_dfs_t[7:0] = p_x_y_1_2; PlDirdfs[1:0] = PlDir;
  //   PLxOMdfs[7:0] = plX; PLyOMdfs[7:0] = plY; WonInpdfs = WonInp
endmodule

module pickUpAnItem (
  input  [7:0] p_x_y,
  input  _1oninp,
  input  _2oninp,
  input  _3oninp,
  input  _4oninp,
  input  _5oninp,
  input  MOVEinited,
  output chMap,
  output InpFl1,
  output ITEMinCELL,
  output INV1ch,
  output INV2ch,
  output INV3ch,
  output INV4ch,
  output INV5ch
);

  wire and_1_out, and_2_out, and_3_out, and_4_out, and_5_out, and_6_out, and_7_out, and_8_out, and_9_out,
       and_10_out, comparator_1_lt, comparator_2_gt, comparator_3_lt, comparator_4_gt, MOVEinited_t, or_2_out;

  and and_1 (and_1_out, _1oninp, MOVEinited, ITEMinCELL);
  quick quick_1 (.IN(and_1_out), .OUT(INV1ch));
  quick quick_2 (.IN(and_2_out), .OUT(INV2ch));
  and and_2 (and_2_out, _2oninp, MOVEinited, ITEMinCELL);
  quick quick_3 (.IN(and_3_out), .OUT(INV3ch));
  and and_3 (and_3_out, _3oninp, MOVEinited, ITEMinCELL);
  and and_4 (and_4_out, _4oninp, MOVEinited, ITEMinCELL);
  quick quick_4 (.IN(and_4_out), .OUT(INV4ch));
  quick quick_5 (.IN(and_5_out), .OUT(INV5ch));
  and and_5 (and_5_out, _5oninp, MOVEinited, ITEMinCELL);
  or or_1 (chMap, and_1_out, and_2_out, and_3_out, and_4_out, and_5_out);
  and and_6 (and_6_out, chMap, MOVEinited);
  and and_7 (and_7_out, ~ITEMinCELL, or_2_out);  // AND_Gate
  and and_8 (and_8_out, and_7_out, MOVEinited_t);
  or or_2 (or_2_out, _1oninp, _2oninp, _3oninp, _4oninp, _5oninp);
  Comparator comparator_1 (.a(p_x_y), .b(8'h65), .lt(comparator_1_lt));  // open: gt, eq
  and and_9 (and_9_out, comparator_1_lt, comparator_2_gt);
  Comparator comparator_2 (.a(p_x_y), .b(8'h60), .gt(comparator_2_gt));  // open: eq, lt
  Comparator comparator_3 (.a(p_x_y), .b(8'h6b), .lt(comparator_3_lt));  // open: gt, eq
  and and_10 (and_10_out, comparator_3_lt, comparator_4_gt);
  Comparator comparator_4 (.a(p_x_y), .b(8'h65), .gt(comparator_4_gt));  // open: eq, lt
  or or_3 (InpFl1, and_6_out, and_8_out);
  or or_4 (ITEMinCELL, and_9_out, and_10_out);

  // Other names for the same wires on the sheet: _1onInppui = _1oninp; _2onInppui = _2oninp; _3onInppui = _3oninp;
  //   _4onInppui = _4oninp; _5onInppui = _5oninp; chMappui = chMap; InpFl1pui = InpFl1; INV1chpui = INV1ch;
  //   INV2chpui = INV2ch; INV3chpui = INV3ch; INV4chpui = INV4ch; INV5chpui = INV5ch; ITEMinCELLpui = ITEMinCELL;
  //   MOVEinitedpui = MOVEinited; p_x_y_pui[7:0] = p_x_y

  // Notes on the sheet:
  //   is it eat in cell
  //   is it weapon in cell
endmodule

module weaponSelected (
  input  [7:0] INVENTORY1p,
  input  [7:0] INVENTORY2p,
  input  [7:0] INVENTORY3p,
  input  [7:0] INVENTORY4p,
  input  [7:0] INVENTORY5p,
  input  _1oninp,
  input  _2oninp,
  input  _3oninp,
  input  _4oninp,
  input  _5oninp,
  output weaponSelected
);

  wire and_1_out, and_2_out, and_3_out, and_4_out, and_5_out, comparator_1_lt, comparator_2_gt,
       comparator_3_lt, comparator_4_gt, comparator_5_lt, comparator_6_gt, comparator_7_lt, comparator_8_gt,
       comparator_9_lt, comparator_10_gt;

  Comparator comparator_1 (.a(INVENTORY1p), .b(8'h6b), .lt(comparator_1_lt));  // open: gt, eq
  Comparator comparator_2 (.a(INVENTORY1p), .b(8'h65), .gt(comparator_2_gt));  // open: eq, lt
  Comparator comparator_3 (.a(INVENTORY2p), .b(8'h6b), .lt(comparator_3_lt));  // open: gt, eq
  Comparator comparator_4 (.a(INVENTORY2p), .b(8'h65), .gt(comparator_4_gt));  // open: eq, lt
  Comparator comparator_5 (.a(INVENTORY3p), .b(8'h6b), .lt(comparator_5_lt));  // open: gt, eq
  Comparator comparator_6 (.a(INVENTORY3p), .b(8'h65), .gt(comparator_6_gt));  // open: eq, lt
  Comparator comparator_7 (.a(INVENTORY4p), .b(8'h6b), .lt(comparator_7_lt));  // open: gt, eq
  Comparator comparator_8 (.a(INVENTORY4p), .b(8'h65), .gt(comparator_8_gt));  // open: eq, lt
  Comparator comparator_9 (.a(INVENTORY5p), .b(8'h6b), .lt(comparator_9_lt));  // open: gt, eq
  Comparator comparator_10 (.a(INVENTORY5p), .b(8'h65), .gt(comparator_10_gt));  // open: eq, lt
  and and_1 (and_1_out, comparator_1_lt, _1oninp, comparator_2_gt);
  and and_2 (and_2_out, comparator_3_lt, _2oninp, comparator_4_gt);
  and and_3 (and_3_out, comparator_5_lt, _3oninp, comparator_6_gt);
  and and_4 (and_4_out, comparator_7_lt, _4oninp, comparator_8_gt);
  and and_5 (and_5_out, comparator_9_lt, _5oninp, comparator_10_gt);
  or or_1 (weaponSelected, and_1_out, and_2_out, and_3_out, and_4_out, and_5_out);

  // Other names for the same wires on the sheet: _1onInpws = _1oninp; _2onInpws = _2oninp; _3onInpws = _3oninp;
  //   _4onInpws = _4oninp; _5onInpws = _5oninp; INVENTORY1pws[7:0] = INVENTORY1p; INVENTORY2pws[7:0] = INVENTORY2p;
  //   INVENTORY3pws[7:0] = INVENTORY3p; INVENTORY4pws[7:0] = INVENTORY4p; INVENTORY5pws[7:0] = INVENTORY5p
endmodule

module moveInitialization (
  input  InpFlare,
  input  MainCLC,
  input  [7:0] objMap,
  input  [11:0] mapW,
  input  [7:0] y,
  input  [7:0] x,
  output [11:0] x_1_y_elonmap,
  output MoveInited,
  output [11:0] x_1_y_elonmap_2,
  output workWithMap,
  output [7:0] p_x_y,
  output [11:0] where,
  output [7:0] p_x_y_1,
  output [11:0] x_y_1_elonmap,
  output [7:0] p_x_y_1_2,
  output [7:0] p_x_1_y,
  output [7:0] p_x_1_y_2,
  output [7:0] p_x_2_y,
  output [11:0] x_y_1_elonmap_2,
  output [7:0] p_x_2_y_2,
  output [7:0] p_x_y_2,
  output [11:0] x_y_elonmap,
  output [7:0] p_x_y_2_2
);

  wire and_1_out, comparator_1_eq, comparator_1_gt, comparator_1_lt, comparator_2_eq, comparator_3_eq,
       comparator_4_eq, comparator_5_eq, comparator_6_eq, comparator_7_eq, comparator_8_eq, comparator_9_eq,
       comparator_10_eq, comparator_11_eq, comparator_12_eq, comparator_13_eq, comparator_14_eq,
       comparator_15_eq, comparator_16_eq, comparator_17_eq, comparator_18_eq, comparator_19_eq;
  wire [3:0] adder_1_out, register_1_q;
  wire [7:0] adder_2_out, adder_3_out, adder_4_out, adder_5_out, subtractor_1_out, subtractor_2_out,
       subtractor_3_out, subtractor_4_out;
  wire [11:0] p_x_2_y__elemOnMap, p_x_2_y__elemOnMap_t, p_x_y_2__elemOnMap, p_x_y_2__elemOnMap_t;

  Adder #(.width(4)) adder_1 (.a(register_1_q), .b(4'b0001), .out(adder_1_out));  // open: cin, cout
  Register #(.width(4)) register_1 (.D(adder_1_out), .Q(register_1_q), .clk(and_1_out), .clr(InpFlare));  // open: en
  and and_1 (and_1_out, workWithMap, MainCLC);
  Comparator #(.width(4)) comparator_1 (
    .a(4'b1100), .b(register_1_q), .gt(comparator_1_gt), .eq(comparator_1_eq), .lt(comparator_1_lt));
  Comparator #(.width(4)) comparator_2 (.a(register_1_q), .b(4'b0010), .eq(comparator_2_eq));  // open: gt, lt
  Comparator #(.width(4)) comparator_3 (.a(register_1_q), .b(4'b0011), .eq(comparator_3_eq));  // open: gt, lt
  Comparator #(.width(4)) comparator_4 (.a(register_1_q), .b(4'b0011), .eq(comparator_4_eq));  // open: gt, lt
  Comparator #(.width(4)) comparator_5 (.a(register_1_q), .b(4'b0100), .eq(comparator_5_eq));  // open: gt, lt
  Comparator #(.width(4)) comparator_6 (.a(register_1_q), .b(4'b0100), .eq(comparator_6_eq));  // open: gt, lt
  Comparator #(.width(4)) comparator_7 (.a(register_1_q), .b(4'b0101), .eq(comparator_7_eq));  // open: gt, lt
  Comparator #(.width(4)) comparator_8 (.a(register_1_q), .b(4'b0101), .eq(comparator_8_eq));  // open: gt, lt
  Comparator #(.width(4)) comparator_9 (.a(register_1_q), .b(4'b0110), .eq(comparator_9_eq));  // open: gt, lt
  Comparator #(.width(4)) comparator_10 (.a(register_1_q), .b(4'b0110), .eq(comparator_10_eq));  // open: gt, lt
  Comparator #(.width(4)) comparator_11 (.a(register_1_q), .b(4'b0111), .eq(comparator_11_eq));  // open: gt, lt
  Comparator #(.width(4)) comparator_12 (.a(register_1_q), .b(4'b0111), .eq(comparator_12_eq));  // open: gt, lt
  Comparator #(.width(4)) comparator_13 (.a(register_1_q), .b(4'b1000), .eq(comparator_13_eq));  // open: gt, lt
  Comparator #(.width(4)) comparator_14 (.a(register_1_q), .b(4'b1000), .eq(comparator_14_eq));  // open: gt, lt
  Comparator #(.width(4)) comparator_15 (.a(register_1_q), .b(4'b1001), .eq(comparator_15_eq));  // open: gt, lt
  Comparator #(.width(4)) comparator_16 (.a(register_1_q), .b(4'b1001), .eq(comparator_16_eq));  // open: gt, lt
  Comparator #(.width(4)) comparator_17 (.a(register_1_q), .b(4'b1010), .eq(comparator_17_eq));  // open: gt, lt
  Comparator #(.width(4)) comparator_18 (.a(register_1_q), .b(4'b1010), .eq(comparator_18_eq));  // open: gt, lt
  Comparator #(.width(4)) comparator_19 (.a(register_1_q), .b(4'b1011), .eq(comparator_19_eq));  // open: gt, lt
  or or_1 (workWithMap, comparator_1_gt, comparator_1_lt);
  Lquick lquick_1 (.IN(comparator_1_eq), .OUT(MoveInited), .CLC(MainCLC));
  assign where = comparator_2_eq ? x_y_elonmap : 12'bz;  // Controlled_Buffer controlled_buffer_1
  Register register_2 (.D(objMap), .Q(p_x_y), .clk(comparator_3_eq));  // open: en, clr
  assign where = comparator_4_eq ? x_y_1_elonmap_2 : 12'bz;  // Controlled_Buffer controlled_buffer_2
  Register register_3 (.D(objMap), .Q(p_x_y_1), .clk(comparator_5_eq));  // open: en, clr
  assign where = comparator_6_eq ? x_y_1_elonmap : 12'bz;  // Controlled_Buffer controlled_buffer_3
  Register register_4 (.D(objMap), .Q(p_x_y_1_2), .clk(comparator_7_eq));  // open: en, clr
  assign where = comparator_8_eq ? x_1_y_elonmap_2 : 12'bz;  // Controlled_Buffer controlled_buffer_4
  Register register_5 (.D(objMap), .Q(p_x_1_y), .clk(comparator_9_eq));  // open: en, clr
  assign where = comparator_10_eq ? x_1_y_elonmap : 12'bz;  // Controlled_Buffer controlled_buffer_5
  Register register_6 (.D(objMap), .Q(p_x_1_y_2), .clk(comparator_11_eq));  // open: en, clr
  assign where = comparator_12_eq ? p_x_2_y__elemOnMap : 12'bz;  // Controlled_Buffer controlled_buffer_6
  Register register_7 (.D(objMap), .Q(p_x_2_y), .clk(comparator_13_eq));  // open: en, clr
  assign where = comparator_14_eq ? p_x_2_y__elemOnMap_t : 12'bz;  // Controlled_Buffer controlled_buffer_7
  Register register_8 (.D(objMap), .Q(p_x_2_y_2), .clk(comparator_15_eq));  // open: en, clr
  assign where = comparator_16_eq ? p_x_y_2__elemOnMap_t : 12'bz;  // Controlled_Buffer controlled_buffer_8
  Register register_9 (.D(objMap), .Q(p_x_y_2), .clk(comparator_17_eq));  // open: en, clr
  assign where = comparator_18_eq ? p_x_y_2__elemOnMap : 12'bz;  // Controlled_Buffer controlled_buffer_9
  Register register_10 (.D(objMap), .Q(p_x_y_2_2), .clk(comparator_19_eq));  // open: en, clr
  Adder adder_2 (.a(y), .b(8'h1), .out(adder_2_out));  // open: cin, cout
  Adder adder_3 (.a(x), .b(8'h1), .out(adder_3_out));  // open: cin, cout
  x_y__to_memory_elem_number x_y_____elem (.H(mapW), .Y(y), .X(x), .ELEM(x_y_elonmap), .START(12'h4));
  x_y__to_memory_elem_number x_y_____elem_2 (.H(mapW), .Y(adder_2_out), .X(x), .ELEM(x_y_1_elonmap), .START(12'h4));
  x_y__to_memory_elem_number x_y_____elem_3 (.H(mapW), .Y(y), .X(adder_3_out), .ELEM(x_1_y_elonmap), .START(12'h4));
  Subtractor subtractor_1 (.a(y), .b(8'h1), .out(subtractor_1_out));  // open: bin, bout
  Subtractor subtractor_2 (.a(x), .b(8'h1), .out(subtractor_2_out));  // open: bin, bout
  Adder adder_4 (.a(x), .b(8'h2), .out(adder_4_out));  // open: cin, cout
  x_y__to_memory_elem_number x_y_____elem_4 (
    .H(mapW), .Y(subtractor_1_out), .X(x), .ELEM(x_y_1_elonmap_2), .START(12'h4));
  x_y__to_memory_elem_number x_y_____elem_5 (
    .H(mapW), .Y(y), .X(subtractor_2_out), .ELEM(x_1_y_elonmap_2), .START(12'h4));
  x_y__to_memory_elem_number x_y_____elem_6 (
    .H(mapW), .Y(y), .X(adder_4_out), .ELEM(p_x_2_y__elemOnMap), .START(12'h4));
  Subtractor subtractor_3 (.a(y), .b(8'h2), .out(subtractor_3_out));  // open: bin, bout
  Subtractor subtractor_4 (.a(x), .b(8'h2), .out(subtractor_4_out));  // open: bin, bout
  Adder adder_5 (.a(x), .b(8'h2), .out(adder_5_out));  // open: cin, cout
  x_y__to_memory_elem_number x_y_____elem_7 (
    .H(mapW), .Y(subtractor_3_out), .X(x), .ELEM(p_x_y_2__elemOnMap_t), .START(12'h4));
  x_y__to_memory_elem_number x_y_____elem_8 (
    .H(mapW), .Y(y), .X(subtractor_4_out), .ELEM(p_x_2_y__elemOnMap_t), .START(12'h4));
  x_y__to_memory_elem_number x_y_____elem_9 (
    .H(mapW), .Y(adder_5_out), .X(y), .ELEM(p_x_y_2__elemOnMap));  // open: START

  // Other names for the same wires on the sheet: mainClk = MainCLC; MAP_tospace_ELEM[11:0] = where;
  //   objectONmap[7:0] = objMap; p__y_2_mi[7:0] = p_x_y_2_2; p_x_1_y__elemOnMap[11:0] = x_1_y_elonmap;
  //   p_x_1_y__elemOnMap_t[11:0] = x_1_y_elonmap_2; p_x_1_y_mi[7:0] = p_x_1_y_2; p_x_1_y_mi_t[7:0] = p_x_1_y;
  //   p_x_2_y_mi[7:0] = p_x_2_y; p_x_2_y_mi_t[7:0] = p_x_2_y_2; p_x_y_1__elemOnMap[11:0] = x_y_1_elonmap;
  //   p_x_y_1__elemOnMap_t[11:0] = x_y_1_elonmap_2; p_x_y_1_mi[7:0] = p_x_y_1_2; p_x_y_1_mi_t[7:0] = p_x_y_1;
  //   p_x_y_2_mi[7:0] = p_x_y_2; p_x_y__elemOnMap[11:0] = x_y_elonmap; p_x_y_mi[7:0] = p_x_y; PLxOM[7:0] = x;
  //   PLyOM[7:0] = y

  // Notes on the sheet:
  //   GET SOME ADJACENT CELLS
  //   Player (y+1,x) cell
  //   Player (y,x+1) cell
  //   Player cell
  //   Player (y-1,x) cell
  //   Player (y,x-1) cell
  //   Player (y,x+2) cell
  //   GET SOME ADJACENT CELLS COORDINATES
  //   Player (y-2,x) cell
  //   Player (y,x-2) cell
  //   Player (y+2,x) cell
endmodule

module printText (
  input  [25:0] Input,
  output [6:0] char,
  output ptd,
  output res,
  output pTclc
);

  wire comparator_1_eq;
  wire [6:0] adder_1_out, register_1_q;

  Register #(.width(7)) register_1 (.D(adder_1_out), .en(ptd), .Q(register_1_q), .clk(Input[19]), .clr(Input[20]));
  Comparator #(.width(7)) comparator_1 (.a(Input[18:12]), .b(adder_1_out), .eq(comparator_1_eq));  // open: gt, lt
  Adder #(.width(7)) adder_1 (.a(7'b0000001), .b(register_1_q), .out(adder_1_out));  // open: cin, cout
  TextS texts_1 (.enemy_item(Input[11:6]), .Addr(Input[25:21]), .N(register_1_q), .Char(char));
  not not_1 (ptd, comparator_1_eq);

  assign pTclc = Input[19];
  assign res = Input[20];

  // Other names for the same wires on the sheet: pTres = Input[20]; pEIn[5:0] = Input[11:6];
  //   pTmxLen[6:0] = Input[18:12]; pTptd = ptd; pTtxt[4:0] = Input[25:21]

  // Notes on the sheet:
  //   squre screen length = 21
  //   Item name length = 13
  //   text length = 64
  //   main screen length = 44
endmodule

module printItem (
  input  [7:0] item,
  output [8:0] str1,
  output [8:0] str5,
  output [8:0] str9,
  output [8:0] str2,
  output [8:0] str6,
  output [8:0] str3,
  output [8:0] str7,
  output [8:0] str4,
  output [8:0] str8
);

  wire [3:0] pIitemImg;
  wire [7:0] subtractor_1_out;

  Bit_Extender #(.out_width(4)) bit_extender_1 (.in(subtractor_1_out), .out(pIitemImg));
  Subtractor subtractor_1 (.a(item), .b(8'h60), .out(subtractor_1_out));  // open: bin, bout
  Multiplexer #(.select(4), .width(9), .enable("false")) multiplexer_1 (
    .in0({9{1'b1}}), .out(str1), .sel(pIitemImg));  // open: in1, in2, in3, in4, in5, in6, in7, in8, in9, in10, in11, in12, in13, in14, in15
  Multiplexer #(.select(4), .width(9), .enable("false")) multiplexer_2 (
    .in0({9{1'b1}}), .out(str2), .sel(pIitemImg));  // open: in1, in2, in3, in4, in5, in6, in7, in8, in9, in10, in11, in12, in13, in14, in15
  Multiplexer #(.select(4), .width(9), .enable("false")) multiplexer_3 (
    .in0({9{1'b1}}), .out(str3), .sel(pIitemImg));  // open: in1, in2, in3, in4, in5, in6, in7, in8, in9, in10, in11, in12, in13, in14, in15
  Multiplexer #(.select(4), .width(9), .enable("false")) multiplexer_4 (
    .in0({9{1'b1}}), .out(str4), .sel(pIitemImg));  // open: in1, in2, in3, in4, in5, in6, in7, in8, in9, in10, in11, in12, in13, in14, in15
  Multiplexer #(.select(4), .width(9), .enable("false")) multiplexer_5 (
    .in0({9{1'b1}}), .out(str5), .sel(pIitemImg));  // open: in1, in2, in3, in4, in5, in6, in7, in8, in9, in10, in11, in12, in13, in14, in15
  Multiplexer #(.select(4), .width(9), .enable("false")) multiplexer_6 (
    .in0({9{1'b1}}), .out(str6), .sel(pIitemImg));  // open: in1, in2, in3, in4, in5, in6, in7, in8, in9, in10, in11, in12, in13, in14, in15
  Multiplexer #(.select(4), .width(9), .enable("false")) multiplexer_7 (
    .in0({9{1'b1}}), .out(str7), .sel(pIitemImg));  // open: in1, in2, in3, in4, in5, in6, in7, in8, in9, in10, in11, in12, in13, in14, in15
  Multiplexer #(.select(4), .width(9), .enable("false")) multiplexer_8 (
    .in0({9{1'b1}}), .out(str8), .sel(pIitemImg));  // open: in1, in2, in3, in4, in5, in6, in7, in8, in9, in10, in11, in12, in13, in14, in15
  Multiplexer #(.select(4), .width(9), .enable("false")) multiplexer_9 (
    .in0({9{1'b1}}), .out(str9), .sel(pIitemImg));  // open: in1, in2, in3, in4, in5, in6, in7, in8, in9, in10, in11, in12, in13, in14, in15
endmodule

module printHP (
  input  [7:0] Inp,
  input  print,
  output [3:0] High,
  output [3:0] Low
);

  wire not_1_out;
  wire [3:0] bit_extender_1_out, bit_extender_2_out;
  wire [7:0] divider_1_out, multiplier_1_out, subtractor_1_out;

  Bit_Extender #(.out_width(4)) bit_extender_1 (.in(divider_1_out), .out(bit_extender_1_out));
  Divider divider_1 (.a(Inp), .b(8'ha), .out(divider_1_out));  // open: upper, rem
  Subtractor subtractor_1 (.a(Inp), .b(multiplier_1_out), .out(subtractor_1_out));  // open: bin, bout
  Multiplier multiplier_1 (.a(divider_1_out), .b(8'ha), .out(multiplier_1_out));  // open: cin, cout
  Multiplexer #(.width(4), .enable("false")) multiplexer_1 (
    .in0(bit_extender_1_out), .out(High), .sel(not_1_out));  // open: in1
  Bit_Extender #(.out_width(4)) bit_extender_2 (.in(subtractor_1_out), .out(bit_extender_2_out));
  not not_1 (not_1_out, print);
  Multiplexer #(.width(4), .enable("false")) multiplexer_2 (
    .in0(bit_extender_2_out), .out(Low), .sel(not_1_out));  // open: in1

  // Notes on the sheet:
  //   inp (8 sysytem) to 10 system*
endmodule
module TextS (
  input  [5:0] enemy_item,
  input  [4:0] Addr,
  input  [6:0] N,
  output [6:0] Char
);

  wire and_1_out, and_2_out, and_3_out, and_4_out, and_5_out, comparator_1_eq, comparator_2_eq,
       comparator_3_lt, comparator_4_gt, comparator_5_eq, comparator_6_lt, comparator_7_gt, comparator_8_eq,
       newN11, or_1_out;
  wire [3:0] bit_extender_1_out, bit_extender_2_out;
  wire [6:0] controlled_buffer_1_out, iemN, multiplexer_2_out, multiplexer_4_out, TSbf, TSCh1, TSCh2, TSCh3,
       TSCh4, TSCh5, TSCh6, TSCh7, TSCh8, TSCh9, TSCh10, TSCh11, TSCh12, TSCh13, TSCh14, TSCh15, TSCh16,
       TSCh17, TSCh18, TSCh19, TSCh20, TSCh21, TSCh22, TSCh23, TSCh24, TSCh25, TScu, TSn, TSnb, TSnbn, TSnc,
       TSncf, TSncl, TSncm, TSncr, TSncs, TSns, TSnst, TSnw, undriven, undriven_2, undriven_3;

  Multiplexer #(.width(7), .enable("false")) multiplexer_1 (.in0(N), .in1(iemN), .out(TSn), .sel(newN11));
  ROM #(.addrWidth(7), .dataWidth(7)) rom_1 (.addr(TSn), .data(TSCh1));  // open: sel
  ROM #(.addrWidth(7), .dataWidth(7)) rom_2 (.addr(TSn), .data(TSCh2));  // open: sel
  ROM #(.addrWidth(7), .dataWidth(7)) rom_3 (.addr(TSn), .data(TSCh3));  // open: sel
  ROM #(.addrWidth(7), .dataWidth(7)) rom_4 (.addr(TSn), .data(TSCh4));  // open: sel
  ROM #(.addrWidth(7), .dataWidth(7)) rom_5 (.addr(TSn), .data(TSCh5));  // open: sel
  ROM #(.addrWidth(7), .dataWidth(7)) rom_6 (.addr(TSn), .data(TSCh6));  // open: sel
  ROM #(.addrWidth(7), .dataWidth(7)) rom_7 (.addr(TSn), .data(TSCh7));  // open: sel
  ROM #(.addrWidth(7), .dataWidth(7)) rom_8 (.addr(TSn), .data(TSCh8));  // open: sel
  ROM #(.addrWidth(7), .dataWidth(7)) rom_9 (.addr(TSn), .data(TSCh9));  // open: sel
  Multiplexer #(.select(5), .width(7), .enable("false")) multiplexer_2 (
    .in0({7{1'b0}}), .in1(TSCh1), .in2(TSCh2), .in3(TSCh3), .in4(TSCh4), .in5(TSCh5), .in6(TSCh6),
    .in7(TSCh7), .in8(TSCh8), .in9(TSCh9), .in10(TSCh10), .in11(TSCh11), .in12(TSCh12), .in13(TSCh13),
    .in14(TSCh14), .in15(TSCh15), .in16(TSCh16), .in17(TSCh17), .in18(TSCh18), .in19(TSCh19), .in20(TSCh20),
    .in21(TSCh21), .in22(TSCh22), .in23(TSCh23), .in24(TSCh24), .in25(TSCh25), .out(multiplexer_2_out),
    .sel(Addr));  // open: in26, in27, in28, in29, in30, in31
  Comparator #(.width(5), .mode("unsigned")) comparator_1 (
    .a(Addr), .b(5'b10100), .eq(comparator_1_eq));  // open: gt, lt
  Multiplexer #(.width(7), .enable("false")) multiplexer_3 (
    .in0(multiplexer_2_out), .in1(controlled_buffer_1_out), .out(Char), .sel(and_1_out));
  and and_1 (and_1_out, or_1_out, newN11);
  or or_1 (or_1_out, comparator_1_eq, comparator_2_eq, comparator_5_eq, comparator_8_eq);
  Comparator #(.width(5), .mode("unsigned")) comparator_2 (
    .a(Addr), .b(5'b10101), .eq(comparator_2_eq));  // open: gt, lt
  ROM #(.addrWidth(7), .dataWidth(7)) rom_10 (.addr(TSn), .data(TSCh10));  // open: sel
  ROM #(.addrWidth(7), .dataWidth(7)) rom_11 (.addr(TSn), .data(TSCh11));  // open: sel
  ROM #(.addrWidth(7), .dataWidth(7)) rom_12 (.addr(TSn), .data(TSCh12));  // open: sel
  ROM #(.addrWidth(7), .dataWidth(7)) rom_13 (.addr(TSn), .data(TSCh13));  // open: sel
  ROM #(.addrWidth(7), .dataWidth(7)) rom_14 (.addr(TSn), .data(TSCh15));  // open: sel
  ROM #(.addrWidth(7), .dataWidth(7)) rom_15 (.addr(TSn), .data(TSCh16));  // open: sel
  ROM #(.addrWidth(7), .dataWidth(7)) rom_16 (.addr(TSn), .data(TSCh17));  // open: sel
  ROM #(.addrWidth(7), .dataWidth(7)) rom_17 (.addr(TSn), .data(TSCh18));  // open: sel
  ROM #(.addrWidth(7), .dataWidth(7)) rom_18 (.addr(TSn), .data(TSCh19));  // open: sel
  Comparator #(.width(7), .mode("unsigned")) comparator_3 (
    .a(N), .b(7'b0011001), .lt(comparator_3_lt));  // open: gt, eq
  and and_2 (and_2_out, comparator_3_lt, comparator_4_gt);
  and and_3 (and_3_out, and_2_out, comparator_5_eq);
  Comparator #(.width(7), .mode("unsigned")) comparator_4 (
    .a(N), .b(7'b0001111), .gt(comparator_4_gt));  // open: eq, lt
  Comparator #(.width(5), .mode("unsigned")) comparator_5 (
    .a(Addr), .b(5'b10110), .eq(comparator_5_eq));  // open: gt, lt
  Comparator #(.width(7), .mode("unsigned")) comparator_6 (
    .a(N), .b(7'b0111101), .lt(comparator_6_lt));  // open: gt, eq
  Comparator #(.width(7), .mode("unsigned")) comparator_7 (
    .a(N), .b(7'b0101000), .gt(comparator_7_gt));  // open: eq, lt
  Comparator #(.width(5), .mode("unsigned")) comparator_8 (
    .a(Addr), .b(5'b10111), .eq(comparator_8_eq));  // open: gt, lt
  assign controlled_buffer_1_out = newN11 ? multiplexer_4_out : 7'bz;  // Controlled_Buffer controlled_buffer_1
  and and_4 (and_4_out, comparator_6_lt, comparator_7_gt);
  and and_5 (and_5_out, and_4_out, comparator_8_eq);
  or or_2 (newN11, and_3_out, and_5_out);
  ROM #(.addrWidth(7), .dataWidth(7)) rom_19 (.addr(TSn), .data(TSCh14));  // open: sel
  ROM #(.addrWidth(7), .dataWidth(7)) rom_20 (.addr(TSn), .data(TSCh20));  // open: sel
  ROM #(.addrWidth(7), .dataWidth(7)) rom_21 (.addr(TSn), .data(TSCh21));  // open: sel
  ROM #(.addrWidth(7), .dataWidth(7)) rom_22 (.addr(TSn), .data(TSCh22));  // open: sel
  ROM #(.addrWidth(7), .dataWidth(7)) rom_23 (.addr(TSn), .data(TSCh23));  // open: sel
  ROM #(.addrWidth(7), .dataWidth(7)) rom_24 (.addr(TSn), .data(TSCh24));  // open: sel
  ROM #(.addrWidth(7), .dataWidth(7)) rom_25 (.addr(TSn), .data(TSCh25));  // open: sel
  Multiplexer #(.select(4), .width(7), .enable("false")) multiplexer_4 (
    .in0(TSCh6), .in1(TSCh7), .in2(TSCh8), .in3(TSCh9), .in4(TSCh10), .in5(TSCh11), .in6(TSCh12),
    .in7(TSCh13), .in9(TSCh15), .in10(TSCh16), .in11(TSCh17), .in12(TSCh18), .in13(TSCh19), .in14(undriven),
    .in15(undriven_2), .out(multiplexer_4_out), .sel(bit_extender_1_out));  // open: in8
  Bit_Extender #(.in_width(6), .out_width(4)) bit_extender_1 (.in(enemy_item), .out(bit_extender_1_out));
  Subtractor #(.width(7)) subtractor_1 (.a(N), .b(7'b0100011), .out(TSncr));  // open: bin, bout
  Subtractor #(.width(7)) subtractor_2 (.a(N), .b(7'b0100100), .out(TSncm));  // open: bin, bout
  Subtractor #(.width(7)) subtractor_3 (.a(N), .b(7'b0100101), .out(TSncf));  // open: bin, bout
  Subtractor #(.width(7)) subtractor_4 (.a(N), .b(7'b0100101), .out(TSncs));  // open: bin, bout
  Subtractor #(.width(7)) subtractor_5 (.a(N), .b(7'b0001100), .out(TSnb));  // open: bin, bout
  Subtractor #(.width(7)) subtractor_6 (.a(N), .b(7'b0001110), .out(TSns));  // open: bin, bout
  Subtractor #(.width(7)) subtractor_7 (.a(N), .b(7'b0010000), .out(TSnc));  // open: bin, bout
  Subtractor #(.width(7)) subtractor_8 (.a(N), .b(7'b0001101), .out(TSnw));  // open: bin, bout
  Subtractor #(.width(7)) subtractor_9 (.a(N), .b(7'b0001101), .out(TSnst));  // open: bin, bout
  Subtractor #(.width(7)) subtractor_10 (.a(N), .b(7'b0001101), .out(TSnbn));  // open: bin, bout
  Subtractor #(.width(7)) subtractor_11 (.a(N), .b(7'b0001100), .out(TSncl));  // open: bin, bout
  Subtractor #(.width(7)) subtractor_12 (.a(N), .b(7'b0001110), .out(TScu));  // open: bin, bout
  Subtractor #(.width(7)) subtractor_13 (.a(N), .b(7'b0001110), .out(TSbf));  // open: bin, bout
  Multiplexer #(.select(4), .width(7), .enable("false")) multiplexer_5 (
    .in0(TSncr), .in1(TSncm), .in2(TSncf), .in3(TSncs), .in4(TSnb), .in5(TSns), .in6(TSnc), .in7(TSnw),
    .in9(TSnst), .in10(TSnbn), .in11(TSncl), .in12(TScu), .in13(TSbf), .in14(undriven_3), .out(iemN),
    .sel(bit_extender_2_out));  // open: in8, in15
  Bit_Extender #(.in_width(6), .out_width(4)) bit_extender_2 (.in(enemy_item), .out(bit_extender_2_out));

  // Other names for the same wires on the sheet: TSb[6:0] = N

  // Notes on the sheet:
  //   Welcome to moles burrow!
  //   contents of rom_1 (hex, n*v repeats v):
  //   57 45 4c 43 4f 4d 45 20 54 4f 20 54 48 45 20 4d 4f 4c 45 20 42 55 52 52 4f 57 21 20 20 47 61 6d 65
  //   20 77 68 65 72 65 20 79 6f 75 20 61 72 65 20 4d 6f 6c 65 20 61 67 61 69 6e 73 74 20 65 76 65 72 79
  //   6f 6e 65
  //   contents of rom_2 (hex, n*v repeats v):
  //   4*20 54 48 52 45 45 2d 44 49 4d 45 4e 53 49 4f 4e 41 4c 20 56 49 45 57 20 4f 46 20 54 48 45 20 42 55
  //   52 52 4f 57 4*20
  //   contents of rom_3 (hex, n*v repeats v):
  //   18*20 49 54 20 49 53 20 59 4f 55 17*20
  //   contents of rom_4 (hex, n*v repeats v):
  //   7*20 4d 49 4e 49 4d 41 50 7*20
  //   contents of rom_6 (hex, n*v repeats v):
  //   6*20 53 43 41 52 59 20 52 41 54 5*20
  //   contents of rom_7 (hex, n*v repeats v):
  //   5*20 45 56 49 4c 20 4d 4f 55 53 45 5*20
  //   contents of rom_8 (hex, n*v repeats v):
  //   4*20 43 55 54 45 20 46 45 52 52 45 54 5*20
  //   contents of rom_9 (hex, n*v repeats v):
  //   4*20 4c 49 54 54 4c 45 20 53 4e 41 4b 45 4*20
  //   3d view
  //   its you
  //   minimap(11)
  //   enemy(11)
  //   rat
  //   mouse
  //   ferret
  //   snake
  //   (13)
  //   contents of rom_10 (hex, n*v repeats v):
  //   4*20 42 55 47 4*20
  //   contents of rom_11 (hex, n*v repeats v):
  //   20 20 53 50 49 44 45 52 20 20 20
  //   contents of rom_12 (hex, n*v repeats v):
  //   43 45 4e 54 49 50 45 44 45 20 20
  //   contents of rom_13 (hex, n*v repeats v):
  //   20 20 20 57 4f 52 4d 4*20
  //   contents of rom_14 (hex, n*v repeats v):
  //   20 20 20 53 54 49 43 4b 20 20 20
  //   contents of rom_15 (hex, n*v repeats v):
  //   20 20 20 42 4f 4e 45 4*20
  //   contents of rom_16 (hex, n*v repeats v):
  //   4*20 43 4c 41 57 20 20 20
  //   contents of rom_17 (hex, n*v repeats v):
  //   20 20 43 55 44 47 45 4c 20 20 20
  //   contents of rom_18 (hex, n*v repeats v):
  //   20 20 42 46 47 39 30 30 30 20 20
  //   BUG
  //   SPIDER
  //   CENTIPEDE
  //   WORM
  //   STICK
  //   BONE
  //   CLAW
  //   CUDGEL
  //   BFG9000
  //   (66)
  //   contents of rom_19 (hex, n*v repeats v):
  //   19*20 50 52 45 53 53 20 41 4e 59 20 4b 45 59 20 54 4f 20 53 54 41 52 54 20 47 41 4d 45 20*20
  //   contents of rom_20 (hex, n*v repeats v):
  //   6*20 59 4f 55 20 48 41 56 45 20 44 45 41 4c 54 4*20 44 41 4d 41 47 45 2e 20 54 48 45 20 45 4e 45 4d
  //   59 20 48 41 53 20 44 45 41 4c 54 4*20 44 41 4d 41 47 45 5*20
  //   contents of rom_21 (hex, n*v repeats v):
  //   18*20 59 4f 55 20 48 41 56 45 20 44 45 46 45 41 54 45 44 20 59 4f 55 52 20 45 4e 45 4d 59 21 19*20
  //   contents of rom_22 (hex, n*v repeats v):
  //   6*20 59 4f 55 20 46 4f 55 4e 44 11*20 2e 20 57 48 49 43 48 20 53 4c 4f 54 20 57 49 4c 4c 20 59 4f 55
  //   20 54 41 4b 45 20 49 54 20 54 4f 3f 7*20
  //   contents of rom_23 (hex, n*v repeats v):
  //   17*20 59 4f 55 20 41 52 45 20 55 4e 44 45 52 20 41 54 54 41 43 4b 20 42 59 22*20 21 20 20 20
  //   contents of rom_24 (hex, n*v repeats v):
  //   59 4f 55 52 45 20 41 57 41 4b 45 2e 20 4f 4e 45 20 54 48 49 4e 47 20 49 53 20 43 4c 45 41 52 20 2d
  //   20 49 54 53 20 54 49 4d 45 20 54 4f 20 47 45 54 20 4f 55 54 20 4f 46 20 54 48 45 20 48 4f 4c 45 20
  //   press to continue
  //   you attak enemy
  //   you win
  //   you find
  //   you attaked by enemy
  //   you awake
  //   p
endmodule
