// Logisim project main2.circ as structural Verilog: 7 circuits, main circuit main
module main (
  output out_1,
  output [1:0] out_2
);

  wire and_1_out, and_2_out, and_3_out, and_9_out, and_10_out, and_11_out, and_12_out, and_13_out,
       and_14_out, and_15_out, and_16_out, and_17_out, and_18_out, ATCInpFlpre, ATCnewENclc, button_1_out,
       button_2_out, changePCx, changePCy, comparator_1_eq, comparator_2_eq, comparator_3_eq,
       comparator_4_eq, comparator_5_eq, comparator_6_lt, comparator_7_gt, comparator_8_lt, comparator_9_gt,
       comparator_10_lt, comparator_12_eq, comparator_13_eq, comparator_14_eq, comparator_15_eq,
       comparator_16_eq, comparator_17_eq, comparator_18_eq, comparator_19_eq, comparator_20_eq,
       comparator_21_eq, comparator_22_eq, comparator_23_eq, comparator_24_eq, comparator_25_eq,
       comparator_26_eq, comparator_30_eq, comparator_31_eq, comparator_32_eq, comparator_33_eq,
       comparator_34_eq, comparator_35_gt, comparator_36_gt, comparator_37_gt, comparator_38_gt,
       comparator_39_lt, comparator_40_lt, comparator_41_lt, comparator_42_lt, comparator_43_eq,
       CONSOLE_PRINTER_it_worked, gS0, gS1, gS2, InpFlmove1, InpFlmove2, InpFlmove3, InpFlmove31,
       InpFlmove32, InpFlmove33, InpFlmove34, InpFlmove35, InpFlpre, InpFlpreSTRT, INV1ch, INV2ch, INV3ch,
       INV4ch, INV5ch, INVENTORY1IIn, INVENTORY2IIn, INVENTORY3IIn, INVENTORY4IIn, INVENTORY5IIn, ITEMinCELL,
       letsPrint, LoadMap, mainClk, mainRES, MapLevelCh, mapPREst, memReadyToPrint, not_1_out, not_2_out,
       not_3_out, not_4_out, not_5_out, not_6_out, not_7_out, not_8_out, not_9_out, not_10_out, not_11_out,
       not_12_out, not_13_out, not_14_out, not_15_out, not_16_out, not_17_out, not_18_out, not_19_out,
       not_20_out, not_21_out, not_22_out, not_23_out, not_24_out, not_25_out, not_26_out, not_32_out,
       not_33_out, not_34_out, not_35_out, not_36_out, not_37_out, not_39_out, not_40_out, not_41_out,
       not_42_out, or_2_out, or_4_out, or_6_out, or_8_out, or_10_out, PlDirCh, qres, register_21_q,
       register_22_q, register_25_q, StateCh, stMapCLC, stMapCLC2, TOPRINTCh, TOPRINTRES, WonInp;
  wire [1:0] adder_2_out, ATCcurEN, ATCnewEN, bit_extender_1_out, bit_extender_2_out, bit_extender_3_out,
       bit_extender_4_out, gSto, NewPlDir, PlDir, subtractor_1_out;
  wire [2:0] adder_1_out, register_1_q;
  wire [7:0] adder_3_out, adder_4_out, adder_5_out, adder_6_out, ATCInpKey, CONSOLE_PRINTER_input_char,
       gStdtScrMem, InpKey, INVENTORY1, INVENTORY2, INVENTORY3, INVENTORY4, INVENTORY5, mapLevelCur,
       maps_1_xpp, maps_1_ypp, mapSTDATAreaded, memChar, multiplexer_1_out, multiplexer_2_out,
       multiplexer_6_out, NewMapLevelCh, NewPLxOM, NewPLyOM, NewTextTOPRINT, objectONmap, p_x_1_y, p_x_1_y_t,
       p_x_y, p_x_y_1, p_x_y_1_t, PLxOM, PLyOM, subtractor_2_out, subtractor_3_out, subtractor_4_out,
       subtractor_5_out, subtractor_6_out, subtractor_7_out, subtractor_8_out, subtractor_9_out, textTOPRINT;
  wire [11:0] adder_7_out, MAP_tospace_ELEM, MapH, maps_1_height, maps_1_width, mapSTelemREAD, MapW, memN,
       multiplexer_7_out, p_x_1_y__elemOnMap, p_x_1_y__elemOnMap_t, p_x_y_1__elemOnMap, p_x_y_1__elemOnMap_t,
       tpLen, x_y_____elem_elem;

  or or_1 (letsPrint, memReadyToPrint, gS0);
  not not_1 (not_1_out, InpFlpre);
  Comparator comparator_1 (.a(InpKey), .b(8'h31), .eq(comparator_1_eq));  // open: gt, lt
  Comparator comparator_2 (.a(InpKey), .b(8'h32), .eq(comparator_2_eq));  // open: gt, lt
  Comparator comparator_3 (.a(InpKey), .b(8'h33), .eq(comparator_3_eq));  // open: gt, lt
  Comparator comparator_4 (.a(InpKey), .b(8'h34), .eq(comparator_4_eq));  // open: gt, lt
  Comparator comparator_5 (.a(InpKey), .b(8'h35), .eq(comparator_5_eq));  // open: gt, lt
  Comparator comparator_6 (.a(objectONmap), .b(8'h65), .lt(comparator_6_lt));  // open: gt, eq
  and and_1 (and_1_out, comparator_6_lt, comparator_7_gt);
  Comparator comparator_7 (.a(objectONmap), .b(8'h60), .gt(comparator_7_gt));  // open: eq, lt
  Comparator comparator_8 (.a(objectONmap), .b(8'h6b), .lt(comparator_8_lt));  // open: gt, eq
  and and_2 (and_2_out, comparator_8_lt, comparator_9_gt);
  Comparator comparator_9 (.a(objectONmap), .b(8'h65), .gt(comparator_9_gt));  // open: eq, lt
  Demultiplexer #(.select(2), .disabled(0), .enable("false")) demultiplexer_1 (
    .out0(InpFlpreSTRT), .out1(InpFlpre), .out2(ATCInpFlpre), .in(CONSOLE_PRINTER_it_worked), .sel(out_2));  // open: out3
  consoler CONSOLE_PRINTER (
    .CLK(mainClk), .RESET(letsPrint), .IT_WORKED(CONSOLE_PRINTER_it_worked),
    .INPUT_CHAR(CONSOLE_PRINTER_input_char), .PRINT_SIZE(tpLen), .MEM_A(memN), .MEM_D(memChar));
  Multiplexer #(.width(8), .enable("false")) multiplexer_1 (
    .in0(NewPLxOM), .in1(maps_1_xpp), .out(multiplexer_1_out), .sel(gS0));
  or or_2 (or_2_out, changePCx, LoadMap);
  Register #(.width(12)) u_mapW (.D(maps_1_width), .Q(MapW), .clk(LoadMap));  // open: en, clr
  Register #(.width(3)) register_1 (.D(adder_1_out), .Q(register_1_q), .clk(and_3_out), .clr(TOPRINTRES));  // open: en
  and and_3 (and_3_out, comparator_10_lt, mainClk);
  Register #(.width(1)) register_2 (.D(InpFlpre), .Q(TOPRINTRES), .clk(InpFlpre), .clr(not_2_out));  // open: en
  not not_2 (not_2_out, not_1_out);
  and and_4 (InpFlmove31, comparator_1_eq, ITEMinCELL);
  not not_3 (not_3_out, InpFlmove31);
  and and_5 (InpFlmove32, comparator_2_eq, ITEMinCELL);
  not not_4 (not_4_out, InpFlmove32);
  and and_6 (InpFlmove33, comparator_3_eq, ITEMinCELL);
  not not_5 (not_5_out, InpFlmove33);
  and and_7 (InpFlmove34, comparator_4_eq, ITEMinCELL);
  not not_6 (not_6_out, InpFlmove34);
  and and_8 (InpFlmove35, comparator_5_eq, ITEMinCELL);
  not not_7 (not_7_out, InpFlmove35);
  or or_3 (ITEMinCELL, and_1_out, and_2_out);
  Demultiplexer #(.select(2), .width(8), .disabled(0), .enable("false")) demultiplexer_2 (
    .out1(InpKey), .out2(ATCInpKey), .in(CONSOLE_PRINTER_input_char), .sel(out_2));  // open: out0, out3
  Register Xpp (.D(multiplexer_1_out), .Q(PLxOM), .clk(or_2_out));  // open: en, clr
  Adder #(.width(3)) adder_1 (.a(3'b001), .b(register_1_q), .out(adder_1_out));  // open: cin, cout
  Comparator #(.width(3)) comparator_10 (.a(3'b111), .b(register_1_q), .gt(out_1), .lt(comparator_10_lt));  // open: eq
  // Probe on InpKey
  Comparator comparator_11 (.a(InpKey), .b(8'h77), .eq(WonInp));  // open: gt, lt
  Comparator #(.width(2)) comparator_12 (.a(PlDir), .b(2'b00), .eq(comparator_12_eq));  // open: gt, lt
  Comparator #(.width(2)) comparator_13 (.a(PlDir), .b(2'b10), .eq(comparator_13_eq));  // open: gt, lt
  Comparator #(.width(2)) comparator_14 (.a(PlDir), .b(2'b01), .eq(comparator_14_eq));  // open: gt, lt
  Comparator #(.width(2)) comparator_15 (.a(PlDir), .b(2'b11), .eq(comparator_15_eq));  // open: gt, lt
  Register #(.width(1)) register_3 (.D(InpFlmove31), .Q(INV1ch), .clk(InpFlmove31), .clr(not_8_out));  // open: en
  not not_8 (not_8_out, not_3_out);
  Register #(.width(1)) register_4 (.D(InpFlmove32), .Q(INV2ch), .clk(InpFlmove32), .clr(not_9_out));  // open: en
  not not_9 (not_9_out, not_4_out);
  Register #(.width(1)) register_5 (.D(InpFlmove33), .Q(INV3ch), .clk(InpFlmove33), .clr(not_10_out));  // open: en
  not not_10 (not_10_out, not_5_out);
  Register #(.width(1)) register_6 (.D(InpFlmove34), .Q(INV4ch), .clk(InpFlmove34), .clr(not_11_out));  // open: en
  not not_11 (not_11_out, not_6_out);
  Register #(.width(1)) register_7 (.D(InpFlmove35), .Q(INV5ch), .clk(InpFlmove35), .clr(not_12_out));  // open: en
  not not_12 (not_12_out, not_7_out);
  Register Ypp (.D(multiplexer_2_out), .Q(PLyOM), .clk(or_4_out));  // open: en, clr
  Multiplexer #(.width(8), .enable("false")) multiplexer_2 (
    .in0(NewPLyOM), .in1(maps_1_ypp), .out(multiplexer_2_out), .sel(gS0));
  or or_4 (or_4_out, changePCy, LoadMap);
  maps maps_1 (
    .ADDR(mapLevelCur), .ELEM(mapSTelemREAD), .DATA(mapSTDATAreaded), .Xpp(maps_1_xpp), .Ypp(maps_1_ypp),
    .Width(maps_1_width), .Height(maps_1_height));  // open: LEN
  Register #(.width(12)) u_mapH (.D(maps_1_height), .Q(MapH), .clk(LoadMap));  // open: en, clr
  Comparator comparator_16 (.a(p_x_y_1_t), .b(8'h23), .eq(comparator_16_eq));  // open: gt, lt
  not not_13 (not_13_out, comparator_16_eq);
  Comparator comparator_17 (.a(p_x_y_1), .b(8'h23), .eq(comparator_17_eq));  // open: gt, lt
  not not_14 (not_14_out, comparator_17_eq);
  not not_15 (not_15_out, comparator_18_eq);
  Comparator comparator_18 (.a(p_x_1_y), .b(8'h23), .eq(comparator_18_eq));  // open: gt, lt
  Comparator comparator_19 (.a(p_x_1_y_t), .b(8'h23), .eq(comparator_19_eq));  // open: gt, lt
  not not_16 (not_16_out, comparator_19_eq);
  or or_5 (InpFlmove3, InpFlmove31, InpFlmove32, InpFlmove33, InpFlmove34, InpFlmove35);
  Register register_8 (.D(NewMapLevelCh), .Q(mapLevelCur), .clk(MapLevelCh), .clr(mainRES));  // open: en
  Register register_9 (.D(NewTextTOPRINT), .Q(textTOPRINT), .clk(TOPRINTCh), .clr(or_6_out));  // open: en
  or or_6 (or_6_out, mainRES, TOPRINTRES);
  Comparator comparator_20 (.a(InpKey), .b(8'h61), .eq(comparator_20_eq));  // open: gt, lt
  not not_17 (not_17_out, InpFlmove1);
  or or_7 (InpFlmove1, comparator_20_eq, comparator_21_eq);
  Comparator comparator_21 (.a(InpKey), .b(8'h64), .eq(comparator_21_eq));  // open: gt, lt
  and and_9 (and_9_out, not_13_out, WonInp, comparator_12_eq);
  and and_10 (and_10_out, not_14_out, WonInp, comparator_13_eq);
  and and_11 (and_11_out, not_15_out, WonInp, comparator_14_eq);
  and and_12 (and_12_out, not_16_out, WonInp, comparator_15_eq);
  Register register_10 (.D(p_x_y), .Q(INVENTORY1), .clk(INV1ch), .clr(mainRES));  // open: en
  Register register_11 (.D(p_x_y), .Q(INVENTORY2), .clk(INV2ch), .clr(mainRES));  // open: en
  Register register_12 (.D(p_x_y), .Q(INVENTORY3), .clk(INV3ch), .clr(mainRES));  // open: en
  Register register_13 (.D(p_x_y), .Q(INVENTORY4), .clk(INV4ch), .clr(mainRES));  // open: en
  Register register_14 (.D(p_x_y), .Q(INVENTORY5), .clk(INV5ch), .clr(mainRES));  // open: en
  Adder #(.width(2)) adder_2 (.a(PlDir), .b(2'b01), .out(adder_2_out));  // open: cin, cout
  Subtractor #(.width(2)) subtractor_1 (.a(PlDir), .b(2'b01), .out(subtractor_1_out));  // open: bin, bout
  not not_18 (not_18_out, not_17_out);
  Register #(.width(1)) register_15 (.D(not_18_out), .Q(PlDirCh), .clk(not_18_out), .clr(not_20_out));  // open: en
  not not_19 (not_19_out, not_18_out);
  not not_20 (not_20_out, not_19_out);
  assign NewPLyOM = and_9_out ? subtractor_2_out : 8'bz;  // Controlled_Buffer controlled_buffer_1
  Subtractor subtractor_2 (.a(PLyOM), .b(8'h1), .out(subtractor_2_out));  // open: bin, bout
  assign NewPLyOM = and_10_out ? adder_3_out : 8'bz;  // Controlled_Buffer controlled_buffer_2
  Adder adder_3 (.a(PLyOM), .b(8'h1), .out(adder_3_out));  // open: cin, cout
  Adder adder_4 (.a(PLxOM), .b(8'h1), .out(adder_4_out));  // open: cin, cout
  assign NewPLxOM = and_11_out ? adder_4_out : 8'bz;  // Controlled_Buffer controlled_buffer_3
  Subtractor subtractor_3 (.a(PLxOM), .b(8'h1), .out(subtractor_3_out));  // open: bin, bout
  assign NewPLxOM = and_12_out ? subtractor_3_out : 8'bz;  // Controlled_Buffer controlled_buffer_4
  Register #(.width(2)) register_16 (.D(gSto), .Q(out_2), .clk(StateCh), .clr(mainRES));  // open: en
  Multiplexer #(.width(2), .enable("false")) multiplexer_3 (
    .in0(adder_2_out), .in1(subtractor_1_out), .out(NewPlDir), .sel(comparator_20_eq));
  Comparator comparator_22 (.a(INVENTORY1), .b({8{1'b0}}), .eq(comparator_22_eq));  // open: gt, lt
  Comparator comparator_23 (.a(INVENTORY2), .b({8{1'b0}}), .eq(comparator_23_eq));  // open: gt, lt
  Comparator comparator_24 (.a(INVENTORY3), .b({8{1'b0}}), .eq(comparator_24_eq));  // open: gt, lt
  Comparator comparator_25 (.a(INVENTORY4), .b({8{1'b0}}), .eq(comparator_25_eq));  // open: gt, lt
  Comparator comparator_26 (.a(INVENTORY5), .b({8{1'b0}}), .eq(comparator_26_eq));  // open: gt, lt
  Comparator #(.width(2)) comparator_27 (.a(2'b00), .b(out_2), .eq(gS0));  // open: gt, lt
  Comparator #(.width(2)) comparator_28 (.a(2'b01), .b(out_2), .eq(gS1));  // open: gt, lt
  Comparator #(.width(2)) comparator_29 (.a(2'b10), .b(out_2), .eq(gS2));  // open: gt, lt
  Register #(.width(2)) register_17 (.D(NewPlDir), .Q(PlDir), .clk(PlDirCh), .clr(mainRES));  // open: en
  Register #(.width(1)) register_18 (
    .D(comparator_30_eq), .Q(qres), .clk(comparator_30_eq), .clr(not_22_out));  // open: en
  Comparator comparator_30 (.a(InpKey), .b(8'h71), .eq(comparator_30_eq));  // open: gt, lt
  not not_21 (not_21_out, comparator_30_eq);
  not not_22 (not_22_out, not_21_out);
  Register #(.width(1)) register_19 (.D(or_8_out), .Q(changePCy), .clk(or_8_out), .clr(not_23_out));  // open: en
  or or_8 (or_8_out, and_9_out, and_10_out);
  not not_23 (not_23_out, not_24_out);
  not not_24 (not_24_out, or_8_out);
  or or_9 (InpFlmove2, or_8_out, or_10_out);
  Register #(.width(1)) register_20 (.D(or_10_out), .Q(changePCx), .clk(or_10_out), .clr(not_26_out));  // open: en
  or or_10 (or_10_out, and_11_out, and_12_out);
  not not_25 (not_25_out, or_10_out);
  not not_26 (not_26_out, not_25_out);
  not not_27 (INVENTORY1IIn, comparator_22_eq);
  not not_28 (INVENTORY2IIn, comparator_23_eq);
  not not_29 (INVENTORY3IIn, comparator_24_eq);
  not not_30 (INVENTORY4IIn, comparator_25_eq);
  not not_31 (INVENTORY5IIn, comparator_26_eq);
  Register #(.width(1)) register_21 (
    .D(and_13_out), .Q(register_21_q), .clk(and_13_out), .clr(not_32_out));  // open: en
  and and_13 (and_13_out, InpFlpreSTRT, gS0);
  not not_32 (not_32_out, not_33_out);
  not not_33 (not_33_out, and_13_out);
  buf buffer_1 (LoadMap, and_13_out);
  Register #(.width(1)) register_22 (
    .D(ATCnewENclc), .Q(register_22_q), .clk(ATCnewENclc), .clr(not_35_out));  // open: en
  not not_34 (not_34_out, ATCnewENclc);
  not not_35 (not_35_out, not_34_out);
  Comparator #(.width(2)) comparator_31 (.a(PlDir), .b(2'b00), .eq(comparator_31_eq));  // open: gt, lt
  Comparator #(.width(2)) comparator_32 (.a(PlDir), .b(2'b10), .eq(comparator_32_eq));  // open: gt, lt
  Comparator #(.width(2)) comparator_33 (.a(PlDir), .b(2'b01), .eq(comparator_33_eq));  // open: gt, lt
  Comparator #(.width(2)) comparator_34 (.a(PlDir), .b(2'b11), .eq(comparator_34_eq));  // open: gt, lt
  or or_11 (StateCh, register_21_q, register_22_q);
  Multiplexer #(.select(2), .width(2), .enable("false")) multiplexer_4 (
    .in0(2'b01), .in1(2'b10), .in2(2'b01), .out(gSto), .sel({gS2, gS1}));  // open: in3
  Multiplexer #(.select(2), .width(8), .enable("false")) multiplexer_5 (
    .in0(8'h1f), .in1({8{1'b0}}), .in2(8'h1e), .out(gStdtScrMem), .sel({gS2, gS1}));  // open: in3
  Subtractor subtractor_4 (.a(PLyOM), .b(8'h1), .out(subtractor_4_out));  // open: bin, bout
  Adder adder_5 (.a(PLyOM), .b(8'h1), .out(adder_5_out));  // open: cin, cout
  Subtractor subtractor_5 (.a(PLxOM), .b(8'h1), .out(subtractor_5_out));  // open: bin, bout
  Adder adder_6 (.a(PLxOM), .b(8'h1), .out(adder_6_out));  // open: cin, cout
  Register #(.width(2)) register_23 (.D(ATCnewEN), .Q(ATCcurEN), .clk(ATCnewENclc), .clr(mainRES));  // open: en
  Comparator comparator_35 (.a(p_x_y_1_t), .b(8'h30), .gt(comparator_35_gt));  // open: eq, lt
  Comparator comparator_36 (.a(p_x_y_1), .b(8'h30), .gt(comparator_36_gt));  // open: eq, lt
  Comparator comparator_37 (.a(p_x_1_y), .b(8'h30), .gt(comparator_37_gt));  // open: eq, lt
  Comparator comparator_38 (.a(p_x_1_y_t), .b(8'h30), .gt(comparator_38_gt));  // open: eq, lt
  x_y__to_memory_elem_number x_y_____elem (.H(MapW), .Y(PLyOM), .X(PLxOM), .ELEM(x_y_____elem_elem), .START(12'h4));
  x_y__to_memory_elem_number x_y_____elem_2 (
    .H(MapW), .Y(subtractor_4_out), .X(PLxOM), .ELEM(p_x_y_1__elemOnMap_t), .START(12'h4));
  x_y__to_memory_elem_number x_y_____elem_3 (
    .H(MapW), .Y(adder_5_out), .X(PLxOM), .ELEM(p_x_y_1__elemOnMap), .START(12'h4));
  x_y__to_memory_elem_number x_y_____elem_4 (
    .H(MapW), .Y(PLyOM), .X(subtractor_5_out), .ELEM(p_x_1_y__elemOnMap_t), .START(12'h4));
  x_y__to_memory_elem_number x_y_____elem_5 (
    .H(MapW), .Y(PLyOM), .X(adder_6_out), .ELEM(p_x_1_y__elemOnMap), .START(12'h4));
  Comparator comparator_39 (.a(p_x_y_1_t), .b(8'h35), .lt(comparator_39_lt));  // open: gt, eq
  Comparator comparator_40 (.a(p_x_y_1), .b(8'h35), .lt(comparator_40_lt));  // open: gt, eq
  Comparator comparator_41 (.a(p_x_1_y), .b(8'h35), .lt(comparator_41_lt));  // open: gt, eq
  Comparator comparator_42 (.a(p_x_1_y_t), .b(8'h35), .lt(comparator_42_lt));  // open: gt, eq
  assign MAP_tospace_ELEM = InpFlmove2 ? x_y_____elem_elem : 12'bz;  // Controlled_Buffer controlled_buffer_5
  Subtractor subtractor_6 (.a(p_x_y_1_t), .b(8'h31), .out(subtractor_6_out));  // open: bin, bout
  Subtractor subtractor_7 (.a(p_x_1_y_t), .b(8'h31), .out(subtractor_7_out));  // open: bin, bout
  assign MAP_tospace_ELEM = and_14_out ? p_x_y_1__elemOnMap_t : 12'bz;  // Controlled_Buffer controlled_buffer_6
  Bit_Extender #(.out_width(2)) bit_extender_1 (.in(subtractor_6_out), .out(bit_extender_1_out));
  assign ATCnewEN = and_14_out ? bit_extender_1_out : 2'bz;  // Controlled_Buffer controlled_buffer_7
  and and_14 (and_14_out, comparator_35_gt, comparator_39_lt, comparator_31_eq);
  and and_15 (and_15_out, comparator_36_gt, comparator_40_lt, comparator_32_eq);
  and and_16 (and_16_out, comparator_37_gt, comparator_41_lt, comparator_33_eq);
  and and_17 (and_17_out, comparator_38_gt, comparator_42_lt, comparator_34_eq);
  Bit_Extender #(.out_width(2)) bit_extender_2 (.in(subtractor_7_out), .out(bit_extender_2_out));
  assign ATCnewEN = and_17_out ? bit_extender_2_out : 2'bz;  // Controlled_Buffer controlled_buffer_8
  assign MAP_tospace_ELEM = and_17_out ? p_x_1_y__elemOnMap_t : 12'bz;  // Controlled_Buffer controlled_buffer_9
  Multiplexer #(.width(8), .enable("false")) multiplexer_6 (
    .in0(8'h20), .in1(mapSTDATAreaded), .out(multiplexer_6_out), .sel(not_40_out));
  Subtractor subtractor_8 (.a(p_x_y_1), .b(8'h31), .out(subtractor_8_out));  // open: bin, bout
  not not_36 (not_36_out, not_37_out);
  not not_37 (not_37_out, ATCnewENclc);
  or or_12 (ATCnewENclc, and_14_out, and_15_out, and_16_out, and_17_out);
  Subtractor subtractor_9 (.a(p_x_1_y), .b(8'h31), .out(subtractor_9_out));  // open: bin, bout
  Multiplexer #(.width(12), .enable("false")) multiplexer_7 (
    .in0(MAP_tospace_ELEM), .in1(mapSTelemREAD), .out(multiplexer_7_out), .sel(not_40_out));
  and and_18 (and_18_out, not_40_out, mainClk);
  Clock clock_1 (.out(mainClk));
  Button button_1 (.out(button_1_out));
  or or_13 (mainRES, button_1_out, qres);
  maps maps_2 (.ADDR(mapLevelCur), .ELEM(x_y_____elem_elem), .DATA(p_x_y));  // open: LEN, Xpp, Ypp, Width, Height
  maps maps_3 (
    .ADDR(mapLevelCur), .ELEM(p_x_y_1__elemOnMap_t), .DATA(p_x_y_1_t));  // open: LEN, Xpp, Ypp, Width, Height
  maps maps_4 (.ADDR(mapLevelCur), .ELEM(p_x_y_1__elemOnMap), .DATA(p_x_y_1));  // open: LEN, Xpp, Ypp, Width, Height
  maps maps_5 (
    .ADDR(mapLevelCur), .ELEM(p_x_1_y__elemOnMap_t), .DATA(p_x_1_y_t));  // open: LEN, Xpp, Ypp, Width, Height
  maps maps_6 (.ADDR(mapLevelCur), .ELEM(p_x_1_y__elemOnMap), .DATA(p_x_1_y));  // open: LEN, Xpp, Ypp, Width, Height
  assign MAP_tospace_ELEM = and_15_out ? p_x_y_1__elemOnMap : 12'bz;  // Controlled_Buffer controlled_buffer_10
  assign ATCnewEN = and_15_out ? bit_extender_3_out : 2'bz;  // Controlled_Buffer controlled_buffer_11
  Bit_Extender #(.out_width(2)) bit_extender_3 (.in(subtractor_8_out), .out(bit_extender_3_out));
  not not_38 (stMapCLC2, not_39_out);
  not not_39 (not_39_out, not_36_out);
  assign ATCnewEN = and_16_out ? bit_extender_4_out : 2'bz;  // Controlled_Buffer controlled_buffer_12
  Bit_Extender #(.out_width(2)) bit_extender_4 (.in(subtractor_9_out), .out(bit_extender_4_out));
  assign MAP_tospace_ELEM = and_16_out ? p_x_1_y__elemOnMap : 12'bz;  // Controlled_Buffer controlled_buffer_13
  Register #(.width(12)) register_24 (.D(adder_7_out), .Q(mapSTelemREAD), .clk(and_18_out), .clr(mainRES));  // open: en
  Adder #(.width(12)) adder_7 (.a(mapSTelemREAD), .b(12'h1), .out(adder_7_out));  // open: cin, cout
  graphic_elems graphic_elems_1 (.ADDR(gStdtScrMem), .ELEM(memN), .DATA(memChar), .LEN(tpLen));
  RAM #(.addrWidth(12), .bus("separate")) ram_1 (
    .addr(multiplexer_7_out), .din(multiplexer_6_out), .data(objectONmap), .str(mapPREst), .clk(stMapCLC));  // open: sel, ld, clr
  not not_40 (not_40_out, comparator_43_eq);
  Comparator #(.width(12)) comparator_43 (.a(mapSTelemREAD), .b(12'h94), .eq(comparator_43_eq));  // open: gt, lt
  or or_14 (stMapCLC, and_18_out, stMapCLC2, InpFlmove3);
  or or_15 (memReadyToPrint, button_2_out, register_25_q);
  Button button_2 (.out(button_2_out));
  Register #(.width(1)) register_25 (.D(out_1), .Q(register_25_q), .clk(out_1), .clr(not_41_out));  // open: en
  not not_41 (not_41_out, not_42_out);
  not not_42 (not_42_out, out_1);
  or or_16 (mapPREst, not_40_out, ATCnewENclc, InpFlmove3);
  enemies enemies_1 (.ADDR(ATCcurEN));  // open: ELEMIm, ELEMNm, Img, Txt, HP, DMG

  // Other names for the same wires on the sheet: gameState[1:0] = out_2; InpFl = out_1; chGM = ATCnewENclc;
  //   mapPREst2 = ATCnewENclc; p_x_y_obj[7:0] = objectONmap; mapPREst1 = InpFlmove3; stMapCLC1 = InpFlmove3

  // Notes on the sheet:
  //   its eat in cell
  //   inp: 1
  //   inp: 2
  //   inp: 3
  //   inp: 4
  //   inp: 5
  //   its weapon in cell
  //   MOVE PART
  //   inp: w
  //   START
  //   INVENTORY
  //   item теряется если взять вместо него
  //   inp: a
  //   inp: d
  //   Curent map level
  //   Curent text toprint
  //   Game state
  //   0 - start screen 1 - walking 2 - atack
  //   0
  //   ->
  //   3
  //   1
  //   2
  //   inp: q
  //   Player Direction
  //   ATACK MODE
  //   ПереРАБОТАТЬ КУСОК
  //   Player (y-1,x) cell
  //   Player (y+1,x) cell
  //   Player (y,x-1) cell
  //   Player (y,x+1) cell
  //   Current Enemy number
  //   СДЕЛАТЬ ЗНАЧЕНИЯ ЗАПОЛНЯЕМЫМИ С ДИНАМИЧЕСКОЙ КАРТЫ
  //   Player cell
  //   Player cell
  //   1 
  //   1 если прочитан вход
  //   (КОРОТКИЙ ИЛИ ДЛИННЫЙ)
  //   MAP
endmodule

// CP
module consoler (
  input  [7:0] MEM_D,
  input  CLK,
  input  [11:0] PRINT_SIZE,
  input  RESET,
  output IT_WORKED,
  output [7:0] INPUT_CHAR,
  output [11:0] MEM_A
);

  wire adder_1_out, and_3_out, and_4_out, clc, comparator_1_eq, not_1_out, not_2_out, not_3_out, not_4_out,
       not_5_out, or_1_out, PRND, readConsole, register_1_q, register_2_q, RES, RESET_MEMORY_COUNTER_out,
       uart_1_p3, uart_1_p6, uart_1_p8;
  wire [7:0] uart_1_p1;
  wire [11:0] adder_2_out;

  and and_1 (IT_WORKED, not_2_out, PRND, register_1_q);
  Register #(.width(1)) register_1 (.D(adder_1_out), .Q(register_1_q), .clk(or_1_out));  // open: en, clr
  or or_1 (or_1_out, RES, uart_1_p3);
  and and_2 (clc, CLK, not_1_out);
  not not_1 (not_1_out, RES);
  not not_2 (not_2_out, uart_1_p3);
  Adder #(.width(1)) adder_1 (.a(register_1_q), .b(1'b1), .out(adder_1_out));  // open: cin, cout
  not not_3 (not_3_out, RESET);
  and and_3 (and_3_out, clc, comparator_1_eq);
  Register #(.width(1)) register_2 (.D(RESET), .Q(register_2_q), .clk(RESET), .clr(not_4_out));  // open: en
  not not_4 (not_4_out, not_3_out);
  Register register_3 (.D(uart_1_p1), .Q(INPUT_CHAR), .clk(and_3_out), .clr(RES));  // open: en
  or or_2 (RES, register_2_q, RESET_MEMORY_COUNTER_out);
  Button RESET_MEMORY_COUNTER (.out(RESET_MEMORY_COUNTER_out));
  Comparator comparator_1 (.a(INPUT_CHAR), .b({8{1'b0}}), .eq(comparator_1_eq));  // open: gt, lt
  not not_5 (not_5_out, PRND);
  Register #(.width(12)) register_4 (.D(adder_2_out), .Q(MEM_A), .clk(and_4_out), .clr(RES));  // open: en
  not not_6 (readConsole, PRND);
  and and_4 (and_4_out, not_5_out, clc);
  // UART uart_1: pin names not known; wires that end beside it: uart_1_p1, MEM_D, uart_1_p3, clc, uart_1_p3, uart_1_p6, uart_1_p6, uart_1_p8
  Adder #(.width(12)) adder_2 (.a(MEM_A), .b(12'h1), .out(adder_2_out));  // open: cin, cout
  or or_3 (uart_1_p8, uart_1_p3, readConsole);
  Comparator #(.width(12)) comparator_2 (.a(MEM_A), .b(PRINT_SIZE), .eq(PRND));  // open: gt, lt

  // Notes on the sheet:
  //   Input writened
  //   12 бит адрес
  //   Frame Printed
  //   Print Frame
  //   A - Адрес к каторому обращается
  //   B - элемент по адресу
endmodule

// GE
module graphic_elems (
  input  [7:0] ADDR,
  input  [11:0] ELEM,
  output [7:0] DATA,
  output [11:0] LEN
);

  wire [7:0] deMux1, geD0, geD1, geD2, geD2_0, geD2_1, geD3, geD4, geD5, geD6, geD7, geD8, geD9, geD10,
       geD11, geD12, geD13, geD14, geD15;
  wire [11:0] deMuxl1;

  ROM #(.addrWidth(12)) rom_1 (.addr(ELEM), .data(geD0));  // open: sel
  ROM #(.addrWidth(12)) rom_2 (.addr(ELEM), .data(geD1));  // open: sel
  ROM #(.addrWidth(12)) rom_3 (.addr(ELEM), .data(geD2));  // open: sel
  ROM #(.addrWidth(12)) rom_4 (.addr(ELEM), .data(geD3));  // open: sel
  ROM #(.addrWidth(12)) rom_5 (.addr(ELEM), .data(geD4));  // open: sel
  ROM #(.addrWidth(12)) rom_6 (.addr(ELEM), .data(geD5));  // open: sel
  ROM #(.addrWidth(12)) rom_7 (.addr(ELEM), .data(geD6));  // open: sel
  ROM #(.addrWidth(12)) rom_8 (.addr(ELEM), .data(geD7));  // open: sel
  ROM #(.addrWidth(12)) rom_9 (.addr(ELEM), .data(geD8));  // open: sel
  ROM #(.addrWidth(12)) rom_10 (.addr(ELEM), .data(geD9));  // open: sel
  ROM #(.addrWidth(12)) rom_11 (.addr(ELEM), .data(geD10));  // open: sel
  ROM #(.addrWidth(12)) rom_12 (.addr(ELEM), .data(geD11));  // open: sel
  ROM #(.addrWidth(12)) rom_13 (.addr(ELEM), .data(geD12));  // open: sel
  ROM #(.addrWidth(12)) rom_14 (.addr(ELEM), .data(geD13));  // open: sel
  ROM #(.addrWidth(12)) rom_15 (.addr(ELEM), .data(geD14));  // open: sel
  ROM #(.addrWidth(12)) rom_16 (.addr(ELEM), .data(geD15));  // open: sel
  ROM #(.addrWidth(12)) rom_17 (.addr(ELEM), .data(geD2_0));  // open: sel
  ROM #(.addrWidth(12)) rom_18 (.addr(ELEM), .data(geD2_1));  // open: sel
  Multiplexer #(.select(5), .width(8), .enable("false")) multiplexer_1 (
    .in0(geD0), .in1(geD1), .in2(geD2), .in3(geD3), .in4(geD4), .in5(geD5), .in6(geD6), .in7(geD7),
    .in8(geD8), .in9(geD9), .in10(geD10), .in11(geD11), .in12(geD12), .in13(geD13), .in14(geD14),
    .in15(geD15), .in30(geD2_1), .in31(geD2_0), .out(deMux1), .sel(ADDR[4:0]));  // open: in16, in17, in18, in19, in20, in21, in22, in23, in24, in25, in26, in27, in28, in29
  Multiplexer #(.select(5), .width(12), .enable("false")) multiplexer_2 (
    .in0(12'had5), .in1(12'h596), .in2(12'h596), .in3(12'h596), .in4(12'h596), .in5(12'h596), .in6(12'h596),
    .in7(12'h596), .in8(12'h596), .in9(12'h596), .in10(12'h596), .in11(12'h596), .in12(12'h596),
    .in13(12'h596), .in14(12'h596), .in15(12'h596), .in30(12'had5), .in31(12'had5), .out(deMuxl1),
    .sel(ADDR[4:0]));  // open: in16, in17, in18, in19, in20, in21, in22, in23, in24, in25, in26, in27, in28, in29
  Multiplexer #(.select(3), .width(8), .enable("false")) multiplexer_3 (
    .in0(deMux1), .out(DATA), .sel(ADDR[7:5]));  // open: in1, in2, in3, in4, in5, in6, in7
  Multiplexer #(.select(3), .width(12), .enable("false")) multiplexer_4 (
    .in0(deMuxl1), .out(LEN), .sel(ADDR[7:5]));  // open: in1, in2, in3, in4, in5, in6, in7

  // Other names for the same wires on the sheet: geAddr1[4:0] = ADDR[4:0]; geAddr2[2:0] = ADDR[7:5];
  //   geEl[11:0] = ELEM

  // Notes on the sheet:
  //   BOARD
  //   contents of rom_1 (hex, n*v repeats v):
  //   0 76*23 a 23 52*20 23 21*20 23 a 23 52*20 23 21*20 23 a 23 52*20 23 21*20 23 a 23 52*20 23 21*20 23
  //   a 23 52*20 23 21*20 23 a 23 52*20 23 21*20 23 a 23 52*20 23 21*20 23 a 23 52*20 23 21*20 23 a 23
  //   52*20 23 21*20 23 a 23 52*20 23 21*20 23 a 23 52*20 23 21*20 23 a 23 52*20 23 21*20 23 a 23 52*20 23
  //   21*20 23 a 23 52*20 23 21*20 23 a 23 52*20 23 21*20 23 a 23 52*20 23 21*20 23 a 23 52*20 23 21*20 23
  //   a 23 52*20 23 21*20 23 a 23 52*20 23 21*20 23 a 23 52*20 23 21*20 23 a 23 52*20 23 21*20 23 a 23
  //   52*20 23*23 a 23 52*20 23 21*20 23 a 23 52*20 23 21*20 23 a 23 52*20 23 21*20 23 a 23 52*20 23 21*20
  //   23 a 23 52*20 23 21*20 23 a 76*23 a 23 74*20 23 a 76*23 a 23 9*20 23 9*20 23 9*20 23 9*20 23 9*20 23
  //   20 48 50 20 7c 10*20 7c 28 20 20 2f 31 30 29 20 23 a 23 9*20 23 9*20 23 9*20 23 9*20 23 9*20 23 20
  //   53 54 20 7c 10*20 7c 28 20 20 2f 31 30 29 20 23 a 23 9*20 23 9*20 23 9*20 23 9*20 23 9*20 23 20 48
  //   47 20 7c 10*20 7c 28 20 20 2f 31 30 29 20 23 a 23 9*20 23 9*20 23 9*20 23 9*20 23 9*20 23 24*20 23 a
  //   76*23 a 52*20
  //   FFL
  //   contents of rom_2 (hex, n*v repeats v):
  //   0 51*20 a 52*20 a 52*20 a 9*20 34*5f 9*20 a 8*20 7c 34*23 7c 8*20 a 8*20 7c 34*23 7c 8*20 a 8*20 7c
  //   34*23 7c 8*20 a 8*20 7c 34*23 7c 8*20 a 8*20 7c 34*23 7c 8*20 a 8*20 7c 34*23 7c 8*20 a 8*20 7c
  //   34*23 7c 8*20 a 8*20 7c 34*23 7c 8*20 a 8*20 7c 34*23 7c 8*20 a 8*20 7c 34*23 7c 8*20 a 8*20 7c
  //   34*23 7c 8*20 a 8*20 7c 34*23 7c 8*20 a 8*20 7c 34*23 7c 8*20 a 8*20 7c 34*23 7c 8*20 a 8*20 7c
  //   34*23 7c 8*20 a 8*20 7c 34*23 7c 8*20 a 8*20 7c 34*23 7c 8*20 a 8*20 7c 34*23 7c 8*20 a 8*20 7c
  //   34*23 7c 8*20 a 52*20 a 52*20 a 52*20 a 52*20
  //   FFFL
  //   contents of rom_3 (hex, n*v repeats v):
  //   0 51*20 a 52*20 a 52*20 a 52*20 a 52*20 a 52*20 a 52*20 a 18*20 16*5f 18*20 a 17*20 7c 16*23 7c
  //   17*20 a 17*20 7c 16*23 7c 17*20 a 17*20 7c 16*23 7c 17*20 a 17*20 7c 16*23 7c 17*20 a 17*20 7c 16*23
  //   7c 17*20 a 17*20 7c 16*23 7c 17*20 a 17*20 7c 16*23 7c 17*20 a 17*20 7c 16*23 7c 17*20 a 17*20 7c
  //   16*23 7c 17*20 a 17*20 7c 16*23 7c 17*20 a 17*20 7c 16*23 7c 17*20 a 52*20 a 52*20 a 52*20 a 52*20 a
  //   52*20 a 52*20 a 52*20 a 52*20
  //   FFFFL
  //   contents of rom_4 (hex, n*v repeats v):
  //   0 51*20 a 52*20 a 52*20 a 52*20 a 52*20 a 52*20 a 52*20 a 52*20 a 52*20 a 52*20 a 24*20 4*5f 24*20 a
  //   23*20 7c 4*23 7c 23*20 a 23*20 7c 4*23 7c 23*20 a 23*20 7c 4*23 7c 23*20 a 23*20 7c 4*23 7c 23*20 a
  //   23*20 7c 4*23 7c 23*20 a 52*20 a 52*20 a 52*20 a 52*20 a 52*20 a 52*20 a 52*20 a 52*20 a 52*20 a
  //   52*20 a 52*20
  //   LFL
  //   contents of rom_5 (hex, n*v repeats v):
  //   0 5c 5f 49*20 a 23 23 5c 5f 48*20 a 4*23 5c 5f 46*20 a 6*23 5c 5f 44*20 a 8*23 7c 43*20 a 8*23 7c
  //   43*20 a 8*23 7c 43*20 a 8*23 7c 43*20 a 8*23 7c 43*20 a 8*23 7c 43*20 a 8*23 7c 43*20 a 8*23 7c
  //   43*20 a 8*23 7c 43*20 a 8*23 7c 43*20 a 8*23 7c 43*20 a 8*23 7c 43*20 a 8*23 7c 43*20 a 8*23 7c
  //   43*20 a 8*23 7c 43*20 a 8*23 7c 43*20 a 8*23 7c 43*20 a 8*23 7c 43*20 a 8*23 7c 43*20 a 6*23 2f
  //   45*20 a 4*23 2f 47*20 a 23 23 2f 49*20 a 2f 51*20
  //   LFFL
  //   contents of rom_6 (hex, n*v repeats v):
  //   0 51*20 a 52*20 a 52*20 a 8*5f 44*20 a 8*23 7c 43*20 a 8*23 7c 43*20 a 8*23 7c 43*20 a 8*23 7c 43*20
  //   a 8*23 7c 43*20 a 8*23 7c 43*20 a 8*23 7c 43*20 a 8*23 7c 43*20 a 8*23 7c 43*20 a 8*23 7c 43*20 a
  //   8*23 7c 43*20 a 8*23 7c 43*20 a 8*23 7c 43*20 a 8*23 7c 43*20 a 8*23 7c 43*20 a 8*23 7c 43*20 a 8*23
  //   7c 43*20 a 8*23 7c 43*20 a 8*23 7c 43*20 a 52*20 a 52*20 a 52*20 a 52*20
  //   LFFFL
  //   contents of rom_7 (hex, n*v repeats v):
  //   0 51*20 a 52*20 a 52*20 a 52*20 a 52*20 a 52*20 a 52*20 a 17*5f 35*20 a 17*23 7c 34*20 a 17*23 7c
  //   34*20 a 17*23 7c 34*20 a 17*23 7c 34*20 a 17*23 7c 34*20 a 17*23 7c 34*20 a 17*23 7c 34*20 a 17*23
  //   7c 34*20 a 17*23 7c 34*20 a 17*23 7c 34*20 a 17*23 7c 34*20 a 52*20 a 52*20 a 52*20 a 52*20 a 52*20
  //   a 52*20 a 52*20 a 52*20
  //   LFFFFL
  //   contents of rom_8 (hex, n*v repeats v):
  //   0 51*20 a 52*20 a 52*20 a 52*20 a 52*20 a 52*20 a 52*20 a 52*20 a 52*20 a 52*20 a 18*20 5*5f 29*20 a
  //   17*20 7c 5*23 7c 28*20 a 17*20 7c 5*23 7c 28*20 a 17*20 7c 5*23 7c 28*20 a 17*20 7c 5*23 7c 28*20 a
  //   17*20 7c 5*23 7c 28*20 a 52*20 a 52*20 a 52*20 a 52*20 a 52*20 a 52*20 a 52*20 a 52*20 a 52*20 a
  //   52*20 a 52*20
  //   RFL
  //   contents of rom_9 (hex, n*v repeats v):
  //   0 50*20 5f 2f a 48*20 5f 2f 23 23 a 46*20 5f 2f 4*23 a 44*20 5f 2f 6*23 a 43*20 7c 8*23 a 43*20 7c
  //   8*23 a 43*20 7c 8*23 a 43*20 7c 8*23 a 43*20 7c 8*23 a 43*20 7c 8*23 a 43*20 7c 8*23 a 43*20 7c 8*23
  //   a 43*20 7c 8*23 a 43*20 7c 8*23 a 43*20 7c 8*23 a 43*20 7c 8*23 a 43*20 7c 8*23 a 43*20 7c 8*23 a
  //   43*20 7c 8*23 a 43*20 7c 8*23 a 43*20 7c 8*23 a 43*20 7c 8*23 a 43*20 7c 8*23 a 45*20 5c 6*23 a
  //   47*20 5c 4*23 a 49*20 5c 23 23 a 51*20 5c
  //   RFFL
  //   contents of rom_10 (hex, n*v repeats v):
  //   0 51*20 a 52*20 a 52*20 a 52*20 a 41*20 5f 2f 7c 8*20 a 39*20 5f 2f 23 23 7c 8*20 a 37*20 5f 2f 4*23
  //   7c 8*20 a 35*20 5f 2f 6*23 7c 8*20 a 34*20 7c 8*23 7c 8*20 a 34*20 7c 8*23 7c 8*20 a 34*20 7c 8*23
  //   7c 8*20 a 34*20 7c 8*23 7c 8*20 a 34*20 7c 8*23 7c 8*20 a 34*20 7c 8*23 7c 8*20 a 34*20 7c 8*23 7c
  //   8*20 a 34*20 7c 8*23 7c 8*20 a 34*20 7c 8*23 7c 8*20 a 34*20 7c 8*23 7c 8*20 a 34*20 7c 8*23 7c 8*20
  //   a 36*20 5c 6*23 7c 8*20 a 38*20 5c 4*23 7c 8*20 a 40*20 5c 23 23 7c 8*20 a 42*20 5c 7c 8*20 a 52*20
  //   a 52*20 a 52*20 a 52*20
  //   RFFFL
  //   contents of rom_11 (hex, n*v repeats v):
  //   0 51*20 a 52*20 a 52*20 a 52*20 a 52*20 a 52*20 a 52*20 a 35*20 17*5f a 34*20 7c 17*23 a 34*20 7c
  //   17*23 a 34*20 7c 17*23 a 34*20 7c 17*23 a 34*20 7c 17*23 a 34*20 7c 17*23 a 34*20 7c 17*23 a 34*20
  //   7c 17*23 a 34*20 7c 17*23 a 34*20 7c 17*23 a 34*20 7c 17*23 a 52*20 a 52*20 a 52*20 a 52*20 a 52*20
  //   a 52*20 a 52*20 a 52*20
  //   RFFFFL
  //   contents of rom_12 (hex, n*v repeats v):
  //   0 51*20 a 52*20 a 52*20 a 52*20 a 52*20 a 52*20 a 52*20 a 52*20 a 52*20 a 52*20 a 29*20 5*5f 18*20 a
  //   28*20 7c 5*23 7c 17*20 a 28*20 7c 5*23 7c 17*20 a 28*20 7c 5*23 7c 17*20 a 28*20 7c 5*23 7c 17*20 a
  //   28*20 7c 5*23 7c 17*20 a 52*20 a 52*20 a 52*20 a 52*20 a 52*20 a 52*20 a 52*20 a 52*20 a 52*20 a
  //   52*20 a 52*20
  //   FRFL
  //   contents of rom_13 (hex, n*v repeats v):
  //   0 51*20 a 52*20 a 52*20 a 52*20 a 41*20 5f 2f 7c 8*20 a 39*20 5f 2f 23 23 7c 8*20 a 37*20 5f 2f 4*23
  //   7c 8*20 a 35*20 5f 2f 6*23 7c 8*20 a 34*20 7c 8*23 7c 8*20 a 34*20 7c 8*23 7c 8*20 a 34*20 7c 8*23
  //   7c 8*20 a 34*20 7c 8*23 7c 8*20 a 34*20 7c 8*23 7c 8*20 a 34*20 7c 8*23 7c 8*20 a 34*20 7c 8*23 7c
  //   8*20 a 34*20 7c 8*23 7c 8*20 a 34*20 7c 8*23 7c 8*20 a 34*20 7c 8*23 7c 8*20 a 34*20 7c 8*23 7c 8*20
  //   a 36*20 5c 6*23 7c 8*20 a 38*20 5c 4*23 7c 8*20 a 40*20 5c 23 23 7c 8*20 a 42*20 5c 7c 8*20 a 52*20
  //   a 52*20 a 52*20 a 52*20
  //   FLFL
  //   contents of rom_14 (hex, n*v repeats v):
  //   0 51*20 a 52*20 a 52*20 a 52*20 a 8*20 7c 5c 5f 41*20 a 8*20 7c 23 23 5c 5f 39*20 a 8*20 7c 4*23 5c
  //   5f 37*20 a 8*20 7c 6*23 5c 5f 35*20 a 8*20 7c 8*23 7c 34*20 a 8*20 7c 8*23 7c 34*20 a 8*20 7c 8*23
  //   7c 34*20 a 8*20 7c 8*23 7c 34*20 a 8*20 7c 8*23 7c 34*20 a 8*20 7c 8*23 7c 34*20 a 8*20 7c 8*23 7c
  //   34*20 a 8*20 7c 8*23 7c 34*20 a 8*20 7c 8*23 7c 34*20 a 8*20 7c 8*23 7c 34*20 a 8*20 7c 8*23 7c
  //   34*20 a 8*20 7c 6*23 2f 36*20 a 8*20 7c 4*23 2f 38*20 a 8*20 7c 23 23 2f 40*20 a 8*20 7c 2f 42*20 a
  //   52*20 a 52*20 a 52*20 a 52*20
  //   FFRFL
  //   contents of rom_15 (hex, n*v repeats v):
  //   0 51*20 a 52*20 a 52*20 a 52*20 a 52*20 a 52*20 a 52*20 a 52*20 a 32*20 5f 2f 7c 17*20 a 30*20 5f 2f
  //   23 23 7c 17*20 a 29*20 2f 4*23 7c 17*20 a 28*20 7c 5*23 7c 17*20 a 28*20 7c 5*23 7c 17*20 a 28*20 7c
  //   5*23 7c 17*20 a 28*20 7c 5*23 7c 17*20 a 28*20 7c 5*23 7c 17*20 a 29*20 5c 4*23 7c 17*20 a 31*20 5c
  //   23 23 7c 17*20 a 33*20 5c 7c 17*20 a 52*20 a 52*20 a 52*20 a 52*20 a 52*20 a 52*20 a 52*20 a 52*20
  //   FFLFL
  //   contents of rom_16 (hex, n*v repeats v):
  //   0 51*20 a 52*20 a 52*20 a 52*20 a 52*20 a 52*20 a 52*20 a 52*20 a 17*20 7c 5c 5f 32*20 a 17*20 7c 23
  //   23 5c 5f 30*20 a 17*20 7c 4*23 5c 29*20 a 17*20 7c 5*23 7c 28*20 a 17*20 7c 5*23 7c 28*20 a 17*20 7c
  //   5*23 7c 28*20 a 17*20 7c 5*23 7c 28*20 a 17*20 7c 5*23 7c 28*20 a 17*20 7c 4*23 2f 29*20 a 17*20 7c
  //   23 23 2f 31*20 a 17*20 7c 2f 33*20 a 52*20 a 52*20 a 52*20 a 52*20 a 52*20 a 52*20 a 52*20 a 52*20
  //   contents of rom_17 (hex, n*v repeats v):
  //   0 76*23 a 23 74*20 23 a 23 74*20 23 a 23 74*20 23 a 23 26*20 5*5f 20 20 5f 40*20 23 a 23 25*20 7c 5f
  //   20 20 20 5f 7c 7c 20 7c 39*20 23 a 23 27*20 7c 20 7c 20 20 7c 20 7c 5f 5f 4*20 5f 5f 5f 30*20 23 a
  //   23 27*20 7c 20 7c 20 20 7c 20 27 5f 20 5c 20 20 2f 20 5f 20 5c 29*20 23 a 23 27*20 7c 20 7c 20 20 7c
  //   20 7c 20 7c 20 7c 7c 20 20 5f 5f 2f 29*20 23 a 23 27*20 5c 5f 2f 20 20 7c 5f 7c 20 7c 5f 7c 20 5c 5f
  //   5f 5f 7c 29*20 23 a 23 20 5f 5f 5f 20 20 5f 5f 5f 8*20 5f 7*20 5f 7*20 5f 40*20 23 a 23 20 7c 20 20
  //   5c 2f 20 20 7c 7*20 7c 20 7c 5*20 28 20 29 5*20 7c 20 7c 39*20 23 a 23 20 7c 20 2e 20 20 2e 20 7c 20
  //   20 5f 5f 5f 20 20 7c 20 7c 20 20 5f 5f 5f 7c 2f 20 5f 5f 5f 20 20 7c 20 7c 5f 5f 20 20 20 5f 20 20
  //   20 5f 20 20 5f 20 5f 5f 20 20 5f 20 5f 5f 20 20 5f 5f 5f 20 5f 5f 6*20 5f 5f 20 23 a 23 20 7c 20 7c
  //   5c 2f 7c 20 7c 20 2f 20 5f 20 5c 20 7c 20 7c 20 2f 20 5f 20 5c 20 2f 20 5f 5f 7c 20 7c 20 27 5f 20
  //   5c 20 7c 20 7c 20 7c 20 7c 7c 20 27 5f 5f 7c 7c 20 27 5f 5f 7c 2f 20 5f 20 5c 5c 20 5c 20 2f 5c 20
  //   2f 20 2f 20 23 a 23 20 7c 20 7c 20 20 7c 20 7c 7c 20 28 5f 29 20 7c 7c 20 7c 7c 20 20 5f 5f 2f 20 5c
  //   5f 5f 20 5c 20 7c 20 7c 5f 29 20 7c 7c 20 7c 5f 7c 20 7c 7c 20 7c 20 20 20 7c 20 7c 20 20 7c 20 28
  //   5f 29 20 7c 5c 20 56 20 20 56 20 2f 20 20 23 a 23 20 5c 5f 7c 20 20 7c 5f 2f 20 5c 5f 5f 5f 2f 20 7c
  //   5f 7c 20 5c 5f 5f 5f 7c 20 7c 5f 5f 5f 2f 20 7c 5f 2e 5f 5f 2f 20 20 5c 5f 5f 2c 5f 7c 7c 5f 7c 20
  //   20 20 7c 5f 7c 20 20 20 5c 5f 5f 5f 2f 20 20 5c 5f 2f 5c 5f 2f 20 20 20 23 a 23 74*20 23 a 23 74*20
  //   23 a 23 74*20 23 a 23 74*20 23 a 23 74*20 23 a 23 74*20 23 a 23 74*20 23 a 23 74*20 23 a 23 74*20 23
  //   a 23 74*20 23 a 23 74*20 23 a 23 74*20 23 a 23 74*20 23 a 23 74*20 23 a 23 74*20 23 a 23 74*20 23 a
  //   23 74*20 23 a 23 39*20 50 52 45 53 53 20 41 4e 59 20 4b 45 59 20 54 4f 20 43 4f 4e 54 49 4e 55 45 2e
  //   2e 2e 7*20 23 a 23 74*20 23 a 76*23 a 52*20
  //   contents of rom_18 (hex, n*v repeats v):
  //   0 76*23 a 23 74*20 23 a 23 74*20 23 a 23 74*20 23 a 23 74*20 23 a 23 74*20 23 a 23 74*20 23 a 23
  //   74*20 23 a 23 74*20 23 a 23 9*20 7c 14*20 7c 13*20 7c 24*20 7c 20 28 20 20 7c 20 20 29 20 20 23 a 23
  //   74*20 23 a 23 74*20 23 a 23 74*20 23 a 23 74*20 23 a 23 74*20 23 a 23 74*20 23 a 23 74*20 23 a 23
  //   74*20 23 a 23 74*20 23 a 23 4*20 65*2d 5*20 23 a 23 74*20 23 a 23 20*20 5e 24*20 2e 28*20 23 a 23
  //   8*20 2e 19*20 2e 10*20 2e 18*20 2e 7*20 2e 7*20 23 a 23 16*20 2e 17*20 2e 17*20 5e 7*20 2e 13*20 23
  //   a 23 23*20 2e 18*20 2e 31*20 23 a 23 6*20 2e 6*20 5e 16*20 5e 23*20 2e 19*20 23 a 23 23*20 2e 11*20
  //   2e 5*20 2e 20*20 5e 11*20 23 a 23 74*20 23 a 76*23 a 23 74*20 23 a 76*23 a 23 9*20 23 9*20 23 9*20
  //   23 9*20 23 9*20 23 20 48 50 20 7c 10*20 7c 28 20 20 2f 31 30 29 20 23 a 23 9*20 23 9*20 23 9*20 23
  //   9*20 23 9*20 23 20 53 54 20 7c 10*20 7c 28 20 20 2f 31 30 29 20 23 a 23 9*20 23 9*20 23 9*20 23 9*20
  //   23 9*20 23 20 48 47 20 7c 10*20 7c 28 20 20 2f 31 30 29 20 23 a 23 9*20 23 9*20 23 9*20 23 9*20 23
  //   9*20 23 24*20 23 a 76*23 a 52*20
  //   START SCREEN
  //   ATACK BOARD
endmodule

// Maps
module maps (
  input  [7:0] ADDR,
  input  [11:0] ELEM,
  output [11:0] Width,
  output [11:0] Height,
  output [7:0] Xpp,
  output [7:0] Ypp,
  output [7:0] DATA,
  output [11:0] LEN
);

  wire [7:0] mgeD0, undriven_4, undriven_5;
  wire [11:0] undriven, undriven_2, undriven_3;

  ROM #(.addrWidth(12)) rom_1 (.addr(ELEM), .data(mgeD0));  // open: sel
  Multiplexer #(.select(5), .width(8), .enable("false")) multiplexer_1 (
    .in0(mgeD0), .out(DATA), .sel(ADDR[4:0]));  // open: in1, in2, in3, in4, in5, in6, in7, in8, in9, in10, in11, in12, in13, in14, in15, in16, in17, in18, in19, in20, in21, in22, in23, in24, in25, in26, in27, in28, in29, in30, in31
  Multiplexer #(.select(5), .width(12), .enable("false")) multiplexer_2 (
    .in0(12'h99), .in30(undriven), .in31(undriven), .out(LEN), .sel(ADDR[4:0]));  // open: in1, in2, in3, in4, in5, in6, in7, in8, in9, in10, in11, in12, in13, in14, in15, in16, in17, in18, in19, in20, in21, in22, in23, in24, in25, in26, in27, in28, in29
  Multiplexer #(.select(5), .width(12), .enable("false")) multiplexer_3 (
    .in0(12'hb), .in30(undriven_2), .in31(undriven_2), .out(Width), .sel(ADDR[4:0]));  // open: in1, in2, in3, in4, in5, in6, in7, in8, in9, in10, in11, in12, in13, in14, in15, in16, in17, in18, in19, in20, in21, in22, in23, in24, in25, in26, in27, in28, in29
  Multiplexer #(.select(5), .width(12), .enable("false")) multiplexer_4 (
    .in0(12'h8), .in30(undriven_3), .in31(undriven_3), .out(Height), .sel(ADDR[4:0]));  // open: in1, in2, in3, in4, in5, in6, in7, in8, in9, in10, in11, in12, in13, in14, in15, in16, in17, in18, in19, in20, in21, in22, in23, in24, in25, in26, in27, in28, in29
  Multiplexer #(.select(5), .width(8), .enable("false")) multiplexer_5 (
    .in0(8'h3), .in30(undriven_4), .in31(undriven_4), .out(Xpp), .sel(ADDR[4:0]));  // open: in1, in2, in3, in4, in5, in6, in7, in8, in9, in10, in11, in12, in13, in14, in15, in16, in17, in18, in19, in20, in21, in22, in23, in24, in25, in26, in27, in28, in29
  Multiplexer #(.select(5), .width(8), .enable("false")) multiplexer_6 (
    .in0(8'h3), .in30(undriven_5), .in31(undriven_5), .out(Ypp), .sel(ADDR[4:0]));  // open: in1, in2, in3, in4, in5, in6, in7, in8, in9, in10, in11, in12, in13, in14, in15, in16, in17, in18, in19, in20, in21, in22, in23, in24, in25, in26, in27, in28, in29

  // Other names for the same wires on the sheet: mdeMux1[7:0] = DATA; mdeMuxl1[11:0] = LEN; mgeAddr1[4:0] = ADDR[4:0];
  //   mgeEl[11:0] = ELEM; mhMuxl1[11:0] = Height; mwMuxl1[11:0] = Width; mXMuxl1[7:0] = Xpp; mYMuxl1[7:0] = Ypp

  // Notes on the sheet:
  //   TEST MAP
  //   contents of rom_1 (hex, n*v repeats v):
  //   0 4 3 2 36*23 20 66 6a 61 20 6*23 20 23 23 20 32 6*23 20 20 23 23 20 36*23
endmodule

module printing_map (
  input  [7:0] Curr_char,
  input  [7:0] height_of_map,
  input  [7:0] length_of_map,
  input  in_4
);

  wire button_1_out, comparator_1_eq, comparator_2_eq, comparator_3_eq, comparator_3_lt;
  wire [7:0] adder_1_out, controlled_buffer_1_out, register_1_q, register_2_q;

  Adder adder_1 (.a(register_1_q), .b(8'h1), .out(adder_1_out));  // open: cin, cout
  Register register_1 (.D(adder_1_out), .Q(register_1_q), .clk(in_4), .clr(button_1_out));  // open: en
  Button button_1 (.out(button_1_out));
  Comparator comparator_1 (.a(8'h1), .b(register_1_q), .eq(comparator_1_eq));  // open: gt, lt
  Comparator comparator_2 (.a(8'h2), .b(register_1_q), .eq(comparator_2_eq));  // open: gt, lt
  Comparator comparator_3 (.a(8'h3), .b(register_1_q), .eq(comparator_3_eq), .lt(comparator_3_lt));  // open: gt
  Register y (.D(Curr_char), .en(comparator_1_eq), .clk(in_4));  // open: Q, clr
  Register x (.D(Curr_char), .en(comparator_2_eq), .clk(in_4));  // open: Q, clr
  Register Direction (.D(Curr_char), .en(comparator_3_eq), .clk(in_4));  // open: Q, clr
  Register register_2 (.D(controlled_buffer_1_out), .Q(register_2_q), .clk(in_4));  // open: en, clr
  assign controlled_buffer_1_out = comparator_3_lt ? Curr_char : 8'bz;  // Controlled_Buffer controlled_buffer_1

  // Other names for the same wires on the sheet: Clock = in_4; height[7:0] = height_of_map;
  //   length[7:0] = length_of_map
endmodule

module x_y__to_memory_elem_number (
  input  [11:0] H,
  input  [7:0] Y,
  input  [7:0] X,
  input  [11:0] START,
  output [11:0] ELEM
);

  wire [11:0] adder_1_out, bit_extender_1_out, bit_extender_2_out, multiplier_1_out;

  assign bit_extender_1_out = {{4{1'b0}}, Y};  // Bit_Extender bit_extender_1
  Multiplier #(.width(12)) multiplier_1 (.a(H), .b(bit_extender_1_out), .out(multiplier_1_out));  // open: cin, cout
  assign bit_extender_2_out = {{4{1'b0}}, X};  // Bit_Extender bit_extender_2
  Adder #(.width(12)) adder_1 (.a(multiplier_1_out), .b(bit_extender_2_out), .out(adder_1_out));  // open: cin, cout
  Adder #(.width(12)) adder_2 (.a(adder_1_out), .b(START), .out(ELEM));  // open: cin, cout
endmodule

module enemies (
  input  [1:0] ADDR,
  input  [7:0] ELEMIm,
  input  [7:0] ELEMNm,
  output [7:0] Img,
  output [7:0] Txt,
  output [7:0] HP,
  output [7:0] DMG
);

  wire [7:0] EnImEl1, EnImEl1txt, EnImEl2, EnImEl2txt, EnImEl3, EnImEl3txt, EnImEl4, EnImEl4txt;

  ROM rom_1 (.addr(ELEMIm), .data(EnImEl1));  // open: sel
  ROM rom_2 (.addr(ELEMIm), .data(EnImEl2));  // open: sel
  ROM rom_3 (.addr(ELEMIm), .data(EnImEl3));  // open: sel
  ROM rom_4 (.addr(ELEMIm), .data(EnImEl4));  // open: sel
  Multiplexer #(.select(2), .width(8), .enable("false")) multiplexer_1 (
    .in0(EnImEl1), .in1(EnImEl2), .in2(EnImEl3), .in3(EnImEl4), .out(Img), .sel(ADDR));
  Multiplexer #(.select(2), .width(8), .enable("false")) multiplexer_2 (
    .in0(EnImEl1txt), .in1(EnImEl2txt), .in2(EnImEl3txt), .in3(EnImEl4txt), .out(Txt), .sel(ADDR));
  Multiplexer #(.select(2), .width(8), .disabled(0), .enable("false")) multiplexer_3 (
    .in0(8'h24), .in1(8'h12), .in2(8'h62), .in3(8'h36), .out(HP), .sel(ADDR));
  Multiplexer #(.select(2), .width(8), .disabled(0), .enable("false")) multiplexer_4 (
    .in0(8'h5), .in1(8'h3), .in2(8'h24), .in3(8'h12), .out(DMG), .sel(ADDR));
  ROM rom_5 (.addr(ELEMIm), .data(EnImEl1txt));  // open: sel
  ROM rom_6 (.addr(ELEMIm), .data(EnImEl2txt));  // open: sel
  ROM rom_7 (.addr(ELEMIm), .data(EnImEl3txt));  // open: sel
  ROM rom_8 (.addr(ELEMIm), .data(EnImEl4txt));  // open: sel

  // Other names for the same wires on the sheet: enaddr1[1:0] = ADDR; EnImEl[7:0] = ELEMIm; EnImEltxt[7:0] = ELEMNm

  // Notes on the sheet:
  //   rat
  //   mouse
  //   ferret
  //   snake
  //   contents of rom_1 (hex, n*v repeats v):
  //   15*20 35 64 6d 67 2e 9*20 2f 5c 5f 2f 5c 16*20 28 20 6f 20 6f 20 29 15*20 2f 20 20 56 20 20 5c 15*20
  //   2f 20 3e 20 20 3c 20 20 5c 12*20 28 20 2f 5*20 5c 20 29 20 20 20 7c 8*20 5c 5f 20 4*2d 20 5f 2f 5f
  //   5f 5f 2f 24*20
  //   contents of rom_2 (hex, n*v repeats v):
  //   13*20 33 64 6d 67 2e 13*20 2f 5e 5c 5e 5c 5f 10*20 2f 4*20 7c 5*20 6f 5c 5f 7*20 7c 4*20 2f 7*20 5f
  //   2f 7*20 5c 20 20 20 2f 6*20 5f 5f 3e 9*20 5c 5f 5f 7c 20 20 20 5f 5f 5f 29 14*20 5c 5f 5f 5f 7c 5c
  //   5f 5f 30*20
  //   contents of rom_3 (hex, n*v repeats v):
  //   14*20 32 30 64 6d 67 2e 8*20 2f 29 5*5f 28 5c 12*20 28 2f 20 6f 20 20 20 6f 20 5c 29 11*20 7c 4*20
  //   4f 4*20 7c 12*20 5c 20 20 2d 5e 2d 20 20 2f 13*20 2f 7*20 5c 12*20 7c 9*20 7c 28*20
  //   contents of rom_4 (hex, n*v repeats v):
  //   14*20 31 30 64 6d 67 2e 4*20 2e 2d 2e 17*20 3e 2d 30 5f 30 29 29 20 20 7c 20 20 2f 20 29 11*20 2f 2f
  //   20 20 20 7c 2e 2f 5f 5f 29 10*20 28 28 5f 2e 2d 2d 27 20 5f 20 20 27 2e 10*20 60 2d 5f 5f 2d 2d 27
  //   20 27 2d 2e 20 29 16*20 5f 5f 2d 2d 27 28*20
  //   rat
  //   mouse
  //   ferret
  //   snake
  //   8x22 = 176
  //   20 chars name len
  //   contents of rom_5 (hex, n*v repeats v):
  //   6*20 53 43 41 52 59 20 52 41 54 5*20
  //   contents of rom_6 (hex, n*v repeats v):
  //   5*20 45 56 49 4c 20 4d 4f 55 53 45 5*20
  //   contents of rom_7 (hex, n*v repeats v):
  //   4*20 43 55 54 45 20 46 45 52 52 45 54 5*20
  //   contents of rom_8 (hex, n*v repeats v):
  //   4*20 4c 49 54 54 4c 45 20 53 4e 41 4b 45 4*20
endmodule
